// Logisim project QR.circ as structural Verilog: 1 circuit, main circuit main
module main (
);

  DotMatrix #(.inputtype("row"), .matrixcols(29), .matrixrows(29)) dotmatrix_1 (
    .row0(29'h1fc4637f), .row1(29'h1040ad41), .row2(29'h17494d5d), .row3(29'h1745445d), .row4(29'h1744ec5d),
    .row5(29'h105ea241), .row6(29'h1fd5557f), .row7(29'h22f00), .row8(29'h12def2a0), .row9(29'h1c9d3149),
    .row10(29'hfcd9f9e), .row11(29'hf399716), .row12(29'h1e6973cb), .row13(29'h1a3b8d80), .row14(29'h72c97f),
    .row15(29'h14a619ca), .row16(29'h3f58922), .row17(29'h1d13f9e9), .row18(29'hbf148b3),
    .row19(29'h1d3c4db3), .row20(29'hece33f4), .row21(29'h184f17), .row22(29'h1fc31552),
    .row23(29'h1059411d), .row24(29'h17463df3), .row25(29'h175d0f7e), .row26(29'h174c8b1d),
    .row27(29'h104f6b92), .row28(29'h1fd2e9fa));
endmodule
