// Logisim project 000.main (lagaet).circ as structural Verilog
module main (
  input  [4:0] minus_2_line,
  input  [5:0] num_1,
  input  [5:0] num_1_2,
  input  [4:0] minus_1_line,
  input  [5:0] num_2,
  input  [5:0] num_2_2,
  input  [4:0] cur_line,
  input  [5:0] num_3,
  input  [5:0] num_3_2,
  input  [4:0] plus_1_line,
  input  [5:0] num_4,
  input  [5:0] num_4_2,
  input  [4:0] plus_2_line,
  input  [5:0] num_5,
  input  [5:0] num_5_2
);

  wire cdm16_1_p1, cdm16_1_p2, cdm16_1_p4, cdm16_1_p5, cdm16_1_p6, cdm16_1_p7, cdm16_1_p8, cdm16_1_p9,
       cdm16_1_p10, cdm16_1_p11, cdm16_1_p12, clock_1_out, clock_2_out, mem, not_1_out, read, word;
  wire [15:0] address_bus, cdm16_1_p17, cdm16_1_p18, data_bus;

  // Debugger debugger_1: pin names not known
  // Probe on cdm16_1_p2
  // Probe on cdm16_1_p1
  // Probe on cdm16_1_p5
  // Probe on cdm16_1_p4
  Clock clock_1 (.out(clock_1_out));
  // Probe on cdm16_1_p6
  // Probe on cdm16_1_p7
  // cdm16 cdm16_1: pin names not known; wires that end beside it: cdm16_1_p1, cdm16_1_p2, clock_1_out, cdm16_1_p4, cdm16_1_p5, cdm16_1_p6, cdm16_1_p7, cdm16_1_p8, cdm16_1_p9, cdm16_1_p10, cdm16_1_p11, cdm16_1_p12, mem, read, word, address_bus, cdm16_1_p17, cdm16_1_p18
  // Probe on cdm16_1_p8
  // Probe on cdm16_1_p9
  assign data_bus = not_1_out ? cdm16_1_p17 : 16'bz;  // Controlled_Buffer controlled_buffer_1
  not not_1 (not_1_out, read);
  assign cdm16_1_p18 = read ? data_bus : 16'bz;  // Controlled_Buffer controlled_buffer_2
  // Probe on cdm16_1_p10
  // Probe on cdm16_1_p11
  // Probe on cdm16_1_p12
  Clock clock_2 (.out(clock_2_out));
  // RAM ram_1: pin names not known; wires that end beside it: address_bus, word, mem, clock_2_out, read, data_bus

  // Other names for the same wires on the sheet: birth[29:0] = {num_5, num_4, num_3, num_2, num_1};
  //   lookAt[24:0] = {plus_2_line, plus_1_line, cur_line, minus_1_line, minus_2_line};
  //   save[29:0] = {num_5_2, num_4_2, num_3_2, num_2_2, num_1_2}

  // Notes on the sheet:
  //   look at
  //   Set up rules
  //   birth
  //   save
endmodule

module alive (
  input  [24:0] neighbours,
  input  [24:0] look_at,
  input  clock,
  input  [29:0] B___birth,
  input  [1:0] input_state,
  input  [29:0] S___save,
  output alive
);

  wire and_2_out, and_3_out, can_cell_born_out, can_cell_save_out, comparator_1_eq, comparator_2_eq,
       comparator_3_eq, comparator_4_eq, comparator_5_eq, comparator_6_eq, comparator_7_eq, comparator_8_eq,
       comparator_9_eq, comparator_10_eq, multiplexer_1_out, multiplexer_2_out, not_1_out, not_2_out,
       or_1_out, or_2_out, or_3_out;
  wire [4:0] B1, B2, B3, B4, B5, newCnt, S1, S2, S3, S4, S5;
  wire [24:0] and_1_out, undriven;

  // Probe on newCnt
  BitAdder #(.width(25)) bitadder_1 (.in0(and_1_out), .out(newCnt));
  assign and_1_out = neighbours & look_at;  // AND_Gate and_1, 25 bits wide
  BS_helper bs_helper_1 (.input_6_bit(B___birth[5:0]), .output_5_bit(B1));
  BS_helper bs_helper_2 (.input_6_bit(B___birth[11:6]), .output_5_bit(B2));
  BS_helper bs_helper_3 (.input_6_bit(B___birth[17:12]), .output_5_bit(B3));
  BS_helper bs_helper_4 (.input_6_bit(B___birth[23:18]), .output_5_bit(B4));
  BS_helper bs_helper_5 (.input_6_bit(B___birth[29:24]), .output_5_bit(B5));
  BS_helper bs_helper_6 (.input_6_bit(S___save[5:0]), .output_5_bit(S1));
  BS_helper bs_helper_7 (.input_6_bit(S___save[11:6]), .output_5_bit(S2));
  BS_helper bs_helper_8 (.input_6_bit(S___save[17:12]), .output_5_bit(S3));
  BS_helper bs_helper_9 (.input_6_bit(S___save[23:18]), .output_5_bit(S4));
  BS_helper bs_helper_10 (.input_6_bit(S___save[29:24]), .output_5_bit(S5));
  // Probe on nothing
  // Probe on nothing
  // Probe on nothing
  // Probe on nothing
  // Probe on nothing
  // Probe on nothing
  // Probe on nothing
  // Probe on nothing
  // Probe on nothing
  // Probe on nothing
  // Probe on undriven[4:0]
  // Probe on undriven[9:5]
  // Probe on undriven[14:10]
  // Probe on undriven[19:15]
  // Probe on undriven[24:20]
  Comparator #(.width(5), .mode("unsigned")) comparator_1 (.a(newCnt), .b(B1), .eq(comparator_1_eq));  // open: gt, lt
  Comparator #(.width(5), .mode("unsigned")) comparator_2 (.a(newCnt), .b(B2), .eq(comparator_2_eq));  // open: gt, lt
  Comparator #(.width(5), .mode("unsigned")) comparator_3 (.a(newCnt), .b(B3), .eq(comparator_3_eq));  // open: gt, lt
  Comparator #(.width(5), .mode("unsigned")) comparator_4 (.a(newCnt), .b(B4), .eq(comparator_4_eq));  // open: gt, lt
  Comparator #(.width(5), .mode("unsigned")) comparator_5 (.a(newCnt), .b(B5), .eq(comparator_5_eq));  // open: gt, lt
  Comparator #(.width(5), .mode("unsigned")) comparator_6 (.a(newCnt), .b(S1), .eq(comparator_6_eq));  // open: gt, lt
  Comparator #(.width(5), .mode("unsigned")) comparator_7 (.a(newCnt), .b(S2), .eq(comparator_7_eq));  // open: gt, lt
  Comparator #(.width(5), .mode("unsigned")) comparator_8 (.a(newCnt), .b(S3), .eq(comparator_8_eq));  // open: gt, lt
  Comparator #(.width(5), .mode("unsigned")) comparator_9 (.a(newCnt), .b(S4), .eq(comparator_9_eq));  // open: gt, lt
  Comparator #(.width(5), .mode("unsigned")) comparator_10 (.a(newCnt), .b(S5), .eq(comparator_10_eq));  // open: gt, lt
  or can_cell_born (can_cell_born_out, comparator_1_eq, comparator_2_eq, comparator_3_eq, comparator_4_eq, comparator_5_eq);
  or can_cell_save (can_cell_save_out, comparator_6_eq, comparator_7_eq, comparator_8_eq, comparator_9_eq, comparator_10_eq);
  Multiplexer #(.disabled(0)) multiplexer_1 (
    .in0(can_cell_born_out), .in1(can_cell_save_out), .out(multiplexer_1_out), .sel(neighbours[12]));  // open: en
  not not_1 (not_1_out, input_state[0]);
  or or_1 (or_1_out, input_state[1], input_state[0]);
  and and_2 (and_2_out, not_2_out, input_state[0]);
  or or_2 (or_2_out, and_2_out, and_3_out);
  and and_3 (and_3_out, not_1_out, multiplexer_1_out);
  or or_3 (or_3_out, or_1_out, clock);
  not not_2 (not_2_out, alive);
  Register #(.width(1), .trigger("falling")) register_1 (
    .D(multiplexer_2_out), .Q(alive), .clk(or_3_out));  // open: en, clr
  Multiplexer #(.disabled(0)) multiplexer_2 (
    .in0(or_2_out), .in1(input_state[0]), .out(multiplexer_2_out), .sel(input_state[1]));  // open: en

  // Other names for the same wires on the sheet: cur = neighbours[12]

  // Notes on the sheet:
  //   B___birth: pull=up
  //   look_at: pull=down
  //   input_state: pull=down
  //   neighbours: pull=down
  //   S___save: pull=up
  //   floating → 0
  //   floating → 0
  //   floating → 1
  //   floating → 1
  //   DEBUG TOOLS
  //   DEBUG TOO↑↓
  //   if cur cell is dead (= 0) try birth,
  //   alive (= 1) — try save
  //   invert?
  //   1 (high bit)
  //   0 (low bit)
  //   00 — by rules
  //   01 — invert
  //   10 — set DEAD
  //   11 — set ALIVE
endmodule

module BS_helper (
  input  [5:0] input_6_bit,
  output [4:0] output_5_bit
);

  Multiplexer #(.width(5)) multiplexer_1 (
    .in0(input_6_bit[4:0]), .in1({5{1'b1}}), .out(output_5_bit), .sel(input_6_bit[5]));  // open: en
endmodule

module STATE_helper (
  input  [1:0] input_state,
  input  i,
  input  j,
  output [1:0] output_state
);

  wire [1:1] and_2_out;

  assign output_state = input_state & {2{and_2_out[1]}};  // AND_Gate and_1, 2 bits wide
  and and_2 (and_2_out[1], i, j);
endmodule

module game (
  input  [4:0] i,
  input  [4:0] j,
  input  newState,
  input  pause,
  input  change,
  input  [4:0] _0_line,
  input  [4:0] _1_line,
  input  [4:0] _2_line,
  input  [4:0] _3_line,
  input  [4:0] _4_line,
  input  [4:0] minus_2_line,
  input  [5:0] num_1,
  input  [5:0] num_1_2,
  input  [4:0] minus_1_line,
  input  [5:0] num_2,
  input  [5:0] num_2_2,
  input  [4:0] cur_line,
  input  [5:0] num_3,
  input  [5:0] num_3_2,
  input  [4:0] plus_1_line,
  input  [5:0] num_4,
  input  [5:0] num_4_2,
  input  [4:0] plus_2_line,
  input  [5:0] num_5,
  input  [5:0] num_5_2
);

  wire clock, i0, i1, i2, i3, i4, i5, i6, i7, i8, i9, i10, i11, i12, i13, i14, i15, i16, i17, i18, i19, i20,
       i21, i22, i23, i24, i25, i26, i27, i28, i29, i30, i31, j0, j1, j2, j3, j4, j5, j6, j7, j8, j9, j10,
       j11, j12, j13, j14, j15, j16, j17, j18, j19, j20, j21, j22, j23, j24, j25, j26, j27, j28, j29, j30,
       j31, minus_01_00, minus_01_01, minus_01_01_t, minus_01_02, minus_01_02_t, minus_01_03, minus_02_00,
       minus_02_01, minus_02_01_t, minus_02_02, minus_02_02_t, minus_02_03, pause__0, plus_00_00, plus_00_01,
       plus_00_01_t, plus_00_02, plus_00_02_t, plus_00_03, plus_01_00, plus_01_01, plus_01_01_t, plus_01_02,
       plus_01_02_t, plus_01_03, plus_02_00, plus_02_01, plus_02_01_t, plus_02_02, plus_02_02_t, plus_02_03;
  wire [4:0] undriven, undriven_2, undriven_3, undriven_4, undriven_5;
  wire [24:0] neighbours_1_neighbours, neighbours_2_neighbours;

  DotMatrix #(.inputtype("row"), .matrixrows(5)) dotmatrix_1 (
    .row0(undriven), .row1(undriven_2), .row2(undriven_3), .row3(undriven_5), .row4(undriven_4));
  Decoder #(.select(5)) decoder_1 (
    .out0(i0), .out1(i1), .out2(i2), .out3(i3), .out4(i4), .out5(i5), .out6(i6), .out7(i7), .out8(i8),
    .out9(i9), .out10(i10), .out11(i11), .out12(i12), .out13(i13), .out14(i14), .out15(i15), .out16(i16),
    .out17(i17), .out18(i18), .out19(i19), .out20(i20), .out21(i21), .out22(i22), .out23(i23), .out24(i24),
    .out25(i25), .out26(i26), .out27(i27), .out28(i28), .out29(i29), .out30(i30), .out31(i31), .sel(i));  // open: en
  not not_1 (pause__0, pause);
  Decoder #(.select(5)) decoder_2 (
    .out0(j0), .out1(j1), .out2(j2), .out3(j3), .out4(j4), .out5(j5), .out6(j6), .out7(j7), .out8(j8),
    .out9(j9), .out10(j10), .out11(j11), .out12(j12), .out13(j13), .out14(j14), .out15(j15), .out16(j16),
    .out17(j17), .out18(j18), .out19(j19), .out20(j20), .out21(j21), .out22(j22), .out23(j23), .out24(j24),
    .out25(j25), .out26(j26), .out27(j27), .out28(j28), .out29(j29), .out30(j30), .out31(j31), .sel(j));  // open: en
  Clock clock_1 (.out(clock));
  // Probe on num_1
  // Probe on num_2
  // Probe on num_3
  // Probe on num_4
  // Probe on num_5
  // AND_Gate and_1 has open pins: in0=i0, in1=j0, out=open
  // Probe on num_1_2
  // Probe on num_2_2
  // Probe on num_3_2
  // Probe on num_4_2
  // Probe on num_5_2
  neighbours neighbours_1 (
    ._00_00(minus_02_02_t), ._00_01(minus_02_01_t), ._00_02(minus_02_00), ._00_03(minus_02_01),
    ._00_04(minus_02_02), ._01_00(minus_01_02_t), ._01_01(minus_01_01_t), ._01_02(minus_01_00),
    ._01_03(minus_01_01), ._01_04(minus_01_02), ._02_00(plus_00_02_t), ._02_01(plus_00_01_t),
    ._02_02(plus_00_00), ._02_03(plus_00_01), ._02_04(plus_00_02), ._03_00(plus_01_02_t),
    ._03_01(plus_01_01_t), ._03_02(plus_01_00), ._03_03(plus_01_01), ._03_04(plus_01_02),
    ._04_00(plus_02_02_t), ._04_01(plus_02_01_t), ._04_02(plus_02_00), ._04_03(plus_02_01),
    ._04_04(plus_02_02), .neighbours(neighbours_1_neighbours));
  alive alive_1 (
    .neighbours(neighbours_1_neighbours),
    .look_at({plus_2_line, plus_1_line, cur_line, minus_1_line, minus_2_line}),
    .B___birth({num_5, num_4, num_3, num_2, num_1}),
    .S___save({num_5_2, num_4_2, num_3_2, num_2_2, num_1_2}), .alive(plus_00_00), .clock(clock));  // open: input_state
  // AND_Gate and_2 has open pins: in0=i0, in1=j0, in2=change, out=open
  neighbours neighbours_2 (
    ._00_00(minus_02_01_t), ._00_01(minus_02_00), ._00_02(minus_02_01), ._00_03(minus_02_02),
    ._00_04(minus_02_03), ._01_00(minus_01_01_t), ._01_01(minus_01_00), ._01_02(minus_01_01),
    ._01_03(minus_01_02), ._01_04(minus_01_03), ._02_00(plus_00_01_t), ._02_01(plus_00_00),
    ._02_02(plus_00_01), ._02_03(plus_00_02), ._02_04(plus_00_03), ._03_00(plus_01_01_t),
    ._03_01(plus_01_00), ._03_02(plus_01_01), ._03_03(plus_01_02), ._03_04(plus_01_03),
    ._04_00(plus_02_01_t), ._04_01(plus_02_00), ._04_02(plus_02_01), ._04_03(plus_02_02),
    ._04_04(plus_02_03), .neighbours(neighbours_2_neighbours));
  // AND_Gate and_3 has open pins: in0=i0, in1=j1, in2=change, out=open
  alive alive_2 (
    .neighbours(neighbours_2_neighbours),
    .look_at({plus_2_line, plus_1_line, cur_line, minus_1_line, minus_2_line}),
    .B___birth({num_5, num_4, num_3, num_2, num_1}),
    .S___save({num_5_2, num_4_2, num_3_2, num_2_2, num_1_2}), .alive(plus_00_01), .clock(clock));  // open: input_state
  // AND_Gate and_4 is placed but not wired

  // Other names for the same wires on the sheet: birth[29:0] = {num_5, num_4, num_3, num_2, num_1}; chng = change;
  //   lookAt[24:0] = {plus_2_line, plus_1_line, cur_line, minus_1_line, minus_2_line}; NS = newState;
  //   save[29:0] = {num_5_2, num_4_2, num_3_2, num_2_2, num_1_2}

  // Notes on the sheet:
  //   look at
  //   Set up rules
  //   birth
  //   save
endmodule

module example (
  input  [4:0] minus_2_line,
  input  [4:0] in_2,
  input  [4:0] minus_1_line,
  input  [4:0] in_4,
  input  [4:0] cur_line,
  input  [4:0] in_6,
  input  [4:0] _1_line,
  input  [4:0] in_8,
  input  [4:0] _2_line,
  input  [4:0] in_10,
  input  [5:0] B__S,
  input  [5:0] B1,
  input  [5:0] S1,
  input  [5:0] B2,
  input  [5:0] S2,
  input  [5:0] B3,
  input  [5:0] S3,
  input  [5:0] B4,
  input  [5:0] S4,
  input  [5:0] B5,
  input  [5:0] S5,
  input  clock
);

  wire [11:0] undriven, undriven_2;
  wire [12:12] newState;

  DotMatrix #(.inputtype("row"), .matrixrows(5)) dotmatrix_1 (
    .row0(in_2), .row1(in_4), .row2(in_6), .row3(in_8), .row4(in_10));
  alive alive_1 (
    .neighbours({in_10, in_8, in_6, in_4, in_2}),
    .look_at({_2_line, _1_line, cur_line, minus_1_line, minus_2_line}), .B___birth({B5, B4, B3, B2, B1}),
    .S___save({S5, S4, S3, S2, S1}), .alive(newState[12]), .clock(clock));  // open: input_state
  // Probe on in_2
  // Probe on in_4
  // Probe on {in_6[4:3], newState[12], in_6[1:0]}
  // Probe on in_8
  // Probe on in_10
  DotMatrix #(.inputtype("row"), .matrixrows(5)) dotmatrix_2 (
    .row0(in_2), .row1(in_4), .row2({in_6[4:3], newState[12], in_6[1:0]}), .row3(in_8), .row4(in_10));
  // Probe on undriven[4:0]
  // Probe on undriven[9:5]
  // Probe on {undriven_2[1:0], 1'b0, undriven[11:10]}
  // Probe on undriven_2[6:2]
  // Probe on undriven_2[11:7]

  // Other names for the same wires on the sheet: birth[29:0] = {B5, B4, B3, B2, B1};
  //   look_at[24:0] = {_2_line, _1_line, cur_line, minus_1_line, minus_2_line};
  //   neighbours[24:0] = {in_10, in_8, in_6, in_4, in_2};
  //   newState (some bits) = {in_10, in_8, in_6[4:3], in_6[1:0], in_4, in_2}; save[29:0] = {S5, S4, S3, S2, S1}

  // Notes on the sheet:
  //   in_2: pull=down
  //   in_10: pull=down
  //   in_4: pull=down
  //   in_8: pull=down
  //   in_6: pull=down
  //   old state
  //   Old state (You can edit)
  //   Old state
  //   How to use?
  //   New state
  //   New state
  //   How to watch?
  //   X is cell's neighbours
  //   0 is current cell
  //   1) look at 3x3
  //   2) B3/S23
  //   B – birth
  //   STANDART RULES:
  //   ↓ 0 – use number in rules, 1 — don't use
  //   ↑ ↑ ↑ ↑ ↑ binary number from 0 to 25
  //   Look at
  //   You can choose up to 5 numbers from 0 to 25
  //   S – save
endmodule

module neighbours (
  input  _00_00,
  input  _00_01,
  input  _00_02,
  input  _00_03,
  input  _00_04,
  input  _01_00,
  input  _01_01,
  input  _01_02,
  input  _01_03,
  input  _01_04,
  input  _02_00,
  input  _02_01,
  input  _02_02,
  input  _02_03,
  input  _02_04,
  input  _03_00,
  input  _03_01,
  input  _03_02,
  input  _03_03,
  input  _03_04,
  input  _04_00,
  input  _04_01,
  input  _04_02,
  input  _04_03,
  input  _04_04,
  output [24:0] neighbours
);


  assign neighbours = {_04_00, _04_01, _04_02, _04_03, _04_04, _03_00, _03_01, _03_02, _03_03, _03_04, _02_00, _02_01, _02_02, _02_03, _02_04, _01_00, _01_01, _01_02, _01_03, _01_04, _00_00, _00_01, _00_02, _00_03, _00_04};
endmodule

module line (
  input  [31:0] J,
  input  [31:0] minus_2_line,
  input  [31:0] minus_1_line,
  input  [31:0] _1_line,
  input  [31:0] _2_line,
  input  I,
  input  Torus,
  input  [1:0] input_state,
  output [31:0] _0_line__out__2,
  output [31:0] _0_line__out__1,
  output [31:0] display,
  output [31:0] _0_line__out__1_2,
  output [31:0] _0_line__out__2_2
);

  wire clock, minus_01_00, minus_01_01, minus_01_01_t, minus_01_02, minus_01_02_t, minus_01_03, minus_01_04,
       minus_01_05, minus_01_06, minus_01_07, minus_01_08, minus_01_09, minus_01_10, minus_01_11,
       minus_01_12, minus_01_13, minus_01_14, minus_01_15, minus_01_16, minus_01_17, minus_01_18,
       minus_01_19, minus_01_20, minus_01_21, minus_01_22, minus_01_23, minus_01_24, minus_01_25,
       minus_01_26, minus_01_27, minus_01_28, minus_01_29, minus_01_30, minus_01_31, minus_01_32,
       minus_01_33, minus_02_01_t, minus_02_02_t, minus_02_32, minus_02_33, plus_00_01_t, plus_00_02_t,
       plus_00_32, plus_00_33, plus_01_01_t, plus_01_02_t, plus_01_32, plus_01_33, plus_02_01_t,
       plus_02_02_t, plus_02_32, plus_02_33;
  wire [1:0] state_helper_1_output_state, state_helper_2_output_state, state_helper_3_output_state,
       state_helper_4_output_state, state_helper_5_output_state, state_helper_6_output_state,
       state_helper_7_output_state, state_helper_8_output_state, state_helper_9_output_state,
       state_helper_10_output_state, state_helper_11_output_state, state_helper_12_output_state,
       state_helper_13_output_state, state_helper_14_output_state, state_helper_15_output_state,
       state_helper_16_output_state, state_helper_17_output_state, state_helper_18_output_state,
       state_helper_19_output_state, state_helper_20_output_state, state_helper_21_output_state,
       state_helper_22_output_state, state_helper_23_output_state, state_helper_24_output_state,
       state_helper_25_output_state, state_helper_26_output_state, state_helper_27_output_state,
       state_helper_28_output_state, state_helper_29_output_state, state_helper_30_output_state,
       state_helper_31_output_state, state_helper_32_output_state;
  wire [24:0] lookAt, neighbours_1_neighbours, neighbours_2_neighbours, neighbours_3_neighbours,
       neighbours_4_neighbours, neighbours_5_neighbours, neighbours_6_neighbours, neighbours_7_neighbours,
       neighbours_8_neighbours, neighbours_9_neighbours, neighbours_10_neighbours, neighbours_11_neighbours,
       neighbours_12_neighbours, neighbours_13_neighbours, neighbours_14_neighbours,
       neighbours_15_neighbours, neighbours_16_neighbours, neighbours_17_neighbours,
       neighbours_18_neighbours, neighbours_19_neighbours, neighbours_20_neighbours,
       neighbours_21_neighbours, neighbours_22_neighbours, neighbours_23_neighbours,
       neighbours_24_neighbours, neighbours_25_neighbours, neighbours_26_neighbours,
       neighbours_27_neighbours, neighbours_28_neighbours, neighbours_29_neighbours,
       neighbours_30_neighbours, neighbours_31_neighbours, neighbours_32_neighbours;
  wire [29:0] birth, save;

  neighbours neighbours_1 (
    ._00_00(minus_02_02_t), ._00_01(minus_02_01_t), ._00_02(minus_1_line[0]), ._00_03(minus_1_line[1]),
    ._00_04(minus_1_line[2]), ._01_00(minus_01_02_t), ._01_01(minus_01_01_t), ._01_02(minus_01_00),
    ._01_03(minus_01_01), ._01_04(minus_01_02), ._02_00(plus_00_02_t), ._02_01(plus_00_01_t),
    ._02_02(_0_line__out__1[0]), ._02_03(_0_line__out__1[1]), ._02_04(_0_line__out__1[2]),
    ._03_00(plus_01_02_t), ._03_01(plus_01_01_t), ._03_02(_1_line[0]), ._03_03(_1_line[1]),
    ._03_04(_1_line[2]), ._04_00(plus_02_02_t), ._04_01(plus_02_01_t), ._04_02(_2_line[0]),
    ._04_03(_2_line[1]), ._04_04(_2_line[2]), .neighbours(neighbours_1_neighbours));
  and and_1 (minus_02_32, minus_1_line[0], Torus);
  and and_2 (minus_02_33, minus_1_line[1], Torus);
  and and_3 (minus_02_01_t, minus_1_line[31], Torus);
  and and_4 (minus_02_02_t, minus_1_line[30], Torus);
  alive alive_1 (
    .neighbours(neighbours_1_neighbours), .look_at(lookAt), .B___birth(birth), .S___save(save),
    .alive(_0_line__out__1[0]), .input_state(state_helper_1_output_state), .clock(clock));
  STATE_helper state_helper_1 (.input_state(input_state), .output_state(state_helper_1_output_state), .i(I), .j(J[0]));
  and and_5 (minus_01_32, minus_01_00, Torus);
  and and_6 (minus_01_33, minus_01_01, Torus);
  and and_7 (minus_01_01_t, minus_01_31, Torus);
  and and_8 (minus_01_02_t, minus_01_30, Torus);
  neighbours neighbours_2 (
    ._00_00(minus_02_01_t), ._00_01(minus_1_line[0]), ._00_02(minus_1_line[1]), ._00_03(minus_1_line[2]),
    ._00_04(minus_1_line[3]), ._01_00(minus_01_01_t), ._01_01(minus_01_00), ._01_02(minus_01_01),
    ._01_03(minus_01_02), ._01_04(minus_01_03), ._02_00(plus_00_01_t), ._02_01(_0_line__out__1[0]),
    ._02_02(_0_line__out__1[1]), ._02_03(_0_line__out__1[2]), ._02_04(_0_line__out__1[3]),
    ._03_00(plus_01_01_t), ._03_01(_1_line[0]), ._03_02(_1_line[1]), ._03_03(_1_line[2]),
    ._03_04(_1_line[3]), ._04_00(plus_02_01_t), ._04_01(_2_line[0]), ._04_02(_2_line[1]),
    ._04_03(_2_line[2]), ._04_04(_2_line[3]), .neighbours(neighbours_2_neighbours));
  alive alive_2 (
    .neighbours(neighbours_2_neighbours), .look_at(lookAt), .B___birth(birth), .S___save(save),
    .alive(_0_line__out__1[1]), .input_state(state_helper_2_output_state), .clock(clock));
  STATE_helper state_helper_2 (.input_state(input_state), .output_state(state_helper_2_output_state), .i(I), .j(J[1]));
  and and_9 (plus_01_32, _1_line[0], Torus);
  and and_10 (plus_01_33, _1_line[1], Torus);
  and and_11 (plus_01_01_t, _1_line[31], Torus);
  and and_12 (plus_01_02_t, _1_line[30], Torus);
  and and_13 (plus_02_32, _2_line[0], Torus);
  and and_14 (plus_02_33, _2_line[1], Torus);
  and and_15 (plus_02_01_t, _2_line[31], Torus);
  and and_16 (plus_02_02_t, _2_line[30], Torus);
  neighbours neighbours_3 (
    ._00_00(minus_1_line[0]), ._00_01(minus_1_line[1]), ._00_02(minus_1_line[2]), ._00_03(minus_1_line[3]),
    ._00_04(minus_1_line[4]), ._01_00(minus_01_00), ._01_01(minus_01_01), ._01_02(minus_01_02),
    ._01_03(minus_01_03), ._01_04(minus_01_04), ._02_00(_0_line__out__1[0]), ._02_01(_0_line__out__1[1]),
    ._02_02(_0_line__out__1[2]), ._02_03(_0_line__out__1[3]), ._02_04(_0_line__out__1[4]),
    ._03_00(_1_line[0]), ._03_01(_1_line[1]), ._03_02(_1_line[2]), ._03_03(_1_line[3]), ._03_04(_1_line[4]),
    ._04_00(_2_line[0]), ._04_01(_2_line[1]), ._04_02(_2_line[2]), ._04_03(_2_line[3]), ._04_04(_2_line[4]),
    .neighbours(neighbours_3_neighbours));
  alive alive_3 (
    .neighbours(neighbours_3_neighbours), .look_at(lookAt), .B___birth(birth), .S___save(save),
    .alive(_0_line__out__1[2]), .input_state(state_helper_3_output_state), .clock(clock));
  STATE_helper state_helper_3 (.input_state(input_state), .output_state(state_helper_3_output_state), .i(I), .j(J[2]));
  and and_17 (plus_00_32, _0_line__out__1[0], Torus);
  and and_18 (plus_00_33, _0_line__out__1[1], Torus);
  and and_19 (plus_00_01_t, _0_line__out__1[31], Torus);
  and and_20 (plus_00_02_t, _0_line__out__1[30], Torus);
  neighbours neighbours_4 (
    ._00_00(minus_1_line[1]), ._00_01(minus_1_line[2]), ._00_02(minus_1_line[3]), ._00_03(minus_1_line[4]),
    ._00_04(minus_1_line[5]), ._01_00(minus_01_01), ._01_01(minus_01_02), ._01_02(minus_01_03),
    ._01_03(minus_01_04), ._01_04(minus_01_05), ._02_00(_0_line__out__1[1]), ._02_01(_0_line__out__1[2]),
    ._02_02(_0_line__out__1[3]), ._02_03(_0_line__out__1[4]), ._02_04(_0_line__out__1[5]),
    ._03_00(_1_line[1]), ._03_01(_1_line[2]), ._03_02(_1_line[3]), ._03_03(_1_line[4]), ._03_04(_1_line[5]),
    ._04_00(_2_line[1]), ._04_01(_2_line[2]), ._04_02(_2_line[3]), ._04_03(_2_line[4]), ._04_04(_2_line[5]),
    .neighbours(neighbours_4_neighbours));
  alive alive_4 (
    .neighbours(neighbours_4_neighbours), .look_at(lookAt), .B___birth(birth), .S___save(save),
    .alive(_0_line__out__1[3]), .input_state(state_helper_4_output_state), .clock(clock));
  STATE_helper state_helper_4 (.input_state(input_state), .output_state(state_helper_4_output_state), .i(I), .j(J[3]));
  neighbours neighbours_5 (
    ._00_00(minus_1_line[2]), ._00_01(minus_1_line[3]), ._00_02(minus_1_line[4]), ._00_03(minus_1_line[5]),
    ._00_04(minus_1_line[6]), ._01_00(minus_01_02), ._01_01(minus_01_03), ._01_02(minus_01_04),
    ._01_03(minus_01_05), ._01_04(minus_01_06), ._02_00(_0_line__out__1[2]), ._02_01(_0_line__out__1[3]),
    ._02_02(_0_line__out__1[4]), ._02_03(_0_line__out__1[5]), ._02_04(_0_line__out__1[6]),
    ._03_00(_1_line[2]), ._03_01(_1_line[3]), ._03_02(_1_line[4]), ._03_03(_1_line[5]), ._03_04(_1_line[6]),
    ._04_00(_2_line[2]), ._04_01(_2_line[3]), ._04_02(_2_line[4]), ._04_03(_2_line[5]), ._04_04(_2_line[6]),
    .neighbours(neighbours_5_neighbours));
  alive alive_5 (
    .neighbours(neighbours_5_neighbours), .look_at(lookAt), .B___birth(birth), .S___save(save),
    .alive(_0_line__out__1[4]), .input_state(state_helper_5_output_state), .clock(clock));
  STATE_helper state_helper_5 (.input_state(input_state), .output_state(state_helper_5_output_state), .i(I), .j(J[4]));
  neighbours neighbours_6 (
    ._00_00(minus_1_line[3]), ._00_01(minus_1_line[4]), ._00_02(minus_1_line[5]), ._00_03(minus_1_line[6]),
    ._00_04(minus_1_line[7]), ._01_00(minus_01_03), ._01_01(minus_01_04), ._01_02(minus_01_05),
    ._01_03(minus_01_06), ._01_04(minus_01_07), ._02_00(_0_line__out__1[3]), ._02_01(_0_line__out__1[4]),
    ._02_02(_0_line__out__1[5]), ._02_03(_0_line__out__1[6]), ._02_04(_0_line__out__1[7]),
    ._03_00(_1_line[3]), ._03_01(_1_line[4]), ._03_02(_1_line[5]), ._03_03(_1_line[6]), ._03_04(_1_line[7]),
    ._04_00(_2_line[3]), ._04_01(_2_line[4]), ._04_02(_2_line[5]), ._04_03(_2_line[6]), ._04_04(_2_line[7]),
    .neighbours(neighbours_6_neighbours));
  alive alive_6 (
    .neighbours(neighbours_6_neighbours), .look_at(lookAt), .B___birth(birth), .S___save(save),
    .alive(_0_line__out__1[5]), .input_state(state_helper_6_output_state), .clock(clock));
  STATE_helper state_helper_6 (.input_state(input_state), .output_state(state_helper_6_output_state), .i(I), .j(J[5]));
  neighbours neighbours_7 (
    ._00_00(minus_1_line[4]), ._00_01(minus_1_line[5]), ._00_02(minus_1_line[6]), ._00_03(minus_1_line[7]),
    ._00_04(minus_1_line[8]), ._01_00(minus_01_04), ._01_01(minus_01_05), ._01_02(minus_01_06),
    ._01_03(minus_01_07), ._01_04(minus_01_08), ._02_00(_0_line__out__1[4]), ._02_01(_0_line__out__1[5]),
    ._02_02(_0_line__out__1[6]), ._02_03(_0_line__out__1[7]), ._02_04(_0_line__out__1[8]),
    ._03_00(_1_line[4]), ._03_01(_1_line[5]), ._03_02(_1_line[6]), ._03_03(_1_line[7]), ._03_04(_1_line[8]),
    ._04_00(_2_line[4]), ._04_01(_2_line[5]), ._04_02(_2_line[6]), ._04_03(_2_line[7]), ._04_04(_2_line[8]),
    .neighbours(neighbours_7_neighbours));
  alive alive_7 (
    .neighbours(neighbours_7_neighbours), .look_at(lookAt), .B___birth(birth), .S___save(save),
    .alive(_0_line__out__1[6]), .input_state(state_helper_7_output_state), .clock(clock));
  STATE_helper state_helper_7 (.input_state(input_state), .output_state(state_helper_7_output_state), .i(I), .j(J[6]));
  neighbours neighbours_8 (
    ._00_00(minus_1_line[5]), ._00_01(minus_1_line[6]), ._00_02(minus_1_line[7]), ._00_03(minus_1_line[8]),
    ._00_04(minus_1_line[9]), ._01_00(minus_01_05), ._01_01(minus_01_06), ._01_02(minus_01_07),
    ._01_03(minus_01_08), ._01_04(minus_01_09), ._02_00(_0_line__out__1[5]), ._02_01(_0_line__out__1[6]),
    ._02_02(_0_line__out__1[7]), ._02_03(_0_line__out__1[8]), ._02_04(_0_line__out__1[9]),
    ._03_00(_1_line[5]), ._03_01(_1_line[6]), ._03_02(_1_line[7]), ._03_03(_1_line[8]), ._03_04(_1_line[9]),
    ._04_00(_2_line[5]), ._04_01(_2_line[6]), ._04_02(_2_line[7]), ._04_03(_2_line[8]), ._04_04(_2_line[9]),
    .neighbours(neighbours_8_neighbours));
  alive alive_8 (
    .neighbours(neighbours_8_neighbours), .look_at(lookAt), .B___birth(birth), .S___save(save),
    .alive(_0_line__out__1[7]), .input_state(state_helper_8_output_state), .clock(clock));
  STATE_helper state_helper_8 (.input_state(input_state), .output_state(state_helper_8_output_state), .i(I), .j(J[7]));
  neighbours neighbours_9 (
    ._00_00(minus_1_line[6]), ._00_01(minus_1_line[7]), ._00_02(minus_1_line[8]), ._00_03(minus_1_line[9]),
    ._00_04(minus_1_line[10]), ._01_00(minus_01_06), ._01_01(minus_01_07), ._01_02(minus_01_08),
    ._01_03(minus_01_09), ._01_04(minus_01_10), ._02_00(_0_line__out__1[6]), ._02_01(_0_line__out__1[7]),
    ._02_02(_0_line__out__1[8]), ._02_03(_0_line__out__1[9]), ._02_04(_0_line__out__1[10]),
    ._03_00(_1_line[6]), ._03_01(_1_line[7]), ._03_02(_1_line[8]), ._03_03(_1_line[9]), ._03_04(_1_line[10]),
    ._04_00(_2_line[6]), ._04_01(_2_line[7]), ._04_02(_2_line[8]), ._04_03(_2_line[9]), ._04_04(_2_line[10]),
    .neighbours(neighbours_9_neighbours));
  alive alive_9 (
    .neighbours(neighbours_9_neighbours), .look_at(lookAt), .B___birth(birth), .S___save(save),
    .alive(_0_line__out__1[8]), .input_state(state_helper_9_output_state), .clock(clock));
  STATE_helper state_helper_9 (.input_state(input_state), .output_state(state_helper_9_output_state), .i(I), .j(J[8]));
  neighbours neighbours_10 (
    ._00_00(minus_1_line[7]), ._00_01(minus_1_line[8]), ._00_02(minus_1_line[9]), ._00_03(minus_1_line[10]),
    ._00_04(minus_1_line[11]), ._01_00(minus_01_07), ._01_01(minus_01_08), ._01_02(minus_01_09),
    ._01_03(minus_01_10), ._01_04(minus_01_11), ._02_00(_0_line__out__1[7]), ._02_01(_0_line__out__1[8]),
    ._02_02(_0_line__out__1[9]), ._02_03(_0_line__out__1[10]), ._02_04(_0_line__out__1[11]),
    ._03_00(_1_line[7]), ._03_01(_1_line[8]), ._03_02(_1_line[9]), ._03_03(_1_line[10]),
    ._03_04(_1_line[11]), ._04_00(_2_line[7]), ._04_01(_2_line[8]), ._04_02(_2_line[9]),
    ._04_03(_2_line[10]), ._04_04(_2_line[11]), .neighbours(neighbours_10_neighbours));
  alive alive_10 (
    .neighbours(neighbours_10_neighbours), .look_at(lookAt), .B___birth(birth), .S___save(save),
    .alive(_0_line__out__1[9]), .input_state(state_helper_10_output_state), .clock(clock));
  STATE_helper state_helper_10 (
    .input_state(input_state), .output_state(state_helper_10_output_state), .i(I), .j(J[9]));
  neighbours neighbours_11 (
    ._00_00(minus_1_line[8]), ._00_01(minus_1_line[9]), ._00_02(minus_1_line[10]), ._00_03(minus_1_line[11]),
    ._00_04(minus_1_line[12]), ._01_00(minus_01_08), ._01_01(minus_01_09), ._01_02(minus_01_10),
    ._01_03(minus_01_11), ._01_04(minus_01_12), ._02_00(_0_line__out__1[8]), ._02_01(_0_line__out__1[9]),
    ._02_02(_0_line__out__1[10]), ._02_03(_0_line__out__1[11]), ._02_04(_0_line__out__1[12]),
    ._03_00(_1_line[8]), ._03_01(_1_line[9]), ._03_02(_1_line[10]), ._03_03(_1_line[11]),
    ._03_04(_1_line[12]), ._04_00(_2_line[8]), ._04_01(_2_line[9]), ._04_02(_2_line[10]),
    ._04_03(_2_line[11]), ._04_04(_2_line[12]), .neighbours(neighbours_11_neighbours));
  alive alive_11 (
    .neighbours(neighbours_11_neighbours), .look_at(lookAt), .B___birth(birth), .S___save(save),
    .alive(_0_line__out__1[10]), .input_state(state_helper_11_output_state), .clock(clock));
  STATE_helper state_helper_11 (
    .input_state(input_state), .output_state(state_helper_11_output_state), .i(I), .j(J[10]));
  neighbours neighbours_12 (
    ._00_00(minus_1_line[9]), ._00_01(minus_1_line[10]), ._00_02(minus_1_line[11]),
    ._00_03(minus_1_line[12]), ._00_04(minus_1_line[13]), ._01_00(minus_01_09), ._01_01(minus_01_10),
    ._01_02(minus_01_11), ._01_03(minus_01_12), ._01_04(minus_01_13), ._02_00(_0_line__out__1[9]),
    ._02_01(_0_line__out__1[10]), ._02_02(_0_line__out__1[11]), ._02_03(_0_line__out__1[12]),
    ._02_04(_0_line__out__1[13]), ._03_00(_1_line[9]), ._03_01(_1_line[10]), ._03_02(_1_line[11]),
    ._03_03(_1_line[12]), ._03_04(_1_line[13]), ._04_00(_2_line[9]), ._04_01(_2_line[10]),
    ._04_02(_2_line[11]), ._04_03(_2_line[12]), ._04_04(_2_line[13]), .neighbours(neighbours_12_neighbours));
  alive alive_12 (
    .neighbours(neighbours_12_neighbours), .look_at(lookAt), .B___birth(birth), .S___save(save),
    .alive(_0_line__out__1[11]), .input_state(state_helper_12_output_state), .clock(clock));
  STATE_helper state_helper_12 (
    .input_state(input_state), .output_state(state_helper_12_output_state), .i(I), .j(J[11]));
  neighbours neighbours_13 (
    ._00_00(minus_1_line[10]), ._00_01(minus_1_line[11]), ._00_02(minus_1_line[12]),
    ._00_03(minus_1_line[13]), ._00_04(minus_1_line[14]), ._01_00(minus_01_10), ._01_01(minus_01_11),
    ._01_02(minus_01_12), ._01_03(minus_01_13), ._01_04(minus_01_14), ._02_00(_0_line__out__1[10]),
    ._02_01(_0_line__out__1[11]), ._02_02(_0_line__out__1[12]), ._02_03(_0_line__out__1[13]),
    ._02_04(_0_line__out__1[14]), ._03_00(_1_line[10]), ._03_01(_1_line[11]), ._03_02(_1_line[12]),
    ._03_03(_1_line[13]), ._03_04(_1_line[14]), ._04_00(_2_line[10]), ._04_01(_2_line[11]),
    ._04_02(_2_line[12]), ._04_03(_2_line[13]), ._04_04(_2_line[14]), .neighbours(neighbours_13_neighbours));
  alive alive_13 (
    .neighbours(neighbours_13_neighbours), .look_at(lookAt), .B___birth(birth), .S___save(save),
    .alive(_0_line__out__1[12]), .input_state(state_helper_13_output_state), .clock(clock));
  STATE_helper state_helper_13 (
    .input_state(input_state), .output_state(state_helper_13_output_state), .i(I), .j(J[12]));
  neighbours neighbours_14 (
    ._00_00(minus_1_line[11]), ._00_01(minus_1_line[12]), ._00_02(minus_1_line[13]),
    ._00_03(minus_1_line[14]), ._00_04(minus_1_line[15]), ._01_00(minus_01_11), ._01_01(minus_01_12),
    ._01_02(minus_01_13), ._01_03(minus_01_14), ._01_04(minus_01_15), ._02_00(_0_line__out__1[11]),
    ._02_01(_0_line__out__1[12]), ._02_02(_0_line__out__1[13]), ._02_03(_0_line__out__1[14]),
    ._02_04(_0_line__out__1[15]), ._03_00(_1_line[11]), ._03_01(_1_line[12]), ._03_02(_1_line[13]),
    ._03_03(_1_line[14]), ._03_04(_1_line[15]), ._04_00(_2_line[11]), ._04_01(_2_line[12]),
    ._04_02(_2_line[13]), ._04_03(_2_line[14]), ._04_04(_2_line[15]), .neighbours(neighbours_14_neighbours));
  alive alive_14 (
    .neighbours(neighbours_14_neighbours), .look_at(lookAt), .B___birth(birth), .S___save(save),
    .alive(_0_line__out__1[13]), .input_state(state_helper_14_output_state), .clock(clock));
  STATE_helper state_helper_14 (
    .input_state(input_state), .output_state(state_helper_14_output_state), .i(I), .j(J[13]));
  neighbours neighbours_15 (
    ._00_00(minus_1_line[12]), ._00_01(minus_1_line[13]), ._00_02(minus_1_line[14]),
    ._00_03(minus_1_line[15]), ._00_04(minus_1_line[16]), ._01_00(minus_01_12), ._01_01(minus_01_13),
    ._01_02(minus_01_14), ._01_03(minus_01_15), ._01_04(minus_01_16), ._02_00(_0_line__out__1[12]),
    ._02_01(_0_line__out__1[13]), ._02_02(_0_line__out__1[14]), ._02_03(_0_line__out__1[15]),
    ._02_04(_0_line__out__1[16]), ._03_00(_1_line[12]), ._03_01(_1_line[13]), ._03_02(_1_line[14]),
    ._03_03(_1_line[15]), ._03_04(_1_line[16]), ._04_00(_2_line[12]), ._04_01(_2_line[13]),
    ._04_02(_2_line[14]), ._04_03(_2_line[15]), ._04_04(_2_line[16]), .neighbours(neighbours_15_neighbours));
  alive alive_15 (
    .neighbours(neighbours_15_neighbours), .look_at(lookAt), .B___birth(birth), .S___save(save),
    .alive(_0_line__out__1[14]), .input_state(state_helper_15_output_state), .clock(clock));
  STATE_helper state_helper_15 (
    .input_state(input_state), .output_state(state_helper_15_output_state), .i(I), .j(J[14]));
  neighbours neighbours_16 (
    ._00_00(minus_1_line[13]), ._00_01(minus_1_line[14]), ._00_02(minus_1_line[15]),
    ._00_03(minus_1_line[16]), ._00_04(minus_1_line[17]), ._01_00(minus_01_13), ._01_01(minus_01_14),
    ._01_02(minus_01_15), ._01_03(minus_01_16), ._01_04(minus_01_17), ._02_00(_0_line__out__1[13]),
    ._02_01(_0_line__out__1[14]), ._02_02(_0_line__out__1[15]), ._02_03(_0_line__out__1[16]),
    ._02_04(_0_line__out__1[17]), ._03_00(_1_line[13]), ._03_01(_1_line[14]), ._03_02(_1_line[15]),
    ._03_03(_1_line[16]), ._03_04(_1_line[17]), ._04_00(_2_line[13]), ._04_01(_2_line[14]),
    ._04_02(_2_line[15]), ._04_03(_2_line[16]), ._04_04(_2_line[17]), .neighbours(neighbours_16_neighbours));
  alive alive_16 (
    .neighbours(neighbours_16_neighbours), .look_at(lookAt), .B___birth(birth), .S___save(save),
    .alive(_0_line__out__1[15]), .input_state(state_helper_16_output_state), .clock(clock));
  STATE_helper state_helper_16 (
    .input_state(input_state), .output_state(state_helper_16_output_state), .i(I), .j(J[15]));
  neighbours neighbours_17 (
    ._00_00(minus_1_line[14]), ._00_01(minus_1_line[15]), ._00_02(minus_1_line[16]),
    ._00_03(minus_1_line[17]), ._00_04(minus_1_line[18]), ._01_00(minus_01_14), ._01_01(minus_01_15),
    ._01_02(minus_01_16), ._01_03(minus_01_17), ._01_04(minus_01_18), ._02_00(_0_line__out__1[14]),
    ._02_01(_0_line__out__1[15]), ._02_02(_0_line__out__1[16]), ._02_03(_0_line__out__1[17]),
    ._02_04(_0_line__out__1[18]), ._03_00(_1_line[14]), ._03_01(_1_line[15]), ._03_02(_1_line[16]),
    ._03_03(_1_line[17]), ._03_04(_1_line[18]), ._04_00(_2_line[14]), ._04_01(_2_line[15]),
    ._04_02(_2_line[16]), ._04_03(_2_line[17]), ._04_04(_2_line[18]), .neighbours(neighbours_17_neighbours));
  alive alive_17 (
    .neighbours(neighbours_17_neighbours), .look_at(lookAt), .B___birth(birth), .S___save(save),
    .alive(_0_line__out__1[16]), .input_state(state_helper_17_output_state), .clock(clock));
  STATE_helper state_helper_17 (
    .input_state(input_state), .output_state(state_helper_17_output_state), .i(I), .j(J[16]));
  neighbours neighbours_18 (
    ._00_00(minus_1_line[15]), ._00_01(minus_1_line[16]), ._00_02(minus_1_line[17]),
    ._00_03(minus_1_line[18]), ._00_04(minus_1_line[19]), ._01_00(minus_01_15), ._01_01(minus_01_16),
    ._01_02(minus_01_17), ._01_03(minus_01_18), ._01_04(minus_01_19), ._02_00(_0_line__out__1[15]),
    ._02_01(_0_line__out__1[16]), ._02_02(_0_line__out__1[17]), ._02_03(_0_line__out__1[18]),
    ._02_04(_0_line__out__1[19]), ._03_00(_1_line[15]), ._03_01(_1_line[16]), ._03_02(_1_line[17]),
    ._03_03(_1_line[18]), ._03_04(_1_line[19]), ._04_00(_2_line[15]), ._04_01(_2_line[16]),
    ._04_02(_2_line[17]), ._04_03(_2_line[18]), ._04_04(_2_line[19]), .neighbours(neighbours_18_neighbours));
  alive alive_18 (
    .neighbours(neighbours_18_neighbours), .look_at(lookAt), .B___birth(birth), .S___save(save),
    .alive(_0_line__out__1[17]), .input_state(state_helper_18_output_state), .clock(clock));
  STATE_helper state_helper_18 (
    .input_state(input_state), .output_state(state_helper_18_output_state), .i(I), .j(J[17]));
  neighbours neighbours_19 (
    ._00_00(minus_1_line[16]), ._00_01(minus_1_line[17]), ._00_02(minus_1_line[18]),
    ._00_03(minus_1_line[19]), ._00_04(minus_1_line[20]), ._01_00(minus_01_16), ._01_01(minus_01_17),
    ._01_02(minus_01_18), ._01_03(minus_01_19), ._01_04(minus_01_20), ._02_00(_0_line__out__1[16]),
    ._02_01(_0_line__out__1[17]), ._02_02(_0_line__out__1[18]), ._02_03(_0_line__out__1[19]),
    ._02_04(_0_line__out__1[20]), ._03_00(_1_line[16]), ._03_01(_1_line[17]), ._03_02(_1_line[18]),
    ._03_03(_1_line[19]), ._03_04(_1_line[20]), ._04_00(_2_line[16]), ._04_01(_2_line[17]),
    ._04_02(_2_line[18]), ._04_03(_2_line[19]), ._04_04(_2_line[20]), .neighbours(neighbours_19_neighbours));
  alive alive_19 (
    .neighbours(neighbours_19_neighbours), .look_at(lookAt), .B___birth(birth), .S___save(save),
    .alive(_0_line__out__1[18]), .input_state(state_helper_19_output_state), .clock(clock));
  STATE_helper state_helper_19 (
    .input_state(input_state), .output_state(state_helper_19_output_state), .i(I), .j(J[18]));
  neighbours neighbours_20 (
    ._00_00(minus_1_line[17]), ._00_01(minus_1_line[18]), ._00_02(minus_1_line[19]),
    ._00_03(minus_1_line[20]), ._00_04(minus_1_line[21]), ._01_00(minus_01_17), ._01_01(minus_01_18),
    ._01_02(minus_01_19), ._01_03(minus_01_20), ._01_04(minus_01_21), ._02_00(_0_line__out__1[17]),
    ._02_01(_0_line__out__1[18]), ._02_02(_0_line__out__1[19]), ._02_03(_0_line__out__1[20]),
    ._02_04(_0_line__out__1[21]), ._03_00(_1_line[17]), ._03_01(_1_line[18]), ._03_02(_1_line[19]),
    ._03_03(_1_line[20]), ._03_04(_1_line[21]), ._04_00(_2_line[17]), ._04_01(_2_line[18]),
    ._04_02(_2_line[19]), ._04_03(_2_line[20]), ._04_04(_2_line[21]), .neighbours(neighbours_20_neighbours));
  alive alive_20 (
    .neighbours(neighbours_20_neighbours), .look_at(lookAt), .B___birth(birth), .S___save(save),
    .alive(_0_line__out__1[19]), .input_state(state_helper_20_output_state), .clock(clock));
  STATE_helper state_helper_20 (
    .input_state(input_state), .output_state(state_helper_20_output_state), .i(I), .j(J[19]));
  neighbours neighbours_21 (
    ._00_00(minus_1_line[18]), ._00_01(minus_1_line[19]), ._00_02(minus_1_line[20]),
    ._00_03(minus_1_line[21]), ._00_04(minus_1_line[22]), ._01_00(minus_01_18), ._01_01(minus_01_19),
    ._01_02(minus_01_20), ._01_03(minus_01_21), ._01_04(minus_01_22), ._02_00(_0_line__out__1[18]),
    ._02_01(_0_line__out__1[19]), ._02_02(_0_line__out__1[20]), ._02_03(_0_line__out__1[21]),
    ._02_04(_0_line__out__1[22]), ._03_00(_1_line[18]), ._03_01(_1_line[19]), ._03_02(_1_line[20]),
    ._03_03(_1_line[21]), ._03_04(_1_line[22]), ._04_00(_2_line[18]), ._04_01(_2_line[19]),
    ._04_02(_2_line[20]), ._04_03(_2_line[21]), ._04_04(_2_line[22]), .neighbours(neighbours_21_neighbours));
  alive alive_21 (
    .neighbours(neighbours_21_neighbours), .look_at(lookAt), .B___birth(birth), .S___save(save),
    .alive(_0_line__out__1[20]), .input_state(state_helper_21_output_state), .clock(clock));
  STATE_helper state_helper_21 (
    .input_state(input_state), .output_state(state_helper_21_output_state), .i(I), .j(J[22]));
  neighbours neighbours_22 (
    ._00_00(minus_1_line[19]), ._00_01(minus_1_line[20]), ._00_02(minus_1_line[21]),
    ._00_03(minus_1_line[22]), ._00_04(minus_1_line[23]), ._01_00(minus_01_19), ._01_01(minus_01_20),
    ._01_02(minus_01_21), ._01_03(minus_01_22), ._01_04(minus_01_23), ._02_00(_0_line__out__1[19]),
    ._02_01(_0_line__out__1[20]), ._02_02(_0_line__out__1[21]), ._02_03(_0_line__out__1[22]),
    ._02_04(_0_line__out__1[23]), ._03_00(_1_line[19]), ._03_01(_1_line[20]), ._03_02(_1_line[21]),
    ._03_03(_1_line[22]), ._03_04(_1_line[23]), ._04_00(_2_line[19]), ._04_01(_2_line[20]),
    ._04_02(_2_line[21]), ._04_03(_2_line[22]), ._04_04(_2_line[23]), .neighbours(neighbours_22_neighbours));
  alive alive_22 (
    .neighbours(neighbours_22_neighbours), .look_at(lookAt), .B___birth(birth), .S___save(save),
    .alive(_0_line__out__1[21]), .input_state(state_helper_22_output_state), .clock(clock));
  STATE_helper state_helper_22 (
    .input_state(input_state), .output_state(state_helper_22_output_state), .i(I), .j(J[21]));
  neighbours neighbours_23 (
    ._00_00(minus_1_line[20]), ._00_01(minus_1_line[21]), ._00_02(minus_1_line[22]),
    ._00_03(minus_1_line[23]), ._00_04(minus_1_line[24]), ._01_00(minus_01_20), ._01_01(minus_01_21),
    ._01_02(minus_01_22), ._01_03(minus_01_23), ._01_04(minus_01_24), ._02_00(_0_line__out__1[20]),
    ._02_01(_0_line__out__1[21]), ._02_02(_0_line__out__1[22]), ._02_03(_0_line__out__1[23]),
    ._02_04(_0_line__out__1[24]), ._03_00(_1_line[20]), ._03_01(_1_line[21]), ._03_02(_1_line[22]),
    ._03_03(_1_line[23]), ._03_04(_1_line[24]), ._04_00(_2_line[20]), ._04_01(_2_line[21]),
    ._04_02(_2_line[22]), ._04_03(_2_line[23]), ._04_04(_2_line[24]), .neighbours(neighbours_23_neighbours));
  alive alive_23 (
    .neighbours(neighbours_23_neighbours), .look_at(lookAt), .B___birth(birth), .S___save(save),
    .alive(_0_line__out__1[22]), .input_state(state_helper_23_output_state), .clock(clock));
  STATE_helper state_helper_23 (
    .input_state(input_state), .output_state(state_helper_23_output_state), .i(I), .j(J[22]));
  neighbours neighbours_24 (
    ._00_00(minus_1_line[21]), ._00_01(minus_1_line[22]), ._00_02(minus_1_line[23]),
    ._00_03(minus_1_line[24]), ._00_04(minus_1_line[25]), ._01_00(minus_01_21), ._01_01(minus_01_22),
    ._01_02(minus_01_23), ._01_03(minus_01_24), ._01_04(minus_01_25), ._02_00(_0_line__out__1[21]),
    ._02_01(_0_line__out__1[22]), ._02_02(_0_line__out__1[23]), ._02_03(_0_line__out__1[24]),
    ._02_04(_0_line__out__1[25]), ._03_00(_1_line[21]), ._03_01(_1_line[22]), ._03_02(_1_line[23]),
    ._03_03(_1_line[24]), ._03_04(_1_line[25]), ._04_00(_2_line[21]), ._04_01(_2_line[22]),
    ._04_02(_2_line[23]), ._04_03(_2_line[24]), ._04_04(_2_line[25]), .neighbours(neighbours_24_neighbours));
  alive alive_24 (
    .neighbours(neighbours_24_neighbours), .look_at(lookAt), .B___birth(birth), .S___save(save),
    .alive(_0_line__out__1[23]), .input_state(state_helper_24_output_state), .clock(clock));
  STATE_helper state_helper_24 (
    .input_state(input_state), .output_state(state_helper_24_output_state), .i(I), .j(J[23]));
  neighbours neighbours_25 (
    ._00_00(minus_1_line[22]), ._00_01(minus_1_line[23]), ._00_02(minus_1_line[24]),
    ._00_03(minus_1_line[25]), ._00_04(minus_1_line[26]), ._01_00(minus_01_22), ._01_01(minus_01_23),
    ._01_02(minus_01_24), ._01_03(minus_01_25), ._01_04(minus_01_26), ._02_00(_0_line__out__1[22]),
    ._02_01(_0_line__out__1[23]), ._02_02(_0_line__out__1[24]), ._02_03(_0_line__out__1[25]),
    ._02_04(_0_line__out__1[26]), ._03_00(_1_line[22]), ._03_01(_1_line[23]), ._03_02(_1_line[24]),
    ._03_03(_1_line[25]), ._03_04(_1_line[26]), ._04_00(_2_line[22]), ._04_01(_2_line[23]),
    ._04_02(_2_line[24]), ._04_03(_2_line[25]), ._04_04(_2_line[26]), .neighbours(neighbours_25_neighbours));
  alive alive_25 (
    .neighbours(neighbours_25_neighbours), .look_at(lookAt), .B___birth(birth), .S___save(save),
    .alive(_0_line__out__1[24]), .input_state(state_helper_25_output_state), .clock(clock));
  STATE_helper state_helper_25 (
    .input_state(input_state), .output_state(state_helper_25_output_state), .i(I), .j(J[24]));
  neighbours neighbours_26 (
    ._00_00(minus_1_line[23]), ._00_01(minus_1_line[24]), ._00_02(minus_1_line[25]),
    ._00_03(minus_1_line[26]), ._00_04(minus_1_line[27]), ._01_00(minus_01_23), ._01_01(minus_01_24),
    ._01_02(minus_01_25), ._01_03(minus_01_26), ._01_04(minus_01_27), ._02_00(_0_line__out__1[23]),
    ._02_01(_0_line__out__1[24]), ._02_02(_0_line__out__1[25]), ._02_03(_0_line__out__1[26]),
    ._02_04(_0_line__out__1[27]), ._03_00(_1_line[23]), ._03_01(_1_line[24]), ._03_02(_1_line[25]),
    ._03_03(_1_line[26]), ._03_04(_1_line[27]), ._04_00(_2_line[23]), ._04_01(_2_line[24]),
    ._04_02(_2_line[25]), ._04_03(_2_line[26]), ._04_04(_2_line[27]), .neighbours(neighbours_26_neighbours));
  alive alive_26 (
    .neighbours(neighbours_26_neighbours), .look_at(lookAt), .B___birth(birth), .S___save(save),
    .alive(_0_line__out__1[25]), .input_state(state_helper_26_output_state), .clock(clock));
  STATE_helper state_helper_26 (
    .input_state(input_state), .output_state(state_helper_26_output_state), .i(I), .j(J[25]));
  neighbours neighbours_27 (
    ._00_00(minus_1_line[24]), ._00_01(minus_1_line[25]), ._00_02(minus_1_line[26]),
    ._00_03(minus_1_line[27]), ._00_04(minus_1_line[28]), ._01_00(minus_01_24), ._01_01(minus_01_25),
    ._01_02(minus_01_26), ._01_03(minus_01_27), ._01_04(minus_01_28), ._02_00(_0_line__out__1[24]),
    ._02_01(_0_line__out__1[25]), ._02_02(_0_line__out__1[26]), ._02_03(_0_line__out__1[27]),
    ._02_04(_0_line__out__1[28]), ._03_00(_1_line[24]), ._03_01(_1_line[25]), ._03_02(_1_line[26]),
    ._03_03(_1_line[27]), ._03_04(_1_line[28]), ._04_00(_2_line[24]), ._04_01(_2_line[25]),
    ._04_02(_2_line[26]), ._04_03(_2_line[27]), ._04_04(_2_line[28]), .neighbours(neighbours_27_neighbours));
  alive alive_27 (
    .neighbours(neighbours_27_neighbours), .look_at(lookAt), .B___birth(birth), .S___save(save),
    .alive(_0_line__out__1[26]), .input_state(state_helper_27_output_state), .clock(clock));
  STATE_helper state_helper_27 (
    .input_state(input_state), .output_state(state_helper_27_output_state), .i(I), .j(J[26]));
  neighbours neighbours_28 (
    ._00_00(minus_1_line[25]), ._00_01(minus_1_line[26]), ._00_02(minus_1_line[27]),
    ._00_03(minus_1_line[28]), ._00_04(minus_1_line[29]), ._01_00(minus_01_25), ._01_01(minus_01_26),
    ._01_02(minus_01_27), ._01_03(minus_01_28), ._01_04(minus_01_29), ._02_00(_0_line__out__1[25]),
    ._02_01(_0_line__out__1[26]), ._02_02(_0_line__out__1[27]), ._02_03(_0_line__out__1[28]),
    ._02_04(_0_line__out__1[29]), ._03_00(_1_line[25]), ._03_01(_1_line[26]), ._03_02(_1_line[27]),
    ._03_03(_1_line[28]), ._03_04(_1_line[29]), ._04_00(_2_line[25]), ._04_01(_2_line[26]),
    ._04_02(_2_line[27]), ._04_03(_2_line[28]), ._04_04(_2_line[29]), .neighbours(neighbours_28_neighbours));
  alive alive_28 (
    .neighbours(neighbours_28_neighbours), .look_at(lookAt), .B___birth(birth), .S___save(save),
    .alive(_0_line__out__1[27]), .input_state(state_helper_28_output_state), .clock(clock));
  STATE_helper state_helper_28 (
    .input_state(input_state), .output_state(state_helper_28_output_state), .i(I), .j(J[27]));
  neighbours neighbours_29 (
    ._00_00(minus_1_line[26]), ._00_01(minus_1_line[27]), ._00_02(minus_1_line[28]),
    ._00_03(minus_1_line[29]), ._00_04(minus_1_line[30]), ._01_00(minus_01_26), ._01_01(minus_01_27),
    ._01_02(minus_01_28), ._01_03(minus_01_29), ._01_04(minus_01_30), ._02_00(_0_line__out__1[26]),
    ._02_01(_0_line__out__1[27]), ._02_02(_0_line__out__1[28]), ._02_03(_0_line__out__1[29]),
    ._02_04(_0_line__out__1[30]), ._03_00(_1_line[26]), ._03_01(_1_line[27]), ._03_02(_1_line[28]),
    ._03_03(_1_line[29]), ._03_04(_1_line[30]), ._04_00(_2_line[26]), ._04_01(_2_line[27]),
    ._04_02(_2_line[28]), ._04_03(_2_line[29]), ._04_04(_2_line[30]), .neighbours(neighbours_29_neighbours));
  alive alive_29 (
    .neighbours(neighbours_29_neighbours), .look_at(lookAt), .B___birth(birth), .S___save(save),
    .alive(_0_line__out__1[28]), .input_state(state_helper_29_output_state), .clock(clock));
  STATE_helper state_helper_29 (
    .input_state(input_state), .output_state(state_helper_29_output_state), .i(I), .j(J[28]));
  neighbours neighbours_30 (
    ._00_00(minus_1_line[27]), ._00_01(minus_1_line[28]), ._00_02(minus_1_line[29]),
    ._00_03(minus_1_line[30]), ._00_04(minus_1_line[31]), ._01_00(minus_01_27), ._01_01(minus_01_28),
    ._01_02(minus_01_29), ._01_03(minus_01_30), ._01_04(minus_01_31), ._02_00(_0_line__out__1[27]),
    ._02_01(_0_line__out__1[28]), ._02_02(_0_line__out__1[29]), ._02_03(_0_line__out__1[30]),
    ._02_04(_0_line__out__1[31]), ._03_00(_1_line[27]), ._03_01(_1_line[28]), ._03_02(_1_line[29]),
    ._03_03(_1_line[30]), ._03_04(_1_line[31]), ._04_00(_2_line[27]), ._04_01(_2_line[28]),
    ._04_02(_2_line[29]), ._04_03(_2_line[30]), ._04_04(_2_line[31]), .neighbours(neighbours_30_neighbours));
  alive alive_30 (
    .neighbours(neighbours_30_neighbours), .look_at(lookAt), .B___birth(birth), .S___save(save),
    .alive(_0_line__out__1[29]), .input_state(state_helper_30_output_state), .clock(clock));
  STATE_helper state_helper_30 (
    .input_state(input_state), .output_state(state_helper_30_output_state), .i(I), .j(J[29]));
  neighbours neighbours_31 (
    ._00_00(minus_1_line[28]), ._00_01(minus_1_line[29]), ._00_02(minus_1_line[30]),
    ._00_03(minus_1_line[31]), ._00_04(minus_02_32), ._01_00(minus_01_28), ._01_01(minus_01_29),
    ._01_02(minus_01_30), ._01_03(minus_01_31), ._01_04(minus_01_32), ._02_00(_0_line__out__1[28]),
    ._02_01(_0_line__out__1[29]), ._02_02(_0_line__out__1[30]), ._02_03(_0_line__out__1[31]),
    ._02_04(plus_00_32), ._03_00(_1_line[28]), ._03_01(_1_line[29]), ._03_02(_1_line[30]),
    ._03_03(_1_line[31]), ._03_04(plus_01_32), ._04_00(_2_line[28]), ._04_01(_2_line[29]),
    ._04_02(_2_line[30]), ._04_03(_2_line[31]), ._04_04(plus_02_32), .neighbours(neighbours_31_neighbours));
  alive alive_31 (
    .neighbours(neighbours_31_neighbours), .look_at(lookAt), .B___birth(birth), .S___save(save),
    .alive(_0_line__out__1[30]), .input_state(state_helper_31_output_state), .clock(clock));
  STATE_helper state_helper_31 (
    .input_state(input_state), .output_state(state_helper_31_output_state), .i(I), .j(J[30]));
  neighbours neighbours_32 (
    ._00_00(minus_1_line[29]), ._00_01(minus_1_line[30]), ._00_02(minus_1_line[31]), ._00_03(minus_02_32),
    ._00_04(minus_02_33), ._01_00(minus_01_29), ._01_01(minus_01_30), ._01_02(minus_01_31),
    ._01_03(minus_01_32), ._01_04(minus_01_33), ._02_00(_0_line__out__1[29]), ._02_01(_0_line__out__1[30]),
    ._02_02(_0_line__out__1[31]), ._02_03(plus_00_32), ._02_04(plus_00_33), ._03_00(_1_line[29]),
    ._03_01(_1_line[30]), ._03_02(_1_line[31]), ._03_03(plus_01_32), ._03_04(plus_01_33),
    ._04_00(_2_line[29]), ._04_01(_2_line[30]), ._04_02(_2_line[31]), ._04_03(plus_02_32),
    ._04_04(plus_02_33), .neighbours(neighbours_32_neighbours));
  alive alive_32 (
    .neighbours(neighbours_32_neighbours), .look_at(lookAt), .B___birth(birth), .S___save(save),
    .alive(_0_line__out__1[31]), .input_state(state_helper_32_output_state), .clock(clock));
  STATE_helper state_helper_32 (
    .input_state(input_state), .output_state(state_helper_32_output_state), .i(I), .j(J[31]));

  assign _0_line__out__1_2 = _0_line__out__1;
  assign _0_line__out__2 = _0_line__out__1;
  assign _0_line__out__2_2 = _0_line__out__1;
  assign display = _0_line__out__1;
  assign J[20] = J[22];
  assign minus_2_line = minus_1_line;

  // Other names for the same wires on the sheet: plus_00_00 = _0_line__out__1[0]; plus_00_01 = _0_line__out__1[1];
  //   plus_00_02 = _0_line__out__1[2]; plus_00_03 = _0_line__out__1[3]; plus_00_04 = _0_line__out__1[4];
  //   plus_00_05 = _0_line__out__1[5]; plus_00_06 = _0_line__out__1[6]; plus_00_07 = _0_line__out__1[7];
  //   plus_00_08 = _0_line__out__1[8]; plus_00_09 = _0_line__out__1[9]; plus_00_10 = _0_line__out__1[10];
  //   plus_00_11 = _0_line__out__1[11]; plus_00_12 = _0_line__out__1[12]; plus_00_13 = _0_line__out__1[13];
  //   plus_00_14 = _0_line__out__1[14]; plus_00_15 = _0_line__out__1[15]; plus_00_16 = _0_line__out__1[16];
  //   plus_00_17 = _0_line__out__1[17]; plus_00_18 = _0_line__out__1[18]; plus_00_19 = _0_line__out__1[19];
  //   plus_00_20 = _0_line__out__1[20]; plus_00_21 = _0_line__out__1[21]; plus_00_22 = _0_line__out__1[22];
  //   plus_00_23 = _0_line__out__1[23]; plus_00_24 = _0_line__out__1[24]; plus_00_25 = _0_line__out__1[25];
  //   plus_00_26 = _0_line__out__1[26]; plus_00_27 = _0_line__out__1[27]; plus_00_28 = _0_line__out__1[28];
  //   plus_00_29 = _0_line__out__1[29]; plus_00_30 = _0_line__out__1[30]; plus_00_31 = _0_line__out__1[31];
  //   plus_01_00 = _1_line[0]; plus_01_01 = _1_line[1]; plus_01_02 = _1_line[2]; plus_01_03 = _1_line[3];
  //   plus_01_04 = _1_line[4]; plus_01_05 = _1_line[5]; plus_01_06 = _1_line[6]; plus_01_07 = _1_line[7];
  //   plus_01_08 = _1_line[8]; plus_01_09 = _1_line[9]; plus_01_10 = _1_line[10]; plus_01_11 = _1_line[11];
  //   plus_01_12 = _1_line[12]; plus_01_13 = _1_line[13]; plus_01_14 = _1_line[14]; plus_01_15 = _1_line[15];
  //   plus_01_16 = _1_line[16]; plus_01_17 = _1_line[17]; plus_01_18 = _1_line[18]; plus_01_19 = _1_line[19];
  //   plus_01_20 = _1_line[20]; plus_01_21 = _1_line[21]; plus_01_22 = _1_line[22]; plus_01_23 = _1_line[23];
  //   plus_01_24 = _1_line[24]; plus_01_25 = _1_line[25]; plus_01_26 = _1_line[26]; plus_01_27 = _1_line[27];
  //   plus_01_28 = _1_line[28]; plus_01_29 = _1_line[29]; plus_01_30 = _1_line[30]; plus_01_31 = _1_line[31];
  //   plus_02_00 = _2_line[0]; plus_02_01 = _2_line[1]; plus_02_02 = _2_line[2]; plus_02_03 = _2_line[3];
  //   plus_02_04 = _2_line[4]; plus_02_05 = _2_line[5]; plus_02_06 = _2_line[6]; plus_02_07 = _2_line[7];
  //   plus_02_08 = _2_line[8]; plus_02_09 = _2_line[9]; plus_02_10 = _2_line[10]; plus_02_11 = _2_line[11];
  //   plus_02_12 = _2_line[12]; plus_02_13 = _2_line[13]; plus_02_14 = _2_line[14]; plus_02_15 = _2_line[15];
  //   plus_02_16 = _2_line[16]; plus_02_17 = _2_line[17]; plus_02_18 = _2_line[18]; plus_02_19 = _2_line[19];
  //   plus_02_20 = _2_line[20]; plus_02_21 = _2_line[21]; plus_02_22 = _2_line[22]; plus_02_23 = _2_line[23];
  //   plus_02_24 = _2_line[24]; plus_02_25 = _2_line[25]; plus_02_26 = _2_line[26]; plus_02_27 = _2_line[27];
  //   plus_02_28 = _2_line[28]; plus_02_29 = _2_line[29]; plus_02_30 = _2_line[30]; plus_02_31 = _2_line[31];
  //   j20 = J[22]; minus_02_00 = minus_1_line[0]; minus_02_01 = minus_1_line[1]; minus_02_02 = minus_1_line[2];
  //   minus_02_03 = minus_1_line[3]; minus_02_04 = minus_1_line[4]; minus_02_05 = minus_1_line[5];
  //   minus_02_06 = minus_1_line[6]; minus_02_07 = minus_1_line[7]; minus_02_08 = minus_1_line[8];
  //   minus_02_09 = minus_1_line[9]; minus_02_10 = minus_1_line[10]; minus_02_11 = minus_1_line[11];
  //   minus_02_12 = minus_1_line[12]; minus_02_13 = minus_1_line[13]; minus_02_14 = minus_1_line[14];
  //   minus_02_15 = minus_1_line[15]; minus_02_16 = minus_1_line[16]; minus_02_17 = minus_1_line[17];
  //   minus_02_18 = minus_1_line[18]; minus_02_19 = minus_1_line[19]; minus_02_20 = minus_1_line[20];
  //   minus_02_21 = minus_1_line[21]; minus_02_22 = minus_1_line[22]; minus_02_23 = minus_1_line[23];
  //   minus_02_24 = minus_1_line[24]; minus_02_25 = minus_1_line[25]; minus_02_26 = minus_1_line[26];
  //   minus_02_27 = minus_1_line[27]; minus_02_28 = minus_1_line[28]; minus_02_29 = minus_1_line[29];
  //   minus_02_30 = minus_1_line[30]; minus_02_31 = minus_1_line[31]; state[1:0] = input_state
endmodule

module matrix (
  input  [31:0] j,
  input  torus,
  input  [31:0] i
);

  line line_1 (
    .J(j), .I(i[0]), .Torus(torus));  // open: minus_2_line, minus_1_line, _1_line, _2_line, input_state, _0_line__out__2, _0_line__out__1, _0_line__out__1_2, _0_line__out__2_2, display
  line line_2 (
    .J(j), .I(i[1]), .Torus(torus));  // open: minus_2_line, minus_1_line, _1_line, _2_line, input_state, _0_line__out__2, _0_line__out__1, _0_line__out__1_2, _0_line__out__2_2, display
  line line_3 (
    .J(j), .I(i[2]), .Torus(torus));  // open: minus_2_line, minus_1_line, _1_line, _2_line, input_state, _0_line__out__2, _0_line__out__1, _0_line__out__1_2, _0_line__out__2_2, display
  line line_4 (
    .J(j), .I(i[3]), .Torus(torus));  // open: minus_2_line, minus_1_line, _1_line, _2_line, input_state, _0_line__out__2, _0_line__out__1, _0_line__out__1_2, _0_line__out__2_2, display
  line line_5 (
    .J(j), .I(i[4]), .Torus(torus));  // open: minus_2_line, minus_1_line, _1_line, _2_line, input_state, _0_line__out__2, _0_line__out__1, _0_line__out__1_2, _0_line__out__2_2, display
  line line_6 (
    .J(j), .I(i[5]), .Torus(torus));  // open: minus_2_line, minus_1_line, _1_line, _2_line, input_state, _0_line__out__2, _0_line__out__1, _0_line__out__1_2, _0_line__out__2_2, display
  line line_7 (
    .J(j), .I(i[6]), .Torus(torus));  // open: minus_2_line, minus_1_line, _1_line, _2_line, input_state, _0_line__out__2, _0_line__out__1, _0_line__out__1_2, _0_line__out__2_2, display
  line line_8 (
    .J(j), .I(i[7]), .Torus(torus));  // open: minus_2_line, minus_1_line, _1_line, _2_line, input_state, _0_line__out__2, _0_line__out__1, _0_line__out__1_2, _0_line__out__2_2, display
  line line_9 (
    .J(j), .I(i[8]), .Torus(torus));  // open: minus_2_line, minus_1_line, _1_line, _2_line, input_state, _0_line__out__2, _0_line__out__1, _0_line__out__1_2, _0_line__out__2_2, display
  line line_10 (
    .J(j), .I(i[9]), .Torus(torus));  // open: minus_2_line, minus_1_line, _1_line, _2_line, input_state, _0_line__out__2, _0_line__out__1, _0_line__out__1_2, _0_line__out__2_2, display
  line line_11 (
    .J(j), .I(i[10]), .Torus(torus));  // open: minus_2_line, minus_1_line, _1_line, _2_line, input_state, _0_line__out__2, _0_line__out__1, _0_line__out__1_2, _0_line__out__2_2, display
  line line_12 (
    .J(j), .I(i[11]), .Torus(torus));  // open: minus_2_line, minus_1_line, _1_line, _2_line, input_state, _0_line__out__2, _0_line__out__1, _0_line__out__1_2, _0_line__out__2_2, display
  line line_13 (
    .J(j), .I(i[12]), .Torus(torus));  // open: minus_2_line, minus_1_line, _1_line, _2_line, input_state, _0_line__out__2, _0_line__out__1, _0_line__out__1_2, _0_line__out__2_2, display
  line line_14 (
    .J(j), .I(i[13]), .Torus(torus));  // open: minus_2_line, minus_1_line, _1_line, _2_line, input_state, _0_line__out__2, _0_line__out__1, _0_line__out__1_2, _0_line__out__2_2, display
  line line_15 (
    .J(j), .I(i[14]), .Torus(torus));  // open: minus_2_line, minus_1_line, _1_line, _2_line, input_state, _0_line__out__2, _0_line__out__1, _0_line__out__1_2, _0_line__out__2_2, display
  line line_16 (
    .J(j), .I(i[15]), .Torus(torus));  // open: minus_2_line, minus_1_line, _1_line, _2_line, input_state, _0_line__out__2, _0_line__out__1, _0_line__out__1_2, _0_line__out__2_2, display
  line line_17 (
    .J(j), .I(i[16]), .Torus(torus));  // open: minus_2_line, minus_1_line, _1_line, _2_line, input_state, _0_line__out__2, _0_line__out__1, _0_line__out__1_2, _0_line__out__2_2, display
  line line_18 (
    .J(j), .I(i[17]), .Torus(torus));  // open: minus_2_line, minus_1_line, _1_line, _2_line, input_state, _0_line__out__2, _0_line__out__1, _0_line__out__1_2, _0_line__out__2_2, display
  line line_19 (
    .J(j), .I(i[18]), .Torus(torus));  // open: minus_2_line, minus_1_line, _1_line, _2_line, input_state, _0_line__out__2, _0_line__out__1, _0_line__out__1_2, _0_line__out__2_2, display
  line line_20 (
    .J(j), .I(i[19]), .Torus(torus));  // open: minus_2_line, minus_1_line, _1_line, _2_line, input_state, _0_line__out__2, _0_line__out__1, _0_line__out__1_2, _0_line__out__2_2, display
  line line_21 (
    .J(j), .I(i[20]), .Torus(torus));  // open: minus_2_line, minus_1_line, _1_line, _2_line, input_state, _0_line__out__2, _0_line__out__1, _0_line__out__1_2, _0_line__out__2_2, display
  line line_22 (
    .J(j), .I(i[21]), .Torus(torus));  // open: minus_2_line, minus_1_line, _1_line, _2_line, input_state, _0_line__out__2, _0_line__out__1, _0_line__out__1_2, _0_line__out__2_2, display
  line line_23 (
    .J(j), .I(i[22]), .Torus(torus));  // open: minus_2_line, minus_1_line, _1_line, _2_line, input_state, _0_line__out__2, _0_line__out__1, _0_line__out__1_2, _0_line__out__2_2, display
  line line_24 (
    .J(j), .I(i[23]), .Torus(torus));  // open: minus_2_line, minus_1_line, _1_line, _2_line, input_state, _0_line__out__2, _0_line__out__1, _0_line__out__1_2, _0_line__out__2_2, display
  line line_25 (
    .J(j), .I(i[24]), .Torus(torus));  // open: minus_2_line, minus_1_line, _1_line, _2_line, input_state, _0_line__out__2, _0_line__out__1, _0_line__out__1_2, _0_line__out__2_2, display
  line line_26 (
    .J(j), .I(i[25]), .Torus(torus));  // open: minus_2_line, minus_1_line, _1_line, _2_line, input_state, _0_line__out__2, _0_line__out__1, _0_line__out__1_2, _0_line__out__2_2, display
  line line_27 (
    .J(j), .I(i[26]), .Torus(torus));  // open: minus_2_line, minus_1_line, _1_line, _2_line, input_state, _0_line__out__2, _0_line__out__1, _0_line__out__1_2, _0_line__out__2_2, display
  line line_28 (
    .J(j), .I(i[27]), .Torus(torus));  // open: minus_2_line, minus_1_line, _1_line, _2_line, input_state, _0_line__out__2, _0_line__out__1, _0_line__out__1_2, _0_line__out__2_2, display
  line line_29 (
    .J(j), .I(i[28]), .Torus(torus));  // open: minus_2_line, minus_1_line, _1_line, _2_line, input_state, _0_line__out__2, _0_line__out__1, _0_line__out__1_2, _0_line__out__2_2, display
  line line_30 (
    .J(j), .I(i[29]), .Torus(torus));  // open: minus_2_line, minus_1_line, _1_line, _2_line, input_state, _0_line__out__2, _0_line__out__1, _0_line__out__1_2, _0_line__out__2_2, display
  line line_31 (
    .J(j), .I(i[30]), .Torus(torus));  // open: minus_2_line, minus_1_line, _1_line, _2_line, input_state, _0_line__out__2, _0_line__out__1, _0_line__out__1_2, _0_line__out__2_2, display
  line line_32 (
    .J(j), .I(i[31]), .Torus(torus));  // open: minus_2_line, minus_1_line, _1_line, _2_line, input_state, _0_line__out__2, _0_line__out__1, _0_line__out__1_2, _0_line__out__2_2, display
endmodule
