// Logisim project 007.main (i forgot update's name 3).circ as structural Verilog: 12 circuits, main circuit alive?
module main (
  input  pause,
  input  [4:0] minus_2_line,
  input  [5:0] num_1,
  input  [5:0] num_1_2,
  input  [4:0] minus_1_line,
  input  [5:0] num_2,
  input  [5:0] num_2_2,
  input  [4:0] cur_line,
  input  [5:0] num_3,
  input  [5:0] num_3_2,
  input  [4:0] plus_1_line,
  input  [5:0] num_4,
  input  [5:0] num_4_2,
  input  [4:0] plus_2_line,
  input  [5:0] num_5,
  input  [5:0] num_5_2
);

  wire cdm16_1_p1, cdm16_1_p2, cdm16_1_p4, cdm16_1_p5, cdm16_1_p6, cdm16_1_p7, cdm16_1_p8, cdm16_1_p9,
       cdm16_1_p10, cdm16_1_p11, cdm16_1_p12, clock_1_out, clock_2_out, mem, not_1_out, pause__0, read, word;
  wire [15:0] address_bus, cdm16_1_p17, cdm16_1_p18, data_bus;

  // Debugger debugger_1: pin names not known
  // Probe on cdm16_1_p2
  // Probe on cdm16_1_p1
  // Probe on cdm16_1_p4
  // Probe on cdm16_1_p5
  Clock clock_1 (.out(clock_1_out));
  // Probe on cdm16_1_p7
  // Probe on cdm16_1_p6
  // cdm16 cdm16_1: pin names not known; wires that end beside it: cdm16_1_p1, cdm16_1_p2, clock_1_out, cdm16_1_p4, cdm16_1_p5, cdm16_1_p6, cdm16_1_p7, cdm16_1_p8, cdm16_1_p9, cdm16_1_p10, cdm16_1_p11, cdm16_1_p12, mem, read, word, address_bus, cdm16_1_p17, cdm16_1_p18
  // Probe on cdm16_1_p9
  // Probe on cdm16_1_p8
  assign data_bus = not_1_out ? cdm16_1_p17 : 16'bz;  // Controlled_Buffer controlled_buffer_1
  not not_1 (not_1_out, read);
  assign cdm16_1_p18 = read ? data_bus : 16'bz;  // Controlled_Buffer controlled_buffer_2
  // Probe on cdm16_1_p10
  // Probe on cdm16_1_p11
  // Probe on num_1
  // Probe on num_2
  // Probe on num_3
  // Probe on num_4
  // Probe on num_5
  // Probe on cdm16_1_p12
  not not_2 (pause__0, pause);
  Clock clock_2 (.out(clock_2_out));
  // Probe on num_1_2
  // Probe on num_2_2
  // Probe on num_3_2
  // Probe on num_4_2
  // Probe on num_5_2
  // RAM ram_1: pin names not known; wires that end beside it: address_bus, word, mem, clock_2_out, read, data_bus

  // Other names for the same wires on the sheet: birth[29:0] = {num_5, num_4, num_3, num_2, num_1};
  //   lookAt[24:0] = {plus_2_line, plus_1_line, cur_line, minus_1_line, minus_2_line};
  //   save[29:0] = {num_5_2, num_4_2, num_3_2, num_2_2, num_1_2}

  // Notes on the sheet:
  //   look at
  //   Set up rules (not now :{ )
  //   birth
  //   save
endmodule

module aliveSTD (
  input  [8:0] neighbours,
  input  clock,
  input  [1:0] input_state,
  output alive
);

  wire _2_out, _3_out, and_1_out, and_2_out, multiplexer_1_out, multiplexer_2_out, not_1_out, not_2_out,
       or_1_out, or_2_out, or_3_out, or_4_out;
  wire [3:0] newCnt;

  and _2 (_2_out, ~newCnt[0], newCnt[1], ~newCnt[2], ~newCnt[3]);  // AND_Gate
  and _3 (_3_out, newCnt[0], newCnt[1], ~newCnt[2], ~newCnt[3]);  // AND_Gate
  or or_1 (or_1_out, _2_out, _3_out);
  Multiplexer #(.disabled(0)) multiplexer_1 (
    .in0(_2_out), .in1(or_1_out), .out(multiplexer_1_out), .sel(neighbours[4]));  // open: en
  // Probe on newCnt
  BitAdder bitadder_1 (.in0({neighbours[8:5], neighbours[3:0]}), .out(newCnt));
  and and_1 (and_1_out, not_2_out, input_state[0]);
  not not_1 (not_1_out, input_state[0]);
  and and_2 (and_2_out, not_1_out, multiplexer_1_out);
  or or_2 (or_2_out, input_state[1], input_state[0]);
  or or_3 (or_3_out, and_1_out, and_2_out);
  or or_4 (or_4_out, or_2_out, clock);
  Multiplexer #(.disabled(0)) multiplexer_2 (
    .in0(or_3_out), .in1(input_state[0]), .out(multiplexer_2_out), .sel(input_state[1]));  // open: en
  not not_2 (not_2_out, alive);
  Register #(.width(1), .trigger("falling")) register_1 (
    .D(multiplexer_2_out), .Q(alive), .clk(or_4_out));  // open: en, clr

  // Other names for the same wires on the sheet: cur = neighbours[4]

  // Notes on the sheet:
  //   neighbours: pull=down
  //   input_state: pull=down
  //   ▒ — look at
  //   ▓ — current cell
  //   floating → 0
  //   floating → 0
  //   if cur cell is dead (= 0) try birth,
  //   alive (= 1) — try save
  //   ▒ ▒ ▒
  //   ▒ ▓ ▒
  //   ▒ ▒ ▒
  //   invert?
  //   1 (high bit)
  //   0 (low bit)
  //   00 — by rules
  //   01 — invert
  //   10 — set DEAD
  //   11 — set ALIVE
endmodule

module alive (
  input  [8:0] neighbours,
  input  [8:0] look_at,
  input  [29:0] B___birth,
  input  clock,
  input  [1:0] input_state,
  input  [29:0] S___save,
  output alive
);

  wire and_2_out, and_3_out, can_cell_born_out, can_cell_save_out, comparator_1_eq, comparator_2_eq,
       comparator_3_eq, comparator_4_eq, comparator_5_eq, comparator_6_eq, comparator_7_eq, comparator_8_eq,
       comparator_9_eq, comparator_10_eq, comparator_11_eq, comparator_12_eq, multiplexer_1_out,
       multiplexer_2_out, not_1_out, not_2_out, or_1_out, or_2_out, or_3_out;
  wire [3:0] B1, B2, B3, B4, B5, B6, newCnt, S1, S2, S3, S4, S5, S6;
  wire [8:0] and_1_out, undriven;

  assign and_1_out = neighbours & look_at;  // AND_Gate and_1, 9 bits wide
  BS_helper bs_helper_1 (.input_5_bit(B___birth[4:0]), .output_4_bit(B1));
  BS_helper bs_helper_2 (.input_5_bit(B___birth[9:5]), .output_4_bit(B2));
  BS_helper bs_helper_3 (.input_5_bit(B___birth[14:10]), .output_4_bit(B3));
  BS_helper bs_helper_4 (.input_5_bit(B___birth[19:15]), .output_4_bit(B4));
  BS_helper bs_helper_5 (.input_5_bit(B___birth[24:20]), .output_4_bit(B5));
  BS_helper bs_helper_6 (.input_5_bit(B___birth[29:25]), .output_4_bit(B6));
  BS_helper bs_helper_7 (.input_5_bit(S___save[4:0]), .output_4_bit(S1));
  BS_helper bs_helper_8 (.input_5_bit(S___save[9:5]), .output_4_bit(S2));
  BS_helper bs_helper_9 (.input_5_bit(S___save[14:10]), .output_4_bit(S3));
  BS_helper bs_helper_10 (.input_5_bit(S___save[19:15]), .output_4_bit(S4));
  BS_helper bs_helper_11 (.input_5_bit(S___save[24:20]), .output_4_bit(S5));
  BS_helper bs_helper_12 (.input_5_bit(S___save[29:25]), .output_4_bit(S6));
  // Probe on newCnt
  BitAdder #(.width(9)) bitadder_1 (.in0(and_1_out), .out(newCnt));
  // Probe on nothing
  // Probe on nothing
  // Probe on nothing
  // Probe on nothing
  // Probe on nothing
  // Probe on nothing
  // Probe on nothing
  // Probe on nothing
  // Probe on nothing
  // Probe on nothing
  // Probe on nothing
  // Probe on nothing
  // Probe on undriven[2:0]
  // Probe on undriven[5:3]
  // Probe on undriven[8:6]
  Comparator #(.width(4), .mode("unsigned")) comparator_1 (.a(newCnt), .b(B1), .eq(comparator_1_eq));  // open: gt, lt
  Comparator #(.width(4), .mode("unsigned")) comparator_2 (.a(newCnt), .b(B2), .eq(comparator_2_eq));  // open: gt, lt
  Comparator #(.width(4), .mode("unsigned")) comparator_3 (.a(newCnt), .b(B3), .eq(comparator_3_eq));  // open: gt, lt
  Comparator #(.width(4), .mode("unsigned")) comparator_4 (.a(newCnt), .b(B4), .eq(comparator_4_eq));  // open: gt, lt
  Comparator #(.width(4), .mode("unsigned")) comparator_5 (.a(newCnt), .b(B5), .eq(comparator_5_eq));  // open: gt, lt
  Comparator #(.width(4), .mode("unsigned")) comparator_6 (.a(newCnt), .b(B6), .eq(comparator_6_eq));  // open: gt, lt
  Comparator #(.width(4), .mode("unsigned")) comparator_7 (.a(newCnt), .b(S1), .eq(comparator_7_eq));  // open: gt, lt
  Comparator #(.width(4), .mode("unsigned")) comparator_8 (.a(newCnt), .b(S2), .eq(comparator_8_eq));  // open: gt, lt
  Comparator #(.width(4), .mode("unsigned")) comparator_9 (.a(newCnt), .b(S3), .eq(comparator_9_eq));  // open: gt, lt
  Comparator #(.width(4), .mode("unsigned")) comparator_10 (.a(newCnt), .b(S4), .eq(comparator_10_eq));  // open: gt, lt
  Comparator #(.width(4), .mode("unsigned")) comparator_11 (.a(newCnt), .b(S5), .eq(comparator_11_eq));  // open: gt, lt
  Comparator #(.width(4), .mode("unsigned")) comparator_12 (.a(newCnt), .b(S6), .eq(comparator_12_eq));  // open: gt, lt
  or can_cell_born (can_cell_born_out, comparator_1_eq, comparator_2_eq, comparator_3_eq, comparator_4_eq, comparator_5_eq, comparator_6_eq);
  or can_cell_save (can_cell_save_out, comparator_7_eq, comparator_8_eq, comparator_9_eq, comparator_10_eq, comparator_11_eq, comparator_12_eq);
  Multiplexer #(.disabled(0)) multiplexer_1 (
    .in0(can_cell_born_out), .in1(can_cell_save_out), .out(multiplexer_1_out), .sel(neighbours[4]));  // open: en
  not not_1 (not_1_out, input_state[0]);
  or or_1 (or_1_out, input_state[1], input_state[0]);
  and and_2 (and_2_out, not_2_out, input_state[0]);
  and and_3 (and_3_out, not_1_out, multiplexer_1_out);
  or or_2 (or_2_out, or_1_out, clock);
  or or_3 (or_3_out, and_2_out, and_3_out);
  Register #(.width(1), .trigger("falling")) register_1 (
    .D(multiplexer_2_out), .Q(alive), .clk(or_2_out));  // open: en, clr
  Multiplexer #(.disabled(0)) multiplexer_2 (
    .in0(or_3_out), .in1(input_state[0]), .out(multiplexer_2_out), .sel(input_state[1]));  // open: en
  not not_2 (not_2_out, alive);

  // Other names for the same wires on the sheet: cur = neighbours[4]

  // Notes on the sheet:
  //   neighbours: pull=down
  //   B___birth: pull=up
  //   input_state: pull=down
  //   look_at: pull=down
  //   S___save: pull=up
  //   floating → 0
  //   floating → 0
  //   floating → 1
  //   floating → 1
  //   DEBUG TOOLS
  //   ▒ — look at
  //   DEBUG TOO↑↓
  //   ▒ ▒ ▒
  //   ▒ ▓ ▒
  //   ▓ — current cell
  //   ▒ ▒ ▒
  //   if cur cell is dead (= 0) try birth,
  //   alive (= 1) — try save
  //   invert?
  //   1 (high bit)
  //   0 (low bit)
  //   00 — by rules
  //   01 — invert
  //   11 — set ALIVE
  //   10 — set DEAD
endmodule

module BS_helper (
  input  [4:0] input_5_bit,
  output [3:0] output_4_bit
);

  Multiplexer #(.width(4)) multiplexer_1 (
    .in0(input_5_bit[3:0]), .in1(4'b1111), .out(output_4_bit), .sel(input_5_bit[4]));  // open: en
endmodule

module STATE_helper (
  input  [1:0] input_state,
  input  i,
  input  j,
  output [1:0] output_state
);

  wire [1:1] and_2_out;

  assign output_state = input_state & {2{and_2_out[1]}};  // AND_Gate and_1, 2 bits wide
  and and_2 (and_2_out[1], i, j);
endmodule

module game (
);

  // AND_Gate and_1 is placed but not wired
endmodule

module example (
  input  [2:0] minus_1_line,
  input  [2:0] in_2,
  input  [2:0] cur_line,
  input  [2:0] in_4,
  input  [2:0] _1_line,
  input  [2:0] in_6,
  input  [4:0] B__S,
  input  [4:0] B1,
  input  [4:0] S1,
  input  [4:0] B2,
  input  [4:0] S2,
  input  [4:0] B3,
  input  [4:0] S3,
  input  [4:0] B4,
  input  [4:0] S4,
  input  [4:0] B5,
  input  [4:0] S5,
  input  [4:0] B6,
  input  [4:0] S6,
  input  clock
);

  wire [3:0] undriven, undriven_2;
  wire [4:4] newState;

  DotMatrix #(.inputtype("row"), .matrixcols(3), .matrixrows(3)) dotmatrix_1 (.row0(in_2), .row1(in_4), .row2(in_6));
  alive alive_1 (
    .neighbours({in_6, in_4, in_2}), .look_at({_1_line, cur_line, minus_1_line}),
    .B___birth({B6, B5, B4, B3, B2, B1}), .S___save({S6, S5, S4, S3, S2, S1}), .alive(newState[4]),
    .clock(clock));  // open: input_state
  // Probe on undriven[2:0]
  // Probe on {undriven_2[0], 1'b0, undriven[3]}
  // Probe on undriven_2[3:1]
  // Probe on in_2
  // Probe on {in_4[2], newState[4], in_4[0]}
  // Probe on in_6
  DotMatrix #(.inputtype("row"), .matrixcols(3), .matrixrows(3)) dotmatrix_2 (
    .row0(in_2), .row1({in_4[2], newState[4], in_4[0]}), .row2(in_6));

  // Other names for the same wires on the sheet: birth[29:0] = {B6, B5, B4, B3, B2, B1};
  //   look_at[8:0] = {_1_line, cur_line, minus_1_line}; neighbours[8:0] = {in_6, in_4, in_2};
  //   newState (some bits) = {in_6, in_4[2], in_4[0], in_2}; save[29:0] = {S6, S5, S4, S3, S2, S1}

  // Notes on the sheet:
  //   old state
  //   Old state (You can edit)
  //   Old state
  //   How to use?
  //   New state
  //   New state
  //   How to watch?
  //   X is cell's neighbours
  //   0 is current cell
  //   1) look at 3x3
  //   2) B3/S23
  //   B – birth
  //   STANDART RULES:
  //   ↓ 0 – use number in rules, 1 — don't use
  //   ↑ ↑ ↑ ↑ binary number from 0 to 8
  //   Look at
  //   You can choose up to 6 numbers from 0 to 8
  //   S – save
endmodule

module neighbours (
  input  minus_01_01,
  input  minus_01_00,
  input  minus_01_01_2,
  input  plus_00_01,
  input  plus_00_00,
  input  plus_00_01_2,
  input  plus_01_01,
  input  plus_01_00,
  input  plus_01_01_2,
  output [8:0] neighbours
);


  assign neighbours = {plus_01_01_2, plus_01_00, plus_01_01, plus_00_01_2, plus_00_00, plus_00_01, minus_01_01_2, minus_01_00, minus_01_01};
endmodule

module lineSTD (
  input  [31:0] J,
  input  [31:0] minus_1_line,
  input  [31:0] _1_line,
  input  I,
  input  Torus,
  input  [1:0] input_state,
  output [31:0] _0_line__out__1,
  output [31:0] display,
  output [31:0] _0_line__out__1_2
);

  wire clock, minus_01_00, minus_01_01, minus_01_01_t, minus_01_02, minus_01_03, minus_01_04, minus_01_05,
       minus_01_06, minus_01_07, minus_01_08, minus_01_09, minus_01_10, minus_01_11, minus_01_12,
       minus_01_13, minus_01_14, minus_01_15, minus_01_16, minus_01_17, minus_01_18, minus_01_19,
       minus_01_20, minus_01_21, minus_01_22, minus_01_23, minus_01_24, minus_01_25, minus_01_26,
       minus_01_27, minus_01_28, minus_01_29, minus_01_30, minus_01_31, minus_01_32, plus_00_01_t,
       plus_00_32, plus_01_01_t, plus_01_32;
  wire [1:0] state_helper_1_output_state, state_helper_2_output_state, state_helper_3_output_state,
       state_helper_4_output_state, state_helper_5_output_state, state_helper_6_output_state,
       state_helper_7_output_state, state_helper_8_output_state, state_helper_9_output_state,
       state_helper_10_output_state, state_helper_11_output_state, state_helper_12_output_state,
       state_helper_13_output_state, state_helper_14_output_state, state_helper_15_output_state,
       state_helper_16_output_state, state_helper_17_output_state, state_helper_18_output_state,
       state_helper_19_output_state, state_helper_20_output_state, state_helper_21_output_state,
       state_helper_22_output_state, state_helper_23_output_state, state_helper_24_output_state,
       state_helper_25_output_state, state_helper_26_output_state, state_helper_27_output_state,
       state_helper_28_output_state, state_helper_29_output_state, state_helper_30_output_state,
       state_helper_31_output_state, state_helper_32_output_state;
  wire [8:0] neighbours_1_neighbours, neighbours_2_neighbours, neighbours_3_neighbours,
       neighbours_4_neighbours, neighbours_5_neighbours, neighbours_6_neighbours, neighbours_7_neighbours,
       neighbours_8_neighbours, neighbours_9_neighbours, neighbours_10_neighbours, neighbours_11_neighbours,
       neighbours_12_neighbours, neighbours_13_neighbours, neighbours_14_neighbours,
       neighbours_15_neighbours, neighbours_16_neighbours, neighbours_17_neighbours,
       neighbours_18_neighbours, neighbours_19_neighbours, neighbours_20_neighbours,
       neighbours_21_neighbours, neighbours_22_neighbours, neighbours_23_neighbours,
       neighbours_24_neighbours, neighbours_25_neighbours, neighbours_26_neighbours,
       neighbours_27_neighbours, neighbours_28_neighbours, neighbours_29_neighbours,
       neighbours_30_neighbours, neighbours_31_neighbours, neighbours_32_neighbours;

  neighbours neighbours_1 (
    .minus_01_01(minus_01_01_t), .minus_01_00(minus_01_00), .minus_01_01_2(minus_01_01),
    .plus_00_01(plus_00_01_t), .plus_00_00(_0_line__out__1[0]), .plus_00_01_2(_0_line__out__1[1]),
    .plus_01_01(plus_01_01_t), .plus_01_00(_1_line[0]), .plus_01_01_2(_1_line[1]),
    .neighbours(neighbours_1_neighbours));
  aliveSTD alivestd_1 (
    .neighbours(neighbours_1_neighbours), .clock(clock), .alive(_0_line__out__1[0]),
    .input_state(state_helper_1_output_state));
  STATE_helper state_helper_1 (.input_state(input_state), .output_state(state_helper_1_output_state), .i(I), .j(J[0]));
  and and_1 (minus_01_32, minus_01_00, Torus);
  and and_2 (minus_01_01_t, minus_01_31, Torus);
  neighbours neighbours_2 (
    .minus_01_01(minus_01_00), .minus_01_00(minus_01_01), .minus_01_01_2(minus_01_02),
    .plus_00_01(_0_line__out__1[0]), .plus_00_00(_0_line__out__1[1]), .plus_00_01_2(_0_line__out__1[2]),
    .plus_01_01(_1_line[0]), .plus_01_00(_1_line[1]), .plus_01_01_2(_1_line[2]),
    .neighbours(neighbours_2_neighbours));
  aliveSTD alivestd_2 (
    .neighbours(neighbours_2_neighbours), .clock(clock), .alive(_0_line__out__1[1]),
    .input_state(state_helper_2_output_state));
  STATE_helper state_helper_2 (.input_state(input_state), .output_state(state_helper_2_output_state), .i(I), .j(J[1]));
  and and_3 (plus_01_32, _1_line[0], Torus);
  and and_4 (plus_01_01_t, _1_line[31], Torus);
  and and_5 (plus_00_32, _0_line__out__1[0], Torus);
  and and_6 (plus_00_01_t, _0_line__out__1[31], Torus);
  neighbours neighbours_3 (
    .minus_01_01(minus_01_01), .minus_01_00(minus_01_02), .minus_01_01_2(minus_01_03),
    .plus_00_01(_0_line__out__1[1]), .plus_00_00(_0_line__out__1[2]), .plus_00_01_2(_0_line__out__1[3]),
    .plus_01_01(_1_line[1]), .plus_01_00(_1_line[2]), .plus_01_01_2(_1_line[3]),
    .neighbours(neighbours_3_neighbours));
  aliveSTD alivestd_3 (
    .neighbours(neighbours_3_neighbours), .clock(clock), .alive(_0_line__out__1[2]),
    .input_state(state_helper_3_output_state));
  STATE_helper state_helper_3 (.input_state(input_state), .output_state(state_helper_3_output_state), .i(I), .j(J[2]));
  neighbours neighbours_4 (
    .minus_01_01(minus_01_02), .minus_01_00(minus_01_03), .minus_01_01_2(minus_01_04),
    .plus_00_01(_0_line__out__1[2]), .plus_00_00(_0_line__out__1[3]), .plus_00_01_2(_0_line__out__1[4]),
    .plus_01_01(_1_line[2]), .plus_01_00(_1_line[3]), .plus_01_01_2(_1_line[4]),
    .neighbours(neighbours_4_neighbours));
  aliveSTD alivestd_4 (
    .neighbours(neighbours_4_neighbours), .clock(clock), .alive(_0_line__out__1[3]),
    .input_state(state_helper_4_output_state));
  STATE_helper state_helper_4 (.input_state(input_state), .output_state(state_helper_4_output_state), .i(I), .j(J[3]));
  neighbours neighbours_5 (
    .minus_01_01(minus_01_03), .minus_01_00(minus_01_04), .minus_01_01_2(minus_01_05),
    .plus_00_01(_0_line__out__1[3]), .plus_00_00(_0_line__out__1[4]), .plus_00_01_2(_0_line__out__1[5]),
    .plus_01_01(_1_line[3]), .plus_01_00(_1_line[4]), .plus_01_01_2(_1_line[5]),
    .neighbours(neighbours_5_neighbours));
  aliveSTD alivestd_5 (
    .neighbours(neighbours_5_neighbours), .clock(clock), .alive(_0_line__out__1[4]),
    .input_state(state_helper_5_output_state));
  STATE_helper state_helper_5 (.input_state(input_state), .output_state(state_helper_5_output_state), .i(I), .j(J[4]));
  neighbours neighbours_6 (
    .minus_01_01(minus_01_04), .minus_01_00(minus_01_05), .minus_01_01_2(minus_01_06),
    .plus_00_01(_0_line__out__1[4]), .plus_00_00(_0_line__out__1[5]), .plus_00_01_2(_0_line__out__1[6]),
    .plus_01_01(_1_line[4]), .plus_01_00(_1_line[5]), .plus_01_01_2(_1_line[6]),
    .neighbours(neighbours_6_neighbours));
  aliveSTD alivestd_6 (
    .neighbours(neighbours_6_neighbours), .clock(clock), .alive(_0_line__out__1[5]),
    .input_state(state_helper_6_output_state));
  STATE_helper state_helper_6 (.input_state(input_state), .output_state(state_helper_6_output_state), .i(I), .j(J[5]));
  neighbours neighbours_7 (
    .minus_01_01(minus_01_05), .minus_01_00(minus_01_06), .minus_01_01_2(minus_01_07),
    .plus_00_01(_0_line__out__1[5]), .plus_00_00(_0_line__out__1[6]), .plus_00_01_2(_0_line__out__1[7]),
    .plus_01_01(_1_line[5]), .plus_01_00(_1_line[6]), .plus_01_01_2(_1_line[7]),
    .neighbours(neighbours_7_neighbours));
  aliveSTD alivestd_7 (
    .neighbours(neighbours_7_neighbours), .clock(clock), .alive(_0_line__out__1[6]),
    .input_state(state_helper_7_output_state));
  STATE_helper state_helper_7 (.input_state(input_state), .output_state(state_helper_7_output_state), .i(I), .j(J[6]));
  neighbours neighbours_8 (
    .minus_01_01(minus_01_06), .minus_01_00(minus_01_07), .minus_01_01_2(minus_01_08),
    .plus_00_01(_0_line__out__1[6]), .plus_00_00(_0_line__out__1[7]), .plus_00_01_2(_0_line__out__1[8]),
    .plus_01_01(_1_line[6]), .plus_01_00(_1_line[7]), .plus_01_01_2(_1_line[8]),
    .neighbours(neighbours_8_neighbours));
  aliveSTD alivestd_8 (
    .neighbours(neighbours_8_neighbours), .clock(clock), .alive(_0_line__out__1[7]),
    .input_state(state_helper_8_output_state));
  STATE_helper state_helper_8 (.input_state(input_state), .output_state(state_helper_8_output_state), .i(I), .j(J[7]));
  neighbours neighbours_9 (
    .minus_01_01(minus_01_07), .minus_01_00(minus_01_08), .minus_01_01_2(minus_01_09),
    .plus_00_01(_0_line__out__1[7]), .plus_00_00(_0_line__out__1[8]), .plus_00_01_2(_0_line__out__1[9]),
    .plus_01_01(_1_line[7]), .plus_01_00(_1_line[8]), .plus_01_01_2(_1_line[9]),
    .neighbours(neighbours_9_neighbours));
  aliveSTD alivestd_9 (
    .neighbours(neighbours_9_neighbours), .clock(clock), .alive(_0_line__out__1[8]),
    .input_state(state_helper_9_output_state));
  STATE_helper state_helper_9 (.input_state(input_state), .output_state(state_helper_9_output_state), .i(I), .j(J[8]));
  neighbours neighbours_10 (
    .minus_01_01(minus_01_08), .minus_01_00(minus_01_09), .minus_01_01_2(minus_01_10),
    .plus_00_01(_0_line__out__1[8]), .plus_00_00(_0_line__out__1[9]), .plus_00_01_2(_0_line__out__1[10]),
    .plus_01_01(_1_line[8]), .plus_01_00(_1_line[9]), .plus_01_01_2(_1_line[10]),
    .neighbours(neighbours_10_neighbours));
  aliveSTD alivestd_10 (
    .neighbours(neighbours_10_neighbours), .clock(clock), .alive(_0_line__out__1[9]),
    .input_state(state_helper_10_output_state));
  STATE_helper state_helper_10 (
    .input_state(input_state), .output_state(state_helper_10_output_state), .i(I), .j(J[9]));
  neighbours neighbours_11 (
    .minus_01_01(minus_01_09), .minus_01_00(minus_01_10), .minus_01_01_2(minus_01_11),
    .plus_00_01(_0_line__out__1[9]), .plus_00_00(_0_line__out__1[10]), .plus_00_01_2(_0_line__out__1[11]),
    .plus_01_01(_1_line[9]), .plus_01_00(_1_line[10]), .plus_01_01_2(_1_line[11]),
    .neighbours(neighbours_11_neighbours));
  aliveSTD alivestd_11 (
    .neighbours(neighbours_11_neighbours), .clock(clock), .alive(_0_line__out__1[10]),
    .input_state(state_helper_11_output_state));
  STATE_helper state_helper_11 (
    .input_state(input_state), .output_state(state_helper_11_output_state), .i(I), .j(J[10]));
  neighbours neighbours_12 (
    .minus_01_01(minus_01_10), .minus_01_00(minus_01_11), .minus_01_01_2(minus_01_12),
    .plus_00_01(_0_line__out__1[10]), .plus_00_00(_0_line__out__1[11]), .plus_00_01_2(_0_line__out__1[12]),
    .plus_01_01(_1_line[10]), .plus_01_00(_1_line[11]), .plus_01_01_2(_1_line[12]),
    .neighbours(neighbours_12_neighbours));
  aliveSTD alivestd_12 (
    .neighbours(neighbours_12_neighbours), .clock(clock), .alive(_0_line__out__1[11]),
    .input_state(state_helper_12_output_state));
  STATE_helper state_helper_12 (
    .input_state(input_state), .output_state(state_helper_12_output_state), .i(I), .j(J[11]));
  neighbours neighbours_13 (
    .minus_01_01(minus_01_11), .minus_01_00(minus_01_12), .minus_01_01_2(minus_01_13),
    .plus_00_01(_0_line__out__1[11]), .plus_00_00(_0_line__out__1[12]), .plus_00_01_2(_0_line__out__1[13]),
    .plus_01_01(_1_line[11]), .plus_01_00(_1_line[12]), .plus_01_01_2(_1_line[13]),
    .neighbours(neighbours_13_neighbours));
  aliveSTD alivestd_13 (
    .neighbours(neighbours_13_neighbours), .clock(clock), .alive(_0_line__out__1[12]),
    .input_state(state_helper_13_output_state));
  STATE_helper state_helper_13 (
    .input_state(input_state), .output_state(state_helper_13_output_state), .i(I), .j(J[12]));
  neighbours neighbours_14 (
    .minus_01_01(minus_01_12), .minus_01_00(minus_01_13), .minus_01_01_2(minus_01_14),
    .plus_00_01(_0_line__out__1[12]), .plus_00_00(_0_line__out__1[13]), .plus_00_01_2(_0_line__out__1[14]),
    .plus_01_01(_1_line[12]), .plus_01_00(_1_line[13]), .plus_01_01_2(_1_line[14]),
    .neighbours(neighbours_14_neighbours));
  aliveSTD alivestd_14 (
    .neighbours(neighbours_14_neighbours), .clock(clock), .alive(_0_line__out__1[13]),
    .input_state(state_helper_14_output_state));
  STATE_helper state_helper_14 (
    .input_state(input_state), .output_state(state_helper_14_output_state), .i(I), .j(J[13]));
  neighbours neighbours_15 (
    .minus_01_01(minus_01_13), .minus_01_00(minus_01_14), .minus_01_01_2(minus_01_15),
    .plus_00_01(_0_line__out__1[13]), .plus_00_00(_0_line__out__1[14]), .plus_00_01_2(_0_line__out__1[15]),
    .plus_01_01(_1_line[13]), .plus_01_00(_1_line[14]), .plus_01_01_2(_1_line[15]),
    .neighbours(neighbours_15_neighbours));
  aliveSTD alivestd_15 (
    .neighbours(neighbours_15_neighbours), .clock(clock), .alive(_0_line__out__1[14]),
    .input_state(state_helper_15_output_state));
  STATE_helper state_helper_15 (
    .input_state(input_state), .output_state(state_helper_15_output_state), .i(I), .j(J[14]));
  neighbours neighbours_16 (
    .minus_01_01(minus_01_14), .minus_01_00(minus_01_15), .minus_01_01_2(minus_01_16),
    .plus_00_01(_0_line__out__1[14]), .plus_00_00(_0_line__out__1[15]), .plus_00_01_2(_0_line__out__1[16]),
    .plus_01_01(_1_line[14]), .plus_01_00(_1_line[15]), .plus_01_01_2(_1_line[16]),
    .neighbours(neighbours_16_neighbours));
  aliveSTD alivestd_16 (
    .neighbours(neighbours_16_neighbours), .clock(clock), .alive(_0_line__out__1[15]),
    .input_state(state_helper_16_output_state));
  STATE_helper state_helper_16 (
    .input_state(input_state), .output_state(state_helper_16_output_state), .i(I), .j(J[15]));
  neighbours neighbours_17 (
    .minus_01_01(minus_01_15), .minus_01_00(minus_01_16), .minus_01_01_2(minus_01_17),
    .plus_00_01(_0_line__out__1[15]), .plus_00_00(_0_line__out__1[16]), .plus_00_01_2(_0_line__out__1[17]),
    .plus_01_01(_1_line[15]), .plus_01_00(_1_line[16]), .plus_01_01_2(_1_line[17]),
    .neighbours(neighbours_17_neighbours));
  aliveSTD alivestd_17 (
    .neighbours(neighbours_17_neighbours), .clock(clock), .alive(_0_line__out__1[16]),
    .input_state(state_helper_17_output_state));
  STATE_helper state_helper_17 (
    .input_state(input_state), .output_state(state_helper_17_output_state), .i(I), .j(J[16]));
  neighbours neighbours_18 (
    .minus_01_01(minus_01_16), .minus_01_00(minus_01_17), .minus_01_01_2(minus_01_18),
    .plus_00_01(_0_line__out__1[16]), .plus_00_00(_0_line__out__1[17]), .plus_00_01_2(_0_line__out__1[18]),
    .plus_01_01(_1_line[16]), .plus_01_00(_1_line[17]), .plus_01_01_2(_1_line[18]),
    .neighbours(neighbours_18_neighbours));
  aliveSTD alivestd_18 (
    .neighbours(neighbours_18_neighbours), .clock(clock), .alive(_0_line__out__1[17]),
    .input_state(state_helper_18_output_state));
  STATE_helper state_helper_18 (
    .input_state(input_state), .output_state(state_helper_18_output_state), .i(I), .j(J[17]));
  neighbours neighbours_19 (
    .minus_01_01(minus_01_17), .minus_01_00(minus_01_18), .minus_01_01_2(minus_01_19),
    .plus_00_01(_0_line__out__1[17]), .plus_00_00(_0_line__out__1[18]), .plus_00_01_2(_0_line__out__1[19]),
    .plus_01_01(_1_line[17]), .plus_01_00(_1_line[18]), .plus_01_01_2(_1_line[19]),
    .neighbours(neighbours_19_neighbours));
  aliveSTD alivestd_19 (
    .neighbours(neighbours_19_neighbours), .clock(clock), .alive(_0_line__out__1[18]),
    .input_state(state_helper_19_output_state));
  STATE_helper state_helper_19 (
    .input_state(input_state), .output_state(state_helper_19_output_state), .i(I), .j(J[18]));
  neighbours neighbours_20 (
    .minus_01_01(minus_01_18), .minus_01_00(minus_01_19), .minus_01_01_2(minus_01_20),
    .plus_00_01(_0_line__out__1[18]), .plus_00_00(_0_line__out__1[19]), .plus_00_01_2(_0_line__out__1[20]),
    .plus_01_01(_1_line[18]), .plus_01_00(_1_line[19]), .plus_01_01_2(_1_line[20]),
    .neighbours(neighbours_20_neighbours));
  aliveSTD alivestd_20 (
    .neighbours(neighbours_20_neighbours), .clock(clock), .alive(_0_line__out__1[19]),
    .input_state(state_helper_20_output_state));
  STATE_helper state_helper_20 (
    .input_state(input_state), .output_state(state_helper_20_output_state), .i(I), .j(J[19]));
  neighbours neighbours_21 (
    .minus_01_01(minus_01_19), .minus_01_00(minus_01_20), .minus_01_01_2(minus_01_21),
    .plus_00_01(_0_line__out__1[19]), .plus_00_00(_0_line__out__1[20]), .plus_00_01_2(_0_line__out__1[21]),
    .plus_01_01(_1_line[19]), .plus_01_00(_1_line[20]), .plus_01_01_2(_1_line[21]),
    .neighbours(neighbours_21_neighbours));
  aliveSTD alivestd_21 (
    .neighbours(neighbours_21_neighbours), .clock(clock), .alive(_0_line__out__1[20]),
    .input_state(state_helper_21_output_state));
  STATE_helper state_helper_21 (
    .input_state(input_state), .output_state(state_helper_21_output_state), .i(I), .j(J[22]));
  neighbours neighbours_22 (
    .minus_01_01(minus_01_20), .minus_01_00(minus_01_21), .minus_01_01_2(minus_01_22),
    .plus_00_01(_0_line__out__1[20]), .plus_00_00(_0_line__out__1[21]), .plus_00_01_2(_0_line__out__1[22]),
    .plus_01_01(_1_line[20]), .plus_01_00(_1_line[21]), .plus_01_01_2(_1_line[22]),
    .neighbours(neighbours_22_neighbours));
  aliveSTD alivestd_22 (
    .neighbours(neighbours_22_neighbours), .clock(clock), .alive(_0_line__out__1[21]),
    .input_state(state_helper_22_output_state));
  STATE_helper state_helper_22 (
    .input_state(input_state), .output_state(state_helper_22_output_state), .i(I), .j(J[21]));
  neighbours neighbours_23 (
    .minus_01_01(minus_01_21), .minus_01_00(minus_01_22), .minus_01_01_2(minus_01_23),
    .plus_00_01(_0_line__out__1[21]), .plus_00_00(_0_line__out__1[22]), .plus_00_01_2(_0_line__out__1[23]),
    .plus_01_01(_1_line[21]), .plus_01_00(_1_line[22]), .plus_01_01_2(_1_line[23]),
    .neighbours(neighbours_23_neighbours));
  aliveSTD alivestd_23 (
    .neighbours(neighbours_23_neighbours), .clock(clock), .alive(_0_line__out__1[22]),
    .input_state(state_helper_23_output_state));
  STATE_helper state_helper_23 (
    .input_state(input_state), .output_state(state_helper_23_output_state), .i(I), .j(J[22]));
  neighbours neighbours_24 (
    .minus_01_01(minus_01_22), .minus_01_00(minus_01_23), .minus_01_01_2(minus_01_24),
    .plus_00_01(_0_line__out__1[22]), .plus_00_00(_0_line__out__1[23]), .plus_00_01_2(_0_line__out__1[24]),
    .plus_01_01(_1_line[22]), .plus_01_00(_1_line[23]), .plus_01_01_2(_1_line[24]),
    .neighbours(neighbours_24_neighbours));
  aliveSTD alivestd_24 (
    .neighbours(neighbours_24_neighbours), .clock(clock), .alive(_0_line__out__1[23]),
    .input_state(state_helper_24_output_state));
  STATE_helper state_helper_24 (
    .input_state(input_state), .output_state(state_helper_24_output_state), .i(I), .j(J[23]));
  neighbours neighbours_25 (
    .minus_01_01(minus_01_23), .minus_01_00(minus_01_24), .minus_01_01_2(minus_01_25),
    .plus_00_01(_0_line__out__1[23]), .plus_00_00(_0_line__out__1[24]), .plus_00_01_2(_0_line__out__1[25]),
    .plus_01_01(_1_line[23]), .plus_01_00(_1_line[24]), .plus_01_01_2(_1_line[25]),
    .neighbours(neighbours_25_neighbours));
  aliveSTD alivestd_25 (
    .neighbours(neighbours_25_neighbours), .clock(clock), .alive(_0_line__out__1[24]),
    .input_state(state_helper_25_output_state));
  STATE_helper state_helper_25 (
    .input_state(input_state), .output_state(state_helper_25_output_state), .i(I), .j(J[24]));
  neighbours neighbours_26 (
    .minus_01_01(minus_01_24), .minus_01_00(minus_01_25), .minus_01_01_2(minus_01_26),
    .plus_00_01(_0_line__out__1[24]), .plus_00_00(_0_line__out__1[25]), .plus_00_01_2(_0_line__out__1[26]),
    .plus_01_01(_1_line[24]), .plus_01_00(_1_line[25]), .plus_01_01_2(_1_line[26]),
    .neighbours(neighbours_26_neighbours));
  aliveSTD alivestd_26 (
    .neighbours(neighbours_26_neighbours), .clock(clock), .alive(_0_line__out__1[25]),
    .input_state(state_helper_26_output_state));
  STATE_helper state_helper_26 (
    .input_state(input_state), .output_state(state_helper_26_output_state), .i(I), .j(J[25]));
  neighbours neighbours_27 (
    .minus_01_01(minus_01_25), .minus_01_00(minus_01_26), .minus_01_01_2(minus_01_27),
    .plus_00_01(_0_line__out__1[25]), .plus_00_00(_0_line__out__1[26]), .plus_00_01_2(_0_line__out__1[27]),
    .plus_01_01(_1_line[25]), .plus_01_00(_1_line[26]), .plus_01_01_2(_1_line[27]),
    .neighbours(neighbours_27_neighbours));
  aliveSTD alivestd_27 (
    .neighbours(neighbours_27_neighbours), .clock(clock), .alive(_0_line__out__1[26]),
    .input_state(state_helper_27_output_state));
  STATE_helper state_helper_27 (
    .input_state(input_state), .output_state(state_helper_27_output_state), .i(I), .j(J[26]));
  neighbours neighbours_28 (
    .minus_01_01(minus_01_26), .minus_01_00(minus_01_27), .minus_01_01_2(minus_01_28),
    .plus_00_01(_0_line__out__1[26]), .plus_00_00(_0_line__out__1[27]), .plus_00_01_2(_0_line__out__1[28]),
    .plus_01_01(_1_line[26]), .plus_01_00(_1_line[27]), .plus_01_01_2(_1_line[28]),
    .neighbours(neighbours_28_neighbours));
  aliveSTD alivestd_28 (
    .neighbours(neighbours_28_neighbours), .clock(clock), .alive(_0_line__out__1[27]),
    .input_state(state_helper_28_output_state));
  STATE_helper state_helper_28 (
    .input_state(input_state), .output_state(state_helper_28_output_state), .i(I), .j(J[27]));
  neighbours neighbours_29 (
    .minus_01_01(minus_01_27), .minus_01_00(minus_01_28), .minus_01_01_2(minus_01_29),
    .plus_00_01(_0_line__out__1[27]), .plus_00_00(_0_line__out__1[28]), .plus_00_01_2(_0_line__out__1[29]),
    .plus_01_01(_1_line[27]), .plus_01_00(_1_line[28]), .plus_01_01_2(_1_line[29]),
    .neighbours(neighbours_29_neighbours));
  aliveSTD alivestd_29 (
    .neighbours(neighbours_29_neighbours), .clock(clock), .alive(_0_line__out__1[28]),
    .input_state(state_helper_29_output_state));
  STATE_helper state_helper_29 (
    .input_state(input_state), .output_state(state_helper_29_output_state), .i(I), .j(J[28]));
  neighbours neighbours_30 (
    .minus_01_01(minus_01_28), .minus_01_00(minus_01_29), .minus_01_01_2(minus_01_30),
    .plus_00_01(_0_line__out__1[28]), .plus_00_00(_0_line__out__1[29]), .plus_00_01_2(_0_line__out__1[30]),
    .plus_01_01(_1_line[28]), .plus_01_00(_1_line[29]), .plus_01_01_2(_1_line[30]),
    .neighbours(neighbours_30_neighbours));
  aliveSTD alivestd_30 (
    .neighbours(neighbours_30_neighbours), .clock(clock), .alive(_0_line__out__1[29]),
    .input_state(state_helper_30_output_state));
  STATE_helper state_helper_30 (
    .input_state(input_state), .output_state(state_helper_30_output_state), .i(I), .j(J[29]));
  neighbours neighbours_31 (
    .minus_01_01(minus_01_29), .minus_01_00(minus_01_30), .minus_01_01_2(minus_01_31),
    .plus_00_01(_0_line__out__1[29]), .plus_00_00(_0_line__out__1[30]), .plus_00_01_2(_0_line__out__1[31]),
    .plus_01_01(_1_line[29]), .plus_01_00(_1_line[30]), .plus_01_01_2(_1_line[31]),
    .neighbours(neighbours_31_neighbours));
  aliveSTD alivestd_31 (
    .neighbours(neighbours_31_neighbours), .clock(clock), .alive(_0_line__out__1[30]),
    .input_state(state_helper_31_output_state));
  STATE_helper state_helper_31 (
    .input_state(input_state), .output_state(state_helper_31_output_state), .i(I), .j(J[30]));
  neighbours neighbours_32 (
    .minus_01_01(minus_01_30), .minus_01_00(minus_01_31), .minus_01_01_2(minus_01_32),
    .plus_00_01(_0_line__out__1[30]), .plus_00_00(_0_line__out__1[31]), .plus_00_01_2(plus_00_32),
    .plus_01_01(_1_line[30]), .plus_01_00(_1_line[31]), .plus_01_01_2(plus_01_32),
    .neighbours(neighbours_32_neighbours));
  aliveSTD alivestd_32 (
    .neighbours(neighbours_32_neighbours), .clock(clock), .alive(_0_line__out__1[31]),
    .input_state(state_helper_32_output_state));
  STATE_helper state_helper_32 (
    .input_state(input_state), .output_state(state_helper_32_output_state), .i(I), .j(J[31]));

  assign _0_line__out__1_2 = _0_line__out__1;
  assign display = _0_line__out__1;
  assign J[20] = J[22];

  // Other names for the same wires on the sheet: plus_01_00 = _1_line[0]; plus_01_01 = _1_line[1];
  //   plus_01_02 = _1_line[2]; plus_01_03 = _1_line[3]; plus_01_04 = _1_line[4]; plus_01_05 = _1_line[5];
  //   plus_01_06 = _1_line[6]; plus_01_07 = _1_line[7]; plus_01_08 = _1_line[8]; plus_01_09 = _1_line[9];
  //   plus_01_10 = _1_line[10]; plus_01_11 = _1_line[11]; plus_01_12 = _1_line[12]; plus_01_13 = _1_line[13];
  //   plus_01_14 = _1_line[14]; plus_01_15 = _1_line[15]; plus_01_16 = _1_line[16]; plus_01_17 = _1_line[17];
  //   plus_01_18 = _1_line[18]; plus_01_19 = _1_line[19]; plus_01_20 = _1_line[20]; plus_01_21 = _1_line[21];
  //   plus_01_22 = _1_line[22]; plus_01_23 = _1_line[23]; plus_01_24 = _1_line[24]; plus_01_25 = _1_line[25];
  //   plus_01_26 = _1_line[26]; plus_01_27 = _1_line[27]; plus_01_28 = _1_line[28]; plus_01_29 = _1_line[29];
  //   plus_01_30 = _1_line[30]; plus_01_31 = _1_line[31]; plus_00_00 = _0_line__out__1[0];
  //   plus_00_01 = _0_line__out__1[1]; plus_00_02 = _0_line__out__1[2]; plus_00_03 = _0_line__out__1[3];
  //   plus_00_04 = _0_line__out__1[4]; plus_00_05 = _0_line__out__1[5]; plus_00_06 = _0_line__out__1[6];
  //   plus_00_07 = _0_line__out__1[7]; plus_00_08 = _0_line__out__1[8]; plus_00_09 = _0_line__out__1[9];
  //   plus_00_10 = _0_line__out__1[10]; plus_00_11 = _0_line__out__1[11]; plus_00_12 = _0_line__out__1[12];
  //   plus_00_13 = _0_line__out__1[13]; plus_00_14 = _0_line__out__1[14]; plus_00_15 = _0_line__out__1[15];
  //   plus_00_16 = _0_line__out__1[16]; plus_00_17 = _0_line__out__1[17]; plus_00_18 = _0_line__out__1[18];
  //   plus_00_19 = _0_line__out__1[19]; plus_00_20 = _0_line__out__1[20]; plus_00_21 = _0_line__out__1[21];
  //   plus_00_22 = _0_line__out__1[22]; plus_00_23 = _0_line__out__1[23]; plus_00_24 = _0_line__out__1[24];
  //   plus_00_25 = _0_line__out__1[25]; plus_00_26 = _0_line__out__1[26]; plus_00_27 = _0_line__out__1[27];
  //   plus_00_28 = _0_line__out__1[28]; plus_00_29 = _0_line__out__1[29]; plus_00_30 = _0_line__out__1[30];
  //   plus_00_31 = _0_line__out__1[31]; j20 = J[22]; minus_02_00 = minus_1_line[0]; minus_02_01 = minus_1_line[1];
  //   minus_02_02 = minus_1_line[2]; minus_02_03 = minus_1_line[3]; minus_02_04 = minus_1_line[4];
  //   minus_02_05 = minus_1_line[5]; minus_02_06 = minus_1_line[6]; minus_02_07 = minus_1_line[7];
  //   minus_02_08 = minus_1_line[8]; minus_02_09 = minus_1_line[9]; minus_02_10 = minus_1_line[10];
  //   minus_02_11 = minus_1_line[11]; minus_02_12 = minus_1_line[12]; minus_02_13 = minus_1_line[13];
  //   minus_02_14 = minus_1_line[14]; minus_02_15 = minus_1_line[15]; minus_02_16 = minus_1_line[16];
  //   minus_02_17 = minus_1_line[17]; minus_02_18 = minus_1_line[18]; minus_02_19 = minus_1_line[19];
  //   minus_02_20 = minus_1_line[20]; minus_02_21 = minus_1_line[21]; minus_02_22 = minus_1_line[22];
  //   minus_02_23 = minus_1_line[23]; minus_02_24 = minus_1_line[24]; minus_02_25 = minus_1_line[25];
  //   minus_02_26 = minus_1_line[26]; minus_02_27 = minus_1_line[27]; minus_02_28 = minus_1_line[28];
  //   minus_02_29 = minus_1_line[29]; minus_02_30 = minus_1_line[30]; minus_02_31 = minus_1_line[31];
  //   state[1:0] = input_state
endmodule

module line (
  input  [31:0] J,
  input  [31:0] minus_1_line,
  input  [31:0] _1_line,
  input  I,
  input  Torus,
  input  [1:0] input_state,
  output [31:0] _0_line__out__1,
  output [31:0] display,
  output [31:0] _0_line__out__1_2
);

  wire clock, minus_01_00, minus_01_01, minus_01_01_t, minus_01_02, minus_01_03, minus_01_04, minus_01_05,
       minus_01_06, minus_01_07, minus_01_08, minus_01_09, minus_01_10, minus_01_11, minus_01_12,
       minus_01_13, minus_01_14, minus_01_15, minus_01_16, minus_01_17, minus_01_18, minus_01_19,
       minus_01_20, minus_01_21, minus_01_22, minus_01_23, minus_01_24, minus_01_25, minus_01_26,
       minus_01_27, minus_01_28, minus_01_29, minus_01_30, minus_01_31, minus_01_32, plus_00_01_t,
       plus_00_32, plus_01_01_t, plus_01_32;
  wire [1:0] state_helper_1_output_state, state_helper_2_output_state, state_helper_3_output_state,
       state_helper_4_output_state, state_helper_5_output_state, state_helper_6_output_state,
       state_helper_7_output_state, state_helper_8_output_state, state_helper_9_output_state,
       state_helper_10_output_state, state_helper_11_output_state, state_helper_12_output_state,
       state_helper_13_output_state, state_helper_14_output_state, state_helper_15_output_state,
       state_helper_16_output_state, state_helper_17_output_state, state_helper_18_output_state,
       state_helper_19_output_state, state_helper_20_output_state, state_helper_21_output_state,
       state_helper_22_output_state, state_helper_23_output_state, state_helper_24_output_state,
       state_helper_25_output_state, state_helper_26_output_state, state_helper_27_output_state,
       state_helper_28_output_state, state_helper_29_output_state, state_helper_30_output_state,
       state_helper_31_output_state, state_helper_32_output_state;
  wire [8:0] lookAt, neighbours_1_neighbours, neighbours_2_neighbours, neighbours_3_neighbours,
       neighbours_4_neighbours, neighbours_5_neighbours, neighbours_6_neighbours, neighbours_7_neighbours,
       neighbours_8_neighbours, neighbours_9_neighbours, neighbours_10_neighbours, neighbours_11_neighbours,
       neighbours_12_neighbours, neighbours_13_neighbours, neighbours_14_neighbours,
       neighbours_15_neighbours, neighbours_16_neighbours, neighbours_17_neighbours,
       neighbours_18_neighbours, neighbours_19_neighbours, neighbours_20_neighbours,
       neighbours_21_neighbours, neighbours_22_neighbours, neighbours_23_neighbours,
       neighbours_24_neighbours, neighbours_25_neighbours, neighbours_26_neighbours,
       neighbours_27_neighbours, neighbours_28_neighbours, neighbours_29_neighbours,
       neighbours_30_neighbours, neighbours_31_neighbours, neighbours_32_neighbours;
  wire [29:0] birth, save;

  neighbours neighbours_1 (
    .minus_01_01(minus_01_01_t), .minus_01_00(minus_01_00), .minus_01_01_2(minus_01_01),
    .plus_00_01(plus_00_01_t), .plus_00_00(_0_line__out__1[0]), .plus_00_01_2(_0_line__out__1[1]),
    .plus_01_01(plus_01_01_t), .plus_01_00(_1_line[0]), .plus_01_01_2(_1_line[1]),
    .neighbours(neighbours_1_neighbours));
  alive alive_1 (
    .neighbours(neighbours_1_neighbours), .look_at(lookAt), .B___birth(birth), .S___save(save),
    .alive(_0_line__out__1[0]), .input_state(state_helper_1_output_state), .clock(clock));
  STATE_helper state_helper_1 (.input_state(input_state), .output_state(state_helper_1_output_state), .i(I), .j(J[0]));
  and and_1 (minus_01_32, minus_01_00, Torus);
  and and_2 (minus_01_01_t, minus_01_31, Torus);
  neighbours neighbours_2 (
    .minus_01_01(minus_01_00), .minus_01_00(minus_01_01), .minus_01_01_2(minus_01_02),
    .plus_00_01(_0_line__out__1[0]), .plus_00_00(_0_line__out__1[1]), .plus_00_01_2(_0_line__out__1[2]),
    .plus_01_01(_1_line[0]), .plus_01_00(_1_line[1]), .plus_01_01_2(_1_line[2]),
    .neighbours(neighbours_2_neighbours));
  alive alive_2 (
    .neighbours(neighbours_2_neighbours), .look_at(lookAt), .B___birth(birth), .S___save(save),
    .alive(_0_line__out__1[1]), .input_state(state_helper_2_output_state), .clock(clock));
  STATE_helper state_helper_2 (.input_state(input_state), .output_state(state_helper_2_output_state), .i(I), .j(J[1]));
  and and_3 (plus_01_32, _1_line[0], Torus);
  and and_4 (plus_01_01_t, _1_line[31], Torus);
  and and_5 (plus_00_32, _0_line__out__1[0], Torus);
  and and_6 (plus_00_01_t, _0_line__out__1[31], Torus);
  neighbours neighbours_3 (
    .minus_01_01(minus_01_01), .minus_01_00(minus_01_02), .minus_01_01_2(minus_01_03),
    .plus_00_01(_0_line__out__1[1]), .plus_00_00(_0_line__out__1[2]), .plus_00_01_2(_0_line__out__1[3]),
    .plus_01_01(_1_line[1]), .plus_01_00(_1_line[2]), .plus_01_01_2(_1_line[3]),
    .neighbours(neighbours_3_neighbours));
  alive alive_3 (
    .neighbours(neighbours_3_neighbours), .look_at(lookAt), .B___birth(birth), .S___save(save),
    .alive(_0_line__out__1[2]), .input_state(state_helper_3_output_state), .clock(clock));
  STATE_helper state_helper_3 (.input_state(input_state), .output_state(state_helper_3_output_state), .i(I), .j(J[2]));
  neighbours neighbours_4 (
    .minus_01_01(minus_01_02), .minus_01_00(minus_01_03), .minus_01_01_2(minus_01_04),
    .plus_00_01(_0_line__out__1[2]), .plus_00_00(_0_line__out__1[3]), .plus_00_01_2(_0_line__out__1[4]),
    .plus_01_01(_1_line[2]), .plus_01_00(_1_line[3]), .plus_01_01_2(_1_line[4]),
    .neighbours(neighbours_4_neighbours));
  alive alive_4 (
    .neighbours(neighbours_4_neighbours), .look_at(lookAt), .B___birth(birth), .S___save(save),
    .alive(_0_line__out__1[3]), .input_state(state_helper_4_output_state), .clock(clock));
  STATE_helper state_helper_4 (.input_state(input_state), .output_state(state_helper_4_output_state), .i(I), .j(J[3]));
  neighbours neighbours_5 (
    .minus_01_01(minus_01_03), .minus_01_00(minus_01_04), .minus_01_01_2(minus_01_05),
    .plus_00_01(_0_line__out__1[3]), .plus_00_00(_0_line__out__1[4]), .plus_00_01_2(_0_line__out__1[5]),
    .plus_01_01(_1_line[3]), .plus_01_00(_1_line[4]), .plus_01_01_2(_1_line[5]),
    .neighbours(neighbours_5_neighbours));
  alive alive_5 (
    .neighbours(neighbours_5_neighbours), .look_at(lookAt), .B___birth(birth), .S___save(save),
    .alive(_0_line__out__1[4]), .input_state(state_helper_5_output_state), .clock(clock));
  STATE_helper state_helper_5 (.input_state(input_state), .output_state(state_helper_5_output_state), .i(I), .j(J[4]));
  neighbours neighbours_6 (
    .minus_01_01(minus_01_04), .minus_01_00(minus_01_05), .minus_01_01_2(minus_01_06),
    .plus_00_01(_0_line__out__1[4]), .plus_00_00(_0_line__out__1[5]), .plus_00_01_2(_0_line__out__1[6]),
    .plus_01_01(_1_line[4]), .plus_01_00(_1_line[5]), .plus_01_01_2(_1_line[6]),
    .neighbours(neighbours_6_neighbours));
  alive alive_6 (
    .neighbours(neighbours_6_neighbours), .look_at(lookAt), .B___birth(birth), .S___save(save),
    .alive(_0_line__out__1[5]), .input_state(state_helper_6_output_state), .clock(clock));
  STATE_helper state_helper_6 (.input_state(input_state), .output_state(state_helper_6_output_state), .i(I), .j(J[5]));
  neighbours neighbours_7 (
    .minus_01_01(minus_01_05), .minus_01_00(minus_01_06), .minus_01_01_2(minus_01_07),
    .plus_00_01(_0_line__out__1[5]), .plus_00_00(_0_line__out__1[6]), .plus_00_01_2(_0_line__out__1[7]),
    .plus_01_01(_1_line[5]), .plus_01_00(_1_line[6]), .plus_01_01_2(_1_line[7]),
    .neighbours(neighbours_7_neighbours));
  alive alive_7 (
    .neighbours(neighbours_7_neighbours), .look_at(lookAt), .B___birth(birth), .S___save(save),
    .alive(_0_line__out__1[6]), .input_state(state_helper_7_output_state), .clock(clock));
  STATE_helper state_helper_7 (.input_state(input_state), .output_state(state_helper_7_output_state), .i(I), .j(J[6]));
  neighbours neighbours_8 (
    .minus_01_01(minus_01_06), .minus_01_00(minus_01_07), .minus_01_01_2(minus_01_08),
    .plus_00_01(_0_line__out__1[6]), .plus_00_00(_0_line__out__1[7]), .plus_00_01_2(_0_line__out__1[8]),
    .plus_01_01(_1_line[6]), .plus_01_00(_1_line[7]), .plus_01_01_2(_1_line[8]),
    .neighbours(neighbours_8_neighbours));
  alive alive_8 (
    .neighbours(neighbours_8_neighbours), .look_at(lookAt), .B___birth(birth), .S___save(save),
    .alive(_0_line__out__1[7]), .input_state(state_helper_8_output_state), .clock(clock));
  STATE_helper state_helper_8 (.input_state(input_state), .output_state(state_helper_8_output_state), .i(I), .j(J[7]));
  neighbours neighbours_9 (
    .minus_01_01(minus_01_07), .minus_01_00(minus_01_08), .minus_01_01_2(minus_01_09),
    .plus_00_01(_0_line__out__1[7]), .plus_00_00(_0_line__out__1[8]), .plus_00_01_2(_0_line__out__1[9]),
    .plus_01_01(_1_line[7]), .plus_01_00(_1_line[8]), .plus_01_01_2(_1_line[9]),
    .neighbours(neighbours_9_neighbours));
  alive alive_9 (
    .neighbours(neighbours_9_neighbours), .look_at(lookAt), .B___birth(birth), .S___save(save),
    .alive(_0_line__out__1[8]), .input_state(state_helper_9_output_state), .clock(clock));
  STATE_helper state_helper_9 (.input_state(input_state), .output_state(state_helper_9_output_state), .i(I), .j(J[8]));
  neighbours neighbours_10 (
    .minus_01_01(minus_01_08), .minus_01_00(minus_01_09), .minus_01_01_2(minus_01_10),
    .plus_00_01(_0_line__out__1[8]), .plus_00_00(_0_line__out__1[9]), .plus_00_01_2(_0_line__out__1[10]),
    .plus_01_01(_1_line[8]), .plus_01_00(_1_line[9]), .plus_01_01_2(_1_line[10]),
    .neighbours(neighbours_10_neighbours));
  alive alive_10 (
    .neighbours(neighbours_10_neighbours), .look_at(lookAt), .B___birth(birth), .S___save(save),
    .alive(_0_line__out__1[9]), .input_state(state_helper_10_output_state), .clock(clock));
  STATE_helper state_helper_10 (
    .input_state(input_state), .output_state(state_helper_10_output_state), .i(I), .j(J[9]));
  neighbours neighbours_11 (
    .minus_01_01(minus_01_09), .minus_01_00(minus_01_10), .minus_01_01_2(minus_01_11),
    .plus_00_01(_0_line__out__1[9]), .plus_00_00(_0_line__out__1[10]), .plus_00_01_2(_0_line__out__1[11]),
    .plus_01_01(_1_line[9]), .plus_01_00(_1_line[10]), .plus_01_01_2(_1_line[11]),
    .neighbours(neighbours_11_neighbours));
  alive alive_11 (
    .neighbours(neighbours_11_neighbours), .look_at(lookAt), .B___birth(birth), .S___save(save),
    .alive(_0_line__out__1[10]), .input_state(state_helper_11_output_state), .clock(clock));
  STATE_helper state_helper_11 (
    .input_state(input_state), .output_state(state_helper_11_output_state), .i(I), .j(J[10]));
  neighbours neighbours_12 (
    .minus_01_01(minus_01_10), .minus_01_00(minus_01_11), .minus_01_01_2(minus_01_12),
    .plus_00_01(_0_line__out__1[10]), .plus_00_00(_0_line__out__1[11]), .plus_00_01_2(_0_line__out__1[12]),
    .plus_01_01(_1_line[10]), .plus_01_00(_1_line[11]), .plus_01_01_2(_1_line[12]),
    .neighbours(neighbours_12_neighbours));
  alive alive_12 (
    .neighbours(neighbours_12_neighbours), .look_at(lookAt), .B___birth(birth), .S___save(save),
    .alive(_0_line__out__1[11]), .input_state(state_helper_12_output_state), .clock(clock));
  STATE_helper state_helper_12 (
    .input_state(input_state), .output_state(state_helper_12_output_state), .i(I), .j(J[11]));
  neighbours neighbours_13 (
    .minus_01_01(minus_01_11), .minus_01_00(minus_01_12), .minus_01_01_2(minus_01_13),
    .plus_00_01(_0_line__out__1[11]), .plus_00_00(_0_line__out__1[12]), .plus_00_01_2(_0_line__out__1[13]),
    .plus_01_01(_1_line[11]), .plus_01_00(_1_line[12]), .plus_01_01_2(_1_line[13]),
    .neighbours(neighbours_13_neighbours));
  alive alive_13 (
    .neighbours(neighbours_13_neighbours), .look_at(lookAt), .B___birth(birth), .S___save(save),
    .alive(_0_line__out__1[12]), .input_state(state_helper_13_output_state), .clock(clock));
  STATE_helper state_helper_13 (
    .input_state(input_state), .output_state(state_helper_13_output_state), .i(I), .j(J[12]));
  neighbours neighbours_14 (
    .minus_01_01(minus_01_12), .minus_01_00(minus_01_13), .minus_01_01_2(minus_01_14),
    .plus_00_01(_0_line__out__1[12]), .plus_00_00(_0_line__out__1[13]), .plus_00_01_2(_0_line__out__1[14]),
    .plus_01_01(_1_line[12]), .plus_01_00(_1_line[13]), .plus_01_01_2(_1_line[14]),
    .neighbours(neighbours_14_neighbours));
  alive alive_14 (
    .neighbours(neighbours_14_neighbours), .look_at(lookAt), .B___birth(birth), .S___save(save),
    .alive(_0_line__out__1[13]), .input_state(state_helper_14_output_state), .clock(clock));
  STATE_helper state_helper_14 (
    .input_state(input_state), .output_state(state_helper_14_output_state), .i(I), .j(J[13]));
  neighbours neighbours_15 (
    .minus_01_01(minus_01_13), .minus_01_00(minus_01_14), .minus_01_01_2(minus_01_15),
    .plus_00_01(_0_line__out__1[13]), .plus_00_00(_0_line__out__1[14]), .plus_00_01_2(_0_line__out__1[15]),
    .plus_01_01(_1_line[13]), .plus_01_00(_1_line[14]), .plus_01_01_2(_1_line[15]),
    .neighbours(neighbours_15_neighbours));
  alive alive_15 (
    .neighbours(neighbours_15_neighbours), .look_at(lookAt), .B___birth(birth), .S___save(save),
    .alive(_0_line__out__1[14]), .input_state(state_helper_15_output_state), .clock(clock));
  STATE_helper state_helper_15 (
    .input_state(input_state), .output_state(state_helper_15_output_state), .i(I), .j(J[14]));
  neighbours neighbours_16 (
    .minus_01_01(minus_01_14), .minus_01_00(minus_01_15), .minus_01_01_2(minus_01_16),
    .plus_00_01(_0_line__out__1[14]), .plus_00_00(_0_line__out__1[15]), .plus_00_01_2(_0_line__out__1[16]),
    .plus_01_01(_1_line[14]), .plus_01_00(_1_line[15]), .plus_01_01_2(_1_line[16]),
    .neighbours(neighbours_16_neighbours));
  alive alive_16 (
    .neighbours(neighbours_16_neighbours), .look_at(lookAt), .B___birth(birth), .S___save(save),
    .alive(_0_line__out__1[15]), .input_state(state_helper_16_output_state), .clock(clock));
  STATE_helper state_helper_16 (
    .input_state(input_state), .output_state(state_helper_16_output_state), .i(I), .j(J[15]));
  neighbours neighbours_17 (
    .minus_01_01(minus_01_15), .minus_01_00(minus_01_16), .minus_01_01_2(minus_01_17),
    .plus_00_01(_0_line__out__1[15]), .plus_00_00(_0_line__out__1[16]), .plus_00_01_2(_0_line__out__1[17]),
    .plus_01_01(_1_line[15]), .plus_01_00(_1_line[16]), .plus_01_01_2(_1_line[17]),
    .neighbours(neighbours_17_neighbours));
  alive alive_17 (
    .neighbours(neighbours_17_neighbours), .look_at(lookAt), .B___birth(birth), .S___save(save),
    .alive(_0_line__out__1[16]), .input_state(state_helper_17_output_state), .clock(clock));
  STATE_helper state_helper_17 (
    .input_state(input_state), .output_state(state_helper_17_output_state), .i(I), .j(J[16]));
  neighbours neighbours_18 (
    .minus_01_01(minus_01_16), .minus_01_00(minus_01_17), .minus_01_01_2(minus_01_18),
    .plus_00_01(_0_line__out__1[16]), .plus_00_00(_0_line__out__1[17]), .plus_00_01_2(_0_line__out__1[18]),
    .plus_01_01(_1_line[16]), .plus_01_00(_1_line[17]), .plus_01_01_2(_1_line[18]),
    .neighbours(neighbours_18_neighbours));
  alive alive_18 (
    .neighbours(neighbours_18_neighbours), .look_at(lookAt), .B___birth(birth), .S___save(save),
    .alive(_0_line__out__1[17]), .input_state(state_helper_18_output_state), .clock(clock));
  STATE_helper state_helper_18 (
    .input_state(input_state), .output_state(state_helper_18_output_state), .i(I), .j(J[17]));
  neighbours neighbours_19 (
    .minus_01_01(minus_01_17), .minus_01_00(minus_01_18), .minus_01_01_2(minus_01_19),
    .plus_00_01(_0_line__out__1[17]), .plus_00_00(_0_line__out__1[18]), .plus_00_01_2(_0_line__out__1[19]),
    .plus_01_01(_1_line[17]), .plus_01_00(_1_line[18]), .plus_01_01_2(_1_line[19]),
    .neighbours(neighbours_19_neighbours));
  alive alive_19 (
    .neighbours(neighbours_19_neighbours), .look_at(lookAt), .B___birth(birth), .S___save(save),
    .alive(_0_line__out__1[18]), .input_state(state_helper_19_output_state), .clock(clock));
  STATE_helper state_helper_19 (
    .input_state(input_state), .output_state(state_helper_19_output_state), .i(I), .j(J[18]));
  neighbours neighbours_20 (
    .minus_01_01(minus_01_18), .minus_01_00(minus_01_19), .minus_01_01_2(minus_01_20),
    .plus_00_01(_0_line__out__1[18]), .plus_00_00(_0_line__out__1[19]), .plus_00_01_2(_0_line__out__1[20]),
    .plus_01_01(_1_line[18]), .plus_01_00(_1_line[19]), .plus_01_01_2(_1_line[20]),
    .neighbours(neighbours_20_neighbours));
  alive alive_20 (
    .neighbours(neighbours_20_neighbours), .look_at(lookAt), .B___birth(birth), .S___save(save),
    .alive(_0_line__out__1[19]), .input_state(state_helper_20_output_state), .clock(clock));
  STATE_helper state_helper_20 (
    .input_state(input_state), .output_state(state_helper_20_output_state), .i(I), .j(J[19]));
  neighbours neighbours_21 (
    .minus_01_01(minus_01_19), .minus_01_00(minus_01_20), .minus_01_01_2(minus_01_21),
    .plus_00_01(_0_line__out__1[19]), .plus_00_00(_0_line__out__1[20]), .plus_00_01_2(_0_line__out__1[21]),
    .plus_01_01(_1_line[19]), .plus_01_00(_1_line[20]), .plus_01_01_2(_1_line[21]),
    .neighbours(neighbours_21_neighbours));
  alive alive_21 (
    .neighbours(neighbours_21_neighbours), .look_at(lookAt), .B___birth(birth), .S___save(save),
    .alive(_0_line__out__1[20]), .input_state(state_helper_21_output_state), .clock(clock));
  STATE_helper state_helper_21 (
    .input_state(input_state), .output_state(state_helper_21_output_state), .i(I), .j(J[22]));
  neighbours neighbours_22 (
    .minus_01_01(minus_01_20), .minus_01_00(minus_01_21), .minus_01_01_2(minus_01_22),
    .plus_00_01(_0_line__out__1[20]), .plus_00_00(_0_line__out__1[21]), .plus_00_01_2(_0_line__out__1[22]),
    .plus_01_01(_1_line[20]), .plus_01_00(_1_line[21]), .plus_01_01_2(_1_line[22]),
    .neighbours(neighbours_22_neighbours));
  alive alive_22 (
    .neighbours(neighbours_22_neighbours), .look_at(lookAt), .B___birth(birth), .S___save(save),
    .alive(_0_line__out__1[21]), .input_state(state_helper_22_output_state), .clock(clock));
  STATE_helper state_helper_22 (
    .input_state(input_state), .output_state(state_helper_22_output_state), .i(I), .j(J[21]));
  neighbours neighbours_23 (
    .minus_01_01(minus_01_21), .minus_01_00(minus_01_22), .minus_01_01_2(minus_01_23),
    .plus_00_01(_0_line__out__1[21]), .plus_00_00(_0_line__out__1[22]), .plus_00_01_2(_0_line__out__1[23]),
    .plus_01_01(_1_line[21]), .plus_01_00(_1_line[22]), .plus_01_01_2(_1_line[23]),
    .neighbours(neighbours_23_neighbours));
  alive alive_23 (
    .neighbours(neighbours_23_neighbours), .look_at(lookAt), .B___birth(birth), .S___save(save),
    .alive(_0_line__out__1[22]), .input_state(state_helper_23_output_state), .clock(clock));
  STATE_helper state_helper_23 (
    .input_state(input_state), .output_state(state_helper_23_output_state), .i(I), .j(J[22]));
  neighbours neighbours_24 (
    .minus_01_01(minus_01_22), .minus_01_00(minus_01_23), .minus_01_01_2(minus_01_24),
    .plus_00_01(_0_line__out__1[22]), .plus_00_00(_0_line__out__1[23]), .plus_00_01_2(_0_line__out__1[24]),
    .plus_01_01(_1_line[22]), .plus_01_00(_1_line[23]), .plus_01_01_2(_1_line[24]),
    .neighbours(neighbours_24_neighbours));
  alive alive_24 (
    .neighbours(neighbours_24_neighbours), .look_at(lookAt), .B___birth(birth), .S___save(save),
    .alive(_0_line__out__1[23]), .input_state(state_helper_24_output_state), .clock(clock));
  STATE_helper state_helper_24 (
    .input_state(input_state), .output_state(state_helper_24_output_state), .i(I), .j(J[23]));
  neighbours neighbours_25 (
    .minus_01_01(minus_01_23), .minus_01_00(minus_01_24), .minus_01_01_2(minus_01_25),
    .plus_00_01(_0_line__out__1[23]), .plus_00_00(_0_line__out__1[24]), .plus_00_01_2(_0_line__out__1[25]),
    .plus_01_01(_1_line[23]), .plus_01_00(_1_line[24]), .plus_01_01_2(_1_line[25]),
    .neighbours(neighbours_25_neighbours));
  alive alive_25 (
    .neighbours(neighbours_25_neighbours), .look_at(lookAt), .B___birth(birth), .S___save(save),
    .alive(_0_line__out__1[24]), .input_state(state_helper_25_output_state), .clock(clock));
  STATE_helper state_helper_25 (
    .input_state(input_state), .output_state(state_helper_25_output_state), .i(I), .j(J[24]));
  neighbours neighbours_26 (
    .minus_01_01(minus_01_24), .minus_01_00(minus_01_25), .minus_01_01_2(minus_01_26),
    .plus_00_01(_0_line__out__1[24]), .plus_00_00(_0_line__out__1[25]), .plus_00_01_2(_0_line__out__1[26]),
    .plus_01_01(_1_line[24]), .plus_01_00(_1_line[25]), .plus_01_01_2(_1_line[26]),
    .neighbours(neighbours_26_neighbours));
  alive alive_26 (
    .neighbours(neighbours_26_neighbours), .look_at(lookAt), .B___birth(birth), .S___save(save),
    .alive(_0_line__out__1[25]), .input_state(state_helper_26_output_state), .clock(clock));
  STATE_helper state_helper_26 (
    .input_state(input_state), .output_state(state_helper_26_output_state), .i(I), .j(J[25]));
  neighbours neighbours_27 (
    .minus_01_01(minus_01_25), .minus_01_00(minus_01_26), .minus_01_01_2(minus_01_27),
    .plus_00_01(_0_line__out__1[25]), .plus_00_00(_0_line__out__1[26]), .plus_00_01_2(_0_line__out__1[27]),
    .plus_01_01(_1_line[25]), .plus_01_00(_1_line[26]), .plus_01_01_2(_1_line[27]),
    .neighbours(neighbours_27_neighbours));
  alive alive_27 (
    .neighbours(neighbours_27_neighbours), .look_at(lookAt), .B___birth(birth), .S___save(save),
    .alive(_0_line__out__1[26]), .input_state(state_helper_27_output_state), .clock(clock));
  STATE_helper state_helper_27 (
    .input_state(input_state), .output_state(state_helper_27_output_state), .i(I), .j(J[26]));
  neighbours neighbours_28 (
    .minus_01_01(minus_01_26), .minus_01_00(minus_01_27), .minus_01_01_2(minus_01_28),
    .plus_00_01(_0_line__out__1[26]), .plus_00_00(_0_line__out__1[27]), .plus_00_01_2(_0_line__out__1[28]),
    .plus_01_01(_1_line[26]), .plus_01_00(_1_line[27]), .plus_01_01_2(_1_line[28]),
    .neighbours(neighbours_28_neighbours));
  alive alive_28 (
    .neighbours(neighbours_28_neighbours), .look_at(lookAt), .B___birth(birth), .S___save(save),
    .alive(_0_line__out__1[27]), .input_state(state_helper_28_output_state), .clock(clock));
  STATE_helper state_helper_28 (
    .input_state(input_state), .output_state(state_helper_28_output_state), .i(I), .j(J[27]));
  neighbours neighbours_29 (
    .minus_01_01(minus_01_27), .minus_01_00(minus_01_28), .minus_01_01_2(minus_01_29),
    .plus_00_01(_0_line__out__1[27]), .plus_00_00(_0_line__out__1[28]), .plus_00_01_2(_0_line__out__1[29]),
    .plus_01_01(_1_line[27]), .plus_01_00(_1_line[28]), .plus_01_01_2(_1_line[29]),
    .neighbours(neighbours_29_neighbours));
  alive alive_29 (
    .neighbours(neighbours_29_neighbours), .look_at(lookAt), .B___birth(birth), .S___save(save),
    .alive(_0_line__out__1[28]), .input_state(state_helper_29_output_state), .clock(clock));
  STATE_helper state_helper_29 (
    .input_state(input_state), .output_state(state_helper_29_output_state), .i(I), .j(J[28]));
  neighbours neighbours_30 (
    .minus_01_01(minus_01_28), .minus_01_00(minus_01_29), .minus_01_01_2(minus_01_30),
    .plus_00_01(_0_line__out__1[28]), .plus_00_00(_0_line__out__1[29]), .plus_00_01_2(_0_line__out__1[30]),
    .plus_01_01(_1_line[28]), .plus_01_00(_1_line[29]), .plus_01_01_2(_1_line[30]),
    .neighbours(neighbours_30_neighbours));
  alive alive_30 (
    .neighbours(neighbours_30_neighbours), .look_at(lookAt), .B___birth(birth), .S___save(save),
    .alive(_0_line__out__1[29]), .input_state(state_helper_30_output_state), .clock(clock));
  STATE_helper state_helper_30 (
    .input_state(input_state), .output_state(state_helper_30_output_state), .i(I), .j(J[29]));
  neighbours neighbours_31 (
    .minus_01_01(minus_01_29), .minus_01_00(minus_01_30), .minus_01_01_2(minus_01_31),
    .plus_00_01(_0_line__out__1[29]), .plus_00_00(_0_line__out__1[30]), .plus_00_01_2(_0_line__out__1[31]),
    .plus_01_01(_1_line[29]), .plus_01_00(_1_line[30]), .plus_01_01_2(_1_line[31]),
    .neighbours(neighbours_31_neighbours));
  alive alive_31 (
    .neighbours(neighbours_31_neighbours), .look_at(lookAt), .B___birth(birth), .S___save(save),
    .alive(_0_line__out__1[30]), .input_state(state_helper_31_output_state), .clock(clock));
  STATE_helper state_helper_31 (
    .input_state(input_state), .output_state(state_helper_31_output_state), .i(I), .j(J[30]));
  neighbours neighbours_32 (
    .minus_01_01(minus_01_30), .minus_01_00(minus_01_31), .minus_01_01_2(minus_01_32),
    .plus_00_01(_0_line__out__1[30]), .plus_00_00(_0_line__out__1[31]), .plus_00_01_2(plus_00_32),
    .plus_01_01(_1_line[30]), .plus_01_00(_1_line[31]), .plus_01_01_2(plus_01_32),
    .neighbours(neighbours_32_neighbours));
  alive alive_32 (
    .neighbours(neighbours_32_neighbours), .look_at(lookAt), .B___birth(birth), .S___save(save),
    .alive(_0_line__out__1[31]), .input_state(state_helper_32_output_state), .clock(clock));
  STATE_helper state_helper_32 (
    .input_state(input_state), .output_state(state_helper_32_output_state), .i(I), .j(J[31]));

  assign _0_line__out__1_2 = _0_line__out__1;
  assign display = _0_line__out__1;
  assign J[20] = J[22];

  // Other names for the same wires on the sheet: plus_00_00 = _0_line__out__1[0]; plus_00_01 = _0_line__out__1[1];
  //   plus_00_02 = _0_line__out__1[2]; plus_00_03 = _0_line__out__1[3]; plus_00_04 = _0_line__out__1[4];
  //   plus_00_05 = _0_line__out__1[5]; plus_00_06 = _0_line__out__1[6]; plus_00_07 = _0_line__out__1[7];
  //   plus_00_08 = _0_line__out__1[8]; plus_00_09 = _0_line__out__1[9]; plus_00_10 = _0_line__out__1[10];
  //   plus_00_11 = _0_line__out__1[11]; plus_00_12 = _0_line__out__1[12]; plus_00_13 = _0_line__out__1[13];
  //   plus_00_14 = _0_line__out__1[14]; plus_00_15 = _0_line__out__1[15]; plus_00_16 = _0_line__out__1[16];
  //   plus_00_17 = _0_line__out__1[17]; plus_00_18 = _0_line__out__1[18]; plus_00_19 = _0_line__out__1[19];
  //   plus_00_20 = _0_line__out__1[20]; plus_00_21 = _0_line__out__1[21]; plus_00_22 = _0_line__out__1[22];
  //   plus_00_23 = _0_line__out__1[23]; plus_00_24 = _0_line__out__1[24]; plus_00_25 = _0_line__out__1[25];
  //   plus_00_26 = _0_line__out__1[26]; plus_00_27 = _0_line__out__1[27]; plus_00_28 = _0_line__out__1[28];
  //   plus_00_29 = _0_line__out__1[29]; plus_00_30 = _0_line__out__1[30]; plus_00_31 = _0_line__out__1[31];
  //   plus_01_00 = _1_line[0]; plus_01_01 = _1_line[1]; plus_01_02 = _1_line[2]; plus_01_03 = _1_line[3];
  //   plus_01_04 = _1_line[4]; plus_01_05 = _1_line[5]; plus_01_06 = _1_line[6]; plus_01_07 = _1_line[7];
  //   plus_01_08 = _1_line[8]; plus_01_09 = _1_line[9]; plus_01_10 = _1_line[10]; plus_01_11 = _1_line[11];
  //   plus_01_12 = _1_line[12]; plus_01_13 = _1_line[13]; plus_01_14 = _1_line[14]; plus_01_15 = _1_line[15];
  //   plus_01_16 = _1_line[16]; plus_01_17 = _1_line[17]; plus_01_18 = _1_line[18]; plus_01_19 = _1_line[19];
  //   plus_01_20 = _1_line[20]; plus_01_21 = _1_line[21]; plus_01_22 = _1_line[22]; plus_01_23 = _1_line[23];
  //   plus_01_24 = _1_line[24]; plus_01_25 = _1_line[25]; plus_01_26 = _1_line[26]; plus_01_27 = _1_line[27];
  //   plus_01_28 = _1_line[28]; plus_01_29 = _1_line[29]; plus_01_30 = _1_line[30]; plus_01_31 = _1_line[31];
  //   j20 = J[22]; minus_02_00 = minus_1_line[0]; minus_02_01 = minus_1_line[1]; minus_02_02 = minus_1_line[2];
  //   minus_02_03 = minus_1_line[3]; minus_02_04 = minus_1_line[4]; minus_02_05 = minus_1_line[5];
  //   minus_02_06 = minus_1_line[6]; minus_02_07 = minus_1_line[7]; minus_02_08 = minus_1_line[8];
  //   minus_02_09 = minus_1_line[9]; minus_02_10 = minus_1_line[10]; minus_02_11 = minus_1_line[11];
  //   minus_02_12 = minus_1_line[12]; minus_02_13 = minus_1_line[13]; minus_02_14 = minus_1_line[14];
  //   minus_02_15 = minus_1_line[15]; minus_02_16 = minus_1_line[16]; minus_02_17 = minus_1_line[17];
  //   minus_02_18 = minus_1_line[18]; minus_02_19 = minus_1_line[19]; minus_02_20 = minus_1_line[20];
  //   minus_02_21 = minus_1_line[21]; minus_02_22 = minus_1_line[22]; minus_02_23 = minus_1_line[23];
  //   minus_02_24 = minus_1_line[24]; minus_02_25 = minus_1_line[25]; minus_02_26 = minus_1_line[26];
  //   minus_02_27 = minus_1_line[27]; minus_02_28 = minus_1_line[28]; minus_02_29 = minus_1_line[29];
  //   minus_02_30 = minus_1_line[30]; minus_02_31 = minus_1_line[31]; state[1:0] = input_state
endmodule

module matrix (
  input  [31:0] i,
  input  [31:0] J,
  input  Torus,
  input  [1:0] input_state,
  output [31:0] LINE_0,
  output [31:0] LINE_1,
  output [31:0] LINE_2,
  output [31:0] LINE_3,
  output [31:0] LINE_4,
  output [31:0] LINE_5,
  output [31:0] LINE_6,
  output [31:0] LINE_7,
  output [31:0] LINE_8,
  output [31:0] LINE_9,
  output [31:0] LINE_10,
  output [31:0] LINE_11,
  output [31:0] LINE_12,
  output [31:0] LINE_13,
  output [31:0] LINE_14,
  output [31:0] LINE_15,
  output [31:0] LINE_16,
  output [31:0] LINE_17,
  output [31:0] LINE_18,
  output [31:0] LINE_19,
  output [31:0] LINE_20,
  output [31:0] LINE_21,
  output [31:0] LINE_22,
  output [31:0] LINE_23,
  output [31:0] LINE_24,
  output [31:0] LINE_25,
  output [31:0] LINE_26,
  output [31:0] LINE_27,
  output [31:0] LINE_28,
  output [31:0] LINE_29,
  output [31:0] LINE_30,
  output [31:0] LINE_31
);

  wire [31:0] _0__0_line__out__1_2, _1__0_line__out__1, _1__0_line__out__1_2, _2__0_line__out__1,
       _2__0_line__out__1_2, _3__0_line__out__1, _3__0_line__out__1_2, _4__0_line__out__1,
       _4__0_line__out__1_2, _5__0_line__out__1, _5__0_line__out__1_2, _6__0_line__out__1,
       _6__0_line__out__1_2, _7__0_line__out__1, _7__0_line__out__1_2, _8__0_line__out__1,
       _8__0_line__out__1_2, _9__0_line__out__1, _9__0_line__out__1_2, _10__0_line__out__1,
       _10__0_line__out__1_2, _11__0_line__out__1, _11__0_line__out__1_2, _12__0_line__out__1,
       _12__0_line__out__1_2, _13__0_line__out__1, _13__0_line__out__1_2, _14__0_line__out__1,
       _14__0_line__out__1_2, _15__0_line__out__1, _15__0_line__out__1_2, _16__0_line__out__1,
       _16__0_line__out__1_2, _17__0_line__out__1, _17__0_line__out__1_2, _18__0_line__out__1,
       _18__0_line__out__1_2, _19__0_line__out__1, _19__0_line__out__1_2, _20__0_line__out__1,
       _20__0_line__out__1_2, _21__0_line__out__1, _21__0_line__out__1_2, _22__0_line__out__1,
       _22__0_line__out__1_2, _23__0_line__out__1, _23__0_line__out__1_2, _24__0_line__out__1,
       _24__0_line__out__1_2, _25__0_line__out__1, _25__0_line__out__1_2, _26__0_line__out__1,
       _26__0_line__out__1_2, _27__0_line__out__1, _27__0_line__out__1_2, _28__0_line__out__1,
       _28__0_line__out__1_2, _29__0_line__out__1, _29__0_line__out__1_2, _30__0_line__out__1,
       _30__0_line__out__1_2, _31__0_line__out__1, and_1_out, and_2_out, minus_01, plus_32;

  assign and_1_out = plus_32 & {32{Torus}};  // AND_Gate and_1, 32 bits wide
  lineSTD _0 (
    .J(J), .minus_1_line(and_1_out), ._1_line(_1__0_line__out__1), .I(i[0]), .Torus(Torus),
    .input_state(input_state), ._0_line__out__1(minus_01), .display(LINE_0),
    ._0_line__out__1_2(_0__0_line__out__1_2));
  lineSTD _1 (
    .J(J), .minus_1_line(_0__0_line__out__1_2), ._1_line(_2__0_line__out__1), .I(i[1]), .Torus(Torus),
    .input_state(input_state), ._0_line__out__1(_1__0_line__out__1), .display(LINE_1),
    ._0_line__out__1_2(_1__0_line__out__1_2));
  lineSTD _2 (
    .J(J), .minus_1_line(_1__0_line__out__1_2), ._1_line(_3__0_line__out__1), .I(i[2]), .Torus(Torus),
    .input_state(input_state), ._0_line__out__1(_2__0_line__out__1), .display(LINE_2),
    ._0_line__out__1_2(_2__0_line__out__1_2));
  lineSTD _3 (
    .J(J), .minus_1_line(_2__0_line__out__1_2), ._1_line(_4__0_line__out__1), .I(i[3]), .Torus(Torus),
    .input_state(input_state), ._0_line__out__1(_3__0_line__out__1), .display(LINE_3),
    ._0_line__out__1_2(_3__0_line__out__1_2));
  lineSTD _4 (
    .J(J), .minus_1_line(_3__0_line__out__1_2), ._1_line(_5__0_line__out__1), .I(i[4]), .Torus(Torus),
    .input_state(input_state), ._0_line__out__1(_4__0_line__out__1), .display(LINE_4),
    ._0_line__out__1_2(_4__0_line__out__1_2));
  lineSTD _5 (
    .J(J), .minus_1_line(_4__0_line__out__1_2), ._1_line(_6__0_line__out__1), .I(i[5]), .Torus(Torus),
    .input_state(input_state), ._0_line__out__1(_5__0_line__out__1), .display(LINE_5),
    ._0_line__out__1_2(_5__0_line__out__1_2));
  lineSTD _6 (
    .J(J), .minus_1_line(_5__0_line__out__1_2), ._1_line(_7__0_line__out__1), .I(i[6]), .Torus(Torus),
    .input_state(input_state), ._0_line__out__1(_6__0_line__out__1), .display(LINE_6),
    ._0_line__out__1_2(_6__0_line__out__1_2));
  lineSTD _7 (
    .J(J), .minus_1_line(_6__0_line__out__1_2), ._1_line(_8__0_line__out__1), .I(i[7]), .Torus(Torus),
    .input_state(input_state), ._0_line__out__1(_7__0_line__out__1), .display(LINE_7),
    ._0_line__out__1_2(_7__0_line__out__1_2));
  lineSTD _8 (
    .J(J), .minus_1_line(_7__0_line__out__1_2), ._1_line(_9__0_line__out__1), .I(i[8]), .Torus(Torus),
    .input_state(input_state), ._0_line__out__1(_8__0_line__out__1), .display(LINE_8),
    ._0_line__out__1_2(_8__0_line__out__1_2));
  lineSTD _9 (
    .J(J), .minus_1_line(_8__0_line__out__1_2), ._1_line(_10__0_line__out__1), .I(i[9]), .Torus(Torus),
    .input_state(input_state), ._0_line__out__1(_9__0_line__out__1), .display(LINE_9),
    ._0_line__out__1_2(_9__0_line__out__1_2));
  lineSTD _10 (
    .J(J), .minus_1_line(_9__0_line__out__1_2), ._1_line(_11__0_line__out__1), .I(i[10]), .Torus(Torus),
    .input_state(input_state), ._0_line__out__1(_10__0_line__out__1), .display(LINE_10),
    ._0_line__out__1_2(_10__0_line__out__1_2));
  lineSTD _11 (
    .J(J), .minus_1_line(_10__0_line__out__1_2), ._1_line(_12__0_line__out__1), .I(i[11]), .Torus(Torus),
    .input_state(input_state), ._0_line__out__1(_11__0_line__out__1), .display(LINE_11),
    ._0_line__out__1_2(_11__0_line__out__1_2));
  lineSTD _12 (
    .J(J), .minus_1_line(_11__0_line__out__1_2), ._1_line(_13__0_line__out__1), .I(i[12]), .Torus(Torus),
    .input_state(input_state), ._0_line__out__1(_12__0_line__out__1), .display(LINE_12),
    ._0_line__out__1_2(_12__0_line__out__1_2));
  lineSTD _13 (
    .J(J), .minus_1_line(_12__0_line__out__1_2), ._1_line(_14__0_line__out__1), .I(i[13]), .Torus(Torus),
    .input_state(input_state), ._0_line__out__1(_13__0_line__out__1), .display(LINE_13),
    ._0_line__out__1_2(_13__0_line__out__1_2));
  lineSTD _14 (
    .J(J), .minus_1_line(_13__0_line__out__1_2), ._1_line(_15__0_line__out__1), .I(i[14]), .Torus(Torus),
    .input_state(input_state), ._0_line__out__1(_14__0_line__out__1), .display(LINE_14),
    ._0_line__out__1_2(_14__0_line__out__1_2));
  lineSTD _15 (
    .J(J), .minus_1_line(_14__0_line__out__1_2), ._1_line(_16__0_line__out__1), .I(i[15]), .Torus(Torus),
    .input_state(input_state), ._0_line__out__1(_15__0_line__out__1), .display(LINE_15),
    ._0_line__out__1_2(_15__0_line__out__1_2));
  lineSTD _16 (
    .J(J), .minus_1_line(_15__0_line__out__1_2), ._1_line(_17__0_line__out__1), .I(i[16]), .Torus(Torus),
    .input_state(input_state), ._0_line__out__1(_16__0_line__out__1), .display(LINE_16),
    ._0_line__out__1_2(_16__0_line__out__1_2));
  lineSTD _17 (
    .J(J), .minus_1_line(_16__0_line__out__1_2), ._1_line(_18__0_line__out__1), .I(i[17]), .Torus(Torus),
    .input_state(input_state), ._0_line__out__1(_17__0_line__out__1), .display(LINE_17),
    ._0_line__out__1_2(_17__0_line__out__1_2));
  lineSTD _18 (
    .J(J), .minus_1_line(_17__0_line__out__1_2), ._1_line(_19__0_line__out__1), .I(i[18]), .Torus(Torus),
    .input_state(input_state), ._0_line__out__1(_18__0_line__out__1), .display(LINE_18),
    ._0_line__out__1_2(_18__0_line__out__1_2));
  lineSTD _19 (
    .J(J), .minus_1_line(_18__0_line__out__1_2), ._1_line(_20__0_line__out__1), .I(i[19]), .Torus(Torus),
    .input_state(input_state), ._0_line__out__1(_19__0_line__out__1), .display(LINE_19),
    ._0_line__out__1_2(_19__0_line__out__1_2));
  lineSTD _20 (
    .J(J), .minus_1_line(_19__0_line__out__1_2), ._1_line(_21__0_line__out__1), .I(i[20]), .Torus(Torus),
    .input_state(input_state), ._0_line__out__1(_20__0_line__out__1), .display(LINE_20),
    ._0_line__out__1_2(_20__0_line__out__1_2));
  lineSTD _21 (
    .J(J), .minus_1_line(_20__0_line__out__1_2), ._1_line(_22__0_line__out__1), .I(i[21]), .Torus(Torus),
    .input_state(input_state), ._0_line__out__1(_21__0_line__out__1), .display(LINE_21),
    ._0_line__out__1_2(_21__0_line__out__1_2));
  lineSTD _22 (
    .J(J), .minus_1_line(_21__0_line__out__1_2), ._1_line(_23__0_line__out__1), .I(i[22]), .Torus(Torus),
    .input_state(input_state), ._0_line__out__1(_22__0_line__out__1), .display(LINE_22),
    ._0_line__out__1_2(_22__0_line__out__1_2));
  lineSTD _23 (
    .J(J), .minus_1_line(_22__0_line__out__1_2), ._1_line(_24__0_line__out__1), .I(i[23]), .Torus(Torus),
    .input_state(input_state), ._0_line__out__1(_23__0_line__out__1), .display(LINE_23),
    ._0_line__out__1_2(_23__0_line__out__1_2));
  lineSTD _24 (
    .J(J), .minus_1_line(_23__0_line__out__1_2), ._1_line(_25__0_line__out__1), .I(i[24]), .Torus(Torus),
    .input_state(input_state), ._0_line__out__1(_24__0_line__out__1), .display(LINE_24),
    ._0_line__out__1_2(_24__0_line__out__1_2));
  lineSTD _25 (
    .J(J), .minus_1_line(_24__0_line__out__1_2), ._1_line(_26__0_line__out__1), .I(i[25]), .Torus(Torus),
    .input_state(input_state), ._0_line__out__1(_25__0_line__out__1), .display(LINE_25),
    ._0_line__out__1_2(_25__0_line__out__1_2));
  lineSTD _26 (
    .J(J), .minus_1_line(_25__0_line__out__1_2), ._1_line(_27__0_line__out__1), .I(i[26]), .Torus(Torus),
    .input_state(input_state), ._0_line__out__1(_26__0_line__out__1), .display(LINE_26),
    ._0_line__out__1_2(_26__0_line__out__1_2));
  lineSTD _27 (
    .J(J), .minus_1_line(_26__0_line__out__1_2), ._1_line(_28__0_line__out__1), .I(i[27]), .Torus(Torus),
    .input_state(input_state), ._0_line__out__1(_27__0_line__out__1), .display(LINE_27),
    ._0_line__out__1_2(_27__0_line__out__1_2));
  lineSTD _28 (
    .J(J), .minus_1_line(_27__0_line__out__1_2), ._1_line(_29__0_line__out__1), .I(i[28]), .Torus(Torus),
    .input_state(input_state), ._0_line__out__1(_28__0_line__out__1), .display(LINE_28),
    ._0_line__out__1_2(_28__0_line__out__1_2));
  lineSTD _29 (
    .J(J), .minus_1_line(_28__0_line__out__1_2), ._1_line(_30__0_line__out__1), .I(i[29]), .Torus(Torus),
    .input_state(input_state), ._0_line__out__1(_29__0_line__out__1), .display(LINE_29),
    ._0_line__out__1_2(_29__0_line__out__1_2));
  lineSTD _30 (
    .J(J), .minus_1_line(_29__0_line__out__1_2), ._1_line(_31__0_line__out__1), .I(i[30]), .Torus(Torus),
    .input_state(input_state), ._0_line__out__1(_30__0_line__out__1), .display(LINE_30),
    ._0_line__out__1_2(_30__0_line__out__1_2));
  lineSTD _31 (
    .J(J), .minus_1_line(_30__0_line__out__1_2), ._1_line(and_2_out), .I(i[31]), .Torus(Torus),
    .input_state(input_state), ._0_line__out__1(_31__0_line__out__1), .display(LINE_31),
    ._0_line__out__1_2(plus_32));
  assign and_2_out = {32{Torus}} & minus_01;  // AND_Gate and_2, 32 bits wide

  // Other names for the same wires on the sheet: state[1:0] = input_state

  // Notes on the sheet:
  //   LINE_13: pull=down
  //   LINE_9: pull=down
  //   LINE_20: pull=down
  //   LINE_2: pull=down
  //   LINE_26: pull=down
  //   LINE_27: pull=down
  //   LINE_22: pull=down
  //   LINE_28: pull=down
  //   LINE_30: pull=down
  //   LINE_29: pull=down
  //   LINE_1: pull=down
  //   LINE_0: pull=down
  //   LINE_8: pull=down
  //   LINE_11: pull=down
  //   LINE_17: pull=down
  //   LINE_18: pull=down
  //   LINE_3: pull=down
  //   LINE_10: pull=down
  //   LINE_23: pull=down
  //   LINE_7: pull=down
  //   LINE_12: pull=down
  //   LINE_5: pull=down
  //   LINE_4: pull=down
  //   LINE_15: pull=down
  //   LINE_16: pull=down
  //   LINE_19: pull=down
  //   LINE_31: pull=down
  //   LINE_24: pull=down
  //   LINE_14: pull=down
  //   LINE_6: pull=down
  //   LINE_25: pull=down
  //   LINE_21: pull=down
endmodule

module temp (
);

  matrix matrix_1 ();  // open: i, J, Torus, input_state, LINE_0, LINE_1, LINE_2, LINE_3, LINE_4, LINE_5, LINE_6, LINE_7, LINE_8, LINE_9, LINE_10, LINE_11, LINE_12, LINE_13, LINE_14, LINE_15, LINE_16, LINE_17, LINE_18, LINE_19, LINE_20, LINE_21, LINE_22, LINE_23, LINE_24, LINE_25, LINE_26, LINE_27, LINE_28, LINE_29, LINE_30, LINE_31
endmodule
