// Logisim project 013.main (before rotating J and I cursor).circ as structural Verilog: 19 circuits, main circuit main
module main (
  input  [4:0] minus_2_line,
  input  [5:0] num_1,
  input  [5:0] num_1_2,
  input  [4:0] minus_1_line,
  input  [5:0] num_2,
  input  [5:0] num_2_2,
  input  [4:0] cur_line,
  input  [5:0] num_3,
  input  [5:0] num_3_2,
  input  [4:0] plus_1_line,
  input  [5:0] num_4,
  input  [5:0] num_4_2,
  input  [4:0] plus_2_line,
  input  [5:0] num_5,
  input  [5:0] num_5_2,
  input  [5:0] num_6,
  input  [5:0] num_6_2,
  input  [5:0] B__S
);

  wire cdm16_1_p1, cdm16_1_p2, cdm16_1_p4, cdm16_1_p5, cdm16_1_p6, cdm16_1_p7, cdm16_1_p8, cdm16_1_p9,
       cdm16_1_p10, cdm16_1_p11, cdm16_1_p12, clock, mem, not_1_out, read, word;
  wire [15:0] address_bus, cdm16_1_p17, cdm16_1_p18, data_bus;
  wire [29:0] birth, save;

  // Probe on cdm16_1_p2
  // Probe on cdm16_1_p1
  Clock clock_1 (.out(clock));
  // Probe on cdm16_1_p4
  // Probe on cdm16_1_p5
  // Probe on cdm16_1_p7
  // Probe on cdm16_1_p6
  // cdm16 cdm16_1: pin names not known; wires that end beside it: cdm16_1_p1, cdm16_1_p2, clock, cdm16_1_p4, cdm16_1_p5, cdm16_1_p6, cdm16_1_p7, cdm16_1_p8, cdm16_1_p9, cdm16_1_p10, cdm16_1_p11, cdm16_1_p12, mem, read, word, address_bus, cdm16_1_p17, cdm16_1_p18
  // Probe on cdm16_1_p8
  // Probe on cdm16_1_p9
  assign data_bus = not_1_out ? cdm16_1_p17 : 16'bz;  // Controlled_Buffer controlled_buffer_1
  not not_1 (not_1_out, read);
  assign cdm16_1_p18 = read ? data_bus : 16'bz;  // Controlled_Buffer controlled_buffer_2
  // Probe on cdm16_1_p11
  // Probe on cdm16_1_p10
  // Probe on cdm16_1_p12
  BS_helper bs_helper_1 (.input_6_bit(num_1), .output_5_bit(birth[4:0]));
  // Probe on birth[4:0]
  BS_helper bs_helper_2 (.input_6_bit(num_2), .output_5_bit(birth[9:5]));
  // Probe on birth[9:5]
  BS_helper bs_helper_3 (.input_6_bit(num_3), .output_5_bit(birth[14:10]));
  // Probe on birth[14:10]
  BS_helper bs_helper_4 (.input_6_bit(num_4), .output_5_bit(birth[19:15]));
  // Probe on birth[19:15]
  BS_helper bs_helper_5 (.input_6_bit(num_5), .output_5_bit(birth[24:20]));
  // Probe on birth[24:20]
  BS_helper bs_helper_6 (.input_6_bit(num_6), .output_5_bit(birth[29:25]));
  // Probe on birth[29:25]
  // RAM ram_1: pin names not known; wires that end beside it: address_bus, word, mem, clock, read, data_bus
  BS_helper bs_helper_7 (.input_6_bit(num_1_2), .output_5_bit(save[4:0]));
  // Probe on save[4:0]
  BS_helper bs_helper_8 (.input_6_bit(num_2_2), .output_5_bit(save[9:5]));
  // Probe on save[9:5]
  // Probe on save[14:10]
  BS_helper bs_helper_9 (.input_6_bit(num_3_2), .output_5_bit(save[14:10]));
  // Probe on save[19:15]
  BS_helper bs_helper_10 (.input_6_bit(num_4_2), .output_5_bit(save[19:15]));
  BS_helper bs_helper_11 (.input_6_bit(num_5_2), .output_5_bit(save[24:20]));
  // Probe on save[24:20]
  // Probe on save[29:25]
  BS_helper bs_helper_12 (.input_6_bit(num_6_2), .output_5_bit(save[29:25]));

  // Other names for the same wires on the sheet: lookAt[24:0] = {plus_2_line, plus_1_line, cur_line, minus_1_line, minus_2_line}

  // Notes on the sheet:
  //   look at
  //   Set up rules (not now :{ )
  //   birth
  //   if the number is >25, the rule is inactive
  //   You can choose up to 6 numbers from 0 to 25
  //   ↓ 0 – use number in rules, 1 — don't use
  //   ↑ ↑ ↑ ↑ ↑ binary number from 0 to 25
  //   save
endmodule

module mainCDM8 (
  input  set_0,
  input  set_1,
  input  small_0____big_1__cursor,
  input  UP,
  input  LEFT,
  input  RIGHT,
  input  DOWN,
  input  pause,
  input  [4:0] minus_2_line,
  input  [5:0] num_1,
  input  [5:0] num_1_2,
  input  [4:0] minus_1_line,
  input  [5:0] num_2,
  input  [5:0] num_2_2,
  input  [4:0] cur_line,
  input  [5:0] num_3,
  input  [5:0] num_3_2,
  input  [4:0] plus_1_line,
  input  [5:0] num_4,
  input  [5:0] num_4_2,
  input  [4:0] plus_2_line,
  input  [5:0] num_5,
  input  [5:0] num_5_2,
  input  [5:0] num_6,
  input  [5:0] num_6_2,
  input  [5:0] B__S
);

  wire cdm_8_mark5_1_p1, cdm_8_mark5_1_p2, cdm_8_mark5_1_p4, cdm_8_mark5_1_p5, cdm_8_mark5_1_p6,
       cdm_8_mark5_1_p7, cdm_8_mark5_1_p8, clock, mem, not_1_out, read;
  wire [7:0] addressBus, cdm_8_mark5_1_p12, cdm_8_mark5_1_p13, dataBus;
  wire [29:0] birth, save;

  Clock clock_1 (.out(clock));
  // Debugger debugger_1: pin names not known
  // Probe on cdm_8_mark5_1_p4
  // Probe on cdm_8_mark5_1_p2
  // Probe on cdm_8_mark5_1_p1
  // Probe on cdm_8_mark5_1_p6
  // Probe on cdm_8_mark5_1_p5
  // Probe on cdm_8_mark5_1_p7
  // Probe on cdm_8_mark5_1_p8
  // CdM_8_mark5 cdm_8_mark5_1: pin names not known; wires that end beside it: cdm_8_mark5_1_p1, cdm_8_mark5_1_p2, clock, cdm_8_mark5_1_p4, cdm_8_mark5_1_p5, cdm_8_mark5_1_p6, cdm_8_mark5_1_p7, cdm_8_mark5_1_p8, mem, read, addressBus, cdm_8_mark5_1_p12, cdm_8_mark5_1_p13, small_0____big_1__cursor, set_0, set_1
  assign dataBus = not_1_out ? cdm_8_mark5_1_p12 : 8'bz;  // Controlled_Buffer controlled_buffer_1
  not not_1 (not_1_out, read);
  assign cdm_8_mark5_1_p13 = read ? dataBus : 8'bz;  // Controlled_Buffer controlled_buffer_2
  BS_helper bs_helper_1 (.input_6_bit(num_1), .output_5_bit(birth[4:0]));
  // Probe on birth[4:0]
  BS_helper bs_helper_2 (.input_6_bit(num_2), .output_5_bit(birth[9:5]));
  // Probe on birth[9:5]
  // Probe on birth[14:10]
  BS_helper bs_helper_3 (.input_6_bit(num_3), .output_5_bit(birth[14:10]));
  BS_helper bs_helper_4 (.input_6_bit(num_4), .output_5_bit(birth[19:15]));
  // Probe on birth[19:15]
  BS_helper bs_helper_5 (.input_6_bit(num_5), .output_5_bit(birth[24:20]));
  // Probe on birth[24:20]
  // Probe on birth[29:25]
  BS_helper bs_helper_6 (.input_6_bit(num_6), .output_5_bit(birth[29:25]));
  RAM ram_1 (.addr(addressBus), .data(dataBus), .sel(mem), .clk(clock), .ld(read));  // open: clr
  BS_helper bs_helper_7 (.input_6_bit(num_1_2), .output_5_bit(save[4:0]));
  // Probe on save[4:0]
  // Probe on save[9:5]
  BS_helper bs_helper_8 (.input_6_bit(num_2_2), .output_5_bit(save[9:5]));
  // Probe on save[14:10]
  BS_helper bs_helper_9 (.input_6_bit(num_3_2), .output_5_bit(save[14:10]));
  BS_helper bs_helper_10 (.input_6_bit(num_4_2), .output_5_bit(save[19:15]));
  // Probe on save[19:15]
  BS_helper bs_helper_11 (.input_6_bit(num_5_2), .output_5_bit(save[24:20]));
  // Probe on save[24:20]
  // Probe on save[29:25]
  BS_helper bs_helper_12 (.input_6_bit(num_6_2), .output_5_bit(save[29:25]));

  // Other names for the same wires on the sheet: lookAt[24:0] = {plus_2_line, plus_1_line, cur_line, minus_1_line, minus_2_line}

  // Notes on the sheet:
  //   look at
  //   Set up rules (not now :{ )
  //   birth
  //   if the number is >25, the rule is inactive
  //   You can choose up to 6 numbers from 0 to 25
  //   ↓ 0 – use number in rules, 1 — don't use
  //   ↑ ↑ ↑ ↑ ↑ binary number from 0 to 25
  //   save
endmodule

module aliveSTD (
  input  [8:0] neighbours,
  input  pause,
  input  [1:0] input_state,
  output alive
);

  wire _2_out, _3_out, multiplexer_1_out, multiplexer_2_out, or_1_out, xor_1_out;
  wire [3:0] newCnt;

  and _3 (_3_out, newCnt[0], newCnt[1], ~newCnt[2], ~newCnt[3]);  // AND_Gate
  and _2 (_2_out, ~newCnt[0], newCnt[1], ~newCnt[2], ~newCnt[3]);  // AND_Gate
  // Probe on newCnt
  BitAdder bitadder_1 (.in0({neighbours[8:5], neighbours[3:0]}), .out(newCnt));
  Multiplexer #(.disabled(0)) multiplexer_1 (
    .in0(_3_out), .in1(or_1_out), .out(multiplexer_1_out), .sel(neighbours[4]));  // open: en
  or or_1 (or_1_out, _3_out, _2_out);
  xor xor_1 (xor_1_out, neighbours[4], input_state[0]);
  Multiplexer #(.disabled(0)) multiplexer_2 (
    .in0(xor_1_out), .in1(input_state[0]), .out(multiplexer_2_out), .sel(input_state[1]));  // open: en
  Multiplexer #(.disabled(0)) multiplexer_3 (
    .in0(multiplexer_1_out), .in1(multiplexer_2_out), .out(alive), .sel(pause));  // open: en
  Pull_Resistor pull_resistor_1 (.node(alive));

  // Other names for the same wires on the sheet: cur = neighbours[4]

  // Notes on the sheet:
  //   neighbours: pull=down
  //   input_state: pull=down
  //   ▒ — look at
  //   ▓ — current cell
  //   floating → 0
  //   if cur cell is dead (= 0) try birth,
  //   alive (= 1) — try save
  //   ▒ ▒ ▒
  //   ▒ ▓ ▒
  //   ▒ ▒ ▒
  //   3 if dead
  //   2 or 3 if alive
  //   00 — old
  //   01 — invert
  //   10 — set DEAD
  //   11 — set ALIVE
  //   old or invert
  //   0 (low bit)
  //   1 (high bit)
  //   new
  //   by state
endmodule

module aliveSTD__old (
  input  [8:0] neighbours,
  input  pause,
  input  clock,
  input  [1:0] input_state,
  output alive
);

  wire _2_out, _3_out, multiplexer_1_out, multiplexer_2_out, multiplexer_3_out, not_1_out, or_1_out;
  wire [3:0] newCnt;

  and _3 (_3_out, newCnt[0], newCnt[1], ~newCnt[2], ~newCnt[3]);  // AND_Gate
  and _2 (_2_out, ~newCnt[0], newCnt[1], ~newCnt[2], ~newCnt[3]);  // AND_Gate
  // Probe on newCnt
  BitAdder bitadder_1 (.in0({neighbours[8:5], neighbours[3:0]}), .out(newCnt));
  Multiplexer #(.disabled(0)) multiplexer_1 (
    .in0(_3_out), .in1(or_1_out), .out(multiplexer_1_out), .sel(neighbours[4]));  // open: en
  or or_1 (or_1_out, _3_out, _2_out);
  Multiplexer #(.select(2), .disabled(0)) multiplexer_2 (
    .in0(alive), .in1(not_1_out), .in2(input_state[0]), .in3(input_state[0]), .out(multiplexer_2_out),
    .sel(input_state));  // open: en
  Multiplexer #(.disabled(0)) multiplexer_3 (
    .in0(multiplexer_1_out), .in1(multiplexer_2_out), .out(multiplexer_3_out), .sel(pause));  // open: en
  Register #(.width(1), .trigger("falling")) register_1 (
    .D(multiplexer_3_out), .Q(alive), .clk(clock));  // open: en, clr
  Pull_Resistor pull_resistor_1 (.node(alive));
  not not_1 (not_1_out, alive);

  // Other names for the same wires on the sheet: cur = neighbours[4]

  // Notes on the sheet:
  //   neighbours: pull=down
  //   input_state: pull=down
  //   ▒ — look at
  //   ▓ — current cell
  //   floating → 0
  //   if cur cell is dead (= 0) try birth,
  //   alive (= 1) — try save
  //   ▒ ▒ ▒
  //   ▒ ▓ ▒
  //   ▒ ▒ ▒
  //   3 if dead
  //   2 or 3 if alive
  //   00 — old
  //   01 — invert
  //   10 — set DEAD
  //   11 — set ALIVE
  //   0 (low bit)
  //   1 (high bit)
  //   new
  //   by state
endmodule

module alive (
  input  [24:0] neighbours,
  input  [24:0] look_at,
  input  pause,
  input  [29:0] B___birth,
  input  [1:0] input_state,
  input  [29:0] S___save,
  output alive
);

  wire can_cell_born_out, can_cell_save_out, comparator_1_eq, comparator_2_eq, comparator_3_eq,
       comparator_4_eq, comparator_5_eq, comparator_6_eq, comparator_7_eq, comparator_8_eq, comparator_9_eq,
       comparator_10_eq, comparator_11_eq, comparator_12_eq, multiplexer_1_out, multiplexer_3_out, xor_1_out;
  wire [4:0] newCnt;
  wire [24:0] and_1_out, undriven;

  assign and_1_out = neighbours & look_at;  // AND_Gate and_1, 25 bits wide
  // Probe on newCnt
  BitAdder #(.width(25)) bitadder_1 (.in0(and_1_out), .out(newCnt));
  // Probe on undriven[4:0]
  // Probe on undriven[9:5]
  // Probe on undriven[14:10]
  // Probe on undriven[19:15]
  // Probe on undriven[24:20]
  Comparator #(.width(5), .mode("unsigned")) comparator_1 (
    .a(newCnt), .b(B___birth[4:0]), .eq(comparator_1_eq));  // open: gt, lt
  Comparator #(.width(5), .mode("unsigned")) comparator_2 (
    .a(newCnt), .b(B___birth[9:5]), .eq(comparator_2_eq));  // open: gt, lt
  Comparator #(.width(5), .mode("unsigned")) comparator_3 (
    .a(newCnt), .b(B___birth[14:10]), .eq(comparator_3_eq));  // open: gt, lt
  Comparator #(.width(5), .mode("unsigned")) comparator_4 (
    .a(newCnt), .b(B___birth[19:15]), .eq(comparator_4_eq));  // open: gt, lt
  Comparator #(.width(5), .mode("unsigned")) comparator_5 (
    .a(newCnt), .b(B___birth[24:20]), .eq(comparator_5_eq));  // open: gt, lt
  Comparator #(.width(5), .mode("unsigned")) comparator_6 (
    .a(newCnt), .b(B___birth[29:25]), .eq(comparator_6_eq));  // open: gt, lt
  Comparator #(.width(5), .mode("unsigned")) comparator_7 (
    .a(newCnt), .b(S___save[4:0]), .eq(comparator_7_eq));  // open: gt, lt
  Comparator #(.width(5), .mode("unsigned")) comparator_8 (
    .a(newCnt), .b(S___save[9:5]), .eq(comparator_8_eq));  // open: gt, lt
  Comparator #(.width(5), .mode("unsigned")) comparator_9 (
    .a(newCnt), .b(S___save[14:10]), .eq(comparator_9_eq));  // open: gt, lt
  Comparator #(.width(5), .mode("unsigned")) comparator_10 (
    .a(newCnt), .b(S___save[19:15]), .eq(comparator_10_eq));  // open: gt, lt
  Comparator #(.width(5), .mode("unsigned")) comparator_11 (
    .a(newCnt), .b(S___save[24:20]), .eq(comparator_11_eq));  // open: gt, lt
  Comparator #(.width(5), .mode("unsigned")) comparator_12 (
    .a(newCnt), .b(S___save[29:25]), .eq(comparator_12_eq));  // open: gt, lt
  or can_cell_born (can_cell_born_out, comparator_1_eq, comparator_2_eq, comparator_3_eq, comparator_4_eq, comparator_5_eq, comparator_6_eq);
  or can_cell_save (can_cell_save_out, comparator_7_eq, comparator_8_eq, comparator_9_eq, comparator_10_eq, comparator_11_eq, comparator_12_eq);
  Multiplexer #(.disabled(0)) multiplexer_1 (
    .in0(can_cell_born_out), .in1(can_cell_save_out), .out(multiplexer_1_out), .sel(neighbours[12]));  // open: en
  xor xor_1 (xor_1_out, neighbours[12], input_state[0]);
  Pull_Resistor pull_resistor_1 (.node(alive));
  Multiplexer #(.disabled(0)) multiplexer_2 (
    .in0(multiplexer_1_out), .in1(multiplexer_3_out), .out(alive), .sel(pause));  // open: en
  Multiplexer #(.disabled(0)) multiplexer_3 (
    .in0(xor_1_out), .in1(input_state[0]), .out(multiplexer_3_out), .sel(input_state[1]));  // open: en

  // Other names for the same wires on the sheet: B1[4:0] = B___birth[4:0]; B2[4:0] = B___birth[9:5];
  //   B3[4:0] = B___birth[14:10]; B4[4:0] = B___birth[19:15]; B5[4:0] = B___birth[24:20]; B6[4:0] = B___birth[29:25];
  //   cur = neighbours[12]; S1[4:0] = S___save[4:0]; S2[4:0] = S___save[9:5]; S3[4:0] = S___save[14:10];
  //   S4[4:0] = S___save[19:15]; S5[4:0] = S___save[24:20]; S6[4:0] = S___save[29:25]

  // Notes on the sheet:
  //   input_state: pull=down
  //   look_at: pull=down
  //   S___save: pull=up
  //   B___birth: pull=up
  //   neighbours: pull=down
  //   floating → 0
  //   floating → 0
  //   floating → 1
  //   floating → 1
  //   DEBUG TOOLS
  //   ▒ — neighbours
  //   ▓ — current cell
  //   ▒ ▒ ▒ ▒ ▒
  //   ▒ ▒ ▒ ▒ ▒
  //   ▒ ▒ ▓ ▒ ▒
  //   ▒ ▒ ▒ ▒ ▒
  //   ▒ ▒ ▒ ▒ ▒
  //   if cur cell is dead (= 0) try birth
  //   alive (= 1) — try save
  //   new iteration
  //   by state
  //   old or invert
  //   new: 0 or 1
  //   00 — old
  //   01 — invert
  //   10 — set DEAD
  //   11 — set ALIVE
endmodule

module BS_helperSTD (
  input  [4:0] input_5_bit,
  output [3:0] output_4_bit
);

  Multiplexer #(.width(4)) multiplexer_1 (
    .in0(input_5_bit[3:0]), .in1(4'b1111), .out(output_4_bit), .sel(input_5_bit[4]));  // open: en
endmodule

module BS_helper (
  input  [5:0] input_6_bit,
  output [4:0] output_5_bit
);

  Multiplexer #(.width(5)) multiplexer_1 (
    .in0(input_6_bit[4:0]), .in1({5{1'b1}}), .out(output_5_bit), .sel(input_6_bit[5]));  // open: en
endmodule

module STATE_helper (
  input  [1:0] input_state,
  input  i,
  input  j,
  output [1:0] output_state
);

  wire [1:1] and_2_out;

  assign output_state = input_state & {2{and_2_out[1]}};  // AND_Gate and_1, 2 bits wide
  and and_2 (and_2_out[1], i, j);

  // Notes on the sheet:
  //   i: pull=down
  //   j: pull=down
endmodule

module exampleSTD (
  input  [2:0] Old_state,
  input  [2:0] in_2,
  input  [2:0] in_3,
  input  pause,
  input  [1:0] state
);

  wire [3:0] undriven, undriven_2;
  wire [4:4] newState;

  DotMatrix #(.inputtype("row"), .matrixcols(3), .matrixrows(3)) dotmatrix_1 (
    .row0(Old_state), .row1(in_2), .row2(in_3));
  aliveSTD alivestd_1 (.neighbours({in_3, in_2, Old_state}), .alive(newState[4]), .pause(pause), .input_state(state));
  // Probe on undriven[2:0]
  // Probe on {undriven_2[0], 1'b0, undriven[3]}
  // Probe on undriven_2[3:1]
  // Probe on Old_state
  // Probe on {in_2[2], newState[4], in_2[0]}
  // Probe on in_3
  DotMatrix #(.inputtype("row"), .matrixcols(3), .matrixrows(3)) dotmatrix_2 (
    .row0(Old_state), .row1({in_2[2], newState[4], in_2[0]}), .row2(in_3));

  // Other names for the same wires on the sheet: neighbours[8:0] = {in_3, in_2, Old_state};
  //   newState (some bits) = {in_3, in_2[2], in_2[0], Old_state}

  // Notes on the sheet:
  //   old state
  //   STANDART RULES:
  //   (You can edit)
  //   Old state
  //   How to use?
  //   1) look at 3x3
  //   2) B3/S23
  //   New state
  //   New state
  //   How to watch?
  //   X is cell's neighbours
  //   0 is current cell
endmodule

module example (
  input  [4:0] Old_state,
  input  [4:0] minus_2_line,
  input  [4:0] in_3,
  input  [4:0] minus_1_line,
  input  [4:0] in_5,
  input  [4:0] cur_line,
  input  [4:0] in_7,
  input  [4:0] plus_1_line,
  input  [4:0] in_9,
  input  [4:0] plus_2_line,
  input  [5:0] B__S,
  input  [5:0] num_1,
  input  [5:0] num_1_2,
  input  [5:0] num_2,
  input  [5:0] num_2_2,
  input  [5:0] num_3,
  input  [5:0] num_3_2,
  input  [5:0] num_4,
  input  [5:0] num_4_2,
  input  [5:0] num_5,
  input  [5:0] num_5_2,
  input  [5:0] num_6,
  input  [5:0] num_6_2,
  input  pause,
  input  [1:0] state
);

  wire [11:0] undriven, undriven_2;
  wire [12:12] newState;
  wire [29:0] birth, save;

  DotMatrix #(.inputtype("row"), .matrixrows(5)) dotmatrix_1 (
    .row0(Old_state), .row1(in_3), .row2(in_5), .row3(in_7), .row4(in_9));
  alive alive_1 (
    .neighbours({in_9, in_7, in_5, in_3, Old_state}),
    .look_at({plus_2_line, plus_1_line, cur_line, minus_1_line, minus_2_line}), .B___birth(birth),
    .S___save(save), .alive(newState[12]), .pause(pause), .input_state(state));
  // Probe on Old_state
  // Probe on in_3
  // Probe on {in_5[4:3], newState[12], in_5[1:0]}
  // Probe on in_7
  // Probe on in_9
  DotMatrix #(.inputtype("row"), .matrixrows(5)) dotmatrix_2 (
    .row0(Old_state), .row1(in_3), .row2({in_5[4:3], newState[12], in_5[1:0]}), .row3(in_7), .row4(in_9));
  // Probe on undriven[4:0]
  // Probe on undriven[9:5]
  // Probe on {undriven_2[1:0], 1'b0, undriven[11:10]}
  // Probe on undriven_2[6:2]
  // Probe on undriven_2[11:7]
  // Probe on birth[4:0]
  BS_helper bs_helper_1 (.input_6_bit(num_1), .output_5_bit(birth[4:0]));
  BS_helper bs_helper_2 (.input_6_bit(num_2), .output_5_bit(birth[9:5]));
  // Probe on birth[9:5]
  // Probe on birth[14:10]
  BS_helper bs_helper_3 (.input_6_bit(num_3), .output_5_bit(birth[14:10]));
  BS_helper bs_helper_4 (.input_6_bit(num_4), .output_5_bit(birth[19:15]));
  // Probe on birth[19:15]
  // Probe on birth[24:20]
  BS_helper bs_helper_5 (.input_6_bit(num_5), .output_5_bit(birth[24:20]));
  BS_helper bs_helper_6 (.input_6_bit(num_6), .output_5_bit(birth[29:25]));
  // Probe on birth[29:25]
  BS_helper bs_helper_7 (.input_6_bit(num_1_2), .output_5_bit(save[4:0]));
  // Probe on save[4:0]
  // Probe on save[9:5]
  BS_helper bs_helper_8 (.input_6_bit(num_2_2), .output_5_bit(save[9:5]));
  // Probe on save[14:10]
  BS_helper bs_helper_9 (.input_6_bit(num_3_2), .output_5_bit(save[14:10]));
  BS_helper bs_helper_10 (.input_6_bit(num_4_2), .output_5_bit(save[19:15]));
  // Probe on save[19:15]
  BS_helper bs_helper_11 (.input_6_bit(num_5_2), .output_5_bit(save[24:20]));
  // Probe on save[24:20]
  // Probe on save[29:25]
  BS_helper bs_helper_12 (.input_6_bit(num_6_2), .output_5_bit(save[29:25]));

  // Other names for the same wires on the sheet: lookAt[24:0] = {plus_2_line, plus_1_line, cur_line, minus_1_line, minus_2_line};
  //   neighbours[24:0] = {in_9, in_7, in_5, in_3, Old_state};
  //   newState (some bits) = {in_9, in_7, in_5[4:3], in_5[1:0], in_3, Old_state}

  // Notes on the sheet:
  //   old state
  //   (You can edit)
  //   Old state
  //   How to use?
  //   0~ — old
  //   10 — set DEAD
  //   11 — set ALIVE
  //   New state
  //   New state
  //   How to watch?
  //   X is cell's neighbours
  //   0 is current cell
  //   EDIT RULES:
  //   Standard rules:
  //   1) look at 3x3
  //   2) B3/S23
  //   if the number is >25, the rule is inactive
  //   B – birth
  //   look at
  //   You can choose up to 6 numbers from 0 to 25
  //   S – save
  //   ↓ 0 – use number in rules, 1 — don't use
  //   ↑ ↑ ↑ ↑ ↑ binary number from 0 to 25
endmodule

module neighboursSTD (
  input  minus_01_01,
  input  minus_01_00,
  input  minus_01_01_2,
  input  plus_00_01,
  input  plus_00_00,
  input  plus_00_01_2,
  input  plus_01_01,
  input  plus_01_00,
  input  plus_01_01_2,
  output [8:0] neighbours
);


  assign neighbours = {plus_01_01_2, plus_01_00, plus_01_01, plus_00_01_2, plus_00_00, plus_00_01, minus_01_01_2, minus_01_00, minus_01_01};
endmodule

module neighbours (
  input  minus_02_02,
  input  minus_02_01,
  input  minus_02_00,
  input  minus_02_01_2,
  input  minus_02_02_2,
  input  minus_01_02,
  input  minus_01_01,
  input  minus_01_00,
  input  minus_01_01_2,
  input  minus_01_02_2,
  input  plus_00_02,
  input  plus_00_01,
  input  plus_00_00,
  input  plus_00_01_2,
  input  plus_00_02_2,
  input  plus_01_02,
  input  plus_01_01,
  input  plus_01_00,
  input  plus_01_01_2,
  input  plus_01_02_2,
  input  plus_02_02,
  input  plus_02_01,
  input  plus_02_00,
  input  plus_02_01_2,
  input  plus_02_02_2,
  output [24:0] neighbours
);


  assign neighbours = {plus_02_02_2, plus_02_01_2, plus_02_00, plus_02_01, plus_02_02, plus_01_02_2, plus_01_01_2, plus_01_00, plus_01_01, plus_01_02, plus_00_02_2, plus_00_01_2, plus_00_00, plus_00_01, plus_00_02, minus_01_02_2, minus_01_01_2, minus_01_00, minus_01_01, minus_01_02, minus_02_02_2, minus_02_01_2, minus_02_00, minus_02_01, minus_02_02};
endmodule

module lineSTD (
  input  [31:0] J,
  input  [31:0] minus_1_line,
  input  [31:0] _1_line,
  input  I,
  input  Torus,
  input  [1:0] input_state,
  input  clock,
  input  pause,
  output [31:0] _0_line__out__1,
  output [31:0] display,
  output [31:0] _0_line__out__1_2
);

  wire minus_01_01_t, minus_01_32, plus_00_00new, plus_00_01_t, plus_00_01new, plus_00_02new, plus_00_03new,
       plus_00_04new, plus_00_05new, plus_00_06new, plus_00_07new, plus_00_08new, plus_00_09new,
       plus_00_10new, plus_00_11new, plus_00_12new, plus_00_13new, plus_00_14new, plus_00_15new,
       plus_00_16new, plus_00_17new, plus_00_18new, plus_00_19new, plus_00_20new, plus_00_21new,
       plus_00_22new, plus_00_23new, plus_00_24new, plus_00_25new, plus_00_26new, plus_00_27new,
       plus_00_28new, plus_00_29new, plus_00_30new, plus_00_31new, plus_00_32, plus_01_01_t, plus_01_32;
  wire [1:0] state_helper_1_output_state, state_helper_2_output_state, state_helper_3_output_state,
       state_helper_4_output_state, state_helper_5_output_state, state_helper_6_output_state,
       state_helper_7_output_state, state_helper_8_output_state, state_helper_9_output_state,
       state_helper_10_output_state, state_helper_11_output_state, state_helper_12_output_state,
       state_helper_13_output_state, state_helper_14_output_state, state_helper_15_output_state,
       state_helper_16_output_state, state_helper_17_output_state, state_helper_18_output_state,
       state_helper_19_output_state, state_helper_20_output_state, state_helper_21_output_state,
       state_helper_22_output_state, state_helper_23_output_state, state_helper_24_output_state,
       state_helper_25_output_state, state_helper_26_output_state, state_helper_27_output_state,
       state_helper_28_output_state, state_helper_29_output_state, state_helper_30_output_state,
       state_helper_31_output_state, state_helper_32_output_state;
  wire [8:0] neighboursstd_1_neighbours, neighboursstd_2_neighbours, neighboursstd_3_neighbours,
       neighboursstd_4_neighbours, neighboursstd_5_neighbours, neighboursstd_6_neighbours,
       neighboursstd_7_neighbours, neighboursstd_8_neighbours, neighboursstd_9_neighbours,
       neighboursstd_10_neighbours, neighboursstd_11_neighbours, neighboursstd_12_neighbours,
       neighboursstd_13_neighbours, neighboursstd_14_neighbours, neighboursstd_15_neighbours,
       neighboursstd_16_neighbours, neighboursstd_17_neighbours, neighboursstd_18_neighbours,
       neighboursstd_19_neighbours, neighboursstd_20_neighbours, neighboursstd_21_neighbours,
       neighboursstd_22_neighbours, neighboursstd_23_neighbours, neighboursstd_24_neighbours,
       neighboursstd_25_neighbours, neighboursstd_26_neighbours, neighboursstd_27_neighbours,
       neighboursstd_28_neighbours, neighboursstd_29_neighbours, neighboursstd_30_neighbours,
       neighboursstd_31_neighbours, neighboursstd_32_neighbours;

  neighboursSTD neighboursstd_1 (
    .minus_01_01(minus_01_01_t), .minus_01_00(minus_1_line[0]), .minus_01_01_2(minus_1_line[1]),
    .plus_00_01(plus_00_01_t), .plus_00_00(_0_line__out__1[0]), .plus_00_01_2(_0_line__out__1[1]),
    .plus_01_01(plus_01_01_t), .plus_01_00(_1_line[0]), .plus_01_01_2(_1_line[1]),
    .neighbours(neighboursstd_1_neighbours));
  aliveSTD alivestd_1 (
    .neighbours(neighboursstd_1_neighbours), .alive(plus_00_00new), .pause(pause),
    .input_state(state_helper_1_output_state));
  STATE_helper state_helper_1 (.input_state(input_state), .output_state(state_helper_1_output_state), .i(I), .j(J[0]));
  and and_1 (minus_01_32, minus_1_line[0], Torus);
  and and_2 (minus_01_01_t, minus_1_line[31], Torus);
  neighboursSTD neighboursstd_2 (
    .minus_01_01(minus_1_line[0]), .minus_01_00(minus_1_line[1]), .minus_01_01_2(minus_1_line[2]),
    .plus_00_01(_0_line__out__1[0]), .plus_00_00(_0_line__out__1[1]), .plus_00_01_2(_0_line__out__1[2]),
    .plus_01_01(_1_line[0]), .plus_01_00(_1_line[1]), .plus_01_01_2(_1_line[2]),
    .neighbours(neighboursstd_2_neighbours));
  Register #(.width(32), .trigger("falling")) register_1 (
    .D({plus_00_31new, plus_00_30new, plus_00_29new, plus_00_28new, plus_00_27new, plus_00_26new, plus_00_25new, plus_00_24new, plus_00_23new, plus_00_22new, plus_00_21new, plus_00_20new, plus_00_19new, plus_00_18new, plus_00_17new, plus_00_16new, plus_00_15new, plus_00_14new, plus_00_13new, plus_00_12new, plus_00_11new, plus_00_10new, plus_00_09new, plus_00_08new, plus_00_07new, plus_00_06new, plus_00_05new, plus_00_04new, plus_00_03new, plus_00_02new, plus_00_01new, plus_00_00new}),
    .Q(_0_line__out__1), .clk(clock));  // open: en, clr
  aliveSTD alivestd_2 (
    .neighbours(neighboursstd_2_neighbours), .alive(plus_00_01new), .pause(pause),
    .input_state(state_helper_2_output_state));
  STATE_helper state_helper_2 (.input_state(input_state), .output_state(state_helper_2_output_state), .i(I), .j(J[1]));
  and and_3 (plus_01_32, _1_line[0], Torus);
  and and_4 (plus_01_01_t, _1_line[31], Torus);
  and and_5 (plus_00_32, _0_line__out__1[0], Torus);
  and and_6 (plus_00_01_t, _0_line__out__1[31], Torus);
  neighboursSTD neighboursstd_3 (
    .minus_01_01(minus_1_line[1]), .minus_01_00(minus_1_line[2]), .minus_01_01_2(minus_1_line[3]),
    .plus_00_01(_0_line__out__1[1]), .plus_00_00(_0_line__out__1[2]), .plus_00_01_2(_0_line__out__1[3]),
    .plus_01_01(_1_line[1]), .plus_01_00(_1_line[2]), .plus_01_01_2(_1_line[3]),
    .neighbours(neighboursstd_3_neighbours));
  aliveSTD alivestd_3 (
    .neighbours(neighboursstd_3_neighbours), .alive(plus_00_02new), .pause(pause),
    .input_state(state_helper_3_output_state));
  STATE_helper state_helper_3 (.input_state(input_state), .output_state(state_helper_3_output_state), .i(I), .j(J[2]));
  neighboursSTD neighboursstd_4 (
    .minus_01_01(minus_1_line[2]), .minus_01_00(minus_1_line[3]), .minus_01_01_2(minus_1_line[4]),
    .plus_00_01(_0_line__out__1[2]), .plus_00_00(_0_line__out__1[3]), .plus_00_01_2(_0_line__out__1[4]),
    .plus_01_01(_1_line[2]), .plus_01_00(_1_line[3]), .plus_01_01_2(_1_line[4]),
    .neighbours(neighboursstd_4_neighbours));
  aliveSTD alivestd_4 (
    .neighbours(neighboursstd_4_neighbours), .alive(plus_00_03new), .pause(pause),
    .input_state(state_helper_4_output_state));
  STATE_helper state_helper_4 (.input_state(input_state), .output_state(state_helper_4_output_state), .i(I), .j(J[3]));
  Pull_Resistor pull_resistor_1 (.node(_0_line__out__1[0]));
  Pull_Resistor pull_resistor_2 ();  // open: node
  Pull_Resistor pull_resistor_3 (.node(_0_line__out__1[2]));
  Pull_Resistor pull_resistor_4 ();  // open: node
  Pull_Resistor pull_resistor_5 (.node(_0_line__out__1[4]));
  Pull_Resistor pull_resistor_6 ();  // open: node
  Pull_Resistor pull_resistor_7 (.node(_0_line__out__1[6]));
  Pull_Resistor pull_resistor_8 ();  // open: node
  Pull_Resistor pull_resistor_9 (.node(_0_line__out__1[8]));
  Pull_Resistor pull_resistor_10 ();  // open: node
  Pull_Resistor pull_resistor_11 (.node(_0_line__out__1[10]));
  Pull_Resistor pull_resistor_12 ();  // open: node
  Pull_Resistor pull_resistor_13 (.node(_0_line__out__1[12]));
  Pull_Resistor pull_resistor_14 ();  // open: node
  Pull_Resistor pull_resistor_15 (.node(_0_line__out__1[14]));
  Pull_Resistor pull_resistor_16 ();  // open: node
  Pull_Resistor pull_resistor_17 (.node(_0_line__out__1[16]));
  Pull_Resistor pull_resistor_18 ();  // open: node
  Pull_Resistor pull_resistor_19 (.node(_0_line__out__1[18]));
  Pull_Resistor pull_resistor_20 ();  // open: node
  Pull_Resistor pull_resistor_21 (.node(_0_line__out__1[20]));
  Pull_Resistor pull_resistor_22 ();  // open: node
  Pull_Resistor pull_resistor_23 (.node(_0_line__out__1[22]));
  Pull_Resistor pull_resistor_24 ();  // open: node
  Pull_Resistor pull_resistor_25 (.node(_0_line__out__1[24]));
  Pull_Resistor pull_resistor_26 ();  // open: node
  Pull_Resistor pull_resistor_27 (.node(_0_line__out__1[26]));
  Pull_Resistor pull_resistor_28 ();  // open: node
  Pull_Resistor pull_resistor_29 (.node(_0_line__out__1[28]));
  Pull_Resistor pull_resistor_30 ();  // open: node
  Pull_Resistor pull_resistor_31 (.node(_0_line__out__1[30]));
  Pull_Resistor pull_resistor_32 ();  // open: node
  neighboursSTD neighboursstd_5 (
    .minus_01_01(minus_1_line[3]), .minus_01_00(minus_1_line[4]), .minus_01_01_2(minus_1_line[5]),
    .plus_00_01(_0_line__out__1[3]), .plus_00_00(_0_line__out__1[4]), .plus_00_01_2(_0_line__out__1[5]),
    .plus_01_01(_1_line[3]), .plus_01_00(_1_line[4]), .plus_01_01_2(_1_line[5]),
    .neighbours(neighboursstd_5_neighbours));
  aliveSTD alivestd_5 (
    .neighbours(neighboursstd_5_neighbours), .alive(plus_00_04new), .pause(pause),
    .input_state(state_helper_5_output_state));
  STATE_helper state_helper_5 (.input_state(input_state), .output_state(state_helper_5_output_state), .i(I), .j(J[4]));
  neighboursSTD neighboursstd_6 (
    .minus_01_01(minus_1_line[4]), .minus_01_00(minus_1_line[5]), .minus_01_01_2(minus_1_line[6]),
    .plus_00_01(_0_line__out__1[4]), .plus_00_00(_0_line__out__1[5]), .plus_00_01_2(_0_line__out__1[6]),
    .plus_01_01(_1_line[4]), .plus_01_00(_1_line[5]), .plus_01_01_2(_1_line[6]),
    .neighbours(neighboursstd_6_neighbours));
  aliveSTD alivestd_6 (
    .neighbours(neighboursstd_6_neighbours), .alive(plus_00_05new), .pause(pause),
    .input_state(state_helper_6_output_state));
  STATE_helper state_helper_6 (.input_state(input_state), .output_state(state_helper_6_output_state), .i(I), .j(J[5]));
  neighboursSTD neighboursstd_7 (
    .minus_01_01(minus_1_line[5]), .minus_01_00(minus_1_line[6]), .minus_01_01_2(minus_1_line[7]),
    .plus_00_01(_0_line__out__1[5]), .plus_00_00(_0_line__out__1[6]), .plus_00_01_2(_0_line__out__1[7]),
    .plus_01_01(_1_line[5]), .plus_01_00(_1_line[6]), .plus_01_01_2(_1_line[7]),
    .neighbours(neighboursstd_7_neighbours));
  aliveSTD alivestd_7 (
    .neighbours(neighboursstd_7_neighbours), .alive(plus_00_06new), .pause(pause),
    .input_state(state_helper_7_output_state));
  STATE_helper state_helper_7 (.input_state(input_state), .output_state(state_helper_7_output_state), .i(I), .j(J[6]));
  neighboursSTD neighboursstd_8 (
    .minus_01_01(minus_1_line[6]), .minus_01_00(minus_1_line[7]), .minus_01_01_2(minus_1_line[8]),
    .plus_00_01(_0_line__out__1[6]), .plus_00_00(_0_line__out__1[7]), .plus_00_01_2(_0_line__out__1[8]),
    .plus_01_01(_1_line[6]), .plus_01_00(_1_line[7]), .plus_01_01_2(_1_line[8]),
    .neighbours(neighboursstd_8_neighbours));
  aliveSTD alivestd_8 (
    .neighbours(neighboursstd_8_neighbours), .alive(plus_00_07new), .pause(pause),
    .input_state(state_helper_8_output_state));
  STATE_helper state_helper_8 (.input_state(input_state), .output_state(state_helper_8_output_state), .i(I), .j(J[7]));
  neighboursSTD neighboursstd_9 (
    .minus_01_01(minus_1_line[7]), .minus_01_00(minus_1_line[8]), .minus_01_01_2(minus_1_line[9]),
    .plus_00_01(_0_line__out__1[7]), .plus_00_00(_0_line__out__1[8]), .plus_00_01_2(_0_line__out__1[9]),
    .plus_01_01(_1_line[7]), .plus_01_00(_1_line[8]), .plus_01_01_2(_1_line[9]),
    .neighbours(neighboursstd_9_neighbours));
  aliveSTD alivestd_9 (
    .neighbours(neighboursstd_9_neighbours), .alive(plus_00_08new), .pause(pause),
    .input_state(state_helper_9_output_state));
  STATE_helper state_helper_9 (.input_state(input_state), .output_state(state_helper_9_output_state), .i(I), .j(J[8]));
  neighboursSTD neighboursstd_10 (
    .minus_01_01(minus_1_line[8]), .minus_01_00(minus_1_line[9]), .minus_01_01_2(minus_1_line[10]),
    .plus_00_01(_0_line__out__1[8]), .plus_00_00(_0_line__out__1[9]), .plus_00_01_2(_0_line__out__1[10]),
    .plus_01_01(_1_line[8]), .plus_01_00(_1_line[9]), .plus_01_01_2(_1_line[10]),
    .neighbours(neighboursstd_10_neighbours));
  aliveSTD alivestd_10 (
    .neighbours(neighboursstd_10_neighbours), .alive(plus_00_09new), .pause(pause),
    .input_state(state_helper_10_output_state));
  STATE_helper state_helper_10 (
    .input_state(input_state), .output_state(state_helper_10_output_state), .i(I), .j(J[9]));
  neighboursSTD neighboursstd_11 (
    .minus_01_01(minus_1_line[9]), .minus_01_00(minus_1_line[10]), .minus_01_01_2(minus_1_line[11]),
    .plus_00_01(_0_line__out__1[9]), .plus_00_00(_0_line__out__1[10]), .plus_00_01_2(_0_line__out__1[11]),
    .plus_01_01(_1_line[9]), .plus_01_00(_1_line[10]), .plus_01_01_2(_1_line[11]),
    .neighbours(neighboursstd_11_neighbours));
  aliveSTD alivestd_11 (
    .neighbours(neighboursstd_11_neighbours), .alive(plus_00_10new), .pause(pause),
    .input_state(state_helper_11_output_state));
  STATE_helper state_helper_11 (
    .input_state(input_state), .output_state(state_helper_11_output_state), .i(I), .j(J[10]));
  neighboursSTD neighboursstd_12 (
    .minus_01_01(minus_1_line[10]), .minus_01_00(minus_1_line[11]), .minus_01_01_2(minus_1_line[12]),
    .plus_00_01(_0_line__out__1[10]), .plus_00_00(_0_line__out__1[11]), .plus_00_01_2(_0_line__out__1[12]),
    .plus_01_01(_1_line[10]), .plus_01_00(_1_line[11]), .plus_01_01_2(_1_line[12]),
    .neighbours(neighboursstd_12_neighbours));
  aliveSTD alivestd_12 (
    .neighbours(neighboursstd_12_neighbours), .alive(plus_00_11new), .pause(pause),
    .input_state(state_helper_12_output_state));
  STATE_helper state_helper_12 (
    .input_state(input_state), .output_state(state_helper_12_output_state), .i(I), .j(J[11]));
  neighboursSTD neighboursstd_13 (
    .minus_01_01(minus_1_line[11]), .minus_01_00(minus_1_line[12]), .minus_01_01_2(minus_1_line[13]),
    .plus_00_01(_0_line__out__1[11]), .plus_00_00(_0_line__out__1[12]), .plus_00_01_2(_0_line__out__1[13]),
    .plus_01_01(_1_line[11]), .plus_01_00(_1_line[12]), .plus_01_01_2(_1_line[13]),
    .neighbours(neighboursstd_13_neighbours));
  aliveSTD alivestd_13 (
    .neighbours(neighboursstd_13_neighbours), .alive(plus_00_12new), .pause(pause),
    .input_state(state_helper_13_output_state));
  STATE_helper state_helper_13 (
    .input_state(input_state), .output_state(state_helper_13_output_state), .i(I), .j(J[12]));
  neighboursSTD neighboursstd_14 (
    .minus_01_01(minus_1_line[12]), .minus_01_00(minus_1_line[13]), .minus_01_01_2(minus_1_line[14]),
    .plus_00_01(_0_line__out__1[12]), .plus_00_00(_0_line__out__1[13]), .plus_00_01_2(_0_line__out__1[14]),
    .plus_01_01(_1_line[12]), .plus_01_00(_1_line[13]), .plus_01_01_2(_1_line[14]),
    .neighbours(neighboursstd_14_neighbours));
  aliveSTD alivestd_14 (
    .neighbours(neighboursstd_14_neighbours), .alive(plus_00_13new), .pause(pause),
    .input_state(state_helper_14_output_state));
  STATE_helper state_helper_14 (
    .input_state(input_state), .output_state(state_helper_14_output_state), .i(I), .j(J[13]));
  neighboursSTD neighboursstd_15 (
    .minus_01_01(minus_1_line[13]), .minus_01_00(minus_1_line[14]), .minus_01_01_2(minus_1_line[15]),
    .plus_00_01(_0_line__out__1[13]), .plus_00_00(_0_line__out__1[14]), .plus_00_01_2(_0_line__out__1[15]),
    .plus_01_01(_1_line[13]), .plus_01_00(_1_line[14]), .plus_01_01_2(_1_line[15]),
    .neighbours(neighboursstd_15_neighbours));
  aliveSTD alivestd_15 (
    .neighbours(neighboursstd_15_neighbours), .alive(plus_00_14new), .pause(pause),
    .input_state(state_helper_15_output_state));
  STATE_helper state_helper_15 (
    .input_state(input_state), .output_state(state_helper_15_output_state), .i(I), .j(J[14]));
  neighboursSTD neighboursstd_16 (
    .minus_01_01(minus_1_line[14]), .minus_01_00(minus_1_line[15]), .minus_01_01_2(minus_1_line[16]),
    .plus_00_01(_0_line__out__1[14]), .plus_00_00(_0_line__out__1[15]), .plus_00_01_2(_0_line__out__1[16]),
    .plus_01_01(_1_line[14]), .plus_01_00(_1_line[15]), .plus_01_01_2(_1_line[16]),
    .neighbours(neighboursstd_16_neighbours));
  aliveSTD alivestd_16 (
    .neighbours(neighboursstd_16_neighbours), .alive(plus_00_15new), .pause(pause),
    .input_state(state_helper_16_output_state));
  STATE_helper state_helper_16 (
    .input_state(input_state), .output_state(state_helper_16_output_state), .i(I), .j(J[15]));
  neighboursSTD neighboursstd_17 (
    .minus_01_01(minus_1_line[15]), .minus_01_00(minus_1_line[16]), .minus_01_01_2(minus_1_line[17]),
    .plus_00_01(_0_line__out__1[15]), .plus_00_00(_0_line__out__1[16]), .plus_00_01_2(_0_line__out__1[17]),
    .plus_01_01(_1_line[15]), .plus_01_00(_1_line[16]), .plus_01_01_2(_1_line[17]),
    .neighbours(neighboursstd_17_neighbours));
  aliveSTD alivestd_17 (
    .neighbours(neighboursstd_17_neighbours), .alive(plus_00_16new), .pause(pause),
    .input_state(state_helper_17_output_state));
  STATE_helper state_helper_17 (
    .input_state(input_state), .output_state(state_helper_17_output_state), .i(I), .j(J[16]));
  neighboursSTD neighboursstd_18 (
    .minus_01_01(minus_1_line[16]), .minus_01_00(minus_1_line[17]), .minus_01_01_2(minus_1_line[18]),
    .plus_00_01(_0_line__out__1[16]), .plus_00_00(_0_line__out__1[17]), .plus_00_01_2(_0_line__out__1[18]),
    .plus_01_01(_1_line[16]), .plus_01_00(_1_line[17]), .plus_01_01_2(_1_line[18]),
    .neighbours(neighboursstd_18_neighbours));
  aliveSTD alivestd_18 (
    .neighbours(neighboursstd_18_neighbours), .alive(plus_00_17new), .pause(pause),
    .input_state(state_helper_18_output_state));
  STATE_helper state_helper_18 (
    .input_state(input_state), .output_state(state_helper_18_output_state), .i(I), .j(J[17]));
  neighboursSTD neighboursstd_19 (
    .minus_01_01(minus_1_line[17]), .minus_01_00(minus_1_line[18]), .minus_01_01_2(minus_1_line[19]),
    .plus_00_01(_0_line__out__1[17]), .plus_00_00(_0_line__out__1[18]), .plus_00_01_2(_0_line__out__1[19]),
    .plus_01_01(_1_line[17]), .plus_01_00(_1_line[18]), .plus_01_01_2(_1_line[19]),
    .neighbours(neighboursstd_19_neighbours));
  aliveSTD alivestd_19 (
    .neighbours(neighboursstd_19_neighbours), .alive(plus_00_18new), .pause(pause),
    .input_state(state_helper_19_output_state));
  STATE_helper state_helper_19 (
    .input_state(input_state), .output_state(state_helper_19_output_state), .i(I), .j(J[18]));
  neighboursSTD neighboursstd_20 (
    .minus_01_01(minus_1_line[18]), .minus_01_00(minus_1_line[19]), .minus_01_01_2(minus_1_line[20]),
    .plus_00_01(_0_line__out__1[18]), .plus_00_00(_0_line__out__1[19]), .plus_00_01_2(_0_line__out__1[20]),
    .plus_01_01(_1_line[18]), .plus_01_00(_1_line[19]), .plus_01_01_2(_1_line[20]),
    .neighbours(neighboursstd_20_neighbours));
  aliveSTD alivestd_20 (
    .neighbours(neighboursstd_20_neighbours), .alive(plus_00_19new), .pause(pause),
    .input_state(state_helper_20_output_state));
  STATE_helper state_helper_20 (
    .input_state(input_state), .output_state(state_helper_20_output_state), .i(I), .j(J[19]));
  neighboursSTD neighboursstd_21 (
    .minus_01_01(minus_1_line[19]), .minus_01_00(minus_1_line[20]), .minus_01_01_2(minus_1_line[21]),
    .plus_00_01(_0_line__out__1[19]), .plus_00_00(_0_line__out__1[20]), .plus_00_01_2(_0_line__out__1[21]),
    .plus_01_01(_1_line[19]), .plus_01_00(_1_line[20]), .plus_01_01_2(_1_line[21]),
    .neighbours(neighboursstd_21_neighbours));
  aliveSTD alivestd_21 (
    .neighbours(neighboursstd_21_neighbours), .alive(plus_00_20new), .pause(pause),
    .input_state(state_helper_21_output_state));
  STATE_helper state_helper_21 (
    .input_state(input_state), .output_state(state_helper_21_output_state), .i(I), .j(J[20]));
  neighboursSTD neighboursstd_22 (
    .minus_01_01(minus_1_line[20]), .minus_01_00(minus_1_line[21]), .minus_01_01_2(minus_1_line[22]),
    .plus_00_01(_0_line__out__1[20]), .plus_00_00(_0_line__out__1[21]), .plus_00_01_2(_0_line__out__1[22]),
    .plus_01_01(_1_line[20]), .plus_01_00(_1_line[21]), .plus_01_01_2(_1_line[22]),
    .neighbours(neighboursstd_22_neighbours));
  aliveSTD alivestd_22 (
    .neighbours(neighboursstd_22_neighbours), .alive(plus_00_21new), .pause(pause),
    .input_state(state_helper_22_output_state));
  STATE_helper state_helper_22 (
    .input_state(input_state), .output_state(state_helper_22_output_state), .i(I), .j(J[21]));
  neighboursSTD neighboursstd_23 (
    .minus_01_01(minus_1_line[21]), .minus_01_00(minus_1_line[22]), .minus_01_01_2(minus_1_line[23]),
    .plus_00_01(_0_line__out__1[21]), .plus_00_00(_0_line__out__1[22]), .plus_00_01_2(_0_line__out__1[23]),
    .plus_01_01(_1_line[21]), .plus_01_00(_1_line[22]), .plus_01_01_2(_1_line[23]),
    .neighbours(neighboursstd_23_neighbours));
  aliveSTD alivestd_23 (
    .neighbours(neighboursstd_23_neighbours), .alive(plus_00_22new), .pause(pause),
    .input_state(state_helper_23_output_state));
  STATE_helper state_helper_23 (
    .input_state(input_state), .output_state(state_helper_23_output_state), .i(I), .j(J[22]));
  neighboursSTD neighboursstd_24 (
    .minus_01_01(minus_1_line[22]), .minus_01_00(minus_1_line[23]), .minus_01_01_2(minus_1_line[24]),
    .plus_00_01(_0_line__out__1[22]), .plus_00_00(_0_line__out__1[23]), .plus_00_01_2(_0_line__out__1[24]),
    .plus_01_01(_1_line[22]), .plus_01_00(_1_line[23]), .plus_01_01_2(_1_line[24]),
    .neighbours(neighboursstd_24_neighbours));
  aliveSTD alivestd_24 (
    .neighbours(neighboursstd_24_neighbours), .alive(plus_00_23new), .pause(pause),
    .input_state(state_helper_24_output_state));
  STATE_helper state_helper_24 (
    .input_state(input_state), .output_state(state_helper_24_output_state), .i(I), .j(J[23]));
  neighboursSTD neighboursstd_25 (
    .minus_01_01(minus_1_line[23]), .minus_01_00(minus_1_line[24]), .minus_01_01_2(minus_1_line[25]),
    .plus_00_01(_0_line__out__1[23]), .plus_00_00(_0_line__out__1[24]), .plus_00_01_2(_0_line__out__1[25]),
    .plus_01_01(_1_line[23]), .plus_01_00(_1_line[24]), .plus_01_01_2(_1_line[25]),
    .neighbours(neighboursstd_25_neighbours));
  aliveSTD alivestd_25 (
    .neighbours(neighboursstd_25_neighbours), .alive(plus_00_24new), .pause(pause),
    .input_state(state_helper_25_output_state));
  STATE_helper state_helper_25 (
    .input_state(input_state), .output_state(state_helper_25_output_state), .i(I), .j(J[24]));
  neighboursSTD neighboursstd_26 (
    .minus_01_01(minus_1_line[24]), .minus_01_00(minus_1_line[25]), .minus_01_01_2(minus_1_line[26]),
    .plus_00_01(_0_line__out__1[24]), .plus_00_00(_0_line__out__1[25]), .plus_00_01_2(_0_line__out__1[26]),
    .plus_01_01(_1_line[24]), .plus_01_00(_1_line[25]), .plus_01_01_2(_1_line[26]),
    .neighbours(neighboursstd_26_neighbours));
  aliveSTD alivestd_26 (
    .neighbours(neighboursstd_26_neighbours), .alive(plus_00_25new), .pause(pause),
    .input_state(state_helper_26_output_state));
  STATE_helper state_helper_26 (
    .input_state(input_state), .output_state(state_helper_26_output_state), .i(I), .j(J[25]));
  neighboursSTD neighboursstd_27 (
    .minus_01_01(minus_1_line[25]), .minus_01_00(minus_1_line[26]), .minus_01_01_2(minus_1_line[27]),
    .plus_00_01(_0_line__out__1[25]), .plus_00_00(_0_line__out__1[26]), .plus_00_01_2(_0_line__out__1[27]),
    .plus_01_01(_1_line[25]), .plus_01_00(_1_line[26]), .plus_01_01_2(_1_line[27]),
    .neighbours(neighboursstd_27_neighbours));
  aliveSTD alivestd_27 (
    .neighbours(neighboursstd_27_neighbours), .alive(plus_00_26new), .pause(pause),
    .input_state(state_helper_27_output_state));
  STATE_helper state_helper_27 (
    .input_state(input_state), .output_state(state_helper_27_output_state), .i(I), .j(J[26]));
  neighboursSTD neighboursstd_28 (
    .minus_01_01(minus_1_line[26]), .minus_01_00(minus_1_line[27]), .minus_01_01_2(minus_1_line[28]),
    .plus_00_01(_0_line__out__1[26]), .plus_00_00(_0_line__out__1[27]), .plus_00_01_2(_0_line__out__1[28]),
    .plus_01_01(_1_line[26]), .plus_01_00(_1_line[27]), .plus_01_01_2(_1_line[28]),
    .neighbours(neighboursstd_28_neighbours));
  aliveSTD alivestd_28 (
    .neighbours(neighboursstd_28_neighbours), .alive(plus_00_27new), .pause(pause),
    .input_state(state_helper_28_output_state));
  STATE_helper state_helper_28 (
    .input_state(input_state), .output_state(state_helper_28_output_state), .i(I), .j(J[27]));
  neighboursSTD neighboursstd_29 (
    .minus_01_01(minus_1_line[27]), .minus_01_00(minus_1_line[28]), .minus_01_01_2(minus_1_line[29]),
    .plus_00_01(_0_line__out__1[27]), .plus_00_00(_0_line__out__1[28]), .plus_00_01_2(_0_line__out__1[29]),
    .plus_01_01(_1_line[27]), .plus_01_00(_1_line[28]), .plus_01_01_2(_1_line[29]),
    .neighbours(neighboursstd_29_neighbours));
  aliveSTD alivestd_29 (
    .neighbours(neighboursstd_29_neighbours), .alive(plus_00_28new), .pause(pause),
    .input_state(state_helper_29_output_state));
  STATE_helper state_helper_29 (
    .input_state(input_state), .output_state(state_helper_29_output_state), .i(I), .j(J[28]));
  neighboursSTD neighboursstd_30 (
    .minus_01_01(minus_1_line[28]), .minus_01_00(minus_1_line[29]), .minus_01_01_2(minus_1_line[30]),
    .plus_00_01(_0_line__out__1[28]), .plus_00_00(_0_line__out__1[29]), .plus_00_01_2(_0_line__out__1[30]),
    .plus_01_01(_1_line[28]), .plus_01_00(_1_line[29]), .plus_01_01_2(_1_line[30]),
    .neighbours(neighboursstd_30_neighbours));
  aliveSTD alivestd_30 (
    .neighbours(neighboursstd_30_neighbours), .alive(plus_00_29new), .pause(pause),
    .input_state(state_helper_30_output_state));
  STATE_helper state_helper_30 (
    .input_state(input_state), .output_state(state_helper_30_output_state), .i(I), .j(J[29]));
  neighboursSTD neighboursstd_31 (
    .minus_01_01(minus_1_line[29]), .minus_01_00(minus_1_line[30]), .minus_01_01_2(minus_1_line[31]),
    .plus_00_01(_0_line__out__1[29]), .plus_00_00(_0_line__out__1[30]), .plus_00_01_2(_0_line__out__1[31]),
    .plus_01_01(_1_line[29]), .plus_01_00(_1_line[30]), .plus_01_01_2(_1_line[31]),
    .neighbours(neighboursstd_31_neighbours));
  aliveSTD alivestd_31 (
    .neighbours(neighboursstd_31_neighbours), .alive(plus_00_30new), .pause(pause),
    .input_state(state_helper_31_output_state));
  STATE_helper state_helper_31 (
    .input_state(input_state), .output_state(state_helper_31_output_state), .i(I), .j(J[30]));
  neighboursSTD neighboursstd_32 (
    .minus_01_01(minus_1_line[30]), .minus_01_00(minus_1_line[31]), .minus_01_01_2(minus_01_32),
    .plus_00_01(_0_line__out__1[30]), .plus_00_00(_0_line__out__1[31]), .plus_00_01_2(plus_00_32),
    .plus_01_01(_1_line[30]), .plus_01_00(_1_line[31]), .plus_01_01_2(plus_01_32),
    .neighbours(neighboursstd_32_neighbours));
  aliveSTD alivestd_32 (
    .neighbours(neighboursstd_32_neighbours), .alive(plus_00_31new), .pause(pause),
    .input_state(state_helper_32_output_state));
  STATE_helper state_helper_32 (
    .input_state(input_state), .output_state(state_helper_32_output_state), .i(I), .j(J[31]));

  assign _0_line__out__1_2 = _0_line__out__1;
  assign display = _0_line__out__1;

  // Other names for the same wires on the sheet: plus_01_00 = _1_line[0]; plus_01_01 = _1_line[1];
  //   plus_01_02 = _1_line[2]; plus_01_03 = _1_line[3]; plus_01_04 = _1_line[4]; plus_01_05 = _1_line[5];
  //   plus_01_06 = _1_line[6]; plus_01_07 = _1_line[7]; plus_01_08 = _1_line[8]; plus_01_09 = _1_line[9];
  //   plus_01_10 = _1_line[10]; plus_01_11 = _1_line[11]; plus_01_12 = _1_line[12]; plus_01_13 = _1_line[13];
  //   plus_01_14 = _1_line[14]; plus_01_15 = _1_line[15]; plus_01_16 = _1_line[16]; plus_01_17 = _1_line[17];
  //   plus_01_18 = _1_line[18]; plus_01_19 = _1_line[19]; plus_01_20 = _1_line[20]; plus_01_21 = _1_line[21];
  //   plus_01_22 = _1_line[22]; plus_01_23 = _1_line[23]; plus_01_24 = _1_line[24]; plus_01_25 = _1_line[25];
  //   plus_01_26 = _1_line[26]; plus_01_27 = _1_line[27]; plus_01_28 = _1_line[28]; plus_01_29 = _1_line[29];
  //   plus_01_30 = _1_line[30]; plus_01_31 = _1_line[31]; plus_00_00 = _0_line__out__1[0];
  //   plus_00_01 = _0_line__out__1[1]; plus_00_02 = _0_line__out__1[2]; plus_00_03 = _0_line__out__1[3];
  //   plus_00_04 = _0_line__out__1[4]; plus_00_05 = _0_line__out__1[5]; plus_00_06 = _0_line__out__1[6];
  //   plus_00_07 = _0_line__out__1[7]; plus_00_08 = _0_line__out__1[8]; plus_00_09 = _0_line__out__1[9];
  //   plus_00_10 = _0_line__out__1[10]; plus_00_11 = _0_line__out__1[11]; plus_00_12 = _0_line__out__1[12];
  //   plus_00_13 = _0_line__out__1[13]; plus_00_14 = _0_line__out__1[14]; plus_00_15 = _0_line__out__1[15];
  //   plus_00_16 = _0_line__out__1[16]; plus_00_17 = _0_line__out__1[17]; plus_00_18 = _0_line__out__1[18];
  //   plus_00_19 = _0_line__out__1[19]; plus_00_20 = _0_line__out__1[20]; plus_00_21 = _0_line__out__1[21];
  //   plus_00_22 = _0_line__out__1[22]; plus_00_23 = _0_line__out__1[23]; plus_00_24 = _0_line__out__1[24];
  //   plus_00_25 = _0_line__out__1[25]; plus_00_26 = _0_line__out__1[26]; plus_00_27 = _0_line__out__1[27];
  //   plus_00_28 = _0_line__out__1[28]; plus_00_29 = _0_line__out__1[29]; plus_00_30 = _0_line__out__1[30];
  //   plus_00_31 = _0_line__out__1[31]; minus_01_00 = minus_1_line[0]; minus_01_01 = minus_1_line[1];
  //   minus_01_02 = minus_1_line[2]; minus_01_03 = minus_1_line[3]; minus_01_04 = minus_1_line[4];
  //   minus_01_05 = minus_1_line[5]; minus_01_06 = minus_1_line[6]; minus_01_07 = minus_1_line[7];
  //   minus_01_08 = minus_1_line[8]; minus_01_09 = minus_1_line[9]; minus_01_10 = minus_1_line[10];
  //   minus_01_11 = minus_1_line[11]; minus_01_12 = minus_1_line[12]; minus_01_13 = minus_1_line[13];
  //   minus_01_14 = minus_1_line[14]; minus_01_15 = minus_1_line[15]; minus_01_16 = minus_1_line[16];
  //   minus_01_17 = minus_1_line[17]; minus_01_18 = minus_1_line[18]; minus_01_19 = minus_1_line[19];
  //   minus_01_20 = minus_1_line[20]; minus_01_21 = minus_1_line[21]; minus_01_22 = minus_1_line[22];
  //   minus_01_23 = minus_1_line[23]; minus_01_24 = minus_1_line[24]; minus_01_25 = minus_1_line[25];
  //   minus_01_26 = minus_1_line[26]; minus_01_27 = minus_1_line[27]; minus_01_28 = minus_1_line[28];
  //   minus_01_29 = minus_1_line[29]; minus_01_30 = minus_1_line[30]; minus_01_31 = minus_1_line[31];
  //   state[1:0] = input_state

  // Notes on the sheet:
  //   clock: pull=down
  //   pause: pull=down
endmodule

module lineSTD_old (
  input  [31:0] J,
  input  [31:0] minus_1_line,
  input  [31:0] _1_line,
  input  I,
  input  Torus,
  input  [1:0] input_state,
  input  clock,
  input  pause,
  output [31:0] _0_line__out__1,
  output [31:0] display,
  output [31:0] _0_line__out__1_2
);

  wire minus_01_01_t, minus_01_32, plus_00_01_t, plus_00_32, plus_01_01_t, plus_01_32;
  wire [1:0] alivestd_old_1_p5, alivestd_old_2_p8, alivestd_old_3_p8, alivestd_old_4_p8, alivestd_old_5_p8,
       alivestd_old_6_p8, alivestd_old_7_p8, alivestd_old_8_p8, alivestd_old_9_p8, alivestd_old_10_p8,
       alivestd_old_11_p8, alivestd_old_12_p8, alivestd_old_13_p8, alivestd_old_14_p8, alivestd_old_15_p8,
       alivestd_old_16_p8, alivestd_old_17_p8, alivestd_old_18_p8, alivestd_old_19_p8, alivestd_old_20_p8,
       alivestd_old_21_p8, alivestd_old_22_p8, alivestd_old_23_p8, alivestd_old_24_p8, alivestd_old_25_p8,
       alivestd_old_26_p8, alivestd_old_27_p8, alivestd_old_28_p8, alivestd_old_29_p8, alivestd_old_30_p8,
       alivestd_old_31_p8, alivestd_old_32_p8;
  wire [8:0] lookAt, neighboursstd_1_neighbours, neighboursstd_2_neighbours, neighboursstd_3_neighbours,
       neighboursstd_4_neighbours, neighboursstd_5_neighbours, neighboursstd_6_neighbours,
       neighboursstd_7_neighbours, neighboursstd_8_neighbours, neighboursstd_9_neighbours,
       neighboursstd_10_neighbours, neighboursstd_11_neighbours, neighboursstd_12_neighbours,
       neighboursstd_13_neighbours, neighboursstd_14_neighbours, neighboursstd_15_neighbours,
       neighboursstd_16_neighbours, neighboursstd_17_neighbours, neighboursstd_18_neighbours,
       neighboursstd_19_neighbours, neighboursstd_20_neighbours, neighboursstd_21_neighbours,
       neighboursstd_22_neighbours, neighboursstd_23_neighbours, neighboursstd_24_neighbours,
       neighboursstd_25_neighbours, neighboursstd_26_neighbours, neighboursstd_27_neighbours,
       neighboursstd_28_neighbours, neighboursstd_29_neighbours, neighboursstd_30_neighbours,
       neighboursstd_31_neighbours, neighboursstd_32_neighbours;
  wire [29:0] birth, save;

  neighboursSTD neighboursstd_1 (
    .minus_01_01(minus_01_01_t), .minus_01_00(minus_1_line[0]), .minus_01_01_2(minus_1_line[1]),
    .plus_00_01(plus_00_01_t), .plus_00_00(_0_line__out__1[0]), .plus_00_01_2(_0_line__out__1[1]),
    .plus_01_01(plus_01_01_t), .plus_01_00(_1_line[0]), .plus_01_01_2(_1_line[1]),
    .neighbours(neighboursstd_1_neighbours));
  // aliveSTD__old alivestd_old_1: pin names not known; wires that end beside it: neighboursstd_1_neighbours, clock, _0_line__out__1[0], pause, alivestd_old_1_p5
  STATE_helper state_helper_1 (.input_state(input_state), .output_state(alivestd_old_1_p5), .i(I), .j(J[0]));
  and and_1 (minus_01_32, minus_1_line[0], Torus);
  and and_2 (minus_01_01_t, minus_1_line[31], Torus);
  neighboursSTD neighboursstd_2 (
    .minus_01_01(minus_1_line[0]), .minus_01_00(minus_1_line[1]), .minus_01_01_2(minus_1_line[2]),
    .plus_00_01(_0_line__out__1[0]), .plus_00_00(_0_line__out__1[1]), .plus_00_01_2(_0_line__out__1[2]),
    .plus_01_01(_1_line[0]), .plus_01_00(_1_line[1]), .plus_01_01_2(_1_line[2]),
    .neighbours(neighboursstd_2_neighbours));
  // aliveSTD__old alivestd_old_2: pin names not known; wires that end beside it: neighboursstd_2_neighbours, lookAt, birth, save, clock, _0_line__out__1[1], pause, alivestd_old_2_p8
  STATE_helper state_helper_2 (.input_state(input_state), .output_state(alivestd_old_2_p8), .i(I), .j(J[1]));
  and and_3 (plus_01_32, _1_line[0], Torus);
  and and_4 (plus_01_01_t, _1_line[31], Torus);
  and and_5 (plus_00_32, _0_line__out__1[0], Torus);
  and and_6 (plus_00_01_t, _0_line__out__1[31], Torus);
  neighboursSTD neighboursstd_3 (
    .minus_01_01(minus_1_line[1]), .minus_01_00(minus_1_line[2]), .minus_01_01_2(minus_1_line[3]),
    .plus_00_01(_0_line__out__1[1]), .plus_00_00(_0_line__out__1[2]), .plus_00_01_2(_0_line__out__1[3]),
    .plus_01_01(_1_line[1]), .plus_01_00(_1_line[2]), .plus_01_01_2(_1_line[3]),
    .neighbours(neighboursstd_3_neighbours));
  // aliveSTD__old alivestd_old_3: pin names not known; wires that end beside it: neighboursstd_3_neighbours, lookAt, birth, save, clock, _0_line__out__1[2], pause, alivestd_old_3_p8
  STATE_helper state_helper_3 (.input_state(input_state), .output_state(alivestd_old_3_p8), .i(I), .j(J[2]));
  neighboursSTD neighboursstd_4 (
    .minus_01_01(minus_1_line[2]), .minus_01_00(minus_1_line[3]), .minus_01_01_2(minus_1_line[4]),
    .plus_00_01(_0_line__out__1[2]), .plus_00_00(_0_line__out__1[3]), .plus_00_01_2(_0_line__out__1[4]),
    .plus_01_01(_1_line[2]), .plus_01_00(_1_line[3]), .plus_01_01_2(_1_line[4]),
    .neighbours(neighboursstd_4_neighbours));
  // aliveSTD__old alivestd_old_4: pin names not known; wires that end beside it: neighboursstd_4_neighbours, lookAt, birth, save, clock, _0_line__out__1[3], pause, alivestd_old_4_p8
  STATE_helper state_helper_4 (.input_state(input_state), .output_state(alivestd_old_4_p8), .i(I), .j(J[3]));
  Pull_Resistor pull_resistor_1 (.node(_0_line__out__1[0]));
  Pull_Resistor pull_resistor_2 ();  // open: node
  Pull_Resistor pull_resistor_3 (.node(_0_line__out__1[2]));
  Pull_Resistor pull_resistor_4 ();  // open: node
  Pull_Resistor pull_resistor_5 (.node(_0_line__out__1[4]));
  Pull_Resistor pull_resistor_6 ();  // open: node
  Pull_Resistor pull_resistor_7 (.node(_0_line__out__1[6]));
  Pull_Resistor pull_resistor_8 ();  // open: node
  Pull_Resistor pull_resistor_9 (.node(_0_line__out__1[8]));
  Pull_Resistor pull_resistor_10 ();  // open: node
  Pull_Resistor pull_resistor_11 (.node(_0_line__out__1[10]));
  Pull_Resistor pull_resistor_12 ();  // open: node
  Pull_Resistor pull_resistor_13 (.node(_0_line__out__1[12]));
  Pull_Resistor pull_resistor_14 ();  // open: node
  Pull_Resistor pull_resistor_15 (.node(_0_line__out__1[14]));
  Pull_Resistor pull_resistor_16 ();  // open: node
  Pull_Resistor pull_resistor_17 (.node(_0_line__out__1[16]));
  Pull_Resistor pull_resistor_18 ();  // open: node
  Pull_Resistor pull_resistor_19 (.node(_0_line__out__1[18]));
  Pull_Resistor pull_resistor_20 ();  // open: node
  Pull_Resistor pull_resistor_21 (.node(_0_line__out__1[20]));
  Pull_Resistor pull_resistor_22 ();  // open: node
  Pull_Resistor pull_resistor_23 (.node(_0_line__out__1[22]));
  Pull_Resistor pull_resistor_24 ();  // open: node
  Pull_Resistor pull_resistor_25 (.node(_0_line__out__1[24]));
  Pull_Resistor pull_resistor_26 ();  // open: node
  Pull_Resistor pull_resistor_27 (.node(_0_line__out__1[26]));
  Pull_Resistor pull_resistor_28 ();  // open: node
  Pull_Resistor pull_resistor_29 (.node(_0_line__out__1[28]));
  Pull_Resistor pull_resistor_30 ();  // open: node
  Pull_Resistor pull_resistor_31 (.node(_0_line__out__1[30]));
  Pull_Resistor pull_resistor_32 ();  // open: node
  neighboursSTD neighboursstd_5 (
    .minus_01_01(minus_1_line[3]), .minus_01_00(minus_1_line[4]), .minus_01_01_2(minus_1_line[5]),
    .plus_00_01(_0_line__out__1[3]), .plus_00_00(_0_line__out__1[4]), .plus_00_01_2(_0_line__out__1[5]),
    .plus_01_01(_1_line[3]), .plus_01_00(_1_line[4]), .plus_01_01_2(_1_line[5]),
    .neighbours(neighboursstd_5_neighbours));
  // aliveSTD__old alivestd_old_5: pin names not known; wires that end beside it: neighboursstd_5_neighbours, lookAt, birth, save, clock, _0_line__out__1[4], pause, alivestd_old_5_p8
  STATE_helper state_helper_5 (.input_state(input_state), .output_state(alivestd_old_5_p8), .i(I), .j(J[4]));
  neighboursSTD neighboursstd_6 (
    .minus_01_01(minus_1_line[4]), .minus_01_00(minus_1_line[5]), .minus_01_01_2(minus_1_line[6]),
    .plus_00_01(_0_line__out__1[4]), .plus_00_00(_0_line__out__1[5]), .plus_00_01_2(_0_line__out__1[6]),
    .plus_01_01(_1_line[4]), .plus_01_00(_1_line[5]), .plus_01_01_2(_1_line[6]),
    .neighbours(neighboursstd_6_neighbours));
  // aliveSTD__old alivestd_old_6: pin names not known; wires that end beside it: neighboursstd_6_neighbours, lookAt, birth, save, clock, _0_line__out__1[5], pause, alivestd_old_6_p8
  STATE_helper state_helper_6 (.input_state(input_state), .output_state(alivestd_old_6_p8), .i(I), .j(J[5]));
  neighboursSTD neighboursstd_7 (
    .minus_01_01(minus_1_line[5]), .minus_01_00(minus_1_line[6]), .minus_01_01_2(minus_1_line[7]),
    .plus_00_01(_0_line__out__1[5]), .plus_00_00(_0_line__out__1[6]), .plus_00_01_2(_0_line__out__1[7]),
    .plus_01_01(_1_line[5]), .plus_01_00(_1_line[6]), .plus_01_01_2(_1_line[7]),
    .neighbours(neighboursstd_7_neighbours));
  // aliveSTD__old alivestd_old_7: pin names not known; wires that end beside it: neighboursstd_7_neighbours, lookAt, birth, save, clock, _0_line__out__1[6], pause, alivestd_old_7_p8
  STATE_helper state_helper_7 (.input_state(input_state), .output_state(alivestd_old_7_p8), .i(I), .j(J[6]));
  neighboursSTD neighboursstd_8 (
    .minus_01_01(minus_1_line[6]), .minus_01_00(minus_1_line[7]), .minus_01_01_2(minus_1_line[8]),
    .plus_00_01(_0_line__out__1[6]), .plus_00_00(_0_line__out__1[7]), .plus_00_01_2(_0_line__out__1[8]),
    .plus_01_01(_1_line[6]), .plus_01_00(_1_line[7]), .plus_01_01_2(_1_line[8]),
    .neighbours(neighboursstd_8_neighbours));
  // aliveSTD__old alivestd_old_8: pin names not known; wires that end beside it: neighboursstd_8_neighbours, lookAt, birth, save, clock, _0_line__out__1[7], pause, alivestd_old_8_p8
  STATE_helper state_helper_8 (.input_state(input_state), .output_state(alivestd_old_8_p8), .i(I), .j(J[7]));
  neighboursSTD neighboursstd_9 (
    .minus_01_01(minus_1_line[7]), .minus_01_00(minus_1_line[8]), .minus_01_01_2(minus_1_line[9]),
    .plus_00_01(_0_line__out__1[7]), .plus_00_00(_0_line__out__1[8]), .plus_00_01_2(_0_line__out__1[9]),
    .plus_01_01(_1_line[7]), .plus_01_00(_1_line[8]), .plus_01_01_2(_1_line[9]),
    .neighbours(neighboursstd_9_neighbours));
  // aliveSTD__old alivestd_old_9: pin names not known; wires that end beside it: neighboursstd_9_neighbours, lookAt, birth, save, clock, _0_line__out__1[8], pause, alivestd_old_9_p8
  STATE_helper state_helper_9 (.input_state(input_state), .output_state(alivestd_old_9_p8), .i(I), .j(J[8]));
  neighboursSTD neighboursstd_10 (
    .minus_01_01(minus_1_line[8]), .minus_01_00(minus_1_line[9]), .minus_01_01_2(minus_1_line[10]),
    .plus_00_01(_0_line__out__1[8]), .plus_00_00(_0_line__out__1[9]), .plus_00_01_2(_0_line__out__1[10]),
    .plus_01_01(_1_line[8]), .plus_01_00(_1_line[9]), .plus_01_01_2(_1_line[10]),
    .neighbours(neighboursstd_10_neighbours));
  // aliveSTD__old alivestd_old_10: pin names not known; wires that end beside it: neighboursstd_10_neighbours, lookAt, birth, save, clock, _0_line__out__1[9], pause, alivestd_old_10_p8
  STATE_helper state_helper_10 (.input_state(input_state), .output_state(alivestd_old_10_p8), .i(I), .j(J[9]));
  neighboursSTD neighboursstd_11 (
    .minus_01_01(minus_1_line[9]), .minus_01_00(minus_1_line[10]), .minus_01_01_2(minus_1_line[11]),
    .plus_00_01(_0_line__out__1[9]), .plus_00_00(_0_line__out__1[10]), .plus_00_01_2(_0_line__out__1[11]),
    .plus_01_01(_1_line[9]), .plus_01_00(_1_line[10]), .plus_01_01_2(_1_line[11]),
    .neighbours(neighboursstd_11_neighbours));
  // aliveSTD__old alivestd_old_11: pin names not known; wires that end beside it: neighboursstd_11_neighbours, lookAt, birth, save, clock, _0_line__out__1[10], pause, alivestd_old_11_p8
  STATE_helper state_helper_11 (.input_state(input_state), .output_state(alivestd_old_11_p8), .i(I), .j(J[10]));
  neighboursSTD neighboursstd_12 (
    .minus_01_01(minus_1_line[10]), .minus_01_00(minus_1_line[11]), .minus_01_01_2(minus_1_line[12]),
    .plus_00_01(_0_line__out__1[10]), .plus_00_00(_0_line__out__1[11]), .plus_00_01_2(_0_line__out__1[12]),
    .plus_01_01(_1_line[10]), .plus_01_00(_1_line[11]), .plus_01_01_2(_1_line[12]),
    .neighbours(neighboursstd_12_neighbours));
  // aliveSTD__old alivestd_old_12: pin names not known; wires that end beside it: neighboursstd_12_neighbours, lookAt, birth, save, clock, _0_line__out__1[11], pause, alivestd_old_12_p8
  STATE_helper state_helper_12 (.input_state(input_state), .output_state(alivestd_old_12_p8), .i(I), .j(J[11]));
  neighboursSTD neighboursstd_13 (
    .minus_01_01(minus_1_line[11]), .minus_01_00(minus_1_line[12]), .minus_01_01_2(minus_1_line[13]),
    .plus_00_01(_0_line__out__1[11]), .plus_00_00(_0_line__out__1[12]), .plus_00_01_2(_0_line__out__1[13]),
    .plus_01_01(_1_line[11]), .plus_01_00(_1_line[12]), .plus_01_01_2(_1_line[13]),
    .neighbours(neighboursstd_13_neighbours));
  // aliveSTD__old alivestd_old_13: pin names not known; wires that end beside it: neighboursstd_13_neighbours, lookAt, birth, save, clock, _0_line__out__1[12], pause, alivestd_old_13_p8
  STATE_helper state_helper_13 (.input_state(input_state), .output_state(alivestd_old_13_p8), .i(I), .j(J[12]));
  neighboursSTD neighboursstd_14 (
    .minus_01_01(minus_1_line[12]), .minus_01_00(minus_1_line[13]), .minus_01_01_2(minus_1_line[14]),
    .plus_00_01(_0_line__out__1[12]), .plus_00_00(_0_line__out__1[13]), .plus_00_01_2(_0_line__out__1[14]),
    .plus_01_01(_1_line[12]), .plus_01_00(_1_line[13]), .plus_01_01_2(_1_line[14]),
    .neighbours(neighboursstd_14_neighbours));
  // aliveSTD__old alivestd_old_14: pin names not known; wires that end beside it: neighboursstd_14_neighbours, lookAt, birth, save, clock, _0_line__out__1[13], pause, alivestd_old_14_p8
  STATE_helper state_helper_14 (.input_state(input_state), .output_state(alivestd_old_14_p8), .i(I), .j(J[13]));
  neighboursSTD neighboursstd_15 (
    .minus_01_01(minus_1_line[13]), .minus_01_00(minus_1_line[14]), .minus_01_01_2(minus_1_line[15]),
    .plus_00_01(_0_line__out__1[13]), .plus_00_00(_0_line__out__1[14]), .plus_00_01_2(_0_line__out__1[15]),
    .plus_01_01(_1_line[13]), .plus_01_00(_1_line[14]), .plus_01_01_2(_1_line[15]),
    .neighbours(neighboursstd_15_neighbours));
  // aliveSTD__old alivestd_old_15: pin names not known; wires that end beside it: neighboursstd_15_neighbours, lookAt, birth, save, clock, _0_line__out__1[14], pause, alivestd_old_15_p8
  STATE_helper state_helper_15 (.input_state(input_state), .output_state(alivestd_old_15_p8), .i(I), .j(J[14]));
  neighboursSTD neighboursstd_16 (
    .minus_01_01(minus_1_line[14]), .minus_01_00(minus_1_line[15]), .minus_01_01_2(minus_1_line[16]),
    .plus_00_01(_0_line__out__1[14]), .plus_00_00(_0_line__out__1[15]), .plus_00_01_2(_0_line__out__1[16]),
    .plus_01_01(_1_line[14]), .plus_01_00(_1_line[15]), .plus_01_01_2(_1_line[16]),
    .neighbours(neighboursstd_16_neighbours));
  // aliveSTD__old alivestd_old_16: pin names not known; wires that end beside it: neighboursstd_16_neighbours, lookAt, birth, save, clock, _0_line__out__1[15], pause, alivestd_old_16_p8
  STATE_helper state_helper_16 (.input_state(input_state), .output_state(alivestd_old_16_p8), .i(I), .j(J[15]));
  neighboursSTD neighboursstd_17 (
    .minus_01_01(minus_1_line[15]), .minus_01_00(minus_1_line[16]), .minus_01_01_2(minus_1_line[17]),
    .plus_00_01(_0_line__out__1[15]), .plus_00_00(_0_line__out__1[16]), .plus_00_01_2(_0_line__out__1[17]),
    .plus_01_01(_1_line[15]), .plus_01_00(_1_line[16]), .plus_01_01_2(_1_line[17]),
    .neighbours(neighboursstd_17_neighbours));
  // aliveSTD__old alivestd_old_17: pin names not known; wires that end beside it: neighboursstd_17_neighbours, lookAt, birth, save, clock, _0_line__out__1[16], pause, alivestd_old_17_p8
  STATE_helper state_helper_17 (.input_state(input_state), .output_state(alivestd_old_17_p8), .i(I), .j(J[16]));
  neighboursSTD neighboursstd_18 (
    .minus_01_01(minus_1_line[16]), .minus_01_00(minus_1_line[17]), .minus_01_01_2(minus_1_line[18]),
    .plus_00_01(_0_line__out__1[16]), .plus_00_00(_0_line__out__1[17]), .plus_00_01_2(_0_line__out__1[18]),
    .plus_01_01(_1_line[16]), .plus_01_00(_1_line[17]), .plus_01_01_2(_1_line[18]),
    .neighbours(neighboursstd_18_neighbours));
  // aliveSTD__old alivestd_old_18: pin names not known; wires that end beside it: neighboursstd_18_neighbours, lookAt, birth, save, clock, _0_line__out__1[17], pause, alivestd_old_18_p8
  STATE_helper state_helper_18 (.input_state(input_state), .output_state(alivestd_old_18_p8), .i(I), .j(J[17]));
  neighboursSTD neighboursstd_19 (
    .minus_01_01(minus_1_line[17]), .minus_01_00(minus_1_line[18]), .minus_01_01_2(minus_1_line[19]),
    .plus_00_01(_0_line__out__1[17]), .plus_00_00(_0_line__out__1[18]), .plus_00_01_2(_0_line__out__1[19]),
    .plus_01_01(_1_line[17]), .plus_01_00(_1_line[18]), .plus_01_01_2(_1_line[19]),
    .neighbours(neighboursstd_19_neighbours));
  // aliveSTD__old alivestd_old_19: pin names not known; wires that end beside it: neighboursstd_19_neighbours, lookAt, birth, save, clock, _0_line__out__1[18], pause, alivestd_old_19_p8
  STATE_helper state_helper_19 (.input_state(input_state), .output_state(alivestd_old_19_p8), .i(I), .j(J[18]));
  neighboursSTD neighboursstd_20 (
    .minus_01_01(minus_1_line[18]), .minus_01_00(minus_1_line[19]), .minus_01_01_2(minus_1_line[20]),
    .plus_00_01(_0_line__out__1[18]), .plus_00_00(_0_line__out__1[19]), .plus_00_01_2(_0_line__out__1[20]),
    .plus_01_01(_1_line[18]), .plus_01_00(_1_line[19]), .plus_01_01_2(_1_line[20]),
    .neighbours(neighboursstd_20_neighbours));
  // aliveSTD__old alivestd_old_20: pin names not known; wires that end beside it: neighboursstd_20_neighbours, lookAt, birth, save, clock, _0_line__out__1[19], pause, alivestd_old_20_p8
  STATE_helper state_helper_20 (.input_state(input_state), .output_state(alivestd_old_20_p8), .i(I), .j(J[19]));
  neighboursSTD neighboursstd_21 (
    .minus_01_01(minus_1_line[19]), .minus_01_00(minus_1_line[20]), .minus_01_01_2(minus_1_line[21]),
    .plus_00_01(_0_line__out__1[19]), .plus_00_00(_0_line__out__1[20]), .plus_00_01_2(_0_line__out__1[21]),
    .plus_01_01(_1_line[19]), .plus_01_00(_1_line[20]), .plus_01_01_2(_1_line[21]),
    .neighbours(neighboursstd_21_neighbours));
  // aliveSTD__old alivestd_old_21: pin names not known; wires that end beside it: neighboursstd_21_neighbours, lookAt, birth, save, clock, _0_line__out__1[20], pause, alivestd_old_21_p8
  STATE_helper state_helper_21 (.input_state(input_state), .output_state(alivestd_old_21_p8), .i(I), .j(J[20]));
  neighboursSTD neighboursstd_22 (
    .minus_01_01(minus_1_line[20]), .minus_01_00(minus_1_line[21]), .minus_01_01_2(minus_1_line[22]),
    .plus_00_01(_0_line__out__1[20]), .plus_00_00(_0_line__out__1[21]), .plus_00_01_2(_0_line__out__1[22]),
    .plus_01_01(_1_line[20]), .plus_01_00(_1_line[21]), .plus_01_01_2(_1_line[22]),
    .neighbours(neighboursstd_22_neighbours));
  // aliveSTD__old alivestd_old_22: pin names not known; wires that end beside it: neighboursstd_22_neighbours, lookAt, birth, save, clock, _0_line__out__1[21], pause, alivestd_old_22_p8
  STATE_helper state_helper_22 (.input_state(input_state), .output_state(alivestd_old_22_p8), .i(I), .j(J[21]));
  neighboursSTD neighboursstd_23 (
    .minus_01_01(minus_1_line[21]), .minus_01_00(minus_1_line[22]), .minus_01_01_2(minus_1_line[23]),
    .plus_00_01(_0_line__out__1[21]), .plus_00_00(_0_line__out__1[22]), .plus_00_01_2(_0_line__out__1[23]),
    .plus_01_01(_1_line[21]), .plus_01_00(_1_line[22]), .plus_01_01_2(_1_line[23]),
    .neighbours(neighboursstd_23_neighbours));
  // aliveSTD__old alivestd_old_23: pin names not known; wires that end beside it: neighboursstd_23_neighbours, lookAt, birth, save, clock, _0_line__out__1[22], pause, alivestd_old_23_p8
  STATE_helper state_helper_23 (.input_state(input_state), .output_state(alivestd_old_23_p8), .i(I), .j(J[22]));
  neighboursSTD neighboursstd_24 (
    .minus_01_01(minus_1_line[22]), .minus_01_00(minus_1_line[23]), .minus_01_01_2(minus_1_line[24]),
    .plus_00_01(_0_line__out__1[22]), .plus_00_00(_0_line__out__1[23]), .plus_00_01_2(_0_line__out__1[24]),
    .plus_01_01(_1_line[22]), .plus_01_00(_1_line[23]), .plus_01_01_2(_1_line[24]),
    .neighbours(neighboursstd_24_neighbours));
  // aliveSTD__old alivestd_old_24: pin names not known; wires that end beside it: neighboursstd_24_neighbours, lookAt, birth, save, clock, _0_line__out__1[23], pause, alivestd_old_24_p8
  STATE_helper state_helper_24 (.input_state(input_state), .output_state(alivestd_old_24_p8), .i(I), .j(J[23]));
  neighboursSTD neighboursstd_25 (
    .minus_01_01(minus_1_line[23]), .minus_01_00(minus_1_line[24]), .minus_01_01_2(minus_1_line[25]),
    .plus_00_01(_0_line__out__1[23]), .plus_00_00(_0_line__out__1[24]), .plus_00_01_2(_0_line__out__1[25]),
    .plus_01_01(_1_line[23]), .plus_01_00(_1_line[24]), .plus_01_01_2(_1_line[25]),
    .neighbours(neighboursstd_25_neighbours));
  // aliveSTD__old alivestd_old_25: pin names not known; wires that end beside it: neighboursstd_25_neighbours, lookAt, birth, save, clock, _0_line__out__1[24], pause, alivestd_old_25_p8
  STATE_helper state_helper_25 (.input_state(input_state), .output_state(alivestd_old_25_p8), .i(I), .j(J[24]));
  neighboursSTD neighboursstd_26 (
    .minus_01_01(minus_1_line[24]), .minus_01_00(minus_1_line[25]), .minus_01_01_2(minus_1_line[26]),
    .plus_00_01(_0_line__out__1[24]), .plus_00_00(_0_line__out__1[25]), .plus_00_01_2(_0_line__out__1[26]),
    .plus_01_01(_1_line[24]), .plus_01_00(_1_line[25]), .plus_01_01_2(_1_line[26]),
    .neighbours(neighboursstd_26_neighbours));
  // aliveSTD__old alivestd_old_26: pin names not known; wires that end beside it: neighboursstd_26_neighbours, lookAt, birth, save, clock, _0_line__out__1[25], pause, alivestd_old_26_p8
  STATE_helper state_helper_26 (.input_state(input_state), .output_state(alivestd_old_26_p8), .i(I), .j(J[25]));
  neighboursSTD neighboursstd_27 (
    .minus_01_01(minus_1_line[25]), .minus_01_00(minus_1_line[26]), .minus_01_01_2(minus_1_line[27]),
    .plus_00_01(_0_line__out__1[25]), .plus_00_00(_0_line__out__1[26]), .plus_00_01_2(_0_line__out__1[27]),
    .plus_01_01(_1_line[25]), .plus_01_00(_1_line[26]), .plus_01_01_2(_1_line[27]),
    .neighbours(neighboursstd_27_neighbours));
  // aliveSTD__old alivestd_old_27: pin names not known; wires that end beside it: neighboursstd_27_neighbours, lookAt, birth, save, clock, _0_line__out__1[26], pause, alivestd_old_27_p8
  STATE_helper state_helper_27 (.input_state(input_state), .output_state(alivestd_old_27_p8), .i(I), .j(J[26]));
  neighboursSTD neighboursstd_28 (
    .minus_01_01(minus_1_line[26]), .minus_01_00(minus_1_line[27]), .minus_01_01_2(minus_1_line[28]),
    .plus_00_01(_0_line__out__1[26]), .plus_00_00(_0_line__out__1[27]), .plus_00_01_2(_0_line__out__1[28]),
    .plus_01_01(_1_line[26]), .plus_01_00(_1_line[27]), .plus_01_01_2(_1_line[28]),
    .neighbours(neighboursstd_28_neighbours));
  // aliveSTD__old alivestd_old_28: pin names not known; wires that end beside it: neighboursstd_28_neighbours, lookAt, birth, save, clock, _0_line__out__1[27], pause, alivestd_old_28_p8
  STATE_helper state_helper_28 (.input_state(input_state), .output_state(alivestd_old_28_p8), .i(I), .j(J[27]));
  neighboursSTD neighboursstd_29 (
    .minus_01_01(minus_1_line[27]), .minus_01_00(minus_1_line[28]), .minus_01_01_2(minus_1_line[29]),
    .plus_00_01(_0_line__out__1[27]), .plus_00_00(_0_line__out__1[28]), .plus_00_01_2(_0_line__out__1[29]),
    .plus_01_01(_1_line[27]), .plus_01_00(_1_line[28]), .plus_01_01_2(_1_line[29]),
    .neighbours(neighboursstd_29_neighbours));
  // aliveSTD__old alivestd_old_29: pin names not known; wires that end beside it: neighboursstd_29_neighbours, lookAt, birth, save, clock, _0_line__out__1[28], pause, alivestd_old_29_p8
  STATE_helper state_helper_29 (.input_state(input_state), .output_state(alivestd_old_29_p8), .i(I), .j(J[28]));
  neighboursSTD neighboursstd_30 (
    .minus_01_01(minus_1_line[28]), .minus_01_00(minus_1_line[29]), .minus_01_01_2(minus_1_line[30]),
    .plus_00_01(_0_line__out__1[28]), .plus_00_00(_0_line__out__1[29]), .plus_00_01_2(_0_line__out__1[30]),
    .plus_01_01(_1_line[28]), .plus_01_00(_1_line[29]), .plus_01_01_2(_1_line[30]),
    .neighbours(neighboursstd_30_neighbours));
  // aliveSTD__old alivestd_old_30: pin names not known; wires that end beside it: neighboursstd_30_neighbours, lookAt, birth, save, clock, _0_line__out__1[29], pause, alivestd_old_30_p8
  STATE_helper state_helper_30 (.input_state(input_state), .output_state(alivestd_old_30_p8), .i(I), .j(J[29]));
  neighboursSTD neighboursstd_31 (
    .minus_01_01(minus_1_line[29]), .minus_01_00(minus_1_line[30]), .minus_01_01_2(minus_1_line[31]),
    .plus_00_01(_0_line__out__1[29]), .plus_00_00(_0_line__out__1[30]), .plus_00_01_2(_0_line__out__1[31]),
    .plus_01_01(_1_line[29]), .plus_01_00(_1_line[30]), .plus_01_01_2(_1_line[31]),
    .neighbours(neighboursstd_31_neighbours));
  // aliveSTD__old alivestd_old_31: pin names not known; wires that end beside it: neighboursstd_31_neighbours, lookAt, birth, save, clock, _0_line__out__1[30], pause, alivestd_old_31_p8
  STATE_helper state_helper_31 (.input_state(input_state), .output_state(alivestd_old_31_p8), .i(I), .j(J[30]));
  neighboursSTD neighboursstd_32 (
    .minus_01_01(minus_1_line[30]), .minus_01_00(minus_1_line[31]), .minus_01_01_2(minus_01_32),
    .plus_00_01(_0_line__out__1[30]), .plus_00_00(_0_line__out__1[31]), .plus_00_01_2(plus_00_32),
    .plus_01_01(_1_line[30]), .plus_01_00(_1_line[31]), .plus_01_01_2(plus_01_32),
    .neighbours(neighboursstd_32_neighbours));
  // aliveSTD__old alivestd_old_32: pin names not known; wires that end beside it: neighboursstd_32_neighbours, lookAt, birth, save, clock, _0_line__out__1[31], pause, alivestd_old_32_p8
  STATE_helper state_helper_32 (.input_state(input_state), .output_state(alivestd_old_32_p8), .i(I), .j(J[31]));

  assign _0_line__out__1_2 = _0_line__out__1;
  assign display = _0_line__out__1;

  // Other names for the same wires on the sheet: plus_01_00 = _1_line[0]; plus_01_01 = _1_line[1];
  //   plus_01_02 = _1_line[2]; plus_01_03 = _1_line[3]; plus_01_04 = _1_line[4]; plus_01_05 = _1_line[5];
  //   plus_01_06 = _1_line[6]; plus_01_07 = _1_line[7]; plus_01_08 = _1_line[8]; plus_01_09 = _1_line[9];
  //   plus_01_10 = _1_line[10]; plus_01_11 = _1_line[11]; plus_01_12 = _1_line[12]; plus_01_13 = _1_line[13];
  //   plus_01_14 = _1_line[14]; plus_01_15 = _1_line[15]; plus_01_16 = _1_line[16]; plus_01_17 = _1_line[17];
  //   plus_01_18 = _1_line[18]; plus_01_19 = _1_line[19]; plus_01_20 = _1_line[20]; plus_01_21 = _1_line[21];
  //   plus_01_22 = _1_line[22]; plus_01_23 = _1_line[23]; plus_01_24 = _1_line[24]; plus_01_25 = _1_line[25];
  //   plus_01_26 = _1_line[26]; plus_01_27 = _1_line[27]; plus_01_28 = _1_line[28]; plus_01_29 = _1_line[29];
  //   plus_01_30 = _1_line[30]; plus_01_31 = _1_line[31]; plus_00_00 = _0_line__out__1[0];
  //   plus_00_01 = _0_line__out__1[1]; plus_00_02 = _0_line__out__1[2]; plus_00_03 = _0_line__out__1[3];
  //   plus_00_04 = _0_line__out__1[4]; plus_00_05 = _0_line__out__1[5]; plus_00_06 = _0_line__out__1[6];
  //   plus_00_07 = _0_line__out__1[7]; plus_00_08 = _0_line__out__1[8]; plus_00_09 = _0_line__out__1[9];
  //   plus_00_10 = _0_line__out__1[10]; plus_00_11 = _0_line__out__1[11]; plus_00_12 = _0_line__out__1[12];
  //   plus_00_13 = _0_line__out__1[13]; plus_00_14 = _0_line__out__1[14]; plus_00_15 = _0_line__out__1[15];
  //   plus_00_16 = _0_line__out__1[16]; plus_00_17 = _0_line__out__1[17]; plus_00_18 = _0_line__out__1[18];
  //   plus_00_19 = _0_line__out__1[19]; plus_00_20 = _0_line__out__1[20]; plus_00_21 = _0_line__out__1[21];
  //   plus_00_22 = _0_line__out__1[22]; plus_00_23 = _0_line__out__1[23]; plus_00_24 = _0_line__out__1[24];
  //   plus_00_25 = _0_line__out__1[25]; plus_00_26 = _0_line__out__1[26]; plus_00_27 = _0_line__out__1[27];
  //   plus_00_28 = _0_line__out__1[28]; plus_00_29 = _0_line__out__1[29]; plus_00_30 = _0_line__out__1[30];
  //   plus_00_31 = _0_line__out__1[31]; minus_01_00 = minus_1_line[0]; minus_01_01 = minus_1_line[1];
  //   minus_01_02 = minus_1_line[2]; minus_01_03 = minus_1_line[3]; minus_01_04 = minus_1_line[4];
  //   minus_01_05 = minus_1_line[5]; minus_01_06 = minus_1_line[6]; minus_01_07 = minus_1_line[7];
  //   minus_01_08 = minus_1_line[8]; minus_01_09 = minus_1_line[9]; minus_01_10 = minus_1_line[10];
  //   minus_01_11 = minus_1_line[11]; minus_01_12 = minus_1_line[12]; minus_01_13 = minus_1_line[13];
  //   minus_01_14 = minus_1_line[14]; minus_01_15 = minus_1_line[15]; minus_01_16 = minus_1_line[16];
  //   minus_01_17 = minus_1_line[17]; minus_01_18 = minus_1_line[18]; minus_01_19 = minus_1_line[19];
  //   minus_01_20 = minus_1_line[20]; minus_01_21 = minus_1_line[21]; minus_01_22 = minus_1_line[22];
  //   minus_01_23 = minus_1_line[23]; minus_01_24 = minus_1_line[24]; minus_01_25 = minus_1_line[25];
  //   minus_01_26 = minus_1_line[26]; minus_01_27 = minus_1_line[27]; minus_01_28 = minus_1_line[28];
  //   minus_01_29 = minus_1_line[29]; minus_01_30 = minus_1_line[30]; minus_01_31 = minus_1_line[31];
  //   state[1:0] = input_state

  // Notes on the sheet:
  //   pause: pull=down
  //   clock: pull=down
endmodule
module line (
  input  [31:0] J,
  input  [31:0] minus_2_line,
  input  [31:0] minus_1_line,
  input  [31:0] _1_line,
  input  [31:0] _2_line,
  input  I,
  input  Torus,
  input  [1:0] input_state,
  input  clock,
  input  pause,
  output [31:0] _0_line__out__2,
  output [31:0] _0_line__out__1,
  output [31:0] display,
  output [31:0] _0_line__out__1_2,
  output [31:0] _0_line__out__2_2
);

  wire minus_01_01_t, minus_01_02_t, minus_01_32, minus_01_33, minus_02_01_t, minus_02_02_t, minus_02_32,
       minus_02_33, plus_00_00new, plus_00_01_t, plus_00_01new, plus_00_02_t, plus_00_02new, plus_00_03new,
       plus_00_04new, plus_00_05new, plus_00_06new, plus_00_07new, plus_00_08new, plus_00_09new,
       plus_00_10new, plus_00_11new, plus_00_12new, plus_00_13new, plus_00_14new, plus_00_15new,
       plus_00_16new, plus_00_17new, plus_00_18new, plus_00_19new, plus_00_20new, plus_00_21new,
       plus_00_22new, plus_00_23new, plus_00_24new, plus_00_25new, plus_00_26new, plus_00_27new,
       plus_00_28new, plus_00_29new, plus_00_30new, plus_00_31new, plus_00_32, plus_00_33, plus_01_01_t,
       plus_01_02_t, plus_01_32, plus_01_33, plus_02_01_t, plus_02_02_t, plus_02_32, plus_02_33;
  wire [1:0] state_helper_1_output_state, state_helper_2_output_state, state_helper_3_output_state,
       state_helper_4_output_state, state_helper_5_output_state, state_helper_6_output_state,
       state_helper_7_output_state, state_helper_8_output_state, state_helper_9_output_state,
       state_helper_10_output_state, state_helper_11_output_state, state_helper_12_output_state,
       state_helper_13_output_state, state_helper_14_output_state, state_helper_15_output_state,
       state_helper_16_output_state, state_helper_17_output_state, state_helper_18_output_state,
       state_helper_19_output_state, state_helper_20_output_state, state_helper_21_output_state,
       state_helper_22_output_state, state_helper_23_output_state, state_helper_24_output_state,
       state_helper_25_output_state, state_helper_26_output_state, state_helper_27_output_state,
       state_helper_28_output_state, state_helper_29_output_state, state_helper_30_output_state,
       state_helper_31_output_state, state_helper_32_output_state;
  wire [24:0] lookAt, neighbours_1_neighbours, neighbours_2_neighbours, neighbours_3_neighbours,
       neighbours_4_neighbours, neighbours_5_neighbours, neighbours_6_neighbours, neighbours_7_neighbours,
       neighbours_8_neighbours, neighbours_9_neighbours, neighbours_10_neighbours, neighbours_11_neighbours,
       neighbours_12_neighbours, neighbours_13_neighbours, neighbours_14_neighbours,
       neighbours_15_neighbours, neighbours_16_neighbours, neighbours_17_neighbours,
       neighbours_18_neighbours, neighbours_19_neighbours, neighbours_20_neighbours,
       neighbours_21_neighbours, neighbours_22_neighbours, neighbours_23_neighbours,
       neighbours_24_neighbours, neighbours_25_neighbours, neighbours_26_neighbours,
       neighbours_27_neighbours, neighbours_28_neighbours, neighbours_29_neighbours,
       neighbours_30_neighbours, neighbours_31_neighbours, neighbours_32_neighbours;
  wire [29:0] birth, save;

  neighbours neighbours_1 (
    .minus_02_02(minus_02_02_t), .minus_02_01(minus_02_01_t), .minus_02_00(minus_2_line[0]),
    .minus_02_01_2(minus_2_line[1]), .minus_02_02_2(minus_2_line[2]), .minus_01_02(minus_01_02_t),
    .minus_01_01(minus_01_01_t), .minus_01_00(minus_1_line[0]), .minus_01_01_2(minus_1_line[1]),
    .minus_01_02_2(minus_1_line[2]), .plus_00_02(plus_00_02_t), .plus_00_01(plus_00_01_t),
    .plus_00_00(_0_line__out__1[0]), .neighbours(neighbours_1_neighbours), .plus_00_01_2(_0_line__out__1[1]),
    .plus_00_02_2(_0_line__out__1[2]), .plus_01_02(plus_01_02_t), .plus_01_01(plus_01_01_t),
    .plus_01_00(_1_line[0]), .plus_01_01_2(_1_line[1]), .plus_01_02_2(_1_line[2]), .plus_02_02(plus_02_02_t),
    .plus_02_01(plus_02_01_t), .plus_02_00(_2_line[0]), .plus_02_01_2(_2_line[1]), .plus_02_02_2(_2_line[2]));
  and and_1 (minus_02_32, minus_2_line[0], Torus);
  and and_2 (minus_02_33, minus_2_line[1], Torus);
  and and_3 (minus_02_01_t, minus_2_line[31], Torus);
  and and_4 (minus_02_02_t, minus_2_line[30], Torus);
  alive alive_1 (
    .neighbours(neighbours_1_neighbours), .look_at(lookAt), .B___birth(birth), .S___save(save),
    .alive(plus_00_00new), .pause(pause), .input_state(state_helper_1_output_state));
  STATE_helper state_helper_1 (.input_state(input_state), .output_state(state_helper_1_output_state), .i(I), .j(J[0]));
  and and_5 (minus_01_32, minus_1_line[0], Torus);
  and and_6 (minus_01_33, minus_1_line[1], Torus);
  and and_7 (minus_01_01_t, minus_1_line[31], Torus);
  and and_8 (minus_01_02_t, minus_1_line[30], Torus);
  neighbours neighbours_2 (
    .minus_02_02(minus_02_01_t), .minus_02_01(minus_2_line[0]), .minus_02_00(minus_2_line[1]),
    .minus_02_01_2(minus_2_line[2]), .minus_02_02_2(minus_2_line[3]), .minus_01_02(minus_01_01_t),
    .minus_01_01(minus_1_line[0]), .minus_01_00(minus_1_line[1]), .minus_01_01_2(minus_1_line[2]),
    .minus_01_02_2(minus_1_line[3]), .plus_00_02(plus_00_01_t), .plus_00_01(_0_line__out__1[0]),
    .plus_00_00(_0_line__out__1[1]), .neighbours(neighbours_2_neighbours), .plus_00_01_2(_0_line__out__1[2]),
    .plus_00_02_2(_0_line__out__1[3]), .plus_01_02(plus_01_01_t), .plus_01_01(_1_line[0]),
    .plus_01_00(_1_line[1]), .plus_01_01_2(_1_line[2]), .plus_01_02_2(_1_line[3]), .plus_02_02(plus_02_01_t),
    .plus_02_01(_2_line[0]), .plus_02_00(_2_line[1]), .plus_02_01_2(_2_line[2]), .plus_02_02_2(_2_line[3]));
  Register #(.width(32), .trigger("falling")) register_1 (
    .D({plus_00_31new, plus_00_30new, plus_00_29new, plus_00_28new, plus_00_27new, plus_00_26new, plus_00_25new, plus_00_24new, plus_00_23new, plus_00_22new, plus_00_21new, plus_00_20new, plus_00_19new, plus_00_18new, plus_00_17new, plus_00_16new, plus_00_15new, plus_00_14new, plus_00_13new, plus_00_12new, plus_00_11new, plus_00_10new, plus_00_09new, plus_00_08new, plus_00_07new, plus_00_06new, plus_00_05new, plus_00_04new, plus_00_03new, plus_00_02new, plus_00_01new, plus_00_00new}),
    .Q(_0_line__out__1), .clk(clock));  // open: en, clr
  alive alive_2 (
    .neighbours(neighbours_2_neighbours), .look_at(lookAt), .B___birth(birth), .S___save(save),
    .alive(plus_00_01new), .pause(pause), .input_state(state_helper_2_output_state));
  STATE_helper state_helper_2 (.input_state(input_state), .output_state(state_helper_2_output_state), .i(I), .j(J[1]));
  and and_9 (plus_01_32, _1_line[0], Torus);
  and and_10 (plus_01_33, _1_line[1], Torus);
  and and_11 (plus_01_01_t, _1_line[31], Torus);
  and and_12 (plus_01_02_t, _1_line[30], Torus);
  and and_13 (plus_02_32, _2_line[0], Torus);
  and and_14 (plus_02_33, _2_line[1], Torus);
  and and_15 (plus_02_01_t, _2_line[31], Torus);
  and and_16 (plus_02_02_t, _2_line[30], Torus);
  neighbours neighbours_3 (
    .minus_02_02(minus_2_line[0]), .minus_02_01(minus_2_line[1]), .minus_02_00(minus_2_line[2]),
    .minus_02_01_2(minus_2_line[3]), .minus_02_02_2(minus_2_line[4]), .minus_01_02(minus_1_line[0]),
    .minus_01_01(minus_1_line[1]), .minus_01_00(minus_1_line[2]), .minus_01_01_2(minus_1_line[3]),
    .minus_01_02_2(minus_1_line[4]), .plus_00_02(_0_line__out__1[0]), .plus_00_01(_0_line__out__1[1]),
    .plus_00_00(_0_line__out__1[2]), .neighbours(neighbours_3_neighbours), .plus_00_01_2(_0_line__out__1[3]),
    .plus_00_02_2(_0_line__out__1[4]), .plus_01_02(_1_line[0]), .plus_01_01(_1_line[1]),
    .plus_01_00(_1_line[2]), .plus_01_01_2(_1_line[3]), .plus_01_02_2(_1_line[4]), .plus_02_02(_2_line[0]),
    .plus_02_01(_2_line[1]), .plus_02_00(_2_line[2]), .plus_02_01_2(_2_line[3]), .plus_02_02_2(_2_line[4]));
  alive alive_3 (
    .neighbours(neighbours_3_neighbours), .look_at(lookAt), .B___birth(birth), .S___save(save),
    .alive(plus_00_02new), .pause(pause), .input_state(state_helper_3_output_state));
  STATE_helper state_helper_3 (.input_state(input_state), .output_state(state_helper_3_output_state), .i(I), .j(J[2]));
  and and_17 (plus_00_32, _0_line__out__1[0], Torus);
  and and_18 (plus_00_33, _0_line__out__1[1], Torus);
  and and_19 (plus_00_01_t, _0_line__out__1[31], Torus);
  and and_20 (plus_00_02_t, _0_line__out__1[30], Torus);
  neighbours neighbours_4 (
    .minus_02_02(minus_2_line[1]), .minus_02_01(minus_2_line[2]), .minus_02_00(minus_2_line[3]),
    .minus_02_01_2(minus_2_line[4]), .minus_02_02_2(minus_2_line[5]), .minus_01_02(minus_1_line[1]),
    .minus_01_01(minus_1_line[2]), .minus_01_00(minus_1_line[3]), .minus_01_01_2(minus_1_line[4]),
    .minus_01_02_2(minus_1_line[5]), .plus_00_02(_0_line__out__1[1]), .plus_00_01(_0_line__out__1[2]),
    .plus_00_00(_0_line__out__1[3]), .neighbours(neighbours_4_neighbours), .plus_00_01_2(_0_line__out__1[4]),
    .plus_00_02_2(_0_line__out__1[5]), .plus_01_02(_1_line[1]), .plus_01_01(_1_line[2]),
    .plus_01_00(_1_line[3]), .plus_01_01_2(_1_line[4]), .plus_01_02_2(_1_line[5]), .plus_02_02(_2_line[1]),
    .plus_02_01(_2_line[2]), .plus_02_00(_2_line[3]), .plus_02_01_2(_2_line[4]), .plus_02_02_2(_2_line[5]));
  alive alive_4 (
    .neighbours(neighbours_4_neighbours), .look_at(lookAt), .B___birth(birth), .S___save(save),
    .alive(plus_00_03new), .pause(pause), .input_state(state_helper_4_output_state));
  STATE_helper state_helper_4 (.input_state(input_state), .output_state(state_helper_4_output_state), .i(I), .j(J[3]));
  neighbours neighbours_5 (
    .minus_02_02(minus_2_line[2]), .minus_02_01(minus_2_line[3]), .minus_02_00(minus_2_line[4]),
    .minus_02_01_2(minus_2_line[5]), .minus_02_02_2(minus_2_line[6]), .minus_01_02(minus_1_line[2]),
    .minus_01_01(minus_1_line[3]), .minus_01_00(minus_1_line[4]), .minus_01_01_2(minus_1_line[5]),
    .minus_01_02_2(minus_1_line[6]), .plus_00_02(_0_line__out__1[2]), .plus_00_01(_0_line__out__1[3]),
    .plus_00_00(_0_line__out__1[4]), .neighbours(neighbours_5_neighbours), .plus_00_01_2(_0_line__out__1[5]),
    .plus_00_02_2(_0_line__out__1[6]), .plus_01_02(_1_line[2]), .plus_01_01(_1_line[3]),
    .plus_01_00(_1_line[4]), .plus_01_01_2(_1_line[5]), .plus_01_02_2(_1_line[6]), .plus_02_02(_2_line[2]),
    .plus_02_01(_2_line[3]), .plus_02_00(_2_line[4]), .plus_02_01_2(_2_line[5]), .plus_02_02_2(_2_line[6]));
  alive alive_5 (
    .neighbours(neighbours_5_neighbours), .look_at(lookAt), .B___birth(birth), .S___save(save),
    .alive(plus_00_04new), .pause(pause), .input_state(state_helper_5_output_state));
  STATE_helper state_helper_5 (.input_state(input_state), .output_state(state_helper_5_output_state), .i(I), .j(J[4]));
  neighbours neighbours_6 (
    .minus_02_02(minus_2_line[3]), .minus_02_01(minus_2_line[4]), .minus_02_00(minus_2_line[5]),
    .minus_02_01_2(minus_2_line[6]), .minus_02_02_2(minus_2_line[7]), .minus_01_02(minus_1_line[3]),
    .minus_01_01(minus_1_line[4]), .minus_01_00(minus_1_line[5]), .minus_01_01_2(minus_1_line[6]),
    .minus_01_02_2(minus_1_line[7]), .plus_00_02(_0_line__out__1[3]), .plus_00_01(_0_line__out__1[4]),
    .plus_00_00(_0_line__out__1[5]), .neighbours(neighbours_6_neighbours), .plus_00_01_2(_0_line__out__1[6]),
    .plus_00_02_2(_0_line__out__1[7]), .plus_01_02(_1_line[3]), .plus_01_01(_1_line[4]),
    .plus_01_00(_1_line[5]), .plus_01_01_2(_1_line[6]), .plus_01_02_2(_1_line[7]), .plus_02_02(_2_line[3]),
    .plus_02_01(_2_line[4]), .plus_02_00(_2_line[5]), .plus_02_01_2(_2_line[6]), .plus_02_02_2(_2_line[7]));
  alive alive_6 (
    .neighbours(neighbours_6_neighbours), .look_at(lookAt), .B___birth(birth), .S___save(save),
    .alive(plus_00_05new), .pause(pause), .input_state(state_helper_6_output_state));
  STATE_helper state_helper_6 (.input_state(input_state), .output_state(state_helper_6_output_state), .i(I), .j(J[5]));
  neighbours neighbours_7 (
    .minus_02_02(minus_2_line[4]), .minus_02_01(minus_2_line[5]), .minus_02_00(minus_2_line[6]),
    .minus_02_01_2(minus_2_line[7]), .minus_02_02_2(minus_2_line[8]), .minus_01_02(minus_1_line[4]),
    .minus_01_01(minus_1_line[5]), .minus_01_00(minus_1_line[6]), .minus_01_01_2(minus_1_line[7]),
    .minus_01_02_2(minus_1_line[8]), .plus_00_02(_0_line__out__1[4]), .plus_00_01(_0_line__out__1[5]),
    .plus_00_00(_0_line__out__1[6]), .neighbours(neighbours_7_neighbours), .plus_00_01_2(_0_line__out__1[7]),
    .plus_00_02_2(_0_line__out__1[8]), .plus_01_02(_1_line[4]), .plus_01_01(_1_line[5]),
    .plus_01_00(_1_line[6]), .plus_01_01_2(_1_line[7]), .plus_01_02_2(_1_line[8]), .plus_02_02(_2_line[4]),
    .plus_02_01(_2_line[5]), .plus_02_00(_2_line[6]), .plus_02_01_2(_2_line[7]), .plus_02_02_2(_2_line[8]));
  alive alive_7 (
    .neighbours(neighbours_7_neighbours), .look_at(lookAt), .B___birth(birth), .S___save(save),
    .alive(plus_00_06new), .pause(pause), .input_state(state_helper_7_output_state));
  STATE_helper state_helper_7 (.input_state(input_state), .output_state(state_helper_7_output_state), .i(I), .j(J[6]));
  neighbours neighbours_8 (
    .minus_02_02(minus_2_line[5]), .minus_02_01(minus_2_line[6]), .minus_02_00(minus_2_line[7]),
    .minus_02_01_2(minus_2_line[8]), .minus_02_02_2(minus_2_line[9]), .minus_01_02(minus_1_line[5]),
    .minus_01_01(minus_1_line[6]), .minus_01_00(minus_1_line[7]), .minus_01_01_2(minus_1_line[8]),
    .minus_01_02_2(minus_1_line[9]), .plus_00_02(_0_line__out__1[5]), .plus_00_01(_0_line__out__1[6]),
    .plus_00_00(_0_line__out__1[7]), .neighbours(neighbours_8_neighbours), .plus_00_01_2(_0_line__out__1[8]),
    .plus_00_02_2(_0_line__out__1[9]), .plus_01_02(_1_line[5]), .plus_01_01(_1_line[6]),
    .plus_01_00(_1_line[7]), .plus_01_01_2(_1_line[8]), .plus_01_02_2(_1_line[9]), .plus_02_02(_2_line[5]),
    .plus_02_01(_2_line[6]), .plus_02_00(_2_line[7]), .plus_02_01_2(_2_line[8]), .plus_02_02_2(_2_line[9]));
  alive alive_8 (
    .neighbours(neighbours_8_neighbours), .look_at(lookAt), .B___birth(birth), .S___save(save),
    .alive(plus_00_07new), .pause(pause), .input_state(state_helper_8_output_state));
  STATE_helper state_helper_8 (.input_state(input_state), .output_state(state_helper_8_output_state), .i(I), .j(J[7]));
  neighbours neighbours_9 (
    .minus_02_02(minus_2_line[6]), .minus_02_01(minus_2_line[7]), .minus_02_00(minus_2_line[8]),
    .minus_02_01_2(minus_2_line[9]), .minus_02_02_2(minus_2_line[10]), .minus_01_02(minus_1_line[6]),
    .minus_01_01(minus_1_line[7]), .minus_01_00(minus_1_line[8]), .minus_01_01_2(minus_1_line[9]),
    .minus_01_02_2(minus_1_line[10]), .plus_00_02(_0_line__out__1[6]), .plus_00_01(_0_line__out__1[7]),
    .plus_00_00(_0_line__out__1[8]), .neighbours(neighbours_9_neighbours), .plus_00_01_2(_0_line__out__1[9]),
    .plus_00_02_2(_0_line__out__1[10]), .plus_01_02(_1_line[6]), .plus_01_01(_1_line[7]),
    .plus_01_00(_1_line[8]), .plus_01_01_2(_1_line[9]), .plus_01_02_2(_1_line[10]), .plus_02_02(_2_line[6]),
    .plus_02_01(_2_line[7]), .plus_02_00(_2_line[8]), .plus_02_01_2(_2_line[9]), .plus_02_02_2(_2_line[10]));
  alive alive_9 (
    .neighbours(neighbours_9_neighbours), .look_at(lookAt), .B___birth(birth), .S___save(save),
    .alive(plus_00_08new), .pause(pause), .input_state(state_helper_9_output_state));
  STATE_helper state_helper_9 (.input_state(input_state), .output_state(state_helper_9_output_state), .i(I), .j(J[8]));
  neighbours neighbours_10 (
    .minus_02_02(minus_2_line[7]), .minus_02_01(minus_2_line[8]), .minus_02_00(minus_2_line[9]),
    .minus_02_01_2(minus_2_line[10]), .minus_02_02_2(minus_2_line[11]), .minus_01_02(minus_1_line[7]),
    .minus_01_01(minus_1_line[8]), .minus_01_00(minus_1_line[9]), .minus_01_01_2(minus_1_line[10]),
    .minus_01_02_2(minus_1_line[11]), .plus_00_02(_0_line__out__1[7]), .plus_00_01(_0_line__out__1[8]),
    .plus_00_00(_0_line__out__1[9]), .neighbours(neighbours_10_neighbours),
    .plus_00_01_2(_0_line__out__1[10]), .plus_00_02_2(_0_line__out__1[11]), .plus_01_02(_1_line[7]),
    .plus_01_01(_1_line[8]), .plus_01_00(_1_line[9]), .plus_01_01_2(_1_line[10]), .plus_01_02_2(_1_line[11]),
    .plus_02_02(_2_line[7]), .plus_02_01(_2_line[8]), .plus_02_00(_2_line[9]), .plus_02_01_2(_2_line[10]),
    .plus_02_02_2(_2_line[11]));
  alive alive_10 (
    .neighbours(neighbours_10_neighbours), .look_at(lookAt), .B___birth(birth), .S___save(save),
    .alive(plus_00_09new), .pause(pause), .input_state(state_helper_10_output_state));
  STATE_helper state_helper_10 (
    .input_state(input_state), .output_state(state_helper_10_output_state), .i(I), .j(J[9]));
  neighbours neighbours_11 (
    .minus_02_02(minus_2_line[8]), .minus_02_01(minus_2_line[9]), .minus_02_00(minus_2_line[10]),
    .minus_02_01_2(minus_2_line[11]), .minus_02_02_2(minus_2_line[12]), .minus_01_02(minus_1_line[8]),
    .minus_01_01(minus_1_line[9]), .minus_01_00(minus_1_line[10]), .minus_01_01_2(minus_1_line[11]),
    .minus_01_02_2(minus_1_line[12]), .plus_00_02(_0_line__out__1[8]), .plus_00_01(_0_line__out__1[9]),
    .plus_00_00(_0_line__out__1[10]), .neighbours(neighbours_11_neighbours),
    .plus_00_01_2(_0_line__out__1[11]), .plus_00_02_2(_0_line__out__1[12]), .plus_01_02(_1_line[8]),
    .plus_01_01(_1_line[9]), .plus_01_00(_1_line[10]), .plus_01_01_2(_1_line[11]),
    .plus_01_02_2(_1_line[12]), .plus_02_02(_2_line[8]), .plus_02_01(_2_line[9]), .plus_02_00(_2_line[10]),
    .plus_02_01_2(_2_line[11]), .plus_02_02_2(_2_line[12]));
  alive alive_11 (
    .neighbours(neighbours_11_neighbours), .look_at(lookAt), .B___birth(birth), .S___save(save),
    .alive(plus_00_10new), .pause(pause), .input_state(state_helper_11_output_state));
  STATE_helper state_helper_11 (
    .input_state(input_state), .output_state(state_helper_11_output_state), .i(I), .j(J[10]));
  neighbours neighbours_12 (
    .minus_02_02(minus_2_line[9]), .minus_02_01(minus_2_line[10]), .minus_02_00(minus_2_line[11]),
    .minus_02_01_2(minus_2_line[12]), .minus_02_02_2(minus_2_line[13]), .minus_01_02(minus_1_line[9]),
    .minus_01_01(minus_1_line[10]), .minus_01_00(minus_1_line[11]), .minus_01_01_2(minus_1_line[12]),
    .minus_01_02_2(minus_1_line[13]), .plus_00_02(_0_line__out__1[9]), .plus_00_01(_0_line__out__1[10]),
    .plus_00_00(_0_line__out__1[11]), .neighbours(neighbours_12_neighbours),
    .plus_00_01_2(_0_line__out__1[12]), .plus_00_02_2(_0_line__out__1[13]), .plus_01_02(_1_line[9]),
    .plus_01_01(_1_line[10]), .plus_01_00(_1_line[11]), .plus_01_01_2(_1_line[12]),
    .plus_01_02_2(_1_line[13]), .plus_02_02(_2_line[9]), .plus_02_01(_2_line[10]), .plus_02_00(_2_line[11]),
    .plus_02_01_2(_2_line[12]), .plus_02_02_2(_2_line[13]));
  alive alive_12 (
    .neighbours(neighbours_12_neighbours), .look_at(lookAt), .B___birth(birth), .S___save(save),
    .alive(plus_00_11new), .pause(pause), .input_state(state_helper_12_output_state));
  STATE_helper state_helper_12 (
    .input_state(input_state), .output_state(state_helper_12_output_state), .i(I), .j(J[11]));
  neighbours neighbours_13 (
    .minus_02_02(minus_2_line[10]), .minus_02_01(minus_2_line[11]), .minus_02_00(minus_2_line[12]),
    .minus_02_01_2(minus_2_line[13]), .minus_02_02_2(minus_2_line[14]), .minus_01_02(minus_1_line[10]),
    .minus_01_01(minus_1_line[11]), .minus_01_00(minus_1_line[12]), .minus_01_01_2(minus_1_line[13]),
    .minus_01_02_2(minus_1_line[14]), .plus_00_02(_0_line__out__1[10]), .plus_00_01(_0_line__out__1[11]),
    .plus_00_00(_0_line__out__1[12]), .neighbours(neighbours_13_neighbours),
    .plus_00_01_2(_0_line__out__1[13]), .plus_00_02_2(_0_line__out__1[14]), .plus_01_02(_1_line[10]),
    .plus_01_01(_1_line[11]), .plus_01_00(_1_line[12]), .plus_01_01_2(_1_line[13]),
    .plus_01_02_2(_1_line[14]), .plus_02_02(_2_line[10]), .plus_02_01(_2_line[11]), .plus_02_00(_2_line[12]),
    .plus_02_01_2(_2_line[13]), .plus_02_02_2(_2_line[14]));
  alive alive_13 (
    .neighbours(neighbours_13_neighbours), .look_at(lookAt), .B___birth(birth), .S___save(save),
    .alive(plus_00_12new), .pause(pause), .input_state(state_helper_13_output_state));
  STATE_helper state_helper_13 (
    .input_state(input_state), .output_state(state_helper_13_output_state), .i(I), .j(J[12]));
  neighbours neighbours_14 (
    .minus_02_02(minus_2_line[11]), .minus_02_01(minus_2_line[12]), .minus_02_00(minus_2_line[13]),
    .minus_02_01_2(minus_2_line[14]), .minus_02_02_2(minus_2_line[15]), .minus_01_02(minus_1_line[11]),
    .minus_01_01(minus_1_line[12]), .minus_01_00(minus_1_line[13]), .minus_01_01_2(minus_1_line[14]),
    .minus_01_02_2(minus_1_line[15]), .plus_00_02(_0_line__out__1[11]), .plus_00_01(_0_line__out__1[12]),
    .plus_00_00(_0_line__out__1[13]), .neighbours(neighbours_14_neighbours),
    .plus_00_01_2(_0_line__out__1[14]), .plus_00_02_2(_0_line__out__1[15]), .plus_01_02(_1_line[11]),
    .plus_01_01(_1_line[12]), .plus_01_00(_1_line[13]), .plus_01_01_2(_1_line[14]),
    .plus_01_02_2(_1_line[15]), .plus_02_02(_2_line[11]), .plus_02_01(_2_line[12]), .plus_02_00(_2_line[13]),
    .plus_02_01_2(_2_line[14]), .plus_02_02_2(_2_line[15]));
  alive alive_14 (
    .neighbours(neighbours_14_neighbours), .look_at(lookAt), .B___birth(birth), .S___save(save),
    .alive(plus_00_13new), .pause(pause), .input_state(state_helper_14_output_state));
  STATE_helper state_helper_14 (
    .input_state(input_state), .output_state(state_helper_14_output_state), .i(I), .j(J[13]));
  neighbours neighbours_15 (
    .minus_02_02(minus_2_line[12]), .minus_02_01(minus_2_line[13]), .minus_02_00(minus_2_line[14]),
    .minus_02_01_2(minus_2_line[15]), .minus_02_02_2(minus_2_line[16]), .minus_01_02(minus_1_line[12]),
    .minus_01_01(minus_1_line[13]), .minus_01_00(minus_1_line[14]), .minus_01_01_2(minus_1_line[15]),
    .minus_01_02_2(minus_1_line[16]), .plus_00_02(_0_line__out__1[12]), .plus_00_01(_0_line__out__1[13]),
    .plus_00_00(_0_line__out__1[14]), .neighbours(neighbours_15_neighbours),
    .plus_00_01_2(_0_line__out__1[15]), .plus_00_02_2(_0_line__out__1[16]), .plus_01_02(_1_line[12]),
    .plus_01_01(_1_line[13]), .plus_01_00(_1_line[14]), .plus_01_01_2(_1_line[15]),
    .plus_01_02_2(_1_line[16]), .plus_02_02(_2_line[12]), .plus_02_01(_2_line[13]), .plus_02_00(_2_line[14]),
    .plus_02_01_2(_2_line[15]), .plus_02_02_2(_2_line[16]));
  alive alive_15 (
    .neighbours(neighbours_15_neighbours), .look_at(lookAt), .B___birth(birth), .S___save(save),
    .alive(plus_00_14new), .pause(pause), .input_state(state_helper_15_output_state));
  STATE_helper state_helper_15 (
    .input_state(input_state), .output_state(state_helper_15_output_state), .i(I), .j(J[14]));
  neighbours neighbours_16 (
    .minus_02_02(minus_2_line[13]), .minus_02_01(minus_2_line[14]), .minus_02_00(minus_2_line[15]),
    .minus_02_01_2(minus_2_line[16]), .minus_02_02_2(minus_2_line[17]), .minus_01_02(minus_1_line[13]),
    .minus_01_01(minus_1_line[14]), .minus_01_00(minus_1_line[15]), .minus_01_01_2(minus_1_line[16]),
    .minus_01_02_2(minus_1_line[17]), .plus_00_02(_0_line__out__1[13]), .plus_00_01(_0_line__out__1[14]),
    .plus_00_00(_0_line__out__1[15]), .neighbours(neighbours_16_neighbours),
    .plus_00_01_2(_0_line__out__1[16]), .plus_00_02_2(_0_line__out__1[17]), .plus_01_02(_1_line[13]),
    .plus_01_01(_1_line[14]), .plus_01_00(_1_line[15]), .plus_01_01_2(_1_line[16]),
    .plus_01_02_2(_1_line[17]), .plus_02_02(_2_line[13]), .plus_02_01(_2_line[14]), .plus_02_00(_2_line[15]),
    .plus_02_01_2(_2_line[16]), .plus_02_02_2(_2_line[17]));
  alive alive_16 (
    .neighbours(neighbours_16_neighbours), .look_at(lookAt), .B___birth(birth), .S___save(save),
    .alive(plus_00_15new), .pause(pause), .input_state(state_helper_16_output_state));
  STATE_helper state_helper_16 (
    .input_state(input_state), .output_state(state_helper_16_output_state), .i(I), .j(J[15]));
  neighbours neighbours_17 (
    .minus_02_02(minus_2_line[14]), .minus_02_01(minus_2_line[15]), .minus_02_00(minus_2_line[16]),
    .minus_02_01_2(minus_2_line[17]), .minus_02_02_2(minus_2_line[18]), .minus_01_02(minus_1_line[14]),
    .minus_01_01(minus_1_line[15]), .minus_01_00(minus_1_line[16]), .minus_01_01_2(minus_1_line[17]),
    .minus_01_02_2(minus_1_line[18]), .plus_00_02(_0_line__out__1[14]), .plus_00_01(_0_line__out__1[15]),
    .plus_00_00(_0_line__out__1[16]), .neighbours(neighbours_17_neighbours),
    .plus_00_01_2(_0_line__out__1[17]), .plus_00_02_2(_0_line__out__1[18]), .plus_01_02(_1_line[14]),
    .plus_01_01(_1_line[15]), .plus_01_00(_1_line[16]), .plus_01_01_2(_1_line[17]),
    .plus_01_02_2(_1_line[18]), .plus_02_02(_2_line[14]), .plus_02_01(_2_line[15]), .plus_02_00(_2_line[16]),
    .plus_02_01_2(_2_line[17]), .plus_02_02_2(_2_line[18]));
  alive alive_17 (
    .neighbours(neighbours_17_neighbours), .look_at(lookAt), .B___birth(birth), .S___save(save),
    .alive(plus_00_16new), .pause(pause), .input_state(state_helper_17_output_state));
  STATE_helper state_helper_17 (
    .input_state(input_state), .output_state(state_helper_17_output_state), .i(I), .j(J[16]));
  neighbours neighbours_18 (
    .minus_02_02(minus_2_line[15]), .minus_02_01(minus_2_line[16]), .minus_02_00(minus_2_line[17]),
    .minus_02_01_2(minus_2_line[18]), .minus_02_02_2(minus_2_line[19]), .minus_01_02(minus_1_line[15]),
    .minus_01_01(minus_1_line[16]), .minus_01_00(minus_1_line[17]), .minus_01_01_2(minus_1_line[18]),
    .minus_01_02_2(minus_1_line[19]), .plus_00_02(_0_line__out__1[15]), .plus_00_01(_0_line__out__1[16]),
    .plus_00_00(_0_line__out__1[17]), .neighbours(neighbours_18_neighbours),
    .plus_00_01_2(_0_line__out__1[18]), .plus_00_02_2(_0_line__out__1[19]), .plus_01_02(_1_line[15]),
    .plus_01_01(_1_line[16]), .plus_01_00(_1_line[17]), .plus_01_01_2(_1_line[18]),
    .plus_01_02_2(_1_line[19]), .plus_02_02(_2_line[15]), .plus_02_01(_2_line[16]), .plus_02_00(_2_line[17]),
    .plus_02_01_2(_2_line[18]), .plus_02_02_2(_2_line[19]));
  alive alive_18 (
    .neighbours(neighbours_18_neighbours), .look_at(lookAt), .B___birth(birth), .S___save(save),
    .alive(plus_00_17new), .pause(pause), .input_state(state_helper_18_output_state));
  STATE_helper state_helper_18 (
    .input_state(input_state), .output_state(state_helper_18_output_state), .i(I), .j(J[17]));
  neighbours neighbours_19 (
    .minus_02_02(minus_2_line[16]), .minus_02_01(minus_2_line[17]), .minus_02_00(minus_2_line[18]),
    .minus_02_01_2(minus_2_line[19]), .minus_02_02_2(minus_2_line[20]), .minus_01_02(minus_1_line[16]),
    .minus_01_01(minus_1_line[17]), .minus_01_00(minus_1_line[18]), .minus_01_01_2(minus_1_line[19]),
    .minus_01_02_2(minus_1_line[20]), .plus_00_02(_0_line__out__1[16]), .plus_00_01(_0_line__out__1[17]),
    .plus_00_00(_0_line__out__1[18]), .neighbours(neighbours_19_neighbours),
    .plus_00_01_2(_0_line__out__1[19]), .plus_00_02_2(_0_line__out__1[20]), .plus_01_02(_1_line[16]),
    .plus_01_01(_1_line[17]), .plus_01_00(_1_line[18]), .plus_01_01_2(_1_line[19]),
    .plus_01_02_2(_1_line[20]), .plus_02_02(_2_line[16]), .plus_02_01(_2_line[17]), .plus_02_00(_2_line[18]),
    .plus_02_01_2(_2_line[19]), .plus_02_02_2(_2_line[20]));
  alive alive_19 (
    .neighbours(neighbours_19_neighbours), .look_at(lookAt), .B___birth(birth), .S___save(save),
    .alive(plus_00_18new), .pause(pause), .input_state(state_helper_19_output_state));
  STATE_helper state_helper_19 (
    .input_state(input_state), .output_state(state_helper_19_output_state), .i(I), .j(J[18]));
  neighbours neighbours_20 (
    .minus_02_02(minus_2_line[17]), .minus_02_01(minus_2_line[18]), .minus_02_00(minus_2_line[19]),
    .minus_02_01_2(minus_2_line[20]), .minus_02_02_2(minus_2_line[21]), .minus_01_02(minus_1_line[17]),
    .minus_01_01(minus_1_line[18]), .minus_01_00(minus_1_line[19]), .minus_01_01_2(minus_1_line[20]),
    .minus_01_02_2(minus_1_line[21]), .plus_00_02(_0_line__out__1[17]), .plus_00_01(_0_line__out__1[18]),
    .plus_00_00(_0_line__out__1[19]), .neighbours(neighbours_20_neighbours),
    .plus_00_01_2(_0_line__out__1[20]), .plus_00_02_2(_0_line__out__1[21]), .plus_01_02(_1_line[17]),
    .plus_01_01(_1_line[18]), .plus_01_00(_1_line[19]), .plus_01_01_2(_1_line[20]),
    .plus_01_02_2(_1_line[21]), .plus_02_02(_2_line[17]), .plus_02_01(_2_line[18]), .plus_02_00(_2_line[19]),
    .plus_02_01_2(_2_line[20]), .plus_02_02_2(_2_line[21]));
  alive alive_20 (
    .neighbours(neighbours_20_neighbours), .look_at(lookAt), .B___birth(birth), .S___save(save),
    .alive(plus_00_19new), .pause(pause), .input_state(state_helper_20_output_state));
  STATE_helper state_helper_20 (
    .input_state(input_state), .output_state(state_helper_20_output_state), .i(I), .j(J[19]));
  neighbours neighbours_21 (
    .minus_02_02(minus_2_line[18]), .minus_02_01(minus_2_line[19]), .minus_02_00(minus_2_line[20]),
    .minus_02_01_2(minus_2_line[21]), .minus_02_02_2(minus_2_line[22]), .minus_01_02(minus_1_line[18]),
    .minus_01_01(minus_1_line[19]), .minus_01_00(minus_1_line[20]), .minus_01_01_2(minus_1_line[21]),
    .minus_01_02_2(minus_1_line[22]), .plus_00_02(_0_line__out__1[18]), .plus_00_01(_0_line__out__1[19]),
    .plus_00_00(_0_line__out__1[20]), .neighbours(neighbours_21_neighbours),
    .plus_00_01_2(_0_line__out__1[21]), .plus_00_02_2(_0_line__out__1[22]), .plus_01_02(_1_line[18]),
    .plus_01_01(_1_line[19]), .plus_01_00(_1_line[20]), .plus_01_01_2(_1_line[21]),
    .plus_01_02_2(_1_line[22]), .plus_02_02(_2_line[18]), .plus_02_01(_2_line[19]), .plus_02_00(_2_line[20]),
    .plus_02_01_2(_2_line[21]), .plus_02_02_2(_2_line[22]));
  alive alive_21 (
    .neighbours(neighbours_21_neighbours), .look_at(lookAt), .B___birth(birth), .S___save(save),
    .alive(plus_00_20new), .pause(pause), .input_state(state_helper_21_output_state));
  STATE_helper state_helper_21 (
    .input_state(input_state), .output_state(state_helper_21_output_state), .i(I), .j(J[20]));
  neighbours neighbours_22 (
    .minus_02_02(minus_2_line[19]), .minus_02_01(minus_2_line[20]), .minus_02_00(minus_2_line[21]),
    .minus_02_01_2(minus_2_line[22]), .minus_02_02_2(minus_2_line[23]), .minus_01_02(minus_1_line[19]),
    .minus_01_01(minus_1_line[20]), .minus_01_00(minus_1_line[21]), .minus_01_01_2(minus_1_line[22]),
    .minus_01_02_2(minus_1_line[23]), .plus_00_02(_0_line__out__1[19]), .plus_00_01(_0_line__out__1[20]),
    .plus_00_00(_0_line__out__1[21]), .neighbours(neighbours_22_neighbours),
    .plus_00_01_2(_0_line__out__1[22]), .plus_00_02_2(_0_line__out__1[23]), .plus_01_02(_1_line[19]),
    .plus_01_01(_1_line[20]), .plus_01_00(_1_line[21]), .plus_01_01_2(_1_line[22]),
    .plus_01_02_2(_1_line[23]), .plus_02_02(_2_line[19]), .plus_02_01(_2_line[20]), .plus_02_00(_2_line[21]),
    .plus_02_01_2(_2_line[22]), .plus_02_02_2(_2_line[23]));
  alive alive_22 (
    .neighbours(neighbours_22_neighbours), .look_at(lookAt), .B___birth(birth), .S___save(save),
    .alive(plus_00_21new), .pause(pause), .input_state(state_helper_22_output_state));
  STATE_helper state_helper_22 (
    .input_state(input_state), .output_state(state_helper_22_output_state), .i(I), .j(J[21]));
  neighbours neighbours_23 (
    .minus_02_02(minus_2_line[20]), .minus_02_01(minus_2_line[21]), .minus_02_00(minus_2_line[22]),
    .minus_02_01_2(minus_2_line[23]), .minus_02_02_2(minus_2_line[24]), .minus_01_02(minus_1_line[20]),
    .minus_01_01(minus_1_line[21]), .minus_01_00(minus_1_line[22]), .minus_01_01_2(minus_1_line[23]),
    .minus_01_02_2(minus_1_line[24]), .plus_00_02(_0_line__out__1[20]), .plus_00_01(_0_line__out__1[21]),
    .plus_00_00(_0_line__out__1[22]), .neighbours(neighbours_23_neighbours),
    .plus_00_01_2(_0_line__out__1[23]), .plus_00_02_2(_0_line__out__1[24]), .plus_01_02(_1_line[20]),
    .plus_01_01(_1_line[21]), .plus_01_00(_1_line[22]), .plus_01_01_2(_1_line[23]),
    .plus_01_02_2(_1_line[24]), .plus_02_02(_2_line[20]), .plus_02_01(_2_line[21]), .plus_02_00(_2_line[22]),
    .plus_02_01_2(_2_line[23]), .plus_02_02_2(_2_line[24]));
  alive alive_23 (
    .neighbours(neighbours_23_neighbours), .look_at(lookAt), .B___birth(birth), .S___save(save),
    .alive(plus_00_22new), .pause(pause), .input_state(state_helper_23_output_state));
  STATE_helper state_helper_23 (
    .input_state(input_state), .output_state(state_helper_23_output_state), .i(I), .j(J[22]));
  neighbours neighbours_24 (
    .minus_02_02(minus_2_line[21]), .minus_02_01(minus_2_line[22]), .minus_02_00(minus_2_line[23]),
    .minus_02_01_2(minus_2_line[24]), .minus_02_02_2(minus_2_line[25]), .minus_01_02(minus_1_line[21]),
    .minus_01_01(minus_1_line[22]), .minus_01_00(minus_1_line[23]), .minus_01_01_2(minus_1_line[24]),
    .minus_01_02_2(minus_1_line[25]), .plus_00_02(_0_line__out__1[21]), .plus_00_01(_0_line__out__1[22]),
    .plus_00_00(_0_line__out__1[23]), .neighbours(neighbours_24_neighbours),
    .plus_00_01_2(_0_line__out__1[24]), .plus_00_02_2(_0_line__out__1[25]), .plus_01_02(_1_line[21]),
    .plus_01_01(_1_line[22]), .plus_01_00(_1_line[23]), .plus_01_01_2(_1_line[24]),
    .plus_01_02_2(_1_line[25]), .plus_02_02(_2_line[21]), .plus_02_01(_2_line[22]), .plus_02_00(_2_line[23]),
    .plus_02_01_2(_2_line[24]), .plus_02_02_2(_2_line[25]));
  alive alive_24 (
    .neighbours(neighbours_24_neighbours), .look_at(lookAt), .B___birth(birth), .S___save(save),
    .alive(plus_00_23new), .pause(pause), .input_state(state_helper_24_output_state));
  STATE_helper state_helper_24 (
    .input_state(input_state), .output_state(state_helper_24_output_state), .i(I), .j(J[23]));
  neighbours neighbours_25 (
    .minus_02_02(minus_2_line[22]), .minus_02_01(minus_2_line[23]), .minus_02_00(minus_2_line[24]),
    .minus_02_01_2(minus_2_line[25]), .minus_02_02_2(minus_2_line[26]), .minus_01_02(minus_1_line[22]),
    .minus_01_01(minus_1_line[23]), .minus_01_00(minus_1_line[24]), .minus_01_01_2(minus_1_line[25]),
    .minus_01_02_2(minus_1_line[26]), .plus_00_02(_0_line__out__1[22]), .plus_00_01(_0_line__out__1[23]),
    .plus_00_00(_0_line__out__1[24]), .neighbours(neighbours_25_neighbours),
    .plus_00_01_2(_0_line__out__1[25]), .plus_00_02_2(_0_line__out__1[26]), .plus_01_02(_1_line[22]),
    .plus_01_01(_1_line[23]), .plus_01_00(_1_line[24]), .plus_01_01_2(_1_line[25]),
    .plus_01_02_2(_1_line[26]), .plus_02_02(_2_line[22]), .plus_02_01(_2_line[23]), .plus_02_00(_2_line[24]),
    .plus_02_01_2(_2_line[25]), .plus_02_02_2(_2_line[26]));
  alive alive_25 (
    .neighbours(neighbours_25_neighbours), .look_at(lookAt), .B___birth(birth), .S___save(save),
    .alive(plus_00_24new), .pause(pause), .input_state(state_helper_25_output_state));
  STATE_helper state_helper_25 (
    .input_state(input_state), .output_state(state_helper_25_output_state), .i(I), .j(J[24]));
  neighbours neighbours_26 (
    .minus_02_02(minus_2_line[23]), .minus_02_01(minus_2_line[24]), .minus_02_00(minus_2_line[25]),
    .minus_02_01_2(minus_2_line[26]), .minus_02_02_2(minus_2_line[27]), .minus_01_02(minus_1_line[23]),
    .minus_01_01(minus_1_line[24]), .minus_01_00(minus_1_line[25]), .minus_01_01_2(minus_1_line[26]),
    .minus_01_02_2(minus_1_line[27]), .plus_00_02(_0_line__out__1[23]), .plus_00_01(_0_line__out__1[24]),
    .plus_00_00(_0_line__out__1[25]), .neighbours(neighbours_26_neighbours),
    .plus_00_01_2(_0_line__out__1[26]), .plus_00_02_2(_0_line__out__1[27]), .plus_01_02(_1_line[23]),
    .plus_01_01(_1_line[24]), .plus_01_00(_1_line[25]), .plus_01_01_2(_1_line[26]),
    .plus_01_02_2(_1_line[27]), .plus_02_02(_2_line[23]), .plus_02_01(_2_line[24]), .plus_02_00(_2_line[25]),
    .plus_02_01_2(_2_line[26]), .plus_02_02_2(_2_line[27]));
  alive alive_26 (
    .neighbours(neighbours_26_neighbours), .look_at(lookAt), .B___birth(birth), .S___save(save),
    .alive(plus_00_25new), .pause(pause), .input_state(state_helper_26_output_state));
  STATE_helper state_helper_26 (
    .input_state(input_state), .output_state(state_helper_26_output_state), .i(I), .j(J[25]));
  neighbours neighbours_27 (
    .minus_02_02(minus_2_line[24]), .minus_02_01(minus_2_line[25]), .minus_02_00(minus_2_line[26]),
    .minus_02_01_2(minus_2_line[27]), .minus_02_02_2(minus_2_line[28]), .minus_01_02(minus_1_line[24]),
    .minus_01_01(minus_1_line[25]), .minus_01_00(minus_1_line[26]), .minus_01_01_2(minus_1_line[27]),
    .minus_01_02_2(minus_1_line[28]), .plus_00_02(_0_line__out__1[24]), .plus_00_01(_0_line__out__1[25]),
    .plus_00_00(_0_line__out__1[26]), .neighbours(neighbours_27_neighbours),
    .plus_00_01_2(_0_line__out__1[27]), .plus_00_02_2(_0_line__out__1[28]), .plus_01_02(_1_line[24]),
    .plus_01_01(_1_line[25]), .plus_01_00(_1_line[26]), .plus_01_01_2(_1_line[27]),
    .plus_01_02_2(_1_line[28]), .plus_02_02(_2_line[24]), .plus_02_01(_2_line[25]), .plus_02_00(_2_line[26]),
    .plus_02_01_2(_2_line[27]), .plus_02_02_2(_2_line[28]));
  alive alive_27 (
    .neighbours(neighbours_27_neighbours), .look_at(lookAt), .B___birth(birth), .S___save(save),
    .alive(plus_00_26new), .pause(pause), .input_state(state_helper_27_output_state));
  STATE_helper state_helper_27 (
    .input_state(input_state), .output_state(state_helper_27_output_state), .i(I), .j(J[26]));
  neighbours neighbours_28 (
    .minus_02_02(minus_2_line[25]), .minus_02_01(minus_2_line[26]), .minus_02_00(minus_2_line[27]),
    .minus_02_01_2(minus_2_line[28]), .minus_02_02_2(minus_2_line[29]), .minus_01_02(minus_1_line[25]),
    .minus_01_01(minus_1_line[26]), .minus_01_00(minus_1_line[27]), .minus_01_01_2(minus_1_line[28]),
    .minus_01_02_2(minus_1_line[29]), .plus_00_02(_0_line__out__1[25]), .plus_00_01(_0_line__out__1[26]),
    .plus_00_00(_0_line__out__1[27]), .neighbours(neighbours_28_neighbours),
    .plus_00_01_2(_0_line__out__1[28]), .plus_00_02_2(_0_line__out__1[29]), .plus_01_02(_1_line[25]),
    .plus_01_01(_1_line[26]), .plus_01_00(_1_line[27]), .plus_01_01_2(_1_line[28]),
    .plus_01_02_2(_1_line[29]), .plus_02_02(_2_line[25]), .plus_02_01(_2_line[26]), .plus_02_00(_2_line[27]),
    .plus_02_01_2(_2_line[28]), .plus_02_02_2(_2_line[29]));
  alive alive_28 (
    .neighbours(neighbours_28_neighbours), .look_at(lookAt), .B___birth(birth), .S___save(save),
    .alive(plus_00_27new), .pause(pause), .input_state(state_helper_28_output_state));
  STATE_helper state_helper_28 (
    .input_state(input_state), .output_state(state_helper_28_output_state), .i(I), .j(J[27]));
  neighbours neighbours_29 (
    .minus_02_02(minus_2_line[26]), .minus_02_01(minus_2_line[27]), .minus_02_00(minus_2_line[28]),
    .minus_02_01_2(minus_2_line[29]), .minus_02_02_2(minus_2_line[30]), .minus_01_02(minus_1_line[26]),
    .minus_01_01(minus_1_line[27]), .minus_01_00(minus_1_line[28]), .minus_01_01_2(minus_1_line[29]),
    .minus_01_02_2(minus_1_line[30]), .plus_00_02(_0_line__out__1[26]), .plus_00_01(_0_line__out__1[27]),
    .plus_00_00(_0_line__out__1[28]), .neighbours(neighbours_29_neighbours),
    .plus_00_01_2(_0_line__out__1[29]), .plus_00_02_2(_0_line__out__1[30]), .plus_01_02(_1_line[26]),
    .plus_01_01(_1_line[27]), .plus_01_00(_1_line[28]), .plus_01_01_2(_1_line[29]),
    .plus_01_02_2(_1_line[30]), .plus_02_02(_2_line[26]), .plus_02_01(_2_line[27]), .plus_02_00(_2_line[28]),
    .plus_02_01_2(_2_line[29]), .plus_02_02_2(_2_line[30]));
  alive alive_29 (
    .neighbours(neighbours_29_neighbours), .look_at(lookAt), .B___birth(birth), .S___save(save),
    .alive(plus_00_28new), .pause(pause), .input_state(state_helper_29_output_state));
  STATE_helper state_helper_29 (
    .input_state(input_state), .output_state(state_helper_29_output_state), .i(I), .j(J[28]));
  neighbours neighbours_30 (
    .minus_02_02(minus_2_line[27]), .minus_02_01(minus_2_line[28]), .minus_02_00(minus_2_line[29]),
    .minus_02_01_2(minus_2_line[30]), .minus_02_02_2(minus_2_line[31]), .minus_01_02(minus_1_line[27]),
    .minus_01_01(minus_1_line[28]), .minus_01_00(minus_1_line[29]), .minus_01_01_2(minus_1_line[30]),
    .minus_01_02_2(minus_1_line[31]), .plus_00_02(_0_line__out__1[27]), .plus_00_01(_0_line__out__1[28]),
    .plus_00_00(_0_line__out__1[29]), .neighbours(neighbours_30_neighbours),
    .plus_00_01_2(_0_line__out__1[30]), .plus_00_02_2(_0_line__out__1[31]), .plus_01_02(_1_line[27]),
    .plus_01_01(_1_line[28]), .plus_01_00(_1_line[29]), .plus_01_01_2(_1_line[30]),
    .plus_01_02_2(_1_line[31]), .plus_02_02(_2_line[27]), .plus_02_01(_2_line[28]), .plus_02_00(_2_line[29]),
    .plus_02_01_2(_2_line[30]), .plus_02_02_2(_2_line[31]));
  alive alive_30 (
    .neighbours(neighbours_30_neighbours), .look_at(lookAt), .B___birth(birth), .S___save(save),
    .alive(plus_00_29new), .pause(pause), .input_state(state_helper_30_output_state));
  STATE_helper state_helper_30 (
    .input_state(input_state), .output_state(state_helper_30_output_state), .i(I), .j(J[29]));
  neighbours neighbours_31 (
    .minus_02_02(minus_2_line[28]), .minus_02_01(minus_2_line[29]), .minus_02_00(minus_2_line[30]),
    .minus_02_01_2(minus_2_line[31]), .minus_02_02_2(minus_02_32), .minus_01_02(minus_1_line[28]),
    .minus_01_01(minus_1_line[29]), .minus_01_00(minus_1_line[30]), .minus_01_01_2(minus_1_line[31]),
    .minus_01_02_2(minus_01_32), .plus_00_02(_0_line__out__1[28]), .plus_00_01(_0_line__out__1[29]),
    .plus_00_00(_0_line__out__1[30]), .neighbours(neighbours_31_neighbours),
    .plus_00_01_2(_0_line__out__1[31]), .plus_00_02_2(plus_00_32), .plus_01_02(_1_line[28]),
    .plus_01_01(_1_line[29]), .plus_01_00(_1_line[30]), .plus_01_01_2(_1_line[31]),
    .plus_01_02_2(plus_01_32), .plus_02_02(_2_line[28]), .plus_02_01(_2_line[29]), .plus_02_00(_2_line[30]),
    .plus_02_01_2(_2_line[31]), .plus_02_02_2(plus_02_32));
  alive alive_31 (
    .neighbours(neighbours_31_neighbours), .look_at(lookAt), .B___birth(birth), .S___save(save),
    .alive(plus_00_30new), .pause(pause), .input_state(state_helper_31_output_state));
  STATE_helper state_helper_31 (
    .input_state(input_state), .output_state(state_helper_31_output_state), .i(I), .j(J[30]));
  neighbours neighbours_32 (
    .minus_02_02(minus_2_line[29]), .minus_02_01(minus_2_line[30]), .minus_02_00(minus_2_line[31]),
    .minus_02_01_2(minus_02_32), .minus_02_02_2(minus_02_33), .minus_01_02(minus_1_line[29]),
    .minus_01_01(minus_1_line[30]), .minus_01_00(minus_1_line[31]), .minus_01_01_2(minus_01_32),
    .minus_01_02_2(minus_01_33), .plus_00_02(_0_line__out__1[29]), .plus_00_01(_0_line__out__1[30]),
    .plus_00_00(_0_line__out__1[31]), .neighbours(neighbours_32_neighbours), .plus_00_01_2(plus_00_32),
    .plus_00_02_2(plus_00_33), .plus_01_02(_1_line[29]), .plus_01_01(_1_line[30]), .plus_01_00(_1_line[31]),
    .plus_01_01_2(plus_01_32), .plus_01_02_2(plus_01_33), .plus_02_02(_2_line[29]), .plus_02_01(_2_line[30]),
    .plus_02_00(_2_line[31]), .plus_02_01_2(plus_02_32), .plus_02_02_2(plus_02_33));
  alive alive_32 (
    .neighbours(neighbours_32_neighbours), .look_at(lookAt), .B___birth(birth), .S___save(save),
    .alive(plus_00_31new), .pause(pause), .input_state(state_helper_32_output_state));
  STATE_helper state_helper_32 (
    .input_state(input_state), .output_state(state_helper_32_output_state), .i(I), .j(J[31]));

  assign _0_line__out__1_2 = _0_line__out__1;
  assign _0_line__out__2 = _0_line__out__1;
  assign _0_line__out__2_2 = _0_line__out__1;
  assign display = _0_line__out__1;

  // Other names for the same wires on the sheet: plus_01_00 = _1_line[0]; plus_01_01 = _1_line[1];
  //   plus_01_02 = _1_line[2]; plus_01_03 = _1_line[3]; plus_01_04 = _1_line[4]; plus_01_05 = _1_line[5];
  //   plus_01_06 = _1_line[6]; plus_01_07 = _1_line[7]; plus_01_08 = _1_line[8]; plus_01_09 = _1_line[9];
  //   plus_01_10 = _1_line[10]; plus_01_11 = _1_line[11]; plus_01_12 = _1_line[12]; plus_01_13 = _1_line[13];
  //   plus_01_14 = _1_line[14]; plus_01_15 = _1_line[15]; plus_01_16 = _1_line[16]; plus_01_17 = _1_line[17];
  //   plus_01_18 = _1_line[18]; plus_01_19 = _1_line[19]; plus_01_20 = _1_line[20]; plus_01_21 = _1_line[21];
  //   plus_01_22 = _1_line[22]; plus_01_23 = _1_line[23]; plus_01_24 = _1_line[24]; plus_01_25 = _1_line[25];
  //   plus_01_26 = _1_line[26]; plus_01_27 = _1_line[27]; plus_01_28 = _1_line[28]; plus_01_29 = _1_line[29];
  //   plus_01_30 = _1_line[30]; plus_01_31 = _1_line[31]; plus_02_00 = _2_line[0]; plus_02_01 = _2_line[1];
  //   plus_02_02 = _2_line[2]; plus_02_03 = _2_line[3]; plus_02_04 = _2_line[4]; plus_02_05 = _2_line[5];
  //   plus_02_06 = _2_line[6]; plus_02_07 = _2_line[7]; plus_02_08 = _2_line[8]; plus_02_09 = _2_line[9];
  //   plus_02_10 = _2_line[10]; plus_02_11 = _2_line[11]; plus_02_12 = _2_line[12]; plus_02_13 = _2_line[13];
  //   plus_02_14 = _2_line[14]; plus_02_15 = _2_line[15]; plus_02_16 = _2_line[16]; plus_02_17 = _2_line[17];
  //   plus_02_18 = _2_line[18]; plus_02_19 = _2_line[19]; plus_02_20 = _2_line[20]; plus_02_21 = _2_line[21];
  //   plus_02_22 = _2_line[22]; plus_02_23 = _2_line[23]; plus_02_24 = _2_line[24]; plus_02_25 = _2_line[25];
  //   plus_02_26 = _2_line[26]; plus_02_27 = _2_line[27]; plus_02_28 = _2_line[28]; plus_02_29 = _2_line[29];
  //   plus_02_30 = _2_line[30]; plus_02_31 = _2_line[31]; plus_00_00 = _0_line__out__1[0];
  //   plus_00_01 = _0_line__out__1[1]; plus_00_02 = _0_line__out__1[2]; plus_00_03 = _0_line__out__1[3];
  //   plus_00_04 = _0_line__out__1[4]; plus_00_05 = _0_line__out__1[5]; plus_00_06 = _0_line__out__1[6];
  //   plus_00_07 = _0_line__out__1[7]; plus_00_08 = _0_line__out__1[8]; plus_00_09 = _0_line__out__1[9];
  //   plus_00_10 = _0_line__out__1[10]; plus_00_11 = _0_line__out__1[11]; plus_00_12 = _0_line__out__1[12];
  //   plus_00_13 = _0_line__out__1[13]; plus_00_14 = _0_line__out__1[14]; plus_00_15 = _0_line__out__1[15];
  //   plus_00_16 = _0_line__out__1[16]; plus_00_17 = _0_line__out__1[17]; plus_00_18 = _0_line__out__1[18];
  //   plus_00_19 = _0_line__out__1[19]; plus_00_20 = _0_line__out__1[20]; plus_00_21 = _0_line__out__1[21];
  //   plus_00_22 = _0_line__out__1[22]; plus_00_23 = _0_line__out__1[23]; plus_00_24 = _0_line__out__1[24];
  //   plus_00_25 = _0_line__out__1[25]; plus_00_26 = _0_line__out__1[26]; plus_00_27 = _0_line__out__1[27];
  //   plus_00_28 = _0_line__out__1[28]; plus_00_29 = _0_line__out__1[29]; plus_00_30 = _0_line__out__1[30];
  //   plus_00_31 = _0_line__out__1[31]; minus_01_00 = minus_1_line[0]; minus_01_01 = minus_1_line[1];
  //   minus_01_02 = minus_1_line[2]; minus_01_03 = minus_1_line[3]; minus_01_04 = minus_1_line[4];
  //   minus_01_05 = minus_1_line[5]; minus_01_06 = minus_1_line[6]; minus_01_07 = minus_1_line[7];
  //   minus_01_08 = minus_1_line[8]; minus_01_09 = minus_1_line[9]; minus_01_10 = minus_1_line[10];
  //   minus_01_11 = minus_1_line[11]; minus_01_12 = minus_1_line[12]; minus_01_13 = minus_1_line[13];
  //   minus_01_14 = minus_1_line[14]; minus_01_15 = minus_1_line[15]; minus_01_16 = minus_1_line[16];
  //   minus_01_17 = minus_1_line[17]; minus_01_18 = minus_1_line[18]; minus_01_19 = minus_1_line[19];
  //   minus_01_20 = minus_1_line[20]; minus_01_21 = minus_1_line[21]; minus_01_22 = minus_1_line[22];
  //   minus_01_23 = minus_1_line[23]; minus_01_24 = minus_1_line[24]; minus_01_25 = minus_1_line[25];
  //   minus_01_26 = minus_1_line[26]; minus_01_27 = minus_1_line[27]; minus_01_28 = minus_1_line[28];
  //   minus_01_29 = minus_1_line[29]; minus_01_30 = minus_1_line[30]; minus_01_31 = minus_1_line[31];
  //   minus_02_00 = minus_2_line[0]; minus_02_01 = minus_2_line[1]; minus_02_02 = minus_2_line[2];
  //   minus_02_03 = minus_2_line[3]; minus_02_04 = minus_2_line[4]; minus_02_05 = minus_2_line[5];
  //   minus_02_06 = minus_2_line[6]; minus_02_07 = minus_2_line[7]; minus_02_08 = minus_2_line[8];
  //   minus_02_09 = minus_2_line[9]; minus_02_10 = minus_2_line[10]; minus_02_11 = minus_2_line[11];
  //   minus_02_12 = minus_2_line[12]; minus_02_13 = minus_2_line[13]; minus_02_14 = minus_2_line[14];
  //   minus_02_15 = minus_2_line[15]; minus_02_16 = minus_2_line[16]; minus_02_17 = minus_2_line[17];
  //   minus_02_18 = minus_2_line[18]; minus_02_19 = minus_2_line[19]; minus_02_20 = minus_2_line[20];
  //   minus_02_21 = minus_2_line[21]; minus_02_22 = minus_2_line[22]; minus_02_23 = minus_2_line[23];
  //   minus_02_24 = minus_2_line[24]; minus_02_25 = minus_2_line[25]; minus_02_26 = minus_2_line[26];
  //   minus_02_27 = minus_2_line[27]; minus_02_28 = minus_2_line[28]; minus_02_29 = minus_2_line[29];
  //   minus_02_30 = minus_2_line[30]; minus_02_31 = minus_2_line[31]; state[1:0] = input_state

  // Notes on the sheet:
  //   clock: pull=down
  //   pause: pull=down
endmodule

module matrixSTD (
  input  [31:0] i,
  input  [31:0] J,
  input  Torus,
  input  [1:0] input_state,
  input  clock,
  input  pause,
  output [31:0] LINE_31,
  output [31:0] LINE_30,
  output [31:0] LINE_29,
  output [31:0] LINE_28,
  output [31:0] LINE_27,
  output [31:0] LINE_26,
  output [31:0] LINE_25,
  output [31:0] LINE_24,
  output [31:0] LINE_23,
  output [31:0] LINE_22,
  output [31:0] LINE_21,
  output [31:0] LINE_20,
  output [31:0] LINE_19,
  output [31:0] LINE_18,
  output [31:0] LINE_17,
  output [31:0] LINE_16,
  output [31:0] LINE_15,
  output [31:0] LINE_14,
  output [31:0] LINE_13,
  output [31:0] LINE_12,
  output [31:0] LINE_11,
  output [31:0] LINE_10,
  output [31:0] LINE_9,
  output [31:0] LINE_8,
  output [31:0] LINE_7,
  output [31:0] LINE_6,
  output [31:0] LINE_5,
  output [31:0] LINE_4,
  output [31:0] LINE_3,
  output [31:0] LINE_2,
  output [31:0] LINE_1,
  output [31:0] LINE_0
);

  wire [31:0] _0__0_line__out__1_2, _1__0_line__out__1, _1__0_line__out__1_2, _2__0_line__out__1,
       _2__0_line__out__1_2, _3__0_line__out__1, _3__0_line__out__1_2, _4__0_line__out__1,
       _4__0_line__out__1_2, _5__0_line__out__1, _5__0_line__out__1_2, _6__0_line__out__1,
       _6__0_line__out__1_2, _7__0_line__out__1, _7__0_line__out__1_2, _8__0_line__out__1,
       _8__0_line__out__1_2, _9__0_line__out__1, _9__0_line__out__1_2, _10__0_line__out__1,
       _10__0_line__out__1_2, _11__0_line__out__1, _11__0_line__out__1_2, _12__0_line__out__1,
       _12__0_line__out__1_2, _13__0_line__out__1, _13__0_line__out__1_2, _14__0_line__out__1,
       _14__0_line__out__1_2, _15__0_line__out__1, _15__0_line__out__1_2, _16__0_line__out__1,
       _16__0_line__out__1_2, _17__0_line__out__1, _17__0_line__out__1_2, _18__0_line__out__1,
       _18__0_line__out__1_2, _19__0_line__out__1, _19__0_line__out__1_2, _20__0_line__out__1,
       _20__0_line__out__1_2, _21__0_line__out__1, _21__0_line__out__1_2, _22__0_line__out__1,
       _22__0_line__out__1_2, _23__0_line__out__1, _23__0_line__out__1_2, _24__0_line__out__1,
       _24__0_line__out__1_2, _25__0_line__out__1, _25__0_line__out__1_2, _26__0_line__out__1,
       _26__0_line__out__1_2, _27__0_line__out__1, _27__0_line__out__1_2, _28__0_line__out__1,
       _28__0_line__out__1_2, _29__0_line__out__1, _29__0_line__out__1_2, _30__0_line__out__1,
       _30__0_line__out__1_2, _31__0_line__out__1, and_1_out, and_2_out, minus_01, plus_32;

  assign and_1_out = plus_32 & {32{Torus}};  // AND_Gate and_1, 32 bits wide
  lineSTD _0 (
    .J({J[0], J[1], J[2], J[3], J[4], J[5], J[6], J[7], J[8], J[9], J[10], J[11], J[12], J[13], J[14], J[15], J[16], J[17], J[18], J[19], J[20], J[21], J[22], J[23], J[24], J[25], J[26], J[27], J[28], J[29], J[30], J[31]}),
    .minus_1_line(and_1_out), ._1_line(_1__0_line__out__1), .I(i[31]), .Torus(Torus),
    .input_state(input_state), ._0_line__out__1(minus_01), .display(LINE_31),
    ._0_line__out__1_2(_0__0_line__out__1_2), .clock(clock), .pause(pause));
  lineSTD _1 (
    .J({J[0], J[1], J[2], J[3], J[4], J[5], J[6], J[7], J[8], J[9], J[10], J[11], J[12], J[13], J[14], J[15], J[16], J[17], J[18], J[19], J[20], J[21], J[22], J[23], J[24], J[25], J[26], J[27], J[28], J[29], J[30], J[31]}),
    .minus_1_line(_0__0_line__out__1_2), ._1_line(_2__0_line__out__1), .I(i[30]), .Torus(Torus),
    .input_state(input_state), ._0_line__out__1(_1__0_line__out__1), .display(LINE_30),
    ._0_line__out__1_2(_1__0_line__out__1_2), .clock(clock), .pause(pause));
  lineSTD _2 (
    .J({J[0], J[1], J[2], J[3], J[4], J[5], J[6], J[7], J[8], J[9], J[10], J[11], J[12], J[13], J[14], J[15], J[16], J[17], J[18], J[19], J[20], J[21], J[22], J[23], J[24], J[25], J[26], J[27], J[28], J[29], J[30], J[31]}),
    .minus_1_line(_1__0_line__out__1_2), ._1_line(_3__0_line__out__1), .I(i[29]), .Torus(Torus),
    .input_state(input_state), ._0_line__out__1(_2__0_line__out__1), .display(LINE_29),
    ._0_line__out__1_2(_2__0_line__out__1_2), .clock(clock), .pause(pause));
  lineSTD _3 (
    .J({J[0], J[1], J[2], J[3], J[4], J[5], J[6], J[7], J[8], J[9], J[10], J[11], J[12], J[13], J[14], J[15], J[16], J[17], J[18], J[19], J[20], J[21], J[22], J[23], J[24], J[25], J[26], J[27], J[28], J[29], J[30], J[31]}),
    .minus_1_line(_2__0_line__out__1_2), ._1_line(_4__0_line__out__1), .I(i[28]), .Torus(Torus),
    .input_state(input_state), ._0_line__out__1(_3__0_line__out__1), .display(LINE_28),
    ._0_line__out__1_2(_3__0_line__out__1_2), .clock(clock), .pause(pause));
  lineSTD _4 (
    .J({J[0], J[1], J[2], J[3], J[4], J[5], J[6], J[7], J[8], J[9], J[10], J[11], J[12], J[13], J[14], J[15], J[16], J[17], J[18], J[19], J[20], J[21], J[22], J[23], J[24], J[25], J[26], J[27], J[28], J[29], J[30], J[31]}),
    .minus_1_line(_3__0_line__out__1_2), ._1_line(_5__0_line__out__1), .I(i[27]), .Torus(Torus),
    .input_state(input_state), ._0_line__out__1(_4__0_line__out__1), .display(LINE_27),
    ._0_line__out__1_2(_4__0_line__out__1_2), .clock(clock), .pause(pause));
  lineSTD _5 (
    .J({J[0], J[1], J[2], J[3], J[4], J[5], J[6], J[7], J[8], J[9], J[10], J[11], J[12], J[13], J[14], J[15], J[16], J[17], J[18], J[19], J[20], J[21], J[22], J[23], J[24], J[25], J[26], J[27], J[28], J[29], J[30], J[31]}),
    .minus_1_line(_4__0_line__out__1_2), ._1_line(_6__0_line__out__1), .I(i[26]), .Torus(Torus),
    .input_state(input_state), ._0_line__out__1(_5__0_line__out__1), .display(LINE_26),
    ._0_line__out__1_2(_5__0_line__out__1_2), .clock(clock), .pause(pause));
  lineSTD _6 (
    .J({J[0], J[1], J[2], J[3], J[4], J[5], J[6], J[7], J[8], J[9], J[10], J[11], J[12], J[13], J[14], J[15], J[16], J[17], J[18], J[19], J[20], J[21], J[22], J[23], J[24], J[25], J[26], J[27], J[28], J[29], J[30], J[31]}),
    .minus_1_line(_5__0_line__out__1_2), ._1_line(_7__0_line__out__1), .I(i[25]), .Torus(Torus),
    .input_state(input_state), ._0_line__out__1(_6__0_line__out__1), .display(LINE_25),
    ._0_line__out__1_2(_6__0_line__out__1_2), .clock(clock), .pause(pause));
  lineSTD _7 (
    .J({J[0], J[1], J[2], J[3], J[4], J[5], J[6], J[7], J[8], J[9], J[10], J[11], J[12], J[13], J[14], J[15], J[16], J[17], J[18], J[19], J[20], J[21], J[22], J[23], J[24], J[25], J[26], J[27], J[28], J[29], J[30], J[31]}),
    .minus_1_line(_6__0_line__out__1_2), ._1_line(_8__0_line__out__1), .I(i[24]), .Torus(Torus),
    .input_state(input_state), ._0_line__out__1(_7__0_line__out__1), .display(LINE_24),
    ._0_line__out__1_2(_7__0_line__out__1_2), .clock(clock), .pause(pause));
  lineSTD _8 (
    .J({J[0], J[1], J[2], J[3], J[4], J[5], J[6], J[7], J[8], J[9], J[10], J[11], J[12], J[13], J[14], J[15], J[16], J[17], J[18], J[19], J[20], J[21], J[22], J[23], J[24], J[25], J[26], J[27], J[28], J[29], J[30], J[31]}),
    .minus_1_line(_7__0_line__out__1_2), ._1_line(_9__0_line__out__1), .I(i[23]), .Torus(Torus),
    .input_state(input_state), ._0_line__out__1(_8__0_line__out__1), .display(LINE_23),
    ._0_line__out__1_2(_8__0_line__out__1_2), .clock(clock), .pause(pause));
  lineSTD _9 (
    .J({J[0], J[1], J[2], J[3], J[4], J[5], J[6], J[7], J[8], J[9], J[10], J[11], J[12], J[13], J[14], J[15], J[16], J[17], J[18], J[19], J[20], J[21], J[22], J[23], J[24], J[25], J[26], J[27], J[28], J[29], J[30], J[31]}),
    .minus_1_line(_8__0_line__out__1_2), ._1_line(_10__0_line__out__1), .I(i[22]), .Torus(Torus),
    .input_state(input_state), ._0_line__out__1(_9__0_line__out__1), .display(LINE_22),
    ._0_line__out__1_2(_9__0_line__out__1_2), .clock(clock), .pause(pause));
  lineSTD _10 (
    .J({J[0], J[1], J[2], J[3], J[4], J[5], J[6], J[7], J[8], J[9], J[10], J[11], J[12], J[13], J[14], J[15], J[16], J[17], J[18], J[19], J[20], J[21], J[22], J[23], J[24], J[25], J[26], J[27], J[28], J[29], J[30], J[31]}),
    .minus_1_line(_9__0_line__out__1_2), ._1_line(_11__0_line__out__1), .I(i[21]), .Torus(Torus),
    .input_state(input_state), ._0_line__out__1(_10__0_line__out__1), .display(LINE_21),
    ._0_line__out__1_2(_10__0_line__out__1_2), .clock(clock), .pause(pause));
  lineSTD _11 (
    .J({J[0], J[1], J[2], J[3], J[4], J[5], J[6], J[7], J[8], J[9], J[10], J[11], J[12], J[13], J[14], J[15], J[16], J[17], J[18], J[19], J[20], J[21], J[22], J[23], J[24], J[25], J[26], J[27], J[28], J[29], J[30], J[31]}),
    .minus_1_line(_10__0_line__out__1_2), ._1_line(_12__0_line__out__1), .I(i[20]), .Torus(Torus),
    .input_state(input_state), ._0_line__out__1(_11__0_line__out__1), .display(LINE_20),
    ._0_line__out__1_2(_11__0_line__out__1_2), .clock(clock), .pause(pause));
  lineSTD _12 (
    .J({J[0], J[1], J[2], J[3], J[4], J[5], J[6], J[7], J[8], J[9], J[10], J[11], J[12], J[13], J[14], J[15], J[16], J[17], J[18], J[19], J[20], J[21], J[22], J[23], J[24], J[25], J[26], J[27], J[28], J[29], J[30], J[31]}),
    .minus_1_line(_11__0_line__out__1_2), ._1_line(_13__0_line__out__1), .I(i[19]), .Torus(Torus),
    .input_state(input_state), ._0_line__out__1(_12__0_line__out__1), .display(LINE_19),
    ._0_line__out__1_2(_12__0_line__out__1_2), .clock(clock), .pause(pause));
  lineSTD _13 (
    .J({J[0], J[1], J[2], J[3], J[4], J[5], J[6], J[7], J[8], J[9], J[10], J[11], J[12], J[13], J[14], J[15], J[16], J[17], J[18], J[19], J[20], J[21], J[22], J[23], J[24], J[25], J[26], J[27], J[28], J[29], J[30], J[31]}),
    .minus_1_line(_12__0_line__out__1_2), ._1_line(_14__0_line__out__1), .I(i[18]), .Torus(Torus),
    .input_state(input_state), ._0_line__out__1(_13__0_line__out__1), .display(LINE_18),
    ._0_line__out__1_2(_13__0_line__out__1_2), .clock(clock), .pause(pause));
  lineSTD _14 (
    .J({J[0], J[1], J[2], J[3], J[4], J[5], J[6], J[7], J[8], J[9], J[10], J[11], J[12], J[13], J[14], J[15], J[16], J[17], J[18], J[19], J[20], J[21], J[22], J[23], J[24], J[25], J[26], J[27], J[28], J[29], J[30], J[31]}),
    .minus_1_line(_13__0_line__out__1_2), ._1_line(_15__0_line__out__1), .I(i[17]), .Torus(Torus),
    .input_state(input_state), ._0_line__out__1(_14__0_line__out__1), .display(LINE_17),
    ._0_line__out__1_2(_14__0_line__out__1_2), .clock(clock), .pause(pause));
  lineSTD _15 (
    .J({J[0], J[1], J[2], J[3], J[4], J[5], J[6], J[7], J[8], J[9], J[10], J[11], J[12], J[13], J[14], J[15], J[16], J[17], J[18], J[19], J[20], J[21], J[22], J[23], J[24], J[25], J[26], J[27], J[28], J[29], J[30], J[31]}),
    .minus_1_line(_14__0_line__out__1_2), ._1_line(_16__0_line__out__1), .I(i[16]), .Torus(Torus),
    .input_state(input_state), ._0_line__out__1(_15__0_line__out__1), .display(LINE_16),
    ._0_line__out__1_2(_15__0_line__out__1_2), .clock(clock), .pause(pause));
  lineSTD _16 (
    .J({J[0], J[1], J[2], J[3], J[4], J[5], J[6], J[7], J[8], J[9], J[10], J[11], J[12], J[13], J[14], J[15], J[16], J[17], J[18], J[19], J[20], J[21], J[22], J[23], J[24], J[25], J[26], J[27], J[28], J[29], J[30], J[31]}),
    .minus_1_line(_15__0_line__out__1_2), ._1_line(_17__0_line__out__1), .I(i[15]), .Torus(Torus),
    .input_state(input_state), ._0_line__out__1(_16__0_line__out__1), .display(LINE_15),
    ._0_line__out__1_2(_16__0_line__out__1_2), .clock(clock), .pause(pause));
  lineSTD _17 (
    .J({J[0], J[1], J[2], J[3], J[4], J[5], J[6], J[7], J[8], J[9], J[10], J[11], J[12], J[13], J[14], J[15], J[16], J[17], J[18], J[19], J[20], J[21], J[22], J[23], J[24], J[25], J[26], J[27], J[28], J[29], J[30], J[31]}),
    .minus_1_line(_16__0_line__out__1_2), ._1_line(_18__0_line__out__1), .I(i[14]), .Torus(Torus),
    .input_state(input_state), ._0_line__out__1(_17__0_line__out__1), .display(LINE_14),
    ._0_line__out__1_2(_17__0_line__out__1_2), .clock(clock), .pause(pause));
  lineSTD _18 (
    .J({J[0], J[1], J[2], J[3], J[4], J[5], J[6], J[7], J[8], J[9], J[10], J[11], J[12], J[13], J[14], J[15], J[16], J[17], J[18], J[19], J[20], J[21], J[22], J[23], J[24], J[25], J[26], J[27], J[28], J[29], J[30], J[31]}),
    .minus_1_line(_17__0_line__out__1_2), ._1_line(_19__0_line__out__1), .I(i[13]), .Torus(Torus),
    .input_state(input_state), ._0_line__out__1(_18__0_line__out__1), .display(LINE_13),
    ._0_line__out__1_2(_18__0_line__out__1_2), .clock(clock), .pause(pause));
  lineSTD _19 (
    .J({J[0], J[1], J[2], J[3], J[4], J[5], J[6], J[7], J[8], J[9], J[10], J[11], J[12], J[13], J[14], J[15], J[16], J[17], J[18], J[19], J[20], J[21], J[22], J[23], J[24], J[25], J[26], J[27], J[28], J[29], J[30], J[31]}),
    .minus_1_line(_18__0_line__out__1_2), ._1_line(_20__0_line__out__1), .I(i[12]), .Torus(Torus),
    .input_state(input_state), ._0_line__out__1(_19__0_line__out__1), .display(LINE_12),
    ._0_line__out__1_2(_19__0_line__out__1_2), .clock(clock), .pause(pause));
  lineSTD _20 (
    .J({J[0], J[1], J[2], J[3], J[4], J[5], J[6], J[7], J[8], J[9], J[10], J[11], J[12], J[13], J[14], J[15], J[16], J[17], J[18], J[19], J[20], J[21], J[22], J[23], J[24], J[25], J[26], J[27], J[28], J[29], J[30], J[31]}),
    .minus_1_line(_19__0_line__out__1_2), ._1_line(_21__0_line__out__1), .I(i[11]), .Torus(Torus),
    .input_state(input_state), ._0_line__out__1(_20__0_line__out__1), .display(LINE_11),
    ._0_line__out__1_2(_20__0_line__out__1_2), .clock(clock), .pause(pause));
  lineSTD _21 (
    .J({J[0], J[1], J[2], J[3], J[4], J[5], J[6], J[7], J[8], J[9], J[10], J[11], J[12], J[13], J[14], J[15], J[16], J[17], J[18], J[19], J[20], J[21], J[22], J[23], J[24], J[25], J[26], J[27], J[28], J[29], J[30], J[31]}),
    .minus_1_line(_20__0_line__out__1_2), ._1_line(_22__0_line__out__1), .I(i[10]), .Torus(Torus),
    .input_state(input_state), ._0_line__out__1(_21__0_line__out__1), .display(LINE_10),
    ._0_line__out__1_2(_21__0_line__out__1_2), .clock(clock), .pause(pause));
  lineSTD _22 (
    .J({J[0], J[1], J[2], J[3], J[4], J[5], J[6], J[7], J[8], J[9], J[10], J[11], J[12], J[13], J[14], J[15], J[16], J[17], J[18], J[19], J[20], J[21], J[22], J[23], J[24], J[25], J[26], J[27], J[28], J[29], J[30], J[31]}),
    .minus_1_line(_21__0_line__out__1_2), ._1_line(_23__0_line__out__1), .I(i[9]), .Torus(Torus),
    .input_state(input_state), ._0_line__out__1(_22__0_line__out__1), .display(LINE_9),
    ._0_line__out__1_2(_22__0_line__out__1_2), .clock(clock), .pause(pause));
  lineSTD _23 (
    .J({J[0], J[1], J[2], J[3], J[4], J[5], J[6], J[7], J[8], J[9], J[10], J[11], J[12], J[13], J[14], J[15], J[16], J[17], J[18], J[19], J[20], J[21], J[22], J[23], J[24], J[25], J[26], J[27], J[28], J[29], J[30], J[31]}),
    .minus_1_line(_22__0_line__out__1_2), ._1_line(_24__0_line__out__1), .I(i[8]), .Torus(Torus),
    .input_state(input_state), ._0_line__out__1(_23__0_line__out__1), .display(LINE_8),
    ._0_line__out__1_2(_23__0_line__out__1_2), .clock(clock), .pause(pause));
  lineSTD _24 (
    .J({J[0], J[1], J[2], J[3], J[4], J[5], J[6], J[7], J[8], J[9], J[10], J[11], J[12], J[13], J[14], J[15], J[16], J[17], J[18], J[19], J[20], J[21], J[22], J[23], J[24], J[25], J[26], J[27], J[28], J[29], J[30], J[31]}),
    .minus_1_line(_23__0_line__out__1_2), ._1_line(_25__0_line__out__1), .I(i[7]), .Torus(Torus),
    .input_state(input_state), ._0_line__out__1(_24__0_line__out__1), .display(LINE_7),
    ._0_line__out__1_2(_24__0_line__out__1_2), .clock(clock), .pause(pause));
  lineSTD _25 (
    .J({J[0], J[1], J[2], J[3], J[4], J[5], J[6], J[7], J[8], J[9], J[10], J[11], J[12], J[13], J[14], J[15], J[16], J[17], J[18], J[19], J[20], J[21], J[22], J[23], J[24], J[25], J[26], J[27], J[28], J[29], J[30], J[31]}),
    .minus_1_line(_24__0_line__out__1_2), ._1_line(_26__0_line__out__1), .I(i[6]), .Torus(Torus),
    .input_state(input_state), ._0_line__out__1(_25__0_line__out__1), .display(LINE_6),
    ._0_line__out__1_2(_25__0_line__out__1_2), .clock(clock), .pause(pause));
  lineSTD _26 (
    .J({J[0], J[1], J[2], J[3], J[4], J[5], J[6], J[7], J[8], J[9], J[10], J[11], J[12], J[13], J[14], J[15], J[16], J[17], J[18], J[19], J[20], J[21], J[22], J[23], J[24], J[25], J[26], J[27], J[28], J[29], J[30], J[31]}),
    .minus_1_line(_25__0_line__out__1_2), ._1_line(_27__0_line__out__1), .I(i[5]), .Torus(Torus),
    .input_state(input_state), ._0_line__out__1(_26__0_line__out__1), .display(LINE_5),
    ._0_line__out__1_2(_26__0_line__out__1_2), .clock(clock), .pause(pause));
  lineSTD _27 (
    .J({J[0], J[1], J[2], J[3], J[4], J[5], J[6], J[7], J[8], J[9], J[10], J[11], J[12], J[13], J[14], J[15], J[16], J[17], J[18], J[19], J[20], J[21], J[22], J[23], J[24], J[25], J[26], J[27], J[28], J[29], J[30], J[31]}),
    .minus_1_line(_26__0_line__out__1_2), ._1_line(_28__0_line__out__1), .I(i[4]), .Torus(Torus),
    .input_state(input_state), ._0_line__out__1(_27__0_line__out__1), .display(LINE_4),
    ._0_line__out__1_2(_27__0_line__out__1_2), .clock(clock), .pause(pause));
  lineSTD _28 (
    .J({J[0], J[1], J[2], J[3], J[4], J[5], J[6], J[7], J[8], J[9], J[10], J[11], J[12], J[13], J[14], J[15], J[16], J[17], J[18], J[19], J[20], J[21], J[22], J[23], J[24], J[25], J[26], J[27], J[28], J[29], J[30], J[31]}),
    .minus_1_line(_27__0_line__out__1_2), ._1_line(_29__0_line__out__1), .I(i[3]), .Torus(Torus),
    .input_state(input_state), ._0_line__out__1(_28__0_line__out__1), .display(LINE_3),
    ._0_line__out__1_2(_28__0_line__out__1_2), .clock(clock), .pause(pause));
  lineSTD _29 (
    .J({J[0], J[1], J[2], J[3], J[4], J[5], J[6], J[7], J[8], J[9], J[10], J[11], J[12], J[13], J[14], J[15], J[16], J[17], J[18], J[19], J[20], J[21], J[22], J[23], J[24], J[25], J[26], J[27], J[28], J[29], J[30], J[31]}),
    .minus_1_line(_28__0_line__out__1_2), ._1_line(_30__0_line__out__1), .I(i[2]), .Torus(Torus),
    .input_state(input_state), ._0_line__out__1(_29__0_line__out__1), .display(LINE_2),
    ._0_line__out__1_2(_29__0_line__out__1_2), .clock(clock), .pause(pause));
  lineSTD _30 (
    .J({J[0], J[1], J[2], J[3], J[4], J[5], J[6], J[7], J[8], J[9], J[10], J[11], J[12], J[13], J[14], J[15], J[16], J[17], J[18], J[19], J[20], J[21], J[22], J[23], J[24], J[25], J[26], J[27], J[28], J[29], J[30], J[31]}),
    .minus_1_line(_29__0_line__out__1_2), ._1_line(_31__0_line__out__1), .I(i[1]), .Torus(Torus),
    .input_state(input_state), ._0_line__out__1(_30__0_line__out__1), .display(LINE_1),
    ._0_line__out__1_2(_30__0_line__out__1_2), .clock(clock), .pause(pause));
  lineSTD _31 (
    .J({J[0], J[1], J[2], J[3], J[4], J[5], J[6], J[7], J[8], J[9], J[10], J[11], J[12], J[13], J[14], J[15], J[16], J[17], J[18], J[19], J[20], J[21], J[22], J[23], J[24], J[25], J[26], J[27], J[28], J[29], J[30], J[31]}),
    .minus_1_line(_30__0_line__out__1_2), ._1_line(and_2_out), .I(i[0]), .Torus(Torus),
    .input_state(input_state), ._0_line__out__1(_31__0_line__out__1), .display(LINE_0),
    ._0_line__out__1_2(plus_32), .clock(clock), .pause(pause));
  assign and_2_out = {32{Torus}} & minus_01;  // AND_Gate and_2, 32 bits wide

  // Other names for the same wires on the sheet: i31 = i[0]; i30 = i[1]; i29 = i[2]; i28 = i[3]; i27 = i[4];
  //   i26 = i[5]; i25 = i[6]; i24 = i[7]; i23 = i[8]; i22 = i[9]; i21 = i[10]; i20 = i[11]; i19 = i[12]; i18 = i[13];
  //   i17 = i[14]; i16 = i[15]; i15 = i[16]; i14 = i[17]; i13 = i[18]; i12 = i[19]; i11 = i[20]; i10 = i[21];
  //   i9 = i[22]; i8 = i[23]; i7 = i[24]; i6 = i[25]; i5 = i[26]; i4 = i[27]; i3 = i[28]; i2 = i[29]; i1 = i[30];
  //   i0 = i[31];
  //   J_t[31:0] = {J[0], J[1], J[2], J[3], J[4], J[5], J[6], J[7], J[8], J[9], J[10], J[11], J[12], J[13], J[14], J[15], J[16], J[17], J[18], J[19], J[20], J[21], J[22], J[23], J[24], J[25], J[26], J[27], J[28], J[29], J[30], J[31]};
  //   state[1:0] = input_state

  // Notes on the sheet:
  //   LINE_5: pull=down
  //   LINE_31: pull=down
  //   LINE_3: pull=down
  //   LINE_10: pull=down
  //   LINE_4: pull=down
  //   LINE_30: pull=down
  //   LINE_7: pull=down
  //   LINE_2: pull=down
  //   LINE_9: pull=down
  //   LINE_18: pull=down
  //   LINE_21: pull=down
  //   LINE_26: pull=down
  //   LINE_16: pull=down
  //   LINE_23: pull=down
  //   LINE_13: pull=down
  //   LINE_8: pull=down
  //   LINE_28: pull=down
  //   LINE_14: pull=down
  //   LINE_11: pull=down
  //   LINE_20: pull=down
  //   LINE_0: pull=down
  //   LINE_29: pull=down
  //   LINE_15: pull=down
  //   LINE_19: pull=down
  //   LINE_22: pull=down
  //   LINE_17: pull=down
  //   LINE_27: pull=down
  //   LINE_6: pull=down
  //   LINE_12: pull=down
  //   LINE_25: pull=down
  //   LINE_24: pull=down
  //   LINE_1: pull=down
  //   0~ — old
  //   10 — set DEAD
  //   11 — set ALIVE
endmodule

module matrix (
  input  [31:0] i,
  input  [31:0] J,
  input  Torus,
  input  [1:0] input_state,
  input  clock,
  input  pause,
  output [31:0] LINE_31,
  output [31:0] LINE_30,
  output [31:0] LINE_29,
  output [31:0] LINE_28,
  output [31:0] LINE_27,
  output [31:0] LINE_26,
  output [31:0] LINE_25,
  output [31:0] LINE_24,
  output [31:0] LINE_23,
  output [31:0] LINE_22,
  output [31:0] LINE_21,
  output [31:0] LINE_20,
  output [31:0] LINE_19,
  output [31:0] LINE_18,
  output [31:0] LINE_17,
  output [31:0] LINE_16,
  output [31:0] LINE_15,
  output [31:0] LINE_14,
  output [31:0] LINE_13,
  output [31:0] LINE_12,
  output [31:0] LINE_11,
  output [31:0] LINE_10,
  output [31:0] LINE_9,
  output [31:0] LINE_8,
  output [31:0] LINE_7,
  output [31:0] LINE_6,
  output [31:0] LINE_5,
  output [31:0] LINE_4,
  output [31:0] LINE_3,
  output [31:0] LINE_2,
  output [31:0] LINE_1,
  output [31:0] LINE_0
);

  wire [31:0] and_1_out, and_2_out, and_3_out, and_4_out, line_1__0_line__out__1_2, line_1__0_line__out__2_2,
       line_2__0_line__out__1, line_2__0_line__out__1_2, line_2__0_line__out__2_2, line_3__0_line__out__1,
       line_3__0_line__out__1_2, line_3__0_line__out__2, line_3__0_line__out__2_2, line_4__0_line__out__1,
       line_4__0_line__out__1_2, line_4__0_line__out__2, line_4__0_line__out__2_2, line_5__0_line__out__1,
       line_5__0_line__out__1_2, line_5__0_line__out__2, line_5__0_line__out__2_2, line_6__0_line__out__1,
       line_6__0_line__out__1_2, line_6__0_line__out__2, line_6__0_line__out__2_2, line_7__0_line__out__1,
       line_7__0_line__out__1_2, line_7__0_line__out__2, line_7__0_line__out__2_2, line_8__0_line__out__1,
       line_8__0_line__out__1_2, line_8__0_line__out__2, line_8__0_line__out__2_2, line_9__0_line__out__1,
       line_9__0_line__out__1_2, line_9__0_line__out__2, line_9__0_line__out__2_2, line_10__0_line__out__1,
       line_10__0_line__out__1_2, line_10__0_line__out__2, line_10__0_line__out__2_2,
       line_11__0_line__out__1, line_11__0_line__out__1_2, line_11__0_line__out__2,
       line_11__0_line__out__2_2, line_12__0_line__out__1, line_12__0_line__out__1_2,
       line_12__0_line__out__2, line_12__0_line__out__2_2, line_13__0_line__out__1,
       line_13__0_line__out__1_2, line_13__0_line__out__2, line_13__0_line__out__2_2,
       line_14__0_line__out__1, line_14__0_line__out__1_2, line_14__0_line__out__2,
       line_14__0_line__out__2_2, line_15__0_line__out__1, line_15__0_line__out__1_2,
       line_15__0_line__out__2, line_15__0_line__out__2_2, line_16__0_line__out__1,
       line_16__0_line__out__1_2, line_16__0_line__out__2, line_16__0_line__out__2_2,
       line_17__0_line__out__1, line_17__0_line__out__1_2, line_17__0_line__out__2,
       line_17__0_line__out__2_2, line_18__0_line__out__1, line_18__0_line__out__1_2,
       line_18__0_line__out__2, line_18__0_line__out__2_2, line_19__0_line__out__1,
       line_19__0_line__out__1_2, line_19__0_line__out__2, line_19__0_line__out__2_2,
       line_20__0_line__out__1, line_20__0_line__out__1_2, line_20__0_line__out__2,
       line_20__0_line__out__2_2, line_21__0_line__out__1, line_21__0_line__out__1_2,
       line_21__0_line__out__2, line_21__0_line__out__2_2, line_22__0_line__out__1,
       line_22__0_line__out__1_2, line_22__0_line__out__2, line_22__0_line__out__2_2,
       line_23__0_line__out__1, line_23__0_line__out__1_2, line_23__0_line__out__2,
       line_23__0_line__out__2_2, line_24__0_line__out__1, line_24__0_line__out__1_2,
       line_24__0_line__out__2, line_24__0_line__out__2_2, line_25__0_line__out__1,
       line_25__0_line__out__1_2, line_25__0_line__out__2, line_25__0_line__out__2_2,
       line_26__0_line__out__1, line_26__0_line__out__1_2, line_26__0_line__out__2,
       line_26__0_line__out__2_2, line_27__0_line__out__1, line_27__0_line__out__1_2,
       line_27__0_line__out__2, line_27__0_line__out__2_2, line_28__0_line__out__1,
       line_28__0_line__out__1_2, line_28__0_line__out__2, line_28__0_line__out__2_2,
       line_29__0_line__out__1, line_29__0_line__out__1_2, line_29__0_line__out__2,
       line_29__0_line__out__2_2, line_30__0_line__out__1, line_30__0_line__out__1_2,
       line_30__0_line__out__2, line_30__0_line__out__2_2, line_31__0_line__out__1,
       line_31__0_line__out__1_2, line_31__0_line__out__2, line_32__0_line__out__1, line_32__0_line__out__2,
       minus_01, minus_01_star, minus_02, plus_32, plus_32_star, plus_33;

  assign and_1_out = plus_33 & {32{Torus}};  // AND_Gate and_1, 32 bits wide
  assign and_2_out = plus_32 & {32{Torus}};  // AND_Gate and_2, 32 bits wide
  assign and_3_out = plus_32_star & {32{Torus}};  // AND_Gate and_3, 32 bits wide
  assign and_4_out = {32{Torus}} & minus_01_star;  // AND_Gate and_4, 32 bits wide
  line u_line_1 (
    .J({J[0], J[1], J[2], J[3], J[4], J[5], J[6], J[7], J[8], J[9], J[10], J[11], J[12], J[13], J[14], J[15], J[16], J[17], J[18], J[19], J[20], J[21], J[22], J[23], J[24], J[25], J[26], J[27], J[28], J[29], J[30], J[31]}),
    .minus_2_line(and_1_out), .minus_1_line(and_3_out), ._1_line(line_2__0_line__out__1),
    ._2_line(line_3__0_line__out__2), .I(i[31]), .Torus(Torus), .input_state(input_state),
    ._0_line__out__2(minus_02), ._0_line__out__1(minus_01_star),
    ._0_line__out__1_2(line_1__0_line__out__1_2), ._0_line__out__2_2(line_1__0_line__out__2_2),
    .display(LINE_31), .clock(clock), .pause(pause));
  line u_line_2 (
    .J({J[0], J[1], J[2], J[3], J[4], J[5], J[6], J[7], J[8], J[9], J[10], J[11], J[12], J[13], J[14], J[15], J[16], J[17], J[18], J[19], J[20], J[21], J[22], J[23], J[24], J[25], J[26], J[27], J[28], J[29], J[30], J[31]}),
    .minus_2_line(and_2_out), .minus_1_line(line_1__0_line__out__1_2), ._1_line(line_3__0_line__out__1),
    ._2_line(line_4__0_line__out__2), .I(i[30]), .Torus(Torus), .input_state(input_state),
    ._0_line__out__2(minus_01), ._0_line__out__1(line_2__0_line__out__1),
    ._0_line__out__1_2(line_2__0_line__out__1_2), ._0_line__out__2_2(line_2__0_line__out__2_2),
    .display(LINE_30), .clock(clock), .pause(pause));
  line u_line_3 (
    .J({J[0], J[1], J[2], J[3], J[4], J[5], J[6], J[7], J[8], J[9], J[10], J[11], J[12], J[13], J[14], J[15], J[16], J[17], J[18], J[19], J[20], J[21], J[22], J[23], J[24], J[25], J[26], J[27], J[28], J[29], J[30], J[31]}),
    .minus_2_line(line_1__0_line__out__2_2), .minus_1_line(line_2__0_line__out__1_2),
    ._1_line(line_4__0_line__out__1), ._2_line(line_5__0_line__out__2), .I(i[29]), .Torus(Torus),
    .input_state(input_state), ._0_line__out__2(line_3__0_line__out__2),
    ._0_line__out__1(line_3__0_line__out__1), ._0_line__out__1_2(line_3__0_line__out__1_2),
    ._0_line__out__2_2(line_3__0_line__out__2_2), .display(LINE_29), .clock(clock), .pause(pause));
  line u_line_4 (
    .J({J[0], J[1], J[2], J[3], J[4], J[5], J[6], J[7], J[8], J[9], J[10], J[11], J[12], J[13], J[14], J[15], J[16], J[17], J[18], J[19], J[20], J[21], J[22], J[23], J[24], J[25], J[26], J[27], J[28], J[29], J[30], J[31]}),
    .minus_2_line(line_2__0_line__out__2_2), .minus_1_line(line_3__0_line__out__1_2),
    ._1_line(line_5__0_line__out__1), ._2_line(line_6__0_line__out__2), .I(i[28]), .Torus(Torus),
    .input_state(input_state), ._0_line__out__2(line_4__0_line__out__2),
    ._0_line__out__1(line_4__0_line__out__1), ._0_line__out__1_2(line_4__0_line__out__1_2),
    ._0_line__out__2_2(line_4__0_line__out__2_2), .display(LINE_28), .clock(clock), .pause(pause));
  line u_line_5 (
    .J({J[0], J[1], J[2], J[3], J[4], J[5], J[6], J[7], J[8], J[9], J[10], J[11], J[12], J[13], J[14], J[15], J[16], J[17], J[18], J[19], J[20], J[21], J[22], J[23], J[24], J[25], J[26], J[27], J[28], J[29], J[30], J[31]}),
    .minus_2_line(line_3__0_line__out__2_2), .minus_1_line(line_4__0_line__out__1_2),
    ._1_line(line_6__0_line__out__1), ._2_line(line_7__0_line__out__2), .I(i[27]), .Torus(Torus),
    .input_state(input_state), ._0_line__out__2(line_5__0_line__out__2),
    ._0_line__out__1(line_5__0_line__out__1), ._0_line__out__1_2(line_5__0_line__out__1_2),
    ._0_line__out__2_2(line_5__0_line__out__2_2), .display(LINE_27), .clock(clock), .pause(pause));
  line u_line_6 (
    .J({J[0], J[1], J[2], J[3], J[4], J[5], J[6], J[7], J[8], J[9], J[10], J[11], J[12], J[13], J[14], J[15], J[16], J[17], J[18], J[19], J[20], J[21], J[22], J[23], J[24], J[25], J[26], J[27], J[28], J[29], J[30], J[31]}),
    .minus_2_line(line_4__0_line__out__2_2), .minus_1_line(line_5__0_line__out__1_2),
    ._1_line(line_7__0_line__out__1), ._2_line(line_8__0_line__out__2), .I(i[26]), .Torus(Torus),
    .input_state(input_state), ._0_line__out__2(line_6__0_line__out__2),
    ._0_line__out__1(line_6__0_line__out__1), ._0_line__out__1_2(line_6__0_line__out__1_2),
    ._0_line__out__2_2(line_6__0_line__out__2_2), .display(LINE_26), .clock(clock), .pause(pause));
  line u_line_7 (
    .J({J[0], J[1], J[2], J[3], J[4], J[5], J[6], J[7], J[8], J[9], J[10], J[11], J[12], J[13], J[14], J[15], J[16], J[17], J[18], J[19], J[20], J[21], J[22], J[23], J[24], J[25], J[26], J[27], J[28], J[29], J[30], J[31]}),
    .minus_2_line(line_5__0_line__out__2_2), .minus_1_line(line_6__0_line__out__1_2),
    ._1_line(line_8__0_line__out__1), ._2_line(line_9__0_line__out__2), .I(i[25]), .Torus(Torus),
    .input_state(input_state), ._0_line__out__2(line_7__0_line__out__2),
    ._0_line__out__1(line_7__0_line__out__1), ._0_line__out__1_2(line_7__0_line__out__1_2),
    ._0_line__out__2_2(line_7__0_line__out__2_2), .display(LINE_25), .clock(clock), .pause(pause));
  line u_line_8 (
    .J({J[0], J[1], J[2], J[3], J[4], J[5], J[6], J[7], J[8], J[9], J[10], J[11], J[12], J[13], J[14], J[15], J[16], J[17], J[18], J[19], J[20], J[21], J[22], J[23], J[24], J[25], J[26], J[27], J[28], J[29], J[30], J[31]}),
    .minus_2_line(line_6__0_line__out__2_2), .minus_1_line(line_7__0_line__out__1_2),
    ._1_line(line_9__0_line__out__1), ._2_line(line_10__0_line__out__2), .I(i[24]), .Torus(Torus),
    .input_state(input_state), ._0_line__out__2(line_8__0_line__out__2),
    ._0_line__out__1(line_8__0_line__out__1), ._0_line__out__1_2(line_8__0_line__out__1_2),
    ._0_line__out__2_2(line_8__0_line__out__2_2), .display(LINE_24), .clock(clock), .pause(pause));
  line u_line_9 (
    .J({J[0], J[1], J[2], J[3], J[4], J[5], J[6], J[7], J[8], J[9], J[10], J[11], J[12], J[13], J[14], J[15], J[16], J[17], J[18], J[19], J[20], J[21], J[22], J[23], J[24], J[25], J[26], J[27], J[28], J[29], J[30], J[31]}),
    .minus_2_line(line_7__0_line__out__2_2), .minus_1_line(line_8__0_line__out__1_2),
    ._1_line(line_10__0_line__out__1), ._2_line(line_11__0_line__out__2), .I(i[23]), .Torus(Torus),
    .input_state(input_state), ._0_line__out__2(line_9__0_line__out__2),
    ._0_line__out__1(line_9__0_line__out__1), ._0_line__out__1_2(line_9__0_line__out__1_2),
    ._0_line__out__2_2(line_9__0_line__out__2_2), .display(LINE_23), .clock(clock), .pause(pause));
  line u_line_10 (
    .J({J[0], J[1], J[2], J[3], J[4], J[5], J[6], J[7], J[8], J[9], J[10], J[11], J[12], J[13], J[14], J[15], J[16], J[17], J[18], J[19], J[20], J[21], J[22], J[23], J[24], J[25], J[26], J[27], J[28], J[29], J[30], J[31]}),
    .minus_2_line(line_8__0_line__out__2_2), .minus_1_line(line_9__0_line__out__1_2),
    ._1_line(line_11__0_line__out__1), ._2_line(line_12__0_line__out__2), .I(i[22]), .Torus(Torus),
    .input_state(input_state), ._0_line__out__2(line_10__0_line__out__2),
    ._0_line__out__1(line_10__0_line__out__1), ._0_line__out__1_2(line_10__0_line__out__1_2),
    ._0_line__out__2_2(line_10__0_line__out__2_2), .display(LINE_22), .clock(clock), .pause(pause));
  line u_line_11 (
    .J({J[0], J[1], J[2], J[3], J[4], J[5], J[6], J[7], J[8], J[9], J[10], J[11], J[12], J[13], J[14], J[15], J[16], J[17], J[18], J[19], J[20], J[21], J[22], J[23], J[24], J[25], J[26], J[27], J[28], J[29], J[30], J[31]}),
    .minus_2_line(line_9__0_line__out__2_2), .minus_1_line(line_10__0_line__out__1_2),
    ._1_line(line_12__0_line__out__1), ._2_line(line_13__0_line__out__2), .I(i[21]), .Torus(Torus),
    .input_state(input_state), ._0_line__out__2(line_11__0_line__out__2),
    ._0_line__out__1(line_11__0_line__out__1), ._0_line__out__1_2(line_11__0_line__out__1_2),
    ._0_line__out__2_2(line_11__0_line__out__2_2), .display(LINE_21), .clock(clock), .pause(pause));
  line u_line_12 (
    .J({J[0], J[1], J[2], J[3], J[4], J[5], J[6], J[7], J[8], J[9], J[10], J[11], J[12], J[13], J[14], J[15], J[16], J[17], J[18], J[19], J[20], J[21], J[22], J[23], J[24], J[25], J[26], J[27], J[28], J[29], J[30], J[31]}),
    .minus_2_line(line_10__0_line__out__2_2), .minus_1_line(line_11__0_line__out__1_2),
    ._1_line(line_13__0_line__out__1), ._2_line(line_14__0_line__out__2), .I(i[20]), .Torus(Torus),
    .input_state(input_state), ._0_line__out__2(line_12__0_line__out__2),
    ._0_line__out__1(line_12__0_line__out__1), ._0_line__out__1_2(line_12__0_line__out__1_2),
    ._0_line__out__2_2(line_12__0_line__out__2_2), .display(LINE_20), .clock(clock), .pause(pause));
  line u_line_13 (
    .J({J[0], J[1], J[2], J[3], J[4], J[5], J[6], J[7], J[8], J[9], J[10], J[11], J[12], J[13], J[14], J[15], J[16], J[17], J[18], J[19], J[20], J[21], J[22], J[23], J[24], J[25], J[26], J[27], J[28], J[29], J[30], J[31]}),
    .minus_2_line(line_11__0_line__out__2_2), .minus_1_line(line_12__0_line__out__1_2),
    ._1_line(line_14__0_line__out__1), ._2_line(line_15__0_line__out__2), .I(i[19]), .Torus(Torus),
    .input_state(input_state), ._0_line__out__2(line_13__0_line__out__2),
    ._0_line__out__1(line_13__0_line__out__1), ._0_line__out__1_2(line_13__0_line__out__1_2),
    ._0_line__out__2_2(line_13__0_line__out__2_2), .display(LINE_19), .clock(clock), .pause(pause));
  line u_line_14 (
    .J({J[0], J[1], J[2], J[3], J[4], J[5], J[6], J[7], J[8], J[9], J[10], J[11], J[12], J[13], J[14], J[15], J[16], J[17], J[18], J[19], J[20], J[21], J[22], J[23], J[24], J[25], J[26], J[27], J[28], J[29], J[30], J[31]}),
    .minus_2_line(line_12__0_line__out__2_2), .minus_1_line(line_13__0_line__out__1_2),
    ._1_line(line_15__0_line__out__1), ._2_line(line_16__0_line__out__2), .I(i[18]), .Torus(Torus),
    .input_state(input_state), ._0_line__out__2(line_14__0_line__out__2),
    ._0_line__out__1(line_14__0_line__out__1), ._0_line__out__1_2(line_14__0_line__out__1_2),
    ._0_line__out__2_2(line_14__0_line__out__2_2), .display(LINE_18), .clock(clock), .pause(pause));
  line u_line_15 (
    .J({J[0], J[1], J[2], J[3], J[4], J[5], J[6], J[7], J[8], J[9], J[10], J[11], J[12], J[13], J[14], J[15], J[16], J[17], J[18], J[19], J[20], J[21], J[22], J[23], J[24], J[25], J[26], J[27], J[28], J[29], J[30], J[31]}),
    .minus_2_line(line_13__0_line__out__2_2), .minus_1_line(line_14__0_line__out__1_2),
    ._1_line(line_16__0_line__out__1), ._2_line(line_17__0_line__out__2), .I(i[17]), .Torus(Torus),
    .input_state(input_state), ._0_line__out__2(line_15__0_line__out__2),
    ._0_line__out__1(line_15__0_line__out__1), ._0_line__out__1_2(line_15__0_line__out__1_2),
    ._0_line__out__2_2(line_15__0_line__out__2_2), .display(LINE_17), .clock(clock), .pause(pause));
  line u_line_16 (
    .J({J[0], J[1], J[2], J[3], J[4], J[5], J[6], J[7], J[8], J[9], J[10], J[11], J[12], J[13], J[14], J[15], J[16], J[17], J[18], J[19], J[20], J[21], J[22], J[23], J[24], J[25], J[26], J[27], J[28], J[29], J[30], J[31]}),
    .minus_2_line(line_14__0_line__out__2_2), .minus_1_line(line_15__0_line__out__1_2),
    ._1_line(line_17__0_line__out__1), ._2_line(line_18__0_line__out__2), .I(i[16]), .Torus(Torus),
    .input_state(input_state), ._0_line__out__2(line_16__0_line__out__2),
    ._0_line__out__1(line_16__0_line__out__1), ._0_line__out__1_2(line_16__0_line__out__1_2),
    ._0_line__out__2_2(line_16__0_line__out__2_2), .display(LINE_16), .clock(clock), .pause(pause));
  line u_line_17 (
    .J({J[0], J[1], J[2], J[3], J[4], J[5], J[6], J[7], J[8], J[9], J[10], J[11], J[12], J[13], J[14], J[15], J[16], J[17], J[18], J[19], J[20], J[21], J[22], J[23], J[24], J[25], J[26], J[27], J[28], J[29], J[30], J[31]}),
    .minus_2_line(line_15__0_line__out__2_2), .minus_1_line(line_16__0_line__out__1_2),
    ._1_line(line_18__0_line__out__1), ._2_line(line_19__0_line__out__2), .I(i[15]), .Torus(Torus),
    .input_state(input_state), ._0_line__out__2(line_17__0_line__out__2),
    ._0_line__out__1(line_17__0_line__out__1), ._0_line__out__1_2(line_17__0_line__out__1_2),
    ._0_line__out__2_2(line_17__0_line__out__2_2), .display(LINE_15), .clock(clock), .pause(pause));
  line u_line_18 (
    .J({J[0], J[1], J[2], J[3], J[4], J[5], J[6], J[7], J[8], J[9], J[10], J[11], J[12], J[13], J[14], J[15], J[16], J[17], J[18], J[19], J[20], J[21], J[22], J[23], J[24], J[25], J[26], J[27], J[28], J[29], J[30], J[31]}),
    .minus_2_line(line_16__0_line__out__2_2), .minus_1_line(line_17__0_line__out__1_2),
    ._1_line(line_19__0_line__out__1), ._2_line(line_20__0_line__out__2), .I(i[14]), .Torus(Torus),
    .input_state(input_state), ._0_line__out__2(line_18__0_line__out__2),
    ._0_line__out__1(line_18__0_line__out__1), ._0_line__out__1_2(line_18__0_line__out__1_2),
    ._0_line__out__2_2(line_18__0_line__out__2_2), .display(LINE_14), .clock(clock), .pause(pause));
  line u_line_19 (
    .J({J[0], J[1], J[2], J[3], J[4], J[5], J[6], J[7], J[8], J[9], J[10], J[11], J[12], J[13], J[14], J[15], J[16], J[17], J[18], J[19], J[20], J[21], J[22], J[23], J[24], J[25], J[26], J[27], J[28], J[29], J[30], J[31]}),
    .minus_2_line(line_17__0_line__out__2_2), .minus_1_line(line_18__0_line__out__1_2),
    ._1_line(line_20__0_line__out__1), ._2_line(line_21__0_line__out__2), .I(i[13]), .Torus(Torus),
    .input_state(input_state), ._0_line__out__2(line_19__0_line__out__2),
    ._0_line__out__1(line_19__0_line__out__1), ._0_line__out__1_2(line_19__0_line__out__1_2),
    ._0_line__out__2_2(line_19__0_line__out__2_2), .display(LINE_13), .clock(clock), .pause(pause));
  line u_line_20 (
    .J({J[0], J[1], J[2], J[3], J[4], J[5], J[6], J[7], J[8], J[9], J[10], J[11], J[12], J[13], J[14], J[15], J[16], J[17], J[18], J[19], J[20], J[21], J[22], J[23], J[24], J[25], J[26], J[27], J[28], J[29], J[30], J[31]}),
    .minus_2_line(line_18__0_line__out__2_2), .minus_1_line(line_19__0_line__out__1_2),
    ._1_line(line_21__0_line__out__1), ._2_line(line_22__0_line__out__2), .I(i[12]), .Torus(Torus),
    .input_state(input_state), ._0_line__out__2(line_20__0_line__out__2),
    ._0_line__out__1(line_20__0_line__out__1), ._0_line__out__1_2(line_20__0_line__out__1_2),
    ._0_line__out__2_2(line_20__0_line__out__2_2), .display(LINE_12), .clock(clock), .pause(pause));
  line u_line_21 (
    .J({J[0], J[1], J[2], J[3], J[4], J[5], J[6], J[7], J[8], J[9], J[10], J[11], J[12], J[13], J[14], J[15], J[16], J[17], J[18], J[19], J[20], J[21], J[22], J[23], J[24], J[25], J[26], J[27], J[28], J[29], J[30], J[31]}),
    .minus_2_line(line_19__0_line__out__2_2), .minus_1_line(line_20__0_line__out__1_2),
    ._1_line(line_22__0_line__out__1), ._2_line(line_23__0_line__out__2), .I(i[11]), .Torus(Torus),
    .input_state(input_state), ._0_line__out__2(line_21__0_line__out__2),
    ._0_line__out__1(line_21__0_line__out__1), ._0_line__out__1_2(line_21__0_line__out__1_2),
    ._0_line__out__2_2(line_21__0_line__out__2_2), .display(LINE_11), .clock(clock), .pause(pause));
  line u_line_22 (
    .J({J[0], J[1], J[2], J[3], J[4], J[5], J[6], J[7], J[8], J[9], J[10], J[11], J[12], J[13], J[14], J[15], J[16], J[17], J[18], J[19], J[20], J[21], J[22], J[23], J[24], J[25], J[26], J[27], J[28], J[29], J[30], J[31]}),
    .minus_2_line(line_20__0_line__out__2_2), .minus_1_line(line_21__0_line__out__1_2),
    ._1_line(line_23__0_line__out__1), ._2_line(line_24__0_line__out__2), .I(i[10]), .Torus(Torus),
    .input_state(input_state), ._0_line__out__2(line_22__0_line__out__2),
    ._0_line__out__1(line_22__0_line__out__1), ._0_line__out__1_2(line_22__0_line__out__1_2),
    ._0_line__out__2_2(line_22__0_line__out__2_2), .display(LINE_10), .clock(clock), .pause(pause));
  line u_line_23 (
    .J({J[0], J[1], J[2], J[3], J[4], J[5], J[6], J[7], J[8], J[9], J[10], J[11], J[12], J[13], J[14], J[15], J[16], J[17], J[18], J[19], J[20], J[21], J[22], J[23], J[24], J[25], J[26], J[27], J[28], J[29], J[30], J[31]}),
    .minus_2_line(line_21__0_line__out__2_2), .minus_1_line(line_22__0_line__out__1_2),
    ._1_line(line_24__0_line__out__1), ._2_line(line_25__0_line__out__2), .I(i[9]), .Torus(Torus),
    .input_state(input_state), ._0_line__out__2(line_23__0_line__out__2),
    ._0_line__out__1(line_23__0_line__out__1), ._0_line__out__1_2(line_23__0_line__out__1_2),
    ._0_line__out__2_2(line_23__0_line__out__2_2), .display(LINE_9), .clock(clock), .pause(pause));
  line u_line_24 (
    .J({J[0], J[1], J[2], J[3], J[4], J[5], J[6], J[7], J[8], J[9], J[10], J[11], J[12], J[13], J[14], J[15], J[16], J[17], J[18], J[19], J[20], J[21], J[22], J[23], J[24], J[25], J[26], J[27], J[28], J[29], J[30], J[31]}),
    .minus_2_line(line_22__0_line__out__2_2), .minus_1_line(line_23__0_line__out__1_2),
    ._1_line(line_25__0_line__out__1), ._2_line(line_26__0_line__out__2), .I(i[8]), .Torus(Torus),
    .input_state(input_state), ._0_line__out__2(line_24__0_line__out__2),
    ._0_line__out__1(line_24__0_line__out__1), ._0_line__out__1_2(line_24__0_line__out__1_2),
    ._0_line__out__2_2(line_24__0_line__out__2_2), .display(LINE_8), .clock(clock), .pause(pause));
  line u_line_25 (
    .J({J[0], J[1], J[2], J[3], J[4], J[5], J[6], J[7], J[8], J[9], J[10], J[11], J[12], J[13], J[14], J[15], J[16], J[17], J[18], J[19], J[20], J[21], J[22], J[23], J[24], J[25], J[26], J[27], J[28], J[29], J[30], J[31]}),
    .minus_2_line(line_23__0_line__out__2_2), .minus_1_line(line_24__0_line__out__1_2),
    ._1_line(line_26__0_line__out__1), ._2_line(line_27__0_line__out__2), .I(i[7]), .Torus(Torus),
    .input_state(input_state), ._0_line__out__2(line_25__0_line__out__2),
    ._0_line__out__1(line_25__0_line__out__1), ._0_line__out__1_2(line_25__0_line__out__1_2),
    ._0_line__out__2_2(line_25__0_line__out__2_2), .display(LINE_7), .clock(clock), .pause(pause));
  line u_line_26 (
    .J({J[0], J[1], J[2], J[3], J[4], J[5], J[6], J[7], J[8], J[9], J[10], J[11], J[12], J[13], J[14], J[15], J[16], J[17], J[18], J[19], J[20], J[21], J[22], J[23], J[24], J[25], J[26], J[27], J[28], J[29], J[30], J[31]}),
    .minus_2_line(line_24__0_line__out__2_2), .minus_1_line(line_25__0_line__out__1_2),
    ._1_line(line_27__0_line__out__1), ._2_line(line_28__0_line__out__2), .I(i[6]), .Torus(Torus),
    .input_state(input_state), ._0_line__out__2(line_26__0_line__out__2),
    ._0_line__out__1(line_26__0_line__out__1), ._0_line__out__1_2(line_26__0_line__out__1_2),
    ._0_line__out__2_2(line_26__0_line__out__2_2), .display(LINE_6), .clock(clock), .pause(pause));
  line u_line_27 (
    .J({J[0], J[1], J[2], J[3], J[4], J[5], J[6], J[7], J[8], J[9], J[10], J[11], J[12], J[13], J[14], J[15], J[16], J[17], J[18], J[19], J[20], J[21], J[22], J[23], J[24], J[25], J[26], J[27], J[28], J[29], J[30], J[31]}),
    .minus_2_line(line_25__0_line__out__2_2), .minus_1_line(line_26__0_line__out__1_2),
    ._1_line(line_28__0_line__out__1), ._2_line(line_29__0_line__out__2), .I(i[5]), .Torus(Torus),
    .input_state(input_state), ._0_line__out__2(line_27__0_line__out__2),
    ._0_line__out__1(line_27__0_line__out__1), ._0_line__out__1_2(line_27__0_line__out__1_2),
    ._0_line__out__2_2(line_27__0_line__out__2_2), .display(LINE_5), .clock(clock), .pause(pause));
  line u_line_28 (
    .J({J[0], J[1], J[2], J[3], J[4], J[5], J[6], J[7], J[8], J[9], J[10], J[11], J[12], J[13], J[14], J[15], J[16], J[17], J[18], J[19], J[20], J[21], J[22], J[23], J[24], J[25], J[26], J[27], J[28], J[29], J[30], J[31]}),
    .minus_2_line(line_26__0_line__out__2_2), .minus_1_line(line_27__0_line__out__1_2),
    ._1_line(line_29__0_line__out__1), ._2_line(line_30__0_line__out__2), .I(i[4]), .Torus(Torus),
    .input_state(input_state), ._0_line__out__2(line_28__0_line__out__2),
    ._0_line__out__1(line_28__0_line__out__1), ._0_line__out__1_2(line_28__0_line__out__1_2),
    ._0_line__out__2_2(line_28__0_line__out__2_2), .display(LINE_4), .clock(clock), .pause(pause));
  line u_line_29 (
    .J({J[0], J[1], J[2], J[3], J[4], J[5], J[6], J[7], J[8], J[9], J[10], J[11], J[12], J[13], J[14], J[15], J[16], J[17], J[18], J[19], J[20], J[21], J[22], J[23], J[24], J[25], J[26], J[27], J[28], J[29], J[30], J[31]}),
    .minus_2_line(line_27__0_line__out__2_2), .minus_1_line(line_28__0_line__out__1_2),
    ._1_line(line_30__0_line__out__1), ._2_line(line_31__0_line__out__2), .I(i[3]), .Torus(Torus),
    .input_state(input_state), ._0_line__out__2(line_29__0_line__out__2),
    ._0_line__out__1(line_29__0_line__out__1), ._0_line__out__1_2(line_29__0_line__out__1_2),
    ._0_line__out__2_2(line_29__0_line__out__2_2), .display(LINE_3), .clock(clock), .pause(pause));
  line u_line_30 (
    .J({J[0], J[1], J[2], J[3], J[4], J[5], J[6], J[7], J[8], J[9], J[10], J[11], J[12], J[13], J[14], J[15], J[16], J[17], J[18], J[19], J[20], J[21], J[22], J[23], J[24], J[25], J[26], J[27], J[28], J[29], J[30], J[31]}),
    .minus_2_line(line_28__0_line__out__2_2), .minus_1_line(line_29__0_line__out__1_2),
    ._1_line(line_31__0_line__out__1), ._2_line(line_32__0_line__out__2), .I(i[2]), .Torus(Torus),
    .input_state(input_state), ._0_line__out__2(line_30__0_line__out__2),
    ._0_line__out__1(line_30__0_line__out__1), ._0_line__out__1_2(line_30__0_line__out__1_2),
    ._0_line__out__2_2(line_30__0_line__out__2_2), .display(LINE_2), .clock(clock), .pause(pause));
  line u_line_31 (
    .J({J[0], J[1], J[2], J[3], J[4], J[5], J[6], J[7], J[8], J[9], J[10], J[11], J[12], J[13], J[14], J[15], J[16], J[17], J[18], J[19], J[20], J[21], J[22], J[23], J[24], J[25], J[26], J[27], J[28], J[29], J[30], J[31]}),
    .minus_2_line(line_29__0_line__out__2_2), .minus_1_line(line_30__0_line__out__1_2),
    ._1_line(line_32__0_line__out__1), ._2_line(minus_01), .I(i[1]), .Torus(Torus),
    .input_state(input_state), ._0_line__out__2(line_31__0_line__out__2),
    ._0_line__out__1(line_31__0_line__out__1), ._0_line__out__1_2(line_31__0_line__out__1_2),
    ._0_line__out__2_2(plus_32), .display(LINE_1), .clock(clock), .pause(pause));
  line line_32 (
    .J({J[0], J[1], J[2], J[3], J[4], J[5], J[6], J[7], J[8], J[9], J[10], J[11], J[12], J[13], J[14], J[15], J[16], J[17], J[18], J[19], J[20], J[21], J[22], J[23], J[24], J[25], J[26], J[27], J[28], J[29], J[30], J[31]}),
    .minus_2_line(line_30__0_line__out__2_2), .minus_1_line(line_31__0_line__out__1_2), ._1_line(and_4_out),
    ._2_line(minus_02), .I(i[0]), .Torus(Torus), .input_state(input_state),
    ._0_line__out__2(line_32__0_line__out__2), ._0_line__out__1(line_32__0_line__out__1),
    ._0_line__out__1_2(plus_32_star), ._0_line__out__2_2(plus_33), .display(LINE_0), .clock(clock),
    .pause(pause));

  // Other names for the same wires on the sheet: i31 = i[0]; i30 = i[1]; i29 = i[2]; i28 = i[3]; i27 = i[4];
  //   i26 = i[5]; i25 = i[6]; i24 = i[7]; i23 = i[8]; i22 = i[9]; i21 = i[10]; i20 = i[11]; i19 = i[12]; i18 = i[13];
  //   i17 = i[14]; i16 = i[15]; i15 = i[16]; i14 = i[17]; i13 = i[18]; i12 = i[19]; i11 = i[20]; i10 = i[21];
  //   i9 = i[22]; i8 = i[23]; i7 = i[24]; i6 = i[25]; i5 = i[26]; i4 = i[27]; i3 = i[28]; i2 = i[29]; i1 = i[30];
  //   i0 = i[31];
  //   J_t[31:0] = {J[0], J[1], J[2], J[3], J[4], J[5], J[6], J[7], J[8], J[9], J[10], J[11], J[12], J[13], J[14], J[15], J[16], J[17], J[18], J[19], J[20], J[21], J[22], J[23], J[24], J[25], J[26], J[27], J[28], J[29], J[30], J[31]};
  //   state[1:0] = input_state

  // Notes on the sheet:
  //   LINE_17: pull=down
  //   LINE_15: pull=down
  //   LINE_8: pull=down
  //   LINE_28: pull=down
  //   LINE_1: pull=down
  //   LINE_29: pull=down
  //   LINE_20: pull=down
  //   LINE_21: pull=down
  //   LINE_24: pull=down
  //   LINE_30: pull=down
  //   LINE_10: pull=down
  //   LINE_9: pull=down
  //   LINE_22: pull=down
  //   LINE_11: pull=down
  //   LINE_6: pull=down
  //   LINE_12: pull=down
  //   LINE_27: pull=down
  //   LINE_23: pull=down
  //   LINE_0: pull=down
  //   LINE_16: pull=down
  //   LINE_4: pull=down
  //   LINE_25: pull=down
  //   LINE_14: pull=down
  //   LINE_5: pull=down
  //   LINE_2: pull=down
  //   LINE_26: pull=down
  //   LINE_7: pull=down
  //   LINE_31: pull=down
  //   LINE_19: pull=down
  //   LINE_3: pull=down
  //   LINE_13: pull=down
  //   LINE_18: pull=down
  //   00 — old
  //   01 — invert
  //   10 — set DEAD
  //   11 — set ALIVE
endmodule
module gameSTD (
  input  in_1,
  input  [31:0] i,
  input  in_3,
  input  in_4,
  input  [31:0] j,
  input  torus,
  input  [1:0] state,
  input  pause
);

  wire clock_1_out;
  wire [31:0] matrixstd_1_line_0, matrixstd_1_line_1, matrixstd_1_line_2, matrixstd_1_line_3,
       matrixstd_1_line_4, matrixstd_1_line_5, matrixstd_1_line_6, matrixstd_1_line_7, matrixstd_1_line_8,
       matrixstd_1_line_9, matrixstd_1_line_10, matrixstd_1_line_11, matrixstd_1_line_12,
       matrixstd_1_line_13, matrixstd_1_line_14, matrixstd_1_line_15, matrixstd_1_line_16,
       matrixstd_1_line_17, matrixstd_1_line_18, matrixstd_1_line_19, matrixstd_1_line_20,
       matrixstd_1_line_21, matrixstd_1_line_22, matrixstd_1_line_23, matrixstd_1_line_24,
       matrixstd_1_line_25, matrixstd_1_line_26, matrixstd_1_line_27, matrixstd_1_line_28,
       matrixstd_1_line_29, matrixstd_1_line_30, matrixstd_1_line_31, multiplexer_1_out, multiplexer_2_out,
       multiplexer_3_out;

  Multiplexer #(.width(32)) multiplexer_1 (
    .in0({32{1'b0}}), .in1({32{1'b1}}), .out(multiplexer_1_out), .sel(in_1));  // open: en
  Multiplexer #(.width(32)) multiplexer_2 (
    .in0(i), .in1(multiplexer_1_out), .out(multiplexer_2_out), .sel(in_3));  // open: en
  Multiplexer #(.width(32)) multiplexer_3 (
    .in0(j), .in1(multiplexer_1_out), .out(multiplexer_3_out), .sel(in_4));  // open: en
  Clock clock_1 (.out(clock_1_out));
  matrixSTD matrixstd_1 (
    .i(multiplexer_2_out), .J(multiplexer_3_out), .Torus(torus), .input_state(state), .clock(clock_1_out),
    .pause(pause), .LINE_31(matrixstd_1_line_31), .LINE_30(matrixstd_1_line_30),
    .LINE_29(matrixstd_1_line_29), .LINE_28(matrixstd_1_line_28), .LINE_27(matrixstd_1_line_27),
    .LINE_26(matrixstd_1_line_26), .LINE_25(matrixstd_1_line_25), .LINE_24(matrixstd_1_line_24),
    .LINE_23(matrixstd_1_line_23), .LINE_22(matrixstd_1_line_22), .LINE_21(matrixstd_1_line_21),
    .LINE_20(matrixstd_1_line_20), .LINE_19(matrixstd_1_line_19), .LINE_18(matrixstd_1_line_18),
    .LINE_17(matrixstd_1_line_17), .LINE_16(matrixstd_1_line_16), .LINE_15(matrixstd_1_line_15),
    .LINE_14(matrixstd_1_line_14), .LINE_13(matrixstd_1_line_13), .LINE_12(matrixstd_1_line_12),
    .LINE_11(matrixstd_1_line_11), .LINE_10(matrixstd_1_line_10), .LINE_9(matrixstd_1_line_9),
    .LINE_8(matrixstd_1_line_8), .LINE_7(matrixstd_1_line_7), .LINE_6(matrixstd_1_line_6),
    .LINE_5(matrixstd_1_line_5), .LINE_4(matrixstd_1_line_4), .LINE_3(matrixstd_1_line_3),
    .LINE_2(matrixstd_1_line_2), .LINE_1(matrixstd_1_line_1), .LINE_0(matrixstd_1_line_0));
  DotMatrix #(.inputtype("row"), .matrixcols(32), .matrixrows(32)) dotmatrix_1 (
    .row0(matrixstd_1_line_31), .row1(matrixstd_1_line_30), .row2(matrixstd_1_line_29),
    .row3(matrixstd_1_line_28), .row4(matrixstd_1_line_27), .row5(matrixstd_1_line_26),
    .row6(matrixstd_1_line_25), .row7(matrixstd_1_line_24), .row8(matrixstd_1_line_23),
    .row9(matrixstd_1_line_22), .row10(matrixstd_1_line_21), .row11(matrixstd_1_line_20),
    .row12(matrixstd_1_line_19), .row13(matrixstd_1_line_18), .row14(matrixstd_1_line_17),
    .row15(matrixstd_1_line_16), .row16(matrixstd_1_line_15), .row17(matrixstd_1_line_14),
    .row18(matrixstd_1_line_13), .row19(matrixstd_1_line_12), .row20(matrixstd_1_line_11),
    .row21(matrixstd_1_line_10), .row22(matrixstd_1_line_9), .row23(matrixstd_1_line_8),
    .row24(matrixstd_1_line_7), .row25(matrixstd_1_line_6), .row26(matrixstd_1_line_5),
    .row27(matrixstd_1_line_4), .row28(matrixstd_1_line_3), .row29(matrixstd_1_line_2),
    .row30(matrixstd_1_line_1), .row31(matrixstd_1_line_0));

  // Notes on the sheet:
  //   00 — old
  //   01 — invert
  //   10 — set DEAD
  //   11 — set ALIVE
endmodule

module game (
  input  in_1,
  input  [31:0] i,
  input  in_3,
  input  in_4,
  input  torus,
  input  [1:0] state,
  input  [31:0] j,
  input  pause
);

  wire clock_1_out;
  wire [31:0] matrix_1_line_0, matrix_1_line_1, matrix_1_line_2, matrix_1_line_3, matrix_1_line_4,
       matrix_1_line_5, matrix_1_line_6, matrix_1_line_7, matrix_1_line_8, matrix_1_line_9, matrix_1_line_10,
       matrix_1_line_11, matrix_1_line_12, matrix_1_line_13, matrix_1_line_14, matrix_1_line_15,
       matrix_1_line_16, matrix_1_line_17, matrix_1_line_18, matrix_1_line_19, matrix_1_line_20,
       matrix_1_line_21, matrix_1_line_22, matrix_1_line_23, matrix_1_line_24, matrix_1_line_25,
       matrix_1_line_26, matrix_1_line_27, matrix_1_line_28, matrix_1_line_29, matrix_1_line_30,
       matrix_1_line_31, multiplexer_1_out, multiplexer_2_out, multiplexer_3_out;

  Multiplexer #(.width(32)) multiplexer_1 (
    .in0({32{1'b0}}), .in1({32{1'b1}}), .out(multiplexer_1_out), .sel(in_1));  // open: en
  Multiplexer #(.width(32)) multiplexer_2 (
    .in0(i), .in1(multiplexer_1_out), .out(multiplexer_2_out), .sel(in_3));  // open: en
  Multiplexer #(.width(32)) multiplexer_3 (
    .in0(j), .in1(multiplexer_1_out), .out(multiplexer_3_out), .sel(in_4));  // open: en
  Clock clock_1 (.out(clock_1_out));
  matrix matrix_1 (
    .i(multiplexer_2_out), .J(multiplexer_3_out), .Torus(torus), .input_state(state),
    .LINE_0(matrix_1_line_0), .LINE_1(matrix_1_line_1), .LINE_2(matrix_1_line_2), .LINE_3(matrix_1_line_3),
    .LINE_4(matrix_1_line_4), .LINE_5(matrix_1_line_5), .LINE_6(matrix_1_line_6), .LINE_7(matrix_1_line_7),
    .LINE_8(matrix_1_line_8), .LINE_9(matrix_1_line_9), .LINE_10(matrix_1_line_10),
    .LINE_11(matrix_1_line_11), .LINE_12(matrix_1_line_12), .LINE_13(matrix_1_line_13),
    .LINE_14(matrix_1_line_14), .LINE_15(matrix_1_line_15), .LINE_16(matrix_1_line_16),
    .LINE_17(matrix_1_line_17), .LINE_18(matrix_1_line_18), .LINE_19(matrix_1_line_19),
    .LINE_20(matrix_1_line_20), .LINE_21(matrix_1_line_21), .LINE_22(matrix_1_line_22),
    .LINE_23(matrix_1_line_23), .LINE_24(matrix_1_line_24), .LINE_25(matrix_1_line_25),
    .LINE_26(matrix_1_line_26), .LINE_27(matrix_1_line_27), .LINE_28(matrix_1_line_28),
    .LINE_29(matrix_1_line_29), .LINE_30(matrix_1_line_30), .LINE_31(matrix_1_line_31), .clock(clock_1_out),
    .pause(pause));
  DotMatrix #(.inputtype("row"), .matrixcols(32), .matrixrows(32)) dotmatrix_1 (
    .row0(matrix_1_line_0), .row1(matrix_1_line_1), .row2(matrix_1_line_2), .row3(matrix_1_line_3),
    .row4(matrix_1_line_4), .row5(matrix_1_line_5), .row6(matrix_1_line_6), .row7(matrix_1_line_7),
    .row8(matrix_1_line_8), .row9(matrix_1_line_9), .row10(matrix_1_line_10), .row11(matrix_1_line_11),
    .row12(matrix_1_line_12), .row13(matrix_1_line_13), .row14(matrix_1_line_14), .row15(matrix_1_line_15),
    .row16(matrix_1_line_16), .row17(matrix_1_line_17), .row18(matrix_1_line_18), .row19(matrix_1_line_19),
    .row20(matrix_1_line_20), .row21(matrix_1_line_21), .row22(matrix_1_line_22), .row23(matrix_1_line_23),
    .row24(matrix_1_line_24), .row25(matrix_1_line_25), .row26(matrix_1_line_26), .row27(matrix_1_line_27),
    .row28(matrix_1_line_28), .row29(matrix_1_line_29), .row30(matrix_1_line_30), .row31(matrix_1_line_31));

  // Notes on the sheet:
  //   00 — old
  //   01 — invert
  //   10 — set DEAD
  //   11 — set ALIVE
endmodule
